// Logisim project CS1501_U201514477_华龙_cpu_prediction.circ as structural Verilog: 11 circuits, main circuit MIPS CPU
module MIPS_CPU (
);

  wire alu_1_equal, and_1_out, and_7_out, and_8_out, branch, branch_succeed, clk, clock_1_out, d_ff_1_qn,
       d_ff_2_qn, d_ff_3_qn, Din__DM, Din__DM_half, Din__PC_1, DM_WE, ex_mem_1_mem_halt, EX_RF_WE, goto,
       halting, hit, id_ex_1_ex_predict, if_id_1_id_predict, IR1, IR2, IR3, jump, Load_Use, lock, MEM_RF_WE,
       not_1_out, not_2_out, not_3_out, not_4_out, not_5_out, or_3_out, predictor_1_predict_will_branch,
       pull_resistor_4_node, pull_resistor_5_node, pull_resistor_6_node, rA___v0, rB___a0, rectify,
       redirecter_1_redirect_rf_a, redirecter_1_redirect_rf_b, RST, rW__GPR_31, rW__rd, stop, syscall, W1,
       W2, W3, WB_RF_WE, Wrong_Prediction, X__RF_B, Y__RF_A, Y__S_EXT, \单步执行_out ;
  wire [3:0] ALUOP;
  wire [4:0] EX_rW, MEM_rW, multiplexer_1_out, multiplexer_2_out, multiplexer_4_out, registerfile_1_p8, WB_rW;
  wire [5:0] EX_OP;
  wire [11:0] and_2_out, and_3_out, and_4_out, and_5_out, and_6_out;
  wire [15:0] Count, \load_use次数 , multiplexer_11_out, \插入气泡数 , \无条件分支指令数 , \有条件分支成功跳转 ;
  wire [25:0] id_ex_1_ex_ir;
  wire [27:0] id_ex_1_ex_ctrl;
  wire [31:0] \controller_1_控制信号 , EX_Data, ex_mem_1_mem_alu_r, ex_mem_1_mem_ctrl, ex_mem_1_mem_pc_1,
       ex_mem_1_mem_rf_b, EX_PC, EX_PC_1, extender_1_imm, goto_addr, id_ex_1_ex_imm, id_ex_1_ex_rf_a,
       id_ex_1_ex_rf_b, ID_PC, if_id_1_id_ir, if_id_1_id_pc_1, IF_PC, MEM_Data, MEM_PC, mem_wb_1_wb_alu_r,
       mem_wb_1_wb_ctrl, mem_wb_1_wb_dm_d, mem_wb_1_wb_pc_1, mips_ram_1_p6, multiplexer_5_out,
       multiplexer_6_out, multiplexer_7_out, multiplexer_8_out, multiplexer_9_out, multiplexer_12_out,
       multiplexer_13_out, predictor_1_next_pc, predictor_1_pc_1, redirecter_1_redirected_rf_a,
       redirecter_1_redirected_rf_b, registerfile_1_p9, registerfile_1_p10, RF_W, rom_1_data, SyscallOut,
       WB_PC;

  Button \u_总复位  (.out(RST));
  Button _1 (.out(IR1));
  Button _2 (.out(IR2));
  Button _3 (.out(IR3));
  LED led_1 (.in(W1));
  LED led_2 (.in(W2));
  LED led_3 (.in(W3));
  // Probe on predictor_1_next_pc
  not not_1 (not_1_out, lock);
  Hex_Digit_Display hex_digit_display_1 (.value(SyscallOut[31:28]));  // open: dp
  Register #(.width(32)) PC (.D(predictor_1_next_pc), .en(not_1_out), .Q(IF_PC), .clk(clk), .clr(RST));
  Hex_Digit_Display hex_digit_display_2 (.value(SyscallOut[23:20]));  // open: dp
  Hex_Digit_Display hex_digit_display_3 (.value(SyscallOut[27:24]));  // open: dp
  Predictor predictor_1 (
    .goto_addr(goto_addr), .PC(IF_PC), .PC_1(predictor_1_pc_1),
    .Predict_will_branch(predictor_1_predict_will_branch), .next_PC(predictor_1_next_pc), .EX_PC(EX_PC),
    .Hit(hit), .clk(clk), .Reset(RST), .Wrong_Prediction(Wrong_Prediction), .goto(goto),
    .branch_success(branch_succeed), .rectify(rectify), .EX_PC_2(EX_PC_1));
  Hex_Digit_Display hex_digit_display_4 (.value(SyscallOut[19:16]));  // open: dp
  Hex_Digit_Display hex_digit_display_5 (.value(SyscallOut[15:12]));  // open: dp
  or or_1 (lock, stop, and_1_out);
  and and_1 (and_1_out, ~rectify, Load_Use);  // AND_Gate
  Hex_Digit_Display hex_digit_display_6 (.value(SyscallOut[11:8]));  // open: dp
  Hex_Digit_Display hex_digit_display_7 (.value(SyscallOut[7:4]));  // open: dp
  // Probe on IF_PC
  ROM #(.addrWidth(10), .dataWidth(32)) rom_1 (.addr(IF_PC[11:2]), .data(rom_1_data));  // open: sel
  not not_2 (not_2_out, lock);
  Hex_Digit_Display hex_digit_display_8 (.value(SyscallOut[3:0]));  // open: dp
  IF_ID if_id_1 (
    .IF_PC(IF_PC), .ID_PC(ID_PC), .lock_when_0_stop_transport(not_2_out), .CLK(clk), .\同步清零 (rectify),
    .IF_PC_1(predictor_1_pc_1), .ID_PC_1(if_id_1_id_pc_1), .IF_IR(rom_1_data), .ID_IR(if_id_1_id_ir),
    .IF_Predict(predictor_1_predict_will_branch), .ID_Predict(if_id_1_id_predict));
  Pull_Resistor pull_resistor_1 (.node(rectify));
  Pull_Resistor #(.pull(1)) pull_resistor_2 (.node(not_2_out));
  Controller controller_1 (
    .OP(if_id_1_id_ir[31:26]), .Funct(if_id_1_id_ir[5:0]),
    .\控制信号 ({\controller_1_控制信号 [31:28], rA___v0, rB___a0, rW__rd, rW__GPR_31, \controller_1_控制信号 [23:0]}));
  // Probe on Count
  // Probe on \无条件分支指令数 
  // Probe on \有条件分支成功跳转 
  // Probe on \load_use次数 
  // Probe on \插入气泡数 
  // Probe on RF_W
  Extender extender_1 (
    .extend_IMM(\controller_1_控制信号 [15]), .extend_shamt(\controller_1_控制信号 [16]), .IR(if_id_1_id_ir),
    .zero_extend_IMM(\controller_1_控制信号 [14]), .IMM(extender_1_imm));
  // Probe on WB_rW
  Multiplexer #(.width(5), .enable("false")) multiplexer_1 (
    .in0(if_id_1_id_ir[25:21]), .in1(5'b00010), .out(multiplexer_1_out), .sel(rA___v0));
  Multiplexer #(.width(5), .enable("false")) multiplexer_2 (
    .in0(if_id_1_id_ir[20:16]), .in1(if_id_1_id_ir[15:11]), .out(multiplexer_2_out), .sel(rW__rd));
  // RegisterFile registerfile_1: pin names not known; wires that end beside it: if_id_1_id_ir[31:26], if_id_1_id_ir[5:0], RF_W, clk, WB_RF_WE, WB_rW, multiplexer_1_out, registerfile_1_p8, registerfile_1_p9, registerfile_1_p10
  Multiplexer #(.width(5), .enable("false")) multiplexer_3 (
    .in0(if_id_1_id_ir[20:16]), .in1(5'b00100), .out(registerfile_1_p8), .sel(rB___a0));
  Multiplexer #(.width(5), .enable("false")) multiplexer_4 (
    .in0(multiplexer_2_out), .in1({5{1'b1}}), .out(multiplexer_4_out), .sel(rW__GPR_31));
  // Probe on Count
  assign and_2_out = IF_PC[11:0] & {12{1'b1}};  // AND_Gate and_2, 12 bits wide
  // Probe on and_2_out
  assign and_3_out = ID_PC[11:0] & {12{1'b1}};  // AND_Gate and_3, 12 bits wide
  // Probe on and_3_out
  assign and_4_out = EX_PC[11:0] & {12{1'b1}};  // AND_Gate and_4, 12 bits wide
  // Probe on and_4_out
  assign and_5_out = MEM_PC[11:0] & {12{1'b1}};  // AND_Gate and_5, 12 bits wide
  // Probe on and_5_out
  assign and_6_out = WB_PC[11:0] & {12{1'b1}};  // AND_Gate and_6, 12 bits wide
  // Probe on and_6_out
  // Probe on ID_PC
  Multiplexer #(.width(32), .enable("false")) multiplexer_5 (
    .in0(registerfile_1_p9), .in1(redirecter_1_redirected_rf_a), .out(multiplexer_5_out),
    .sel(redirecter_1_redirect_rf_a));
  Redirecter redirecter_1 (
    .EX_rW(EX_rW), .rA(multiplexer_1_out), .rB(registerfile_1_p8), .MEM_rW(MEM_rW), .EX_RF_WE(EX_RF_WE),
    .MEM_RF_WE(MEM_RF_WE), .Load_Use(Load_Use), .EX_OP(EX_OP),
    .Control_signals({\controller_1_控制信号 [31:28], rA___v0, rB___a0, rW__rd, rW__GPR_31, \controller_1_控制信号 [23:0]}),
    .redirected_RF_A(redirecter_1_redirected_rf_a), .redirected_RF_B(redirecter_1_redirected_rf_b),
    .EX_Data(EX_Data), .MEM_Data(MEM_Data), .redirect_RF_A(redirecter_1_redirect_rf_a),
    .redirect_RF_B(redirecter_1_redirect_rf_b));
  Multiplexer #(.width(32), .enable("false")) multiplexer_6 (
    .in0(registerfile_1_p10), .in1(redirecter_1_redirected_rf_b), .out(multiplexer_6_out),
    .sel(redirecter_1_redirect_rf_b));
  not not_3 (not_3_out, stop);
  // Probe on EX_PC
  ID_EX id_ex_1 (
    .CLK(clk), .\同步清零 (pull_resistor_4_node), .ID_PC(ID_PC), .EX_PC(EX_PC), .ID_PC_1(if_id_1_id_pc_1),
    .EX_PC_1(EX_PC_1), .ID_IR(if_id_1_id_ir), .EX_IR({EX_OP, id_ex_1_ex_ir}),
    .lock_when_0_stop_transport(not_3_out),
    .ID_CTRL({\controller_1_控制信号 [31:28], rA___v0, rB___a0, rW__rd, rW__GPR_31, \controller_1_控制信号 [23:0]}),
    .EX_CTRL({ALUOP, id_ex_1_ex_ctrl[27:24], EX_RF_WE, id_ex_1_ex_ctrl[22:20], X__RF_B, Y__RF_A, Y__S_EXT, id_ex_1_ex_ctrl[16:9], syscall, id_ex_1_ex_ctrl[7:0]}),
    .ID_RF_A(multiplexer_5_out), .EX_RF_A(id_ex_1_ex_rf_a), .ID_RF_B(multiplexer_6_out),
    .EX_RF_B(id_ex_1_ex_rf_b), .ID_IMM(extender_1_imm), .EX_IMM(id_ex_1_ex_imm), .ID_rW(multiplexer_4_out),
    .EX_rW(EX_rW), .ID_Predict(if_id_1_id_predict), .EX_Predict(id_ex_1_ex_predict));
  Pull_Resistor #(.pull(1)) pull_resistor_3 (.node(not_3_out));
  Pull_Resistor pull_resistor_4 (.node(pull_resistor_4_node));
  D_Flip_Flop d_ff_1 (.clk(clk), .D(stop), .Qn(d_ff_1_qn), .reset(RST));  // open: Q, preset, en
  Counter #(.width(16), .max('hffff), .trigger("falling")) \u_总周期计数  (
    .count(d_ff_1_qn), .Q(Count), .clk(clk), .clr(RST));  // open: load, D, carry
  Clock clock_1 (.out(clock_1_out));
  xor xor_1 (clk, clock_1_out, \单步执行_out );
  Button \u_单步执行  (.out(\单步执行_out ));
  or or_2 (pull_resistor_4_node, halting, rectify, Load_Use);
  // Probe on EX_rW
  // Probe on MEM_PC
  NPC npc_1 (
    .ALU_R(EX_Data),
    .CTRL({ALUOP, id_ex_1_ex_ctrl[27:24], EX_RF_WE, id_ex_1_ex_ctrl[22:20], X__RF_B, Y__RF_A, Y__S_EXT, id_ex_1_ex_ctrl[16:9], syscall, id_ex_1_ex_ctrl[7:0]}),
    .IMM(id_ex_1_ex_imm), .PC_1(EX_PC_1), .IR({EX_OP, id_ex_1_ex_ir}), .RF_A(id_ex_1_ex_rf_a),
    .\goto_跳转 (goto), .\jump_无条件跳转 (jump), .\goto_addr_跳转地址 (goto_addr), .ALU_Equal(alu_1_equal),
    .branch_instruction(branch), .\branch_success_成功跳转 (branch_succeed));
  Multiplexer #(.width(32), .enable("false")) multiplexer_7 (
    .in0(id_ex_1_ex_rf_a), .in1(id_ex_1_ex_rf_b), .out(multiplexer_7_out), .sel(X__RF_B));
  Multiplexer #(.width(32), .enable("false")) multiplexer_8 (
    .in0(id_ex_1_ex_rf_b), .in1(id_ex_1_ex_rf_a), .out(multiplexer_8_out), .sel(Y__RF_A));
  Multiplexer #(.width(32), .enable("false")) multiplexer_9 (
    .in0(multiplexer_8_out), .in1(id_ex_1_ex_imm), .out(multiplexer_9_out), .sel(Y__S_EXT));
  D_Flip_Flop d_ff_2 (.clk(clk), .D(not_4_out), .Qn(d_ff_2_qn), .preset(RST));  // open: Q, en, reset
  not not_4 (not_4_out, jump);
  xor xor_2 (Wrong_Prediction, id_ex_1_ex_predict, goto);
  ALU alu_1 (
    .X(multiplexer_7_out), .Y(multiplexer_9_out), .AluOP(ALUOP), .Equal(alu_1_equal), .Result(EX_Data));  // open: Signed_Overflow, UnSigned_Overflow, Result_2
  Counter #(.width(16), .max('hffff), .trigger("falling")) \u_无条件分支指令计数  (
    .count(d_ff_2_qn), .Q(\无条件分支指令数 ), .clk(clk), .clr(RST));  // open: load, D, carry
  Counter #(.width(16), .max('hffff), .trigger("falling")) \Load_Use计数  (
    .count(Load_Use), .Q(\load_use次数 ), .clk(clk), .clr(RST));  // open: load, D, carry
  // Probe on WB_PC
  and and_7 (and_7_out, alu_1_equal, syscall);
  and and_8 (and_8_out, ~alu_1_equal, syscall);  // AND_Gate
  // Probe on EX_Data
  Register #(.width(32)) \u_数码管锁存  (.D(id_ex_1_ex_rf_b), .en(and_8_out), .Q(SyscallOut), .clk(clk), .clr(RST));
  not not_5 (not_5_out, branch_succeed);
  EX_MEM ex_mem_1 (
    .CLK(clk), .\同步清零 (pull_resistor_6_node), .EX_PC(EX_PC), .MEM_PC(MEM_PC), .EX_PC_1(EX_PC_1),
    .MEM_PC_1(ex_mem_1_mem_pc_1),
    .EX_CTRL({ALUOP, id_ex_1_ex_ctrl[27:24], EX_RF_WE, id_ex_1_ex_ctrl[22:20], X__RF_B, Y__RF_A, Y__S_EXT, id_ex_1_ex_ctrl[16:9], syscall, id_ex_1_ex_ctrl[7:0]}),
    .MEM_CTRL({ex_mem_1_mem_ctrl[31:24], MEM_RF_WE, ex_mem_1_mem_ctrl[22:8], DM_WE, ex_mem_1_mem_ctrl[6:0]}),
    .lock_when_0_stop_transport(pull_resistor_5_node), .EX_rW(EX_rW), .MEM_rW(MEM_rW),
    .EX_RF_B(id_ex_1_ex_rf_b), .MEM_RF_B(ex_mem_1_mem_rf_b), .EX_ALU_R(EX_Data),
    .MEM_ALU_R(ex_mem_1_mem_alu_r), .EX_HALT(and_7_out), .MEM_HALT(ex_mem_1_mem_halt));
  D_Flip_Flop d_ff_3 (.clk(clk), .D(not_5_out), .Qn(d_ff_3_qn), .preset(RST));  // open: Q, en, reset
  // Probe on MEM_rW
  Counter #(.width(16), .max('hffff), .trigger("falling")) \u_有条件分支成功跳转计数  (
    .count(d_ff_3_qn), .Q(\有条件分支成功跳转 ), .clk(clk), .clr(RST));  // open: load, D, carry
  Counter #(.width(16), .max('hffff), .trigger("falling")) \u_插入气泡计数  (
    .count(Load_Use), .Q(\插入气泡数 ), .clk(clk), .clr(RST));  // open: load, D, carry
  or or_3 (or_3_out, ex_mem_1_mem_ctrl[21], ex_mem_1_mem_ctrl[20]);
  // Probe on MEM_Data
  Multiplexer #(.width(32), .enable("false")) multiplexer_10 (
    .in0(ex_mem_1_mem_alu_r), .in1(mips_ram_1_p6), .out(MEM_Data), .sel(or_3_out));
  // MIPS_RAM mips_ram_1: pin names not known; wires that end beside it: ex_mem_1_mem_alu_r[13:2], ex_mem_1_mem_rf_b, DM_WE, clk, RST, mips_ram_1_p6
  MEM_WB mem_wb_1 (
    .CLK(clk), .\同步清零 (pull_resistor_6_node), .MEM_PC(MEM_PC), .WB_PC(WB_PC), .MEM_PC_1(ex_mem_1_mem_pc_1),
    .WB_PC_1(mem_wb_1_wb_pc_1),
    .MEM_CTRL({ex_mem_1_mem_ctrl[31:24], MEM_RF_WE, ex_mem_1_mem_ctrl[22:8], DM_WE, ex_mem_1_mem_ctrl[6:0]}),
    .WB_CTRL({mem_wb_1_wb_ctrl[31:24], WB_RF_WE, Din__PC_1, Din__DM, Din__DM_half, mem_wb_1_wb_ctrl[19:0]}),
    .lock_when_0_stop_transport(pull_resistor_5_node), .MEM_rW(MEM_rW), .WB_rW(WB_rW),
    .MEM_ALU_R(ex_mem_1_mem_alu_r), .WB_ALU_R(mem_wb_1_wb_alu_r), .MEM_DM_D(mips_ram_1_p6),
    .WB_DM_D(mem_wb_1_wb_dm_d), .MEM_HALT(ex_mem_1_mem_halt), .WB_HALT(halting));
  Pull_Resistor #(.pull(1)) pull_resistor_5 (.node(pull_resistor_5_node));
  Pull_Resistor pull_resistor_6 (.node(pull_resistor_6_node));
  D_Flip_Flop #(.trigger("falling")) d_ff_4 (.clk(halting), .D(1'b1), .Q(stop), .reset(RST));  // open: Qn, preset, en
  Multiplexer #(.width(16), .enable("false")) multiplexer_11 (
    .in0(mem_wb_1_wb_dm_d[15:0]), .in1(mem_wb_1_wb_dm_d[31:16]), .out(multiplexer_11_out),
    .sel(mem_wb_1_wb_alu_r[1]));
  Multiplexer #(.width(32), .enable("false")) multiplexer_12 (
    .in0(mem_wb_1_wb_alu_r), .in1(mem_wb_1_wb_pc_1), .out(multiplexer_12_out), .sel(Din__PC_1));
  Multiplexer #(.width(32), .enable("false")) multiplexer_13 (
    .in0(mem_wb_1_wb_dm_d), .in1({{16{1'b0}}, multiplexer_11_out}), .out(multiplexer_13_out),
    .sel(Din__DM_half));
  // Probe on RF_W
  Multiplexer #(.width(32), .enable("false")) multiplexer_14 (
    .in0(multiplexer_12_out), .in1(multiplexer_13_out), .out(RF_W), .sel(Din__DM));

  // Other names for the same wires on the sheet: 总周期数[15:0] = Count

  // Notes on the sheet:
  //   中断源
  //   中断等待指示
  //   指令存储器
  //   数码管输出
  //   contents of rom_1 (hex, n*v repeats v):
  //   20110001 8000c05 20110001 20120002 20130003 8000c09 20110001 20120002 20130003 8000c0d 20110001
  //   20120002 20130003 8000c11 20110001 20120002 20130003 c000cb8 20100001 20110001 118fc0 112020
  //   20020022 c 118882 12200001 8000c15 112020 20020022 c 20110001 118880 112020 20020022 c 12200001
  //   8000c1f 20110001 118fc0 112020 20020022 c 1188c3 112020 20020022 c 118903 112020 20020022 c 118903
  //   112020 20020022 c 118903 112020 20020022 c 118903 112020 20020022 c 118903 112020 20020022 c 118903
  //   112020 20020022 c 118903 112020 20020022 c 20100001 109fc0 139fc3 8021 2012000c 24160003 26100001
  //   3210000f 20080008 20090001 139900 2709825 132020 20020022 c 1094022 1500fff9 22100001 2018000f
  //   2188024 108700 20080008 20090001 139902 2709825 132021 20020022 c 1094022 1500fff9 108702 2c9b022
  //   12c00001 8000c50 4020 1084027 84400 3508ffff 82021 20020022 c 2010ffff 20110000 ae300000 22100001
  //   22310004 ae300000 22100001 22310004 ae300000 22100001 22310004 ae300000 22100001 22310004 ae300000
  //   22100001 22310004 ae300000 22100001 22310004 ae300000 22100001 22310004 ae300000 22100001 22310004
  //   ae300000 22100001 22310004 ae300000 22100001 22310004 ae300000 22100001 22310004 ae300000 22100001
  //   22310004 ae300000 22100001 22310004 ae300000 22100001 22310004 ae300000 22100001 22310004 ae300000
  //   22100001 22310004 22100001 8020 2011003c 8e130000 8e340000 274402a 11000002 ae330000 ae140000
  //   2231fffc 1611fff8 102020 20020022 c 22100004 2011003c 1611fff2 2002000a c 20100000 22100001 102020
  //   20020022 c 22100002 102020 20020022 c 22100003 102020 20020022 c 22100004 102020 20020022 c 22100005
  //   102020 20020022 c 22100006 102020 20020022 c 22100007 102020 20020022 c 22100008 102020 20020022
  //   20020022 c 3e00008
  //   寄存器堆
  //   数据存储器
endmodule

module Predictor (
  input  clk,
  input  Reset,
  input  goto,
  input  Wrong_Prediction,
  input  branch_success,
  input  [31:0] goto_addr,
  input  [31:0] PC,
  input  [31:0] EX_PC,
  input  [31:0] EX_PC_2,
  output [31:0] PC_1,
  output [31:0] next_PC,
  output Predict_will_branch,
  output rectify,
  output Hit
);

  wire add_LRU0, add_LRU1, add_LRU2, add_LRU3, and_2_out, and_5_out, and_6_out, and_7_out, and_9_out,
       and_12_out, and_13_out, and_14_out, and_16_out, and_17_out, and_18_out, and_19_out, and_20_out,
       and_21_out, and_23_out, and_24_out, and_25_out, and_26_out, and_30_out, and_31_out, and_32_out,
       and_33_out, comparator_1_eq, comparator_2_eq, comparator_3_lt, comparator_4_lt, comparator_5_lt,
       comparator_6_lt, comparator_7_eq, comparator_8_eq, comparator_9_eq, comparator_10_eq,
       comparator_11_eq, comparator_12_eq, LRU_bits0_carry, LRU_bits1_carry, LRU_bits2_carry,
       LRU_bits3_carry, not_1_out, not_2_out, not_3_out, not_4_out, not_5_out, not_6_out, not_7_out,
       not_8_out, not_9_out, or_1_out, or_2_out, or_3_out, or_4_out, or_5_out, or_6_out, or_7_out, or_9_out,
       or_11_out, or_12_out, or_13_out, or_14_out, PC0_hit_EX_PC, PC0_hit_PC, PC0_predict_success,
       PC1_hit_EX_PC, PC1_hit_PC, PC1_predict_success, PC2_hit_EX_PC, PC2_hit_PC, PC2_predict_success,
       PC3_hit_EX_PC, PC3_hit_PC, PC3_predict_success, priority_encoder_1_gs, priority_encoder_2_gs,
       priority_encoder_4_gs, update_PC0, update_PC1, update_PC2, update_PC3, Vaild0, Vaild1, Vaild2, Vaild3,
       write_table, y1_0, y1_1, y1_2, y1_3, y2_0, y2_1, y2_2, y2_3;
  wire [1:0] LRU_bits0_q, LRU_bits1_q, LRU_bits2_q, LRU_bits3_q, multiplexer_2_out, multiplexer_4_out,
       priority_encoder_1_out, priority_encoder_2_out, priority_encoder_3_out, priority_encoder_4_out,
       register_1_q;
  wire [31:0] Branch_addr0, Branch_addr1, Branch_addr2, Branch_addr3, multiplexer_1_out, multiplexer_3_out,
       multiplexer_5_out, PC0, PC1, PC2, PC3;

  LED led_1 (.in(Vaild0));
  LED led_2 (.in(Vaild1));
  LED led_3 (.in(Vaild2));
  LED led_4 (.in(Vaild3));
  // Probe on goto_addr
  // Probe on PC
  // Probe on EX_PC
  // Probe on PC0
  // Probe on PC1
  // Probe on PC2
  // Probe on PC3
  // Probe on next_PC
  and and_1 (PC0_predict_success, PC0_hit_PC, y2_0);
  // Probe on EX_PC_2
  // Probe on Branch_addr0
  // Probe on Branch_addr1
  // Probe on Branch_addr2
  // Probe on Branch_addr3
  or or_1 (or_1_out, PC0_hit_EX_PC, update_PC0);
  or or_2 (or_2_out, PC1_hit_EX_PC, update_PC1);
  or or_3 (or_3_out, PC2_hit_EX_PC, update_PC2);
  or or_4 (or_4_out, PC3_hit_EX_PC, update_PC3);
  Register #(.width(32), .trigger("falling")) u_PC0 (.D(EX_PC), .en(update_PC0), .Q(PC0), .clk(clk), .clr(Reset));
  Register #(.width(32), .trigger("falling")) BranchAddr0 (
    .D(goto_addr), .en(update_PC0), .Q(Branch_addr0), .clk(clk), .clr(Reset));
  D_Flip_Flop #(.trigger("falling")) y2 (
    .clk(clk), .D(or_6_out), .Q(y2_0), .en(PC0_hit_EX_PC), .reset(or_5_out));  // open: Qn, preset
  D_Flip_Flop #(.trigger("falling")) y1 (
    .clk(clk), .D(branch_success), .Q(y1_0), .en(PC0_hit_EX_PC), .reset(or_5_out));  // open: Qn, preset
  or or_5 (or_5_out, and_2_out, Reset);
  and and_2 (and_2_out, ~clk, update_PC0);  // AND_Gate
  // Probe on y2_0
  // Probe on y2_1
  // Probe on y2_2
  // Probe on y2_3
  D_Flip_Flop #(.trigger("falling")) u_Vaild0 (
    .clk(clk), .D(1'b1), .Q(Vaild0), .en(update_PC0), .reset(Reset));  // open: Qn, preset
  and and_3 (PC0_hit_PC, Vaild0, comparator_1_eq);
  Comparator #(.width(32)) comparator_1 (.a(PC), .b(PC0), .eq(comparator_1_eq));  // open: gt, lt
  and and_4 (PC0_hit_EX_PC, Vaild0, comparator_2_eq);
  Comparator #(.width(32)) comparator_2 (.a(PC0), .b(EX_PC), .eq(comparator_2_eq));  // open: gt, lt
  and and_5 (and_5_out, y2_0, branch_success);
  or or_6 (or_6_out, and_5_out, and_6_out, and_7_out);
  and and_6 (and_6_out, y2_0, y1_0);
  and and_7 (and_7_out, branch_success, y1_0);
  // Probe on y1_0
  // Probe on y1_1
  // Probe on y1_2
  // Probe on y1_3
  Counter #(.width(2), .max('h3), .ongoal("stay"), .trigger("falling")) LRU_bits0 (
    .load(or_1_out), .D(2'b00), .count(add_LRU0), .Q(LRU_bits0_q), .carry(LRU_bits0_carry), .clk(clk),
    .clr(Reset));
  Counter #(.width(2), .max('h3), .ongoal("stay"), .trigger("falling")) LRU_bits1 (
    .load(or_2_out), .D(2'b00), .count(add_LRU1), .Q(LRU_bits1_q), .carry(LRU_bits1_carry), .clk(clk),
    .clr(Reset));
  Counter #(.width(2), .max('h3), .ongoal("stay"), .trigger("falling")) LRU_bits2 (
    .load(or_3_out), .D(2'b00), .count(add_LRU2), .Q(LRU_bits2_q), .carry(LRU_bits2_carry), .clk(clk),
    .clr(Reset));
  Counter #(.width(2), .max('h3), .ongoal("stay"), .trigger("falling")) LRU_bits3 (
    .load(or_4_out), .D(2'b00), .count(add_LRU3), .Q(LRU_bits3_q), .carry(LRU_bits3_carry), .clk(clk),
    .clr(Reset));
  Priority_Encoder #(.select(2), .disabled(0)) priority_encoder_1 (
    .in0(LRU_bits0_carry), .in1(LRU_bits1_carry), .in2(LRU_bits2_carry), .in3(LRU_bits3_carry),
    .out(priority_encoder_1_out), .gs(priority_encoder_1_gs));  // open: en_out, en_in
  Priority_Encoder #(.select(2), .disabled(0)) priority_encoder_2 (
    .in0(PC0_hit_EX_PC), .in1(PC1_hit_EX_PC), .in2(PC2_hit_EX_PC), .in3(PC3_hit_EX_PC),
    .out(priority_encoder_2_out), .gs(priority_encoder_2_gs));  // open: en_out, en_in
  and and_8 (PC1_predict_success, PC1_hit_PC, y2_1);
  Adder #(.width(32)) adder_1 (.a(32'h4), .b(PC), .out(PC_1));  // open: cin, cout
  Multiplexer #(.select(2), .width(32)) multiplexer_1 (
    .in0(Branch_addr0), .in1(Branch_addr1), .in2(Branch_addr2), .in3(Branch_addr3), .out(multiplexer_1_out),
    .sel(priority_encoder_3_out), .en(Predict_will_branch));
  Priority_Encoder #(.select(2), .disabled(0)) priority_encoder_3 (
    .in0(PC0_predict_success), .in1(PC1_predict_success), .in2(PC2_predict_success),
    .in3(PC3_predict_success), .out(priority_encoder_3_out), .gs(Predict_will_branch));  // open: en_out, en_in
  Register #(.width(2)) register_1 (
    .D(priority_encoder_1_out), .en(priority_encoder_1_gs), .Q(register_1_q), .clk(clk));  // open: clr
  not not_1 (not_1_out, Vaild0);
  not not_2 (not_2_out, Vaild1);
  not not_3 (not_3_out, Vaild2);
  not not_4 (not_4_out, Vaild3);
  Multiplexer #(.select(2), .width(2), .disabled(0)) multiplexer_2 (
    .in0(LRU_bits0_q), .in1(LRU_bits1_q), .in2(LRU_bits2_q), .in3(LRU_bits3_q), .out(multiplexer_2_out),
    .sel(priority_encoder_2_out), .en(priority_encoder_2_gs));
  Register #(.width(32), .trigger("falling")) u_PC1 (.D(EX_PC), .en(update_PC1), .Q(PC1), .clk(clk), .clr(Reset));
  Register #(.width(32), .trigger("falling")) BranchAddr1 (
    .D(goto_addr), .en(update_PC1), .Q(Branch_addr1), .clk(clk), .clr(Reset));
  D_Flip_Flop #(.trigger("falling")) u_y2_2 (
    .clk(clk), .D(or_9_out), .Q(y2_1), .en(PC1_hit_EX_PC), .reset(or_7_out));  // open: Qn, preset
  D_Flip_Flop #(.trigger("falling")) u_y1_2 (
    .clk(clk), .D(branch_success), .Q(y1_1), .en(PC1_hit_EX_PC), .reset(or_7_out));  // open: Qn, preset
  or or_7 (or_7_out, and_9_out, Reset);
  and and_9 (and_9_out, ~clk, update_PC1);  // AND_Gate
  or or_8 (Hit, PC0_hit_EX_PC, PC1_hit_EX_PC, PC2_hit_EX_PC, PC3_hit_EX_PC);
  not not_5 (not_5_out, Hit);
  Priority_Encoder #(.select(2), .disabled(0)) priority_encoder_4 (
    .in0(not_1_out), .in1(not_2_out), .in2(not_3_out), .in3(not_4_out), .out(priority_encoder_4_out),
    .gs(priority_encoder_4_gs));  // open: en_out, en_in
  Comparator #(.width(2), .mode("unsigned")) comparator_3 (
    .a(LRU_bits0_q), .b(multiplexer_2_out), .lt(comparator_3_lt));  // open: gt, eq
  Comparator #(.width(2), .mode("unsigned")) comparator_4 (
    .a(LRU_bits1_q), .b(multiplexer_2_out), .lt(comparator_4_lt));  // open: gt, eq
  Comparator #(.width(2), .mode("unsigned")) comparator_5 (
    .a(LRU_bits2_q), .b(multiplexer_2_out), .lt(comparator_5_lt));  // open: gt, eq
  Comparator #(.width(2), .mode("unsigned")) comparator_6 (
    .a(LRU_bits3_q), .b(multiplexer_2_out), .lt(comparator_6_lt));  // open: gt, eq
  D_Flip_Flop #(.trigger("falling")) u_Vaild1 (
    .clk(clk), .D(1'b1), .Q(Vaild1), .en(update_PC1), .reset(Reset));  // open: Qn, preset
  and and_10 (PC1_hit_PC, Vaild1, comparator_7_eq);
  Comparator #(.width(32)) comparator_7 (.a(PC), .b(PC1), .eq(comparator_7_eq));  // open: gt, lt
  and and_11 (PC1_hit_EX_PC, Vaild1, comparator_8_eq);
  Comparator #(.width(32)) comparator_8 (.a(PC1), .b(EX_PC), .eq(comparator_8_eq));  // open: gt, lt
  and and_12 (and_12_out, y2_1, branch_success);
  and and_13 (and_13_out, y2_1, y1_1);
  or or_9 (or_9_out, and_12_out, and_13_out, and_14_out);
  and and_14 (and_14_out, branch_success, y1_1);
  Multiplexer #(.width(32), .enable("false")) multiplexer_3 (
    .in0(PC_1), .in1(multiplexer_1_out), .out(multiplexer_3_out), .sel(Predict_will_branch));
  and and_15 (write_table, branch_success, not_5_out);
  Multiplexer #(.width(2), .disabled(0), .enable("false")) multiplexer_4 (
    .in0(register_1_q), .in1(priority_encoder_4_out), .out(multiplexer_4_out), .sel(priority_encoder_4_gs));
  and and_16 (and_16_out, priority_encoder_2_gs, comparator_3_lt);
  and and_17 (and_17_out, priority_encoder_2_gs, comparator_4_lt);
  and and_18 (and_18_out, priority_encoder_2_gs, comparator_5_lt);
  and and_19 (and_19_out, priority_encoder_2_gs, comparator_6_lt);
  Multiplexer #(.width(32), .enable("false")) multiplexer_5 (
    .in0(multiplexer_3_out), .in1(goto_addr), .out(multiplexer_5_out), .sel(and_20_out));
  Multiplexer #(.width(32), .disabled(0), .enable("false")) multiplexer_6 (
    .in0(multiplexer_5_out), .in1(EX_PC_2), .out(next_PC), .sel(and_21_out));
  and and_20 (and_20_out, goto, Wrong_Prediction);
  and and_21 (and_21_out, ~goto, Wrong_Prediction);  // AND_Gate
  Decoder #(.select(2), .disabled(0)) decoder_1 (
    .out0(update_PC0), .out1(update_PC1), .out2(update_PC2), .out3(update_PC3), .sel(multiplexer_4_out),
    .en(write_table));
  not not_6 (not_6_out, update_PC0);
  not not_7 (not_7_out, update_PC1);
  not not_8 (not_8_out, update_PC2);
  not not_9 (not_9_out, update_PC3);
  and and_22 (PC2_predict_success, PC2_hit_PC, y2_2);
  // Probe on PC_1
  or or_10 (rectify, and_20_out, and_21_out);
  Multiplexer #(.disabled(0), .enable("false")) multiplexer_7 (
    .in0(and_16_out), .in1(not_6_out), .out(add_LRU0), .sel(write_table));
  Multiplexer #(.disabled(0), .enable("false")) multiplexer_8 (
    .in0(and_17_out), .in1(not_7_out), .out(add_LRU1), .sel(write_table));
  Multiplexer #(.disabled(0), .enable("false")) multiplexer_9 (
    .in0(and_18_out), .in1(not_8_out), .out(add_LRU2), .sel(write_table));
  Multiplexer #(.disabled(0), .enable("false")) multiplexer_10 (
    .in0(and_19_out), .in1(not_9_out), .out(add_LRU3), .sel(write_table));
  Register #(.width(32), .trigger("falling")) u_PC2 (.D(EX_PC), .en(update_PC2), .Q(PC2), .clk(clk), .clr(Reset));
  Register #(.width(32), .trigger("falling")) BranchAddr2 (
    .D(goto_addr), .en(update_PC2), .Q(Branch_addr2), .clk(clk), .clr(Reset));
  D_Flip_Flop #(.trigger("falling")) u_y2_3 (
    .clk(clk), .D(or_12_out), .Q(y2_2), .en(PC2_hit_EX_PC), .reset(or_11_out));  // open: Qn, preset
  D_Flip_Flop #(.trigger("falling")) u_y1_3 (
    .clk(clk), .D(branch_success), .Q(y1_2), .en(PC2_hit_EX_PC), .reset(or_11_out));  // open: Qn, preset
  or or_11 (or_11_out, and_23_out, Reset);
  and and_23 (and_23_out, ~clk, update_PC2);  // AND_Gate
  D_Flip_Flop #(.trigger("falling")) u_Vaild2 (
    .clk(clk), .D(1'b1), .Q(Vaild2), .en(update_PC2), .reset(Reset));  // open: Qn, preset
  Comparator #(.width(32)) comparator_9 (.a(PC), .b(PC2), .eq(comparator_9_eq));  // open: gt, lt
  Comparator #(.width(32)) comparator_10 (.a(PC2), .b(EX_PC), .eq(comparator_10_eq));  // open: gt, lt
  and and_24 (and_24_out, y2_2, branch_success);
  and and_25 (and_25_out, y2_2, y1_2);
  and and_26 (and_26_out, branch_success, y1_2);
  and and_27 (PC2_hit_PC, Vaild2, comparator_9_eq);
  and and_28 (PC2_hit_EX_PC, Vaild2, comparator_10_eq);
  or or_12 (or_12_out, and_24_out, and_25_out, and_26_out);
  and and_29 (PC3_predict_success, PC3_hit_PC, y2_3);
  Register #(.width(32), .trigger("falling")) u_PC3 (.D(EX_PC), .en(update_PC3), .Q(PC3), .clk(clk), .clr(Reset));
  Register #(.width(32), .trigger("falling")) BranchAddr3 (
    .D(goto_addr), .en(update_PC3), .Q(Branch_addr3), .clk(clk), .clr(Reset));
  D_Flip_Flop #(.trigger("falling")) y2_4 (
    .clk(clk), .D(or_14_out), .Q(y2_3), .en(PC3_hit_EX_PC), .reset(or_13_out));  // open: Qn, preset
  D_Flip_Flop #(.trigger("falling")) y1_4 (
    .clk(clk), .D(branch_success), .Q(y1_3), .en(PC3_hit_EX_PC), .reset(or_13_out));  // open: Qn, preset
  or or_13 (or_13_out, and_30_out, Reset);
  and and_30 (and_30_out, ~clk, update_PC3);  // AND_Gate
  D_Flip_Flop #(.trigger("falling")) u_Vaild3 (
    .clk(clk), .D(1'b1), .Q(Vaild3), .en(update_PC3), .reset(Reset));  // open: Qn, preset
  Comparator #(.width(32)) comparator_11 (.a(PC), .b(PC3), .eq(comparator_11_eq));  // open: gt, lt
  Comparator #(.width(32)) comparator_12 (.a(PC3), .b(EX_PC), .eq(comparator_12_eq));  // open: gt, lt
  and and_31 (and_31_out, y2_3, branch_success);
  and and_32 (and_32_out, y2_3, y1_3);
  and and_33 (and_33_out, branch_success, y1_3);
  and and_34 (PC3_hit_PC, Vaild3, comparator_11_eq);
  and and_35 (PC3_hit_EX_PC, Vaild3, comparator_12_eq);
  or or_14 (or_14_out, and_31_out, and_32_out, and_33_out);

  // Other names for the same wires on the sheet: branch_succeed = branch_success; EX_PC_1[31:0] = EX_PC_2
endmodule

// Contorller
module Controller (
  input  [5:0] OP,
  input  [5:0] Funct,
  output [31:0] \控制信号 
);

  wire add, addi, addiu, addu, \and , andi, comparator_1_eq, comparator_16_eq, comparator_17_eq,
       comparator_18_eq, comparator_19_eq, comparator_20_eq, comparator_21_eq, comparator_22_eq,
       comparator_23_eq, comparator_24_eq, comparator_25_eq, comparator_26_eq, comparator_27_eq,
       comparator_28_eq, comparator_29_eq, j, lw, \nor , \or , or_2_out, or_3_out, or_4_out, or_5_out,
       or_6_out, or_7_out, or_9_out, or_10_out, or_11_out, or_12_out, or_13_out, or_14_out, or_15_out,
       or_16_out, or_17_out, or_18_out, or_19_out, or_21_out, or_22_out, or_23_out, or_24_out, or_25_out,
       or_26_out, or_27_out, or_28_out, or_30_out, or_31_out, or_32_out, or_33_out, or_34_out, or_35_out,
       or_36_out, or_37_out, or_38_out, or_39_out, or_40_out, or_42_out, or_43_out, or_44_out, or_45_out,
       or_46_out, or_47_out, or_48_out, or_49_out, or_50_out, or_51_out, or_53_out, or_54_out, or_55_out,
       or_56_out, or_57_out, or_58_out, or_59_out, or_60_out, or_61_out, or_62_out, or_63_out, or_65_out,
       or_66_out, or_67_out, or_68_out, or_69_out, or_70_out, or_71_out, or_72_out, or_74_out, or_75_out,
       or_77_out, or_78_out, or_79_out, or_80_out, or_81_out, or_82_out, or_83_out, or_84_out, or_85_out,
       or_86_out, or_87_out, or_89_out, or_91_out, or_92_out, or_93_out, or_94_out, or_95_out, or_96_out,
       or_97_out, or_98_out, or_99_out, or_100_out, or_103_out, ori, sll, slt, slti, sltiu, sltu, sra, srl,
       sub;

  Comparator #(.width(6)) comparator_1 (.a(OP), .b({6{1'b0}}), .eq(comparator_1_eq));  // open: gt, lt
  Comparator #(.width(6)) comparator_2 (.a(OP), .b(6'b000001), .eq(\控制信号 [9]));  // open: gt, lt
  Comparator #(.width(6)) comparator_3 (.a(OP), .b(6'b000010), .eq(j));  // open: gt, lt
  Comparator #(.width(6)) comparator_4 (.a(OP), .b(6'b000011), .eq(\控制信号 [24]));  // open: gt, lt
  Comparator #(.width(6)) comparator_5 (.a(OP), .b(6'b000100), .eq(\控制信号 [11]));  // open: gt, lt
  Comparator #(.width(6)) comparator_6 (.a(OP), .b(6'b000101), .eq(\控制信号 [10]));  // open: gt, lt
  Comparator #(.width(6)) comparator_7 (.a(OP), .b(6'b001000), .eq(addi));  // open: gt, lt
  Comparator #(.width(6)) comparator_8 (.a(OP), .b(6'b001001), .eq(addiu));  // open: gt, lt
  Comparator #(.width(6)) comparator_9 (.a(OP), .b(6'b001010), .eq(slti));  // open: gt, lt
  Comparator #(.width(6)) comparator_10 (.a(OP), .b(6'b001011), .eq(sltiu));  // open: gt, lt
  Comparator #(.width(6)) comparator_11 (.a(OP), .b(6'b001100), .eq(andi));  // open: gt, lt
  Comparator #(.width(6)) comparator_12 (.a(OP), .b(6'b001101), .eq(ori));  // open: gt, lt
  Comparator #(.width(6)) comparator_13 (.a(OP), .b(6'b100001), .eq(\控制信号 [20]));  // open: gt, lt
  Comparator #(.width(6)) comparator_14 (.a(OP), .b(6'b100011), .eq(lw));  // open: gt, lt
  Comparator #(.width(6)) comparator_15 (.a(OP), .b(6'b101011), .eq(\控制信号 [7]));  // open: gt, lt
  Comparator #(.width(6)) comparator_16 (.a(Funct), .b({6{1'b0}}), .eq(comparator_16_eq));  // open: gt, lt
  Comparator #(.width(6)) comparator_17 (.a(Funct), .b(6'b000010), .eq(comparator_17_eq));  // open: gt, lt
  Comparator #(.width(6)) comparator_18 (.a(Funct), .b(6'b000011), .eq(comparator_18_eq));  // open: gt, lt
  Comparator #(.width(6)) comparator_19 (.a(Funct), .b(6'b000110), .eq(comparator_19_eq));  // open: gt, lt
  Comparator #(.width(6)) comparator_20 (.a(Funct), .b(6'b001000), .eq(comparator_20_eq));  // open: gt, lt
  Comparator #(.width(6)) comparator_21 (.a(Funct), .b(6'b001100), .eq(comparator_21_eq));  // open: gt, lt
  Comparator #(.width(6)) comparator_22 (.a(Funct), .b(6'b100000), .eq(comparator_22_eq));  // open: gt, lt
  Comparator #(.width(6)) comparator_23 (.a(Funct), .b(6'b100001), .eq(comparator_23_eq));  // open: gt, lt
  Comparator #(.width(6)) comparator_24 (.a(Funct), .b(6'b100010), .eq(comparator_24_eq));  // open: gt, lt
  Comparator #(.width(6)) comparator_25 (.a(Funct), .b(6'b100100), .eq(comparator_25_eq));  // open: gt, lt
  Comparator #(.width(6)) comparator_26 (.a(Funct), .b(6'b100101), .eq(comparator_26_eq));  // open: gt, lt
  Comparator #(.width(6)) comparator_27 (.a(Funct), .b(6'b100111), .eq(comparator_27_eq));  // open: gt, lt
  Comparator #(.width(6)) comparator_28 (.a(Funct), .b(6'b101010), .eq(comparator_28_eq));  // open: gt, lt
  Comparator #(.width(6)) comparator_29 (.a(Funct), .b(6'b101011), .eq(comparator_29_eq));  // open: gt, lt
  and and_1 (sll, comparator_1_eq, comparator_16_eq);
  and and_2 (srl, comparator_1_eq, comparator_17_eq);
  and and_3 (sra, comparator_1_eq, comparator_18_eq);
  and and_4 (\控制信号 [18], comparator_1_eq, comparator_19_eq);
  and and_5 (\控制信号 [12], comparator_1_eq, comparator_20_eq);
  and and_6 (\控制信号 [27], comparator_1_eq, comparator_21_eq);
  and and_7 (add, comparator_1_eq, comparator_22_eq);
  and and_8 (addu, comparator_1_eq, comparator_23_eq);
  and and_9 (sub, comparator_1_eq, comparator_24_eq);
  and and_10 (\and , comparator_1_eq, comparator_25_eq);
  and and_11 (\or , comparator_1_eq, comparator_26_eq);
  and and_12 (\nor , comparator_1_eq, comparator_27_eq);
  and and_13 (slt, comparator_1_eq, comparator_28_eq);
  and and_14 (sltu, comparator_1_eq, comparator_29_eq);
  or or_1 (\控制信号 [31], \or , or_2_out);
  or or_2 (or_2_out, or_3_out, \nor );
  or or_3 (or_3_out, slt, or_4_out);
  or or_4 (or_4_out, or_5_out, sltu);
  or or_5 (or_5_out, \控制信号 [9], or_6_out);
  or or_6 (or_6_out, or_7_out, slti);
  or or_7 (or_7_out, sltiu, ori);
  // Probe on {\控制信号 [31:27], \控制信号 [27], \控制信号 [25:23], \控制信号 [24], \控制信号 [21:9], \控制信号 [27], \控制信号 [7:5], {5{1'b0}}}
  or or_8 (\控制信号 [30], \控制信号 [27], or_9_out);
  or or_9 (or_9_out, or_10_out, add);
  or or_10 (or_10_out, addu, or_11_out);
  or or_11 (or_11_out, or_12_out, sub);
  or or_12 (or_12_out, \and , or_13_out);
  or or_13 (or_13_out, or_14_out, sltu);
  or or_14 (or_14_out, addi, or_15_out);
  or or_15 (or_15_out, or_16_out, addiu);
  or or_16 (or_16_out, sltiu, or_17_out);
  or or_17 (or_17_out, or_18_out, andi);
  or or_18 (or_18_out, \控制信号 [20], or_19_out);
  or or_19 (or_19_out, lw, \控制信号 [7]);
  or or_20 (\控制信号 [29], srl, or_21_out);
  or or_21 (or_21_out, or_22_out, \控制信号 [18]);
  or or_22 (or_22_out, \控制信号 [27], or_23_out);
  or or_23 (or_23_out, or_24_out, sub);
  or or_24 (or_24_out, \and , or_25_out);
  or or_25 (or_25_out, or_26_out, \nor );
  or or_26 (or_26_out, slt, or_27_out);
  or or_27 (or_27_out, or_28_out, \控制信号 [9]);
  or or_28 (or_28_out, slti, andi);
  or or_29 (\控制信号 [28], sra, or_30_out);
  or or_30 (or_30_out, or_31_out, add);
  or or_31 (or_31_out, addu, or_32_out);
  or or_32 (or_32_out, or_33_out, \and );
  or or_33 (or_33_out, slt, or_34_out);
  or or_34 (or_34_out, or_35_out, \控制信号 [9]);
  or or_35 (or_35_out, addi, or_36_out);
  or or_36 (or_36_out, or_37_out, addiu);
  or or_37 (or_37_out, slti, or_38_out);
  or or_38 (or_38_out, or_39_out, andi);
  or or_39 (or_39_out, \控制信号 [20], or_40_out);
  or or_40 (or_40_out, lw, \控制信号 [7]);
  or or_41 (\控制信号 [25], sll, or_42_out);
  or or_42 (or_42_out, or_43_out, srl);
  or or_43 (or_43_out, sra, or_44_out);
  or or_44 (or_44_out, or_45_out, \控制信号 [18]);
  or or_45 (or_45_out, add, or_46_out);
  or or_46 (or_46_out, or_47_out, addu);
  or or_47 (or_47_out, sub, or_48_out);
  or or_48 (or_48_out, or_49_out, \and );
  or or_49 (or_49_out, \or , or_50_out);
  or or_50 (or_50_out, or_51_out, \nor );
  or or_51 (or_51_out, slt, sltu);
  or or_52 (\控制信号 [23], sll, or_53_out);
  or or_53 (or_53_out, or_54_out, srl);
  or or_54 (or_54_out, sra, or_55_out);
  or or_55 (or_55_out, or_56_out, \控制信号 [18]);
  or or_56 (or_56_out, add, or_57_out);
  or or_57 (or_57_out, or_58_out, addu);
  or or_58 (or_58_out, sub, or_59_out);
  or or_59 (or_59_out, or_60_out, \and );
  or or_60 (or_60_out, \or , or_61_out);
  or or_61 (or_61_out, or_62_out, \nor );
  or or_62 (or_62_out, slt, or_63_out);
  or or_63 (or_63_out, sltu, or_65_out);
  or or_64 (\控制信号 [21], \控制信号 [20], lw);
  or or_65 (or_65_out, \控制信号 [24], or_66_out);
  or or_66 (or_66_out, or_67_out, addi);
  or or_67 (or_67_out, addiu, or_68_out);
  or or_68 (or_68_out, or_69_out, slti);
  or or_69 (or_69_out, sltiu, or_70_out);
  or or_70 (or_70_out, or_71_out, andi);
  or or_71 (or_71_out, ori, or_72_out);
  or or_72 (or_72_out, \控制信号 [20], lw);
  or or_73 (\控制信号 [19], sll, or_74_out);
  or or_74 (or_74_out, or_75_out, srl);
  or or_75 (or_75_out, sra, \控制信号 [18]);
  or or_76 (\控制信号 [17], sll, or_77_out);
  or or_77 (or_77_out, or_78_out, srl);
  or or_78 (or_78_out, sra, or_79_out);
  or or_79 (or_79_out, or_80_out, \控制信号 [27]);
  or or_80 (or_80_out, addi, or_81_out);
  or or_81 (or_81_out, or_82_out, addiu);
  or or_82 (or_82_out, slti, or_83_out);
  or or_83 (or_83_out, or_84_out, sltiu);
  or or_84 (or_84_out, andi, or_85_out);
  or or_85 (or_85_out, or_86_out, ori);
  or or_86 (or_86_out, \控制信号 [20], or_87_out);
  or or_87 (or_87_out, lw, \控制信号 [7]);
  or or_88 (\控制信号 [16], sll, or_89_out);
  or or_89 (or_89_out, srl, sra);
  or or_90 (\控制信号 [15], \控制信号 [9], or_91_out);
  or or_91 (or_91_out, or_92_out, \控制信号 [11]);
  or or_92 (or_92_out, \控制信号 [10], or_93_out);
  or or_93 (or_93_out, or_94_out, addi);
  or or_94 (or_94_out, addiu, or_95_out);
  or or_95 (or_95_out, or_96_out, slti);
  or or_96 (or_96_out, sltiu, or_97_out);
  or or_97 (or_97_out, or_98_out, andi);
  or or_98 (or_98_out, ori, or_99_out);
  or or_99 (or_99_out, or_100_out, \控制信号 [20]);
  or or_100 (or_100_out, lw, \控制信号 [7]);
  or or_101 (\控制信号 [13], \控制信号 [12], or_103_out);
  or or_102 (\控制信号 [14], andi, ori);
  or or_103 (or_103_out, j, \控制信号 [24]);
  or or_104 (\控制信号 [6], \控制信号 [9], \控制信号 [11], \控制信号 [18], \控制信号 [10], \控制信号 [12], addi, addiu, add, slti, addu, sltiu, sub, andi, \and , ori, \or , \控制信号 [20], \nor , lw, slt, \控制信号 [7], sltu);
  or or_105 (\控制信号 [5], \控制信号 [10], sll, srl, sra, add, \控制信号 [7], addu, sltu, sub, slt, \and , \控制信号 [18], \or , \控制信号 [9], \nor , \控制信号 [11]);

  assign {\控制信号 [26], \控制信号 [22], \控制信号 [8], \控制信号 [4:0]} = {\控制信号 [27], \控制信号 [24], \控制信号 [27], {5{1'b0}}};

  // Other names for the same wires on the sheet: read_rB = \控制信号 [5]; read_rA = \控制信号 [6]; sw = \控制信号 [7];
  //   bltz = \控制信号 [9]; bne = \控制信号 [10]; beq = \控制信号 [11]; jr = \控制信号 [12]; srlv = \控制信号 [18]; lh = \控制信号 [20];
  //   jal = \控制信号 [24]; syscall = \控制信号 [27]
endmodule

// 扩展
module Extender (
  input  extend_IMM,
  input  extend_shamt,
  input  [31:0] IR,
  input  zero_extend_IMM,
  output [31:0] IMM
);

  wire [16:0] multiplexer_1_out, multiplexer_2_out, multiplexer_3_out;

  Multiplexer #(.width(17), .enable("false")) multiplexer_1 (
    .in0(17'ha), .in1({{12{1'b0}}, IR[10:6]}), .out(multiplexer_1_out), .sel(extend_shamt));
  Multiplexer #(.width(17), .enable("false")) multiplexer_2 (
    .in0({{2{IR[15]}}, IR[14:0]}), .in1({1'b0, IR[15:0]}), .out(multiplexer_2_out), .sel(zero_extend_IMM));
  Multiplexer #(.width(17), .enable("false")) multiplexer_3 (
    .in0(multiplexer_1_out), .in1(multiplexer_2_out), .out(multiplexer_3_out), .sel(extend_IMM));
  assign IMM = {{15{multiplexer_3_out[16]}}, multiplexer_3_out};  // Bit_Extender bit_extender_1

  // Other names for the same wires on the sheet: zero_ext_IMM = zero_extend_IMM
endmodule

module ALU (
  input  [31:0] X,
  input  [31:0] Y,
  input  [3:0] AluOP,
  output Signed_Overflow,
  output UnSigned_Overflow,
  output Equal,
  output [31:0] Result,
  output [31:0] Result_2
);

  wire adder_1_cout, and_2_out, and_3_out, and_5_out, and_6_out, and_7_out, and_8_out, comparator_2_lt,
       or_2_out, or_4_out;
  wire [0:0] comparator_1_lt, xor_2_out;
  wire [31:0] adder_1_out, and_1_out, divider_1_out, divider_1_rem, multiplexer_2_out, multiplier_1_cout,
       multiplier_1_out, not_1_out, not_2_out, or_1_out, shifter_1_out, shifter_2_out, shifter_3_out,
       xor_1_out;

  // Probe on X
  // Probe on X
  // Probe on Y
  // Probe on Y
  Shifter #(.width(32)) shifter_1 (.in(X), .\dist (Y[4:0]), .out(shifter_1_out));
  Shifter #(.width(32), .shift("ar")) shifter_2 (.in(X), .\dist (Y[4:0]), .out(shifter_2_out));
  Shifter #(.width(32), .shift("lr")) shifter_3 (.in(X), .\dist (Y[4:0]), .out(shifter_3_out));
  Multiplier #(.width(32)) multiplier_1 (.a(X), .b(Y), .out(multiplier_1_out), .cout(multiplier_1_cout));  // open: cin
  Divider #(.width(32)) divider_1 (.a(X), .b(Y), .out(divider_1_out), .rem(divider_1_rem));  // open: upper
  assign and_1_out = X & Y;  // AND_Gate and_1, 32 bits wide
  assign or_1_out = X | Y;  // OR_Gate or_1, 32 bits wide
  assign xor_1_out = X ^ Y;  // XOR_Gate xor_1, 32 bits wide
  Comparator #(.width(32), .mode("unsigned")) comparator_1 (
    .a(X), .b(Y), .eq(Equal), .lt(comparator_1_lt[0]));  // open: gt
  Multiplexer #(.select(4), .width(32), .enable("false")) multiplexer_1 (
    .in0(shifter_1_out), .in1(shifter_2_out), .in2(shifter_3_out), .in3(multiplier_1_out),
    .in4(divider_1_out), .in5(adder_1_out), .in6(adder_1_out), .in7(and_1_out), .in8(or_1_out),
    .in9(xor_1_out), .in10(not_1_out), .in11({{31{1'b0}}, xor_2_out[0]}),
    .in12({{31{1'b0}}, comparator_1_lt[0]}), .in13({32{1'b0}}), .in14({32{1'b0}}), .in15({32{1'b0}}),
    .out(Result), .sel(AluOP));
  assign not_1_out = ~or_1_out;  // NOT_Gate not_1, 32 bits wide
  // Probe on AluOP
  xor xor_2 (xor_2_out[0], xor_1_out[31], comparator_1_lt[0]);
  // Probe on Result
  // Probe on Result
  Multiplexer #(.width(32), .enable("false")) multiplexer_2 (
    .in0(Y), .in1(not_2_out), .out(multiplexer_2_out), .sel(AluOP[1]));
  assign not_2_out = ~Y;  // NOT_Gate not_2, 32 bits wide
  // Probe on Result_2
  Adder #(.width(32)) adder_1 (.a(X), .b(multiplexer_2_out), .out(adder_1_out), .cin(AluOP[1]), .cout(adder_1_cout));
  Multiplexer #(.select(4), .width(32), .disabled(0), .enable("false")) multiplexer_3 (
    .in0({32{1'b0}}), .in1({32{1'b0}}), .in2({32{1'b0}}), .in3(multiplier_1_cout), .in4(divider_1_rem),
    .in5({32{1'b0}}), .in6({32{1'b0}}), .in7({32{1'b0}}), .in8({32{1'b0}}), .in9({32{1'b0}}),
    .in10({32{1'b0}}), .in11({32{1'b0}}), .in12({32{1'b0}}), .in13({32{1'b0}}), .in14({32{1'b0}}),
    .in15({32{1'b0}}), .out(Result_2), .sel(AluOP));
  and and_2 (and_2_out, ~adder_1_out[31], multiplexer_2_out[31], X[31]);  // AND_Gate
  or or_2 (or_2_out, and_2_out, and_3_out);
  and and_3 (and_3_out, adder_1_out[31], ~X[31], ~multiplexer_2_out[31]);  // AND_Gate
  Comparator #(.width(32), .mode("unsigned")) comparator_2 (
    .a(X), .b(adder_1_out), .lt(comparator_2_lt));  // open: gt, eq
  and and_4 (Signed_Overflow, or_2_out, or_4_out);
  or or_3 (UnSigned_Overflow, and_6_out, and_5_out);
  and and_5 (and_5_out, comparator_2_lt, and_8_out);
  and and_6 (and_6_out, adder_1_cout, and_7_out);
  or or_4 (or_4_out, and_7_out, and_8_out);
  and and_7 (and_7_out, AluOP[0], ~AluOP[1], AluOP[2], ~AluOP[3]);  // AND_Gate
  and and_8 (and_8_out, ~AluOP[0], AluOP[1], AluOP[2], ~AluOP[3]);  // AND_Gate

  // Other names for the same wires on the sheet: OF = Signed_Overflow; Result2[31:0] = Result_2; S[3:0] = AluOP;
  //   UOF = UnSigned_Overflow

  // Notes on the sheet:
  //   不要改变此引脚区域内容，也不要改变ALU封装形式
  //   输入引脚
  //   请在下方利用上方输入输出引脚的隧道信号构建ALU电路，ctrl+d复制选择部件
  //   华中科技大学计算机学院 计算机组成原理，鸣谢加州大学伯克利CS61C课程
  //   输出引脚
  //   探测区域
endmodule

module NPC (
  input  ALU_Equal,
  input  [31:0] ALU_R,
  input  [31:0] CTRL,
  input  [31:0] IMM,
  input  [31:0] PC_1,
  input  [31:0] IR,
  input  [31:0] RF_A,
  output branch_instruction,
  output \branch_success_成功跳转 ,
  output \goto_跳转 ,
  output \jump_无条件跳转 ,
  output [31:0] \goto_addr_跳转地址 
);

  wire and_1_out, and_2_out, and_3_out;
  wire [31:0] adder_1_out, multiplexer_1_out;

  or or_1 (branch_instruction, CTRL[9], CTRL[11], CTRL[10]);
  and and_1 (and_1_out, ALU_R[0], CTRL[9]);
  and and_2 (and_2_out, ALU_Equal, CTRL[11]);
  and and_3 (and_3_out, ~ALU_Equal, CTRL[10]);  // AND_Gate
  Adder #(.width(32)) adder_1 (.a({IMM[29:0], 2'b00}), .b(PC_1), .out(adder_1_out));  // open: cin, cout
  or or_2 (\branch_success_成功跳转 , and_1_out, and_2_out, and_3_out);
  Multiplexer #(.width(32), .enable("false")) multiplexer_1 (
    .in0({PC_1[31:28], IR[25:0], 2'b00}), .in1(RF_A), .out(multiplexer_1_out), .sel(CTRL[12]));
  Multiplexer #(.width(32), .enable("false")) multiplexer_2 (
    .in0(adder_1_out), .in1(multiplexer_1_out), .out(\goto_addr_跳转地址 ), .sel(CTRL[13]));
  or or_3 (\goto_跳转 , \branch_success_成功跳转 , CTRL[13]);

  assign \jump_无条件跳转  = CTRL[13];

  // Other names for the same wires on the sheet: bltz = CTRL[9]; bne = CTRL[10]; beq = CTRL[11];
  //   jump_register = CTRL[12]
endmodule

module IF_ID (
  input  CLK,
  input  lock_when_0_stop_transport,
  input  \同步清零 ,
  input  [31:0] IF_PC,
  input  [31:0] IF_PC_1,
  input  [31:0] IF_IR,
  input  IF_Predict,
  output [31:0] ID_PC,
  output [31:0] ID_PC_1,
  output [31:0] ID_IR,
  output ID_Predict
);

  wire multiplexer_4_out;
  wire [31:0] multiplexer_1_out, multiplexer_2_out, multiplexer_3_out;

  Multiplexer #(.width(32), .enable("false")) multiplexer_1 (
    .in0(IF_PC), .in1({32{1'b0}}), .out(multiplexer_1_out), .sel(\同步清零 ));
  Multiplexer #(.width(32), .enable("false")) multiplexer_2 (
    .in0(IF_PC_1), .in1({32{1'b0}}), .out(multiplexer_2_out), .sel(\同步清零 ));
  Multiplexer #(.width(32), .enable("false")) multiplexer_3 (
    .in0(IF_IR), .in1({32{1'b0}}), .out(multiplexer_3_out), .sel(\同步清零 ));
  Multiplexer #(.enable("false")) multiplexer_4 (.in0(IF_Predict), .in1(1'b0), .out(multiplexer_4_out), .sel(\同步清零 ));
  Register #(.width(32)) register_1 (
    .D(multiplexer_1_out), .en(lock_when_0_stop_transport), .Q(ID_PC), .clk(CLK));  // open: clr
  Register #(.width(32)) register_2 (
    .D(multiplexer_2_out), .en(lock_when_0_stop_transport), .Q(ID_PC_1), .clk(CLK));  // open: clr
  Register #(.width(32)) register_3 (
    .D(multiplexer_3_out), .en(lock_when_0_stop_transport), .Q(ID_IR), .clk(CLK));  // open: clr
  Register #(.width(1)) register_4 (
    .D(multiplexer_4_out), .en(lock_when_0_stop_transport), .Q(ID_Predict), .clk(CLK));  // open: clr
endmodule

module ID_EX (
  input  CLK,
  input  lock_when_0_stop_transport,
  input  \同步清零 ,
  input  [31:0] ID_PC,
  input  [31:0] ID_PC_1,
  input  ID_Predict,
  input  [31:0] ID_IR,
  input  [31:0] ID_CTRL,
  input  [31:0] ID_RF_A,
  input  [31:0] ID_RF_B,
  input  [4:0] ID_rW,
  input  [31:0] ID_IMM,
  output [31:0] EX_PC,
  output [31:0] EX_PC_1,
  output EX_Predict,
  output [31:0] EX_IR,
  output [31:0] EX_CTRL,
  output [31:0] EX_RF_A,
  output [31:0] EX_RF_B,
  output [4:0] EX_rW,
  output [31:0] EX_IMM
);

  wire multiplexer_3_out;
  wire [4:0] multiplexer_8_out;
  wire [31:0] multiplexer_1_out, multiplexer_2_out, multiplexer_4_out, multiplexer_5_out, multiplexer_6_out,
       multiplexer_7_out, multiplexer_9_out;

  Multiplexer #(.width(32), .enable("false")) multiplexer_1 (
    .in0(ID_PC), .in1({32{1'b0}}), .out(multiplexer_1_out), .sel(\同步清零 ));
  Multiplexer #(.width(32), .enable("false")) multiplexer_2 (
    .in0(ID_PC_1), .in1({32{1'b0}}), .out(multiplexer_2_out), .sel(\同步清零 ));
  Multiplexer #(.enable("false")) multiplexer_3 (.in0(ID_Predict), .in1(1'b0), .out(multiplexer_3_out), .sel(\同步清零 ));
  Multiplexer #(.width(32), .enable("false")) multiplexer_4 (
    .in0(ID_IR), .in1({32{1'b0}}), .out(multiplexer_4_out), .sel(\同步清零 ));
  Multiplexer #(.width(32), .enable("false")) multiplexer_5 (
    .in0(ID_CTRL), .in1({32{1'b0}}), .out(multiplexer_5_out), .sel(\同步清零 ));
  Multiplexer #(.width(32), .enable("false")) multiplexer_6 (
    .in0(ID_RF_A), .in1({32{1'b0}}), .out(multiplexer_6_out), .sel(\同步清零 ));
  Multiplexer #(.width(32), .enable("false")) multiplexer_7 (
    .in0(ID_RF_B), .in1({32{1'b0}}), .out(multiplexer_7_out), .sel(\同步清零 ));
  Multiplexer #(.width(5), .enable("false")) multiplexer_8 (
    .in0(ID_rW), .in1({5{1'b0}}), .out(multiplexer_8_out), .sel(\同步清零 ));
  Multiplexer #(.width(32), .enable("false")) multiplexer_9 (
    .in0(ID_IMM), .in1({32{1'b0}}), .out(multiplexer_9_out), .sel(\同步清零 ));
  Register #(.width(32)) register_1 (
    .D(multiplexer_1_out), .en(lock_when_0_stop_transport), .Q(EX_PC), .clk(CLK));  // open: clr
  Register #(.width(32)) register_2 (
    .D(multiplexer_2_out), .en(lock_when_0_stop_transport), .Q(EX_PC_1), .clk(CLK));  // open: clr
  Register #(.width(1)) register_3 (
    .D(multiplexer_3_out), .en(lock_when_0_stop_transport), .Q(EX_Predict), .clk(CLK));  // open: clr
  Register #(.width(32)) register_4 (
    .D(multiplexer_4_out), .en(lock_when_0_stop_transport), .Q(EX_IR), .clk(CLK));  // open: clr
  Register #(.width(32)) register_5 (
    .D(multiplexer_5_out), .en(lock_when_0_stop_transport), .Q(EX_CTRL), .clk(CLK));  // open: clr
  Register #(.width(32)) register_6 (
    .D(multiplexer_6_out), .en(lock_when_0_stop_transport), .Q(EX_RF_A), .clk(CLK));  // open: clr
  Register #(.width(32)) register_7 (
    .D(multiplexer_7_out), .en(lock_when_0_stop_transport), .Q(EX_RF_B), .clk(CLK));  // open: clr
  Register #(.width(5)) register_8 (
    .D(multiplexer_8_out), .en(lock_when_0_stop_transport), .Q(EX_rW), .clk(CLK));  // open: clr
  Register #(.width(32)) register_9 (
    .D(multiplexer_9_out), .en(lock_when_0_stop_transport), .Q(EX_IMM), .clk(CLK));  // open: clr
endmodule

module EX_MEM (
  input  CLK,
  input  lock_when_0_stop_transport,
  input  \同步清零 ,
  input  [31:0] EX_PC,
  input  [31:0] EX_PC_1,
  input  [31:0] EX_CTRL,
  input  [4:0] EX_rW,
  input  [31:0] EX_RF_B,
  input  [31:0] EX_ALU_R,
  input  EX_HALT,
  output [31:0] MEM_PC,
  output [31:0] MEM_PC_1,
  output [31:0] MEM_CTRL,
  output [4:0] MEM_rW,
  output [31:0] MEM_RF_B,
  output [31:0] MEM_ALU_R,
  output MEM_HALT
);

  wire multiplexer_7_out;
  wire [4:0] multiplexer_4_out;
  wire [31:0] multiplexer_1_out, multiplexer_2_out, multiplexer_3_out, multiplexer_5_out, multiplexer_6_out;

  Multiplexer #(.width(32), .enable("false")) multiplexer_1 (
    .in0(EX_PC), .in1({32{1'b0}}), .out(multiplexer_1_out), .sel(\同步清零 ));
  Multiplexer #(.width(32), .enable("false")) multiplexer_2 (
    .in0(EX_PC_1), .in1({32{1'b0}}), .out(multiplexer_2_out), .sel(\同步清零 ));
  Multiplexer #(.width(32), .enable("false")) multiplexer_3 (
    .in0(EX_CTRL), .in1({32{1'b0}}), .out(multiplexer_3_out), .sel(\同步清零 ));
  Multiplexer #(.width(5), .enable("false")) multiplexer_4 (
    .in0(EX_rW), .in1({5{1'b0}}), .out(multiplexer_4_out), .sel(\同步清零 ));
  Multiplexer #(.width(32), .enable("false")) multiplexer_5 (
    .in0(EX_RF_B), .in1({32{1'b0}}), .out(multiplexer_5_out), .sel(\同步清零 ));
  Multiplexer #(.width(32), .enable("false")) multiplexer_6 (
    .in0(EX_ALU_R), .in1({32{1'b0}}), .out(multiplexer_6_out), .sel(\同步清零 ));
  Multiplexer #(.enable("false")) multiplexer_7 (.in0(EX_HALT), .in1(1'b0), .out(multiplexer_7_out), .sel(\同步清零 ));
  Register #(.width(32)) register_1 (
    .D(multiplexer_1_out), .en(lock_when_0_stop_transport), .Q(MEM_PC), .clk(CLK));  // open: clr
  Register #(.width(32)) register_2 (
    .D(multiplexer_2_out), .en(lock_when_0_stop_transport), .Q(MEM_PC_1), .clk(CLK));  // open: clr
  Register #(.width(32)) register_3 (
    .D(multiplexer_3_out), .en(lock_when_0_stop_transport), .Q(MEM_CTRL), .clk(CLK));  // open: clr
  Register #(.width(5)) register_4 (
    .D(multiplexer_4_out), .en(lock_when_0_stop_transport), .Q(MEM_rW), .clk(CLK));  // open: clr
  Register #(.width(32)) register_5 (
    .D(multiplexer_5_out), .en(lock_when_0_stop_transport), .Q(MEM_RF_B), .clk(CLK));  // open: clr
  Register #(.width(32)) register_6 (
    .D(multiplexer_6_out), .en(lock_when_0_stop_transport), .Q(MEM_ALU_R), .clk(CLK));  // open: clr
  Register #(.width(1)) register_7 (
    .D(multiplexer_7_out), .en(lock_when_0_stop_transport), .Q(MEM_HALT), .clk(CLK));  // open: clr
endmodule

// MEM//WB
module MEM_WB (
  input  CLK,
  input  lock_when_0_stop_transport,
  input  \同步清零 ,
  input  [31:0] MEM_PC,
  input  [31:0] MEM_PC_1,
  input  [31:0] MEM_CTRL,
  input  [4:0] MEM_rW,
  input  [31:0] MEM_ALU_R,
  input  [31:0] MEM_DM_D,
  input  MEM_HALT,
  output [31:0] WB_PC,
  output [31:0] WB_PC_1,
  output [31:0] WB_CTRL,
  output [4:0] WB_rW,
  output [31:0] WB_ALU_R,
  output [31:0] WB_DM_D,
  output WB_HALT
);

  wire multiplexer_7_out;
  wire [4:0] multiplexer_4_out;
  wire [31:0] multiplexer_1_out, multiplexer_2_out, multiplexer_3_out, multiplexer_5_out, multiplexer_6_out;

  Multiplexer #(.width(32), .enable("false")) multiplexer_1 (
    .in0(MEM_PC), .in1({32{1'b0}}), .out(multiplexer_1_out), .sel(\同步清零 ));
  Multiplexer #(.width(32), .enable("false")) multiplexer_2 (
    .in0(MEM_PC_1), .in1({32{1'b0}}), .out(multiplexer_2_out), .sel(\同步清零 ));
  Multiplexer #(.width(32), .enable("false")) multiplexer_3 (
    .in0(MEM_CTRL), .in1({32{1'b0}}), .out(multiplexer_3_out), .sel(\同步清零 ));
  Multiplexer #(.width(5), .enable("false")) multiplexer_4 (
    .in0(MEM_rW), .in1({5{1'b0}}), .out(multiplexer_4_out), .sel(\同步清零 ));
  Multiplexer #(.width(32), .enable("false")) multiplexer_5 (
    .in0(MEM_ALU_R), .in1({32{1'b0}}), .out(multiplexer_5_out), .sel(\同步清零 ));
  Multiplexer #(.width(32), .enable("false")) multiplexer_6 (
    .in0(MEM_DM_D), .in1({32{1'b0}}), .out(multiplexer_6_out), .sel(\同步清零 ));
  Multiplexer #(.enable("false")) multiplexer_7 (.in0(MEM_HALT), .in1(1'b0), .out(multiplexer_7_out), .sel(\同步清零 ));
  Register #(.width(32)) register_1 (
    .D(multiplexer_1_out), .en(lock_when_0_stop_transport), .Q(WB_PC), .clk(CLK));  // open: clr
  Register #(.width(32)) register_2 (
    .D(multiplexer_2_out), .en(lock_when_0_stop_transport), .Q(WB_PC_1), .clk(CLK));  // open: clr
  Register #(.width(32)) register_3 (
    .D(multiplexer_3_out), .en(lock_when_0_stop_transport), .Q(WB_CTRL), .clk(CLK));  // open: clr
  Register #(.width(5)) register_4 (
    .D(multiplexer_4_out), .en(lock_when_0_stop_transport), .Q(WB_rW), .clk(CLK));  // open: clr
  Register #(.width(32)) register_5 (
    .D(multiplexer_5_out), .en(lock_when_0_stop_transport), .Q(WB_ALU_R), .clk(CLK));  // open: clr
  Register #(.width(32)) register_6 (
    .D(multiplexer_6_out), .en(lock_when_0_stop_transport), .Q(WB_DM_D), .clk(CLK));  // open: clr
  Register #(.width(1)) register_7 (
    .D(multiplexer_7_out), .en(lock_when_0_stop_transport), .Q(WB_HALT), .clk(CLK));  // open: clr
endmodule

module Redirecter (
  input  [31:0] Control_signals,
  input  [5:0] EX_OP,
  input  [4:0] EX_rW,
  input  EX_RF_WE,
  input  [4:0] rA,
  input  [4:0] rB,
  input  [31:0] EX_Data,
  input  [4:0] MEM_rW,
  input  [31:0] MEM_Data,
  input  MEM_RF_WE,
  output redirect_RF_A,
  output [31:0] redirected_RF_A,
  output Load_Use,
  output [31:0] redirected_RF_B,
  output redirect_RF_B
);

  wire and_1_out, and_2_out, and_3_out, and_4_out, and_5_out, and_6_out, and_7_out, and_8_out, and_9_out,
       and_10_out, and_11_out, and_12_out, and_13_out, and_14_out, and_16_out, and_17_out, and_18_out,
       comparator_1_eq, comparator_2_eq, comparator_3_eq, comparator_4_eq, comparator_5_eq, comparator_6_eq,
       comparator_7_eq, comparator_8_eq, comparator_9_eq, comparator_10_eq, EX_lh, EX_lw, EX_sw, \EX段冲突 ,
       \MEM段冲突 , not_1_out, not_2_out, or_3_out, or_4_out, or_5_out, or_6_out, or_10_out, or_12_out,
       or_13_out, or_14_out, \rA在EX段冲突 , \rA在MEM段冲突 , \rB在EX段冲突 , \rB在MEM段冲突 ;

  Comparator #(.width(5)) comparator_1 (.a(EX_rW), .b(rA), .eq(comparator_1_eq));  // open: gt, lt
  Comparator #(.width(5)) comparator_2 (.a(EX_rW), .b(rB), .eq(comparator_2_eq));  // open: gt, lt
  Comparator #(.width(5)) comparator_3 (.a(EX_rW), .b({5{1'b0}}), .eq(comparator_3_eq));  // open: gt, lt
  Comparator #(.width(5)) comparator_4 (.a(EX_rW), .b(5'b00010), .eq(comparator_4_eq));  // open: gt, lt
  Comparator #(.width(5)) comparator_5 (.a(EX_rW), .b(5'b00100), .eq(comparator_5_eq));  // open: gt, lt
  Comparator #(.width(5)) comparator_6 (.a(MEM_rW), .b(rA), .eq(comparator_6_eq));  // open: gt, lt
  Comparator #(.width(5)) comparator_7 (.a(MEM_rW), .b(rB), .eq(comparator_7_eq));  // open: gt, lt
  Comparator #(.width(5)) comparator_8 (.a(MEM_rW), .b({5{1'b0}}), .eq(comparator_8_eq));  // open: gt, lt
  Comparator #(.width(5)) comparator_9 (.a(MEM_rW), .b(5'b00010), .eq(comparator_9_eq));  // open: gt, lt
  Comparator #(.width(5)) comparator_10 (.a(MEM_rW), .b(5'b00100), .eq(comparator_10_eq));  // open: gt, lt
  and and_1 (and_1_out, comparator_1_eq, Control_signals[6]);
  and and_2 (and_2_out, comparator_2_eq, Control_signals[5]);
  and and_3 (and_3_out, comparator_4_eq, Control_signals[8]);
  and and_4 (and_4_out, comparator_5_eq, Control_signals[8]);
  and and_5 (and_5_out, comparator_6_eq, Control_signals[6]);
  and and_6 (and_6_out, comparator_7_eq, Control_signals[5]);
  and and_7 (and_7_out, comparator_9_eq, Control_signals[8]);
  and and_8 (and_8_out, comparator_10_eq, Control_signals[8]);
  Comparator #(.width(6)) comparator_11 (.a(EX_OP), .b(6'b100001), .eq(EX_lh));  // open: gt, lt
  Comparator #(.width(6)) comparator_12 (.a(EX_OP), .b(6'b100011), .eq(EX_lw));  // open: gt, lt
  Comparator #(.width(6)) comparator_13 (.a(EX_OP), .b(6'b101011), .eq(EX_sw));  // open: gt, lt
  or or_1 (\rA在EX段冲突 , and_1_out, and_3_out);
  or or_2 (\rA在MEM段冲突 , and_5_out, and_7_out);
  or or_3 (or_3_out, and_1_out, and_2_out);
  not not_1 (not_1_out, comparator_3_eq);
  or or_4 (or_4_out, and_3_out, and_4_out);
  or or_5 (or_5_out, and_5_out, and_6_out);
  not not_2 (not_2_out, comparator_8_eq);
  or or_6 (or_6_out, and_7_out, and_8_out);
  or or_7 (\rB在MEM段冲突 , and_8_out, and_6_out);
  or or_8 (\rB在EX段冲突 , and_4_out, and_2_out);
  and and_9 (and_9_out, or_3_out, not_1_out, EX_RF_WE);
  and and_10 (and_10_out, EX_RF_WE, or_4_out);
  and and_11 (and_11_out, or_5_out, not_2_out, MEM_RF_WE);
  and and_12 (and_12_out, MEM_RF_WE, or_6_out);
  or or_9 (\EX段冲突 , and_9_out, and_10_out);
  or or_10 (or_10_out, EX_sw, EX_lw, EX_lh);
  or or_11 (\MEM段冲突 , and_11_out, and_12_out);
  and and_13 (and_13_out, \rA在EX段冲突 , \EX段冲突 );
  and and_14 (and_14_out, \rA在MEM段冲突 , \MEM段冲突 );
  and and_15 (Load_Use, \EX段冲突 , or_10_out);
  and and_16 (and_16_out, ~or_10_out, \EX段冲突 );  // AND_Gate
  and and_17 (and_17_out, \MEM段冲突 , \rB在MEM段冲突 );
  and and_18 (and_18_out, \EX段冲突 , \rB在EX段冲突 );
  or or_12 (or_12_out, and_13_out, and_14_out);
  or or_13 (or_13_out, and_16_out, \MEM段冲突 );
  or or_14 (or_14_out, and_17_out, and_18_out);
  and and_19 (redirect_RF_A, or_12_out, or_13_out);
  and and_20 (redirect_RF_B, or_13_out, or_14_out);
  Multiplexer #(.width(32), .enable("false")) multiplexer_1 (
    .in0(MEM_Data), .in1(EX_Data), .out(redirected_RF_A), .sel(and_13_out));
  Multiplexer #(.width(32), .enable("false")) multiplexer_2 (
    .in0(MEM_Data), .in1(EX_Data), .out(redirected_RF_B), .sel(and_18_out));

  // Other names for the same wires on the sheet: read_rB = Control_signals[5]; read_rA = Control_signals[6];
  //   syscall = Control_signals[8]
endmodule
