// Logisim project cpu_interruptible.circ as structural Verilog: 5 circuits, main circuit MIPS CPU
module MIPS_CPU (
);

  wire ALU_Equal, ALU_R_0, and_1_out, and_2_out, and_3_out, and_6_out, and_7_out, and_8_out, and_12_out,
       and_13_out, and_14_out, beq, bltz, bne, branch, clear1, clear2, clear3, clk, clock_1_out, d_ff_1_q,
       d_ff_2_q, d_ff_3_q, d_ff_4_q, d_ff_5_q, d_ff_6_q, d_ff_7_qn, d_ff_8_qn, demultiplexer_1_out0,
       demultiplexer_1_out1, display__a0, EXL, go_Int, halt, IE, IM1, IM2, IM3, Int, IR1, IR1_q, IR2, IR2_q,
       IR3, IR3_q, not_1_out, not_2_out, or_1_out, or_2_out, or_3_out, or_4_out, or_8_out, or_9_out,
       priority_encoder_1_gs, rd_1, RST, stop, W1, W2, W3, \单步执行_out ;
  wire [1:0] Cause;
  wire [3:0] ALUOP;
  wire [4:0] multiplexer_11_out, multiplexer_13_out, multiplexer_14_out, multiplexer_15_out, rom_1_data,
       rom_1_data_2, rom_1_data_5, rom_1_data_6;
  wire [5:0] rom_1_data_3, rom_1_data_4;
  wire [15:0] Count, multiplexer_25_out, \无条件分支指令数 , \有条件分支成功跳转 ;
  wire [16:0] multiplexer_16_out, multiplexer_17_out, multiplexer_18_out;
  wire [23:0] control_signal;
  wire [29:0] bit_extender_1_out_2;
  wire [31:0] and_4_out, and_5_out, branch_addr, EPC, mips_ram_1_p6, multiplexer_1_out, multiplexer_2_out,
       multiplexer_3_out, multiplexer_4_out, multiplexer_5_out, multiplexer_6_out, multiplexer_7_out,
       multiplexer_8_out, multiplexer_9_out, multiplexer_10_out, multiplexer_12_out, multiplexer_19_out,
       multiplexer_20_out, multiplexer_21_out, multiplexer_22_out, multiplexer_23_out, multiplexer_24_out,
       PC_1, PC_q, RF_A, RF_B, SyscallOut;
  wire [31:1] alu_1_result;
  wire [31:2] Status;
  wire [31:30] bit_extender_1_out;

  Button \u_总复位  (.out(RST));
  Button _1 (.out(IR1));
  Button _2 (.out(IR2));
  Button _3 (.out(IR3));
  LED led_1 (.in(W1));
  LED led_2 (.in(W2));
  LED led_3 (.in(W3));
  D_Flip_Flop d_ff_1 (.clk(IR1), .D(1'b1), .Q(d_ff_1_q), .reset(IR1_q));  // open: Qn, preset, en
  D_Flip_Flop d_ff_2 (.clk(clear1), .D(1'b1), .Q(d_ff_2_q));  // open: Qn, preset, en, reset
  D_Flip_Flop d_ff_3 (.clk(IR2), .D(1'b1), .Q(d_ff_3_q), .reset(IR2_q));  // open: Qn, preset, en
  D_Flip_Flop d_ff_4 (.clk(clear2), .D(1'b1), .Q(d_ff_4_q));  // open: Qn, preset, en, reset
  D_Flip_Flop d_ff_5 (.clk(IR3), .D(1'b1), .Q(d_ff_5_q), .reset(IR3_q));  // open: Qn, preset, en
  D_Flip_Flop d_ff_6 (.clk(clear3), .D(1'b1), .Q(d_ff_6_q));  // open: Qn, preset, en, reset
  Hex_Digit_Display hex_digit_display_1 (.value(SyscallOut[31:28]));  // open: dp
  or or_1 (or_1_out, d_ff_1_q, IR1_q);
  and and_1 (and_1_out, or_1_out, ~d_ff_2_q);  // AND_Gate
  or or_2 (or_2_out, d_ff_3_q, IR2_q);
  and and_2 (and_2_out, or_2_out, ~d_ff_4_q);  // AND_Gate
  or or_3 (or_3_out, d_ff_5_q, IR3_q);
  and and_3 (and_3_out, or_3_out, ~d_ff_6_q);  // AND_Gate
  Hex_Digit_Display hex_digit_display_2 (.value(SyscallOut[27:24]));  // open: dp
  Hex_Digit_Display hex_digit_display_3 (.value(SyscallOut[23:20]));  // open: dp
  assign and_4_out = {Status[31:13], IM3, Status[11:9], IM2, Status[7:5], IM1, Status[3:2], EXL, IE} & 32'hfffffffd;  // AND_Gate and_4, 32 bits wide
  D_Flip_Flop u_IR1 (.clk(clk), .D(and_1_out), .Q(IR1_q), .reset(RST));  // open: Qn, preset, en
  D_Flip_Flop u_IR2 (.clk(clk), .D(and_2_out), .Q(IR2_q), .reset(RST));  // open: Qn, preset, en
  D_Flip_Flop u_IR3 (.clk(clk), .D(and_3_out), .Q(IR3_q), .reset(RST));  // open: Qn, preset, en
  Hex_Digit_Display hex_digit_display_4 (.value(SyscallOut[15:12]));  // open: dp
  Hex_Digit_Display hex_digit_display_5 (.value(SyscallOut[19:16]));  // open: dp
  Demultiplexer #(.disabled(0)) demultiplexer_1 (
    .out0(demultiplexer_1_out0), .out1(demultiplexer_1_out1), .in(or_4_out), .sel(rd_1), .en(or_4_out));
  or or_4 (or_4_out, control_signal[1], control_signal[0]);
  Multiplexer #(.width(32), .enable("false")) multiplexer_1 (
    .in0(RF_B), .in1(and_4_out), .out(multiplexer_1_out), .sel(control_signal[0]));
  assign and_5_out = {Status[31:13], IM3, Status[11:9], IM2, Status[7:5], IM1, Status[3:2], EXL, IE} & 32'hfffffffe;  // AND_Gate and_5, 32 bits wide
  or or_5 (W1, d_ff_1_q, IR1_q);
  or or_6 (W2, d_ff_3_q, IR2_q);
  or or_7 (W3, d_ff_5_q, IR3_q);
  Hex_Digit_Display hex_digit_display_6 (.value(SyscallOut[11:8]));  // open: dp
  Hex_Digit_Display hex_digit_display_7 (.value(SyscallOut[7:4]));  // open: dp
  // Probe on multiplexer_2_out
  Multiplexer #(.width(32), .enable("false")) multiplexer_2 (
    .in0(multiplexer_6_out), .in1(RF_B), .out(multiplexer_2_out), .sel(control_signal[1]));
  or or_8 (or_8_out, Int, demultiplexer_1_out1);
  or or_9 (or_9_out, Int, demultiplexer_1_out0);
  Multiplexer #(.width(32), .enable("false")) multiplexer_3 (
    .in0(multiplexer_1_out), .in1(and_5_out), .out(multiplexer_3_out), .sel(Int));
  and and_6 (and_6_out, IM1, IR1_q);
  and and_7 (and_7_out, IM2, IR2_q);
  and and_8 (and_8_out, IM3, IR3_q);
  Hex_Digit_Display hex_digit_display_8 (.value(SyscallOut[3:0]));  // open: dp
  Register #(.width(32), .trigger("falling")) u_EPC (
    .D(multiplexer_2_out), .en(or_8_out), .Q(EPC), .clk(clk), .clr(RST));
  Register #(.width(32), .trigger("falling")) u_Status (
    .D(multiplexer_3_out), .en(or_9_out),
    .Q({Status[31:13], IM3, Status[11:9], IM2, Status[7:5], IM1, Status[3:2], EXL, IE}), .clk(clk), .clr(RST));
  Priority_Encoder #(.select(2)) priority_encoder_1 (
    .in0(1'b0), .in1(and_6_out), .in2(and_7_out), .in3(and_8_out), .out(Cause), .gs(priority_encoder_1_gs));  // open: en_out, en_in
  Clock clock_1 (.out(clock_1_out));
  xor xor_1 (clk, clock_1_out, \单步执行_out );
  Button \u_单步执行  (.out(\单步执行_out ));
  Multiplexer #(.width(32), .enable("false")) multiplexer_4 (
    .in0(multiplexer_6_out), .in1(EPC), .out(multiplexer_4_out), .sel(control_signal[0]));
  Multiplexer #(.select(2), .width(32)) multiplexer_5 (
    .in1(32'h337c), .in2(32'h3424), .in3(32'h34cc), .out(multiplexer_5_out), .sel(Cause), .en(go_Int));  // open: in0
  Demultiplexer #(.select(2), .disabled(0)) demultiplexer_2 (
    .out1(clear1), .out2(clear2), .out3(clear3), .in(Int), .sel(Cause), .en(Int));  // open: out0
  and and_9 (Int, priority_encoder_1_gs, IE, ~EXL);  // AND_Gate
  D_Flip_Flop d_ff_7 (.clk(Int), .D(d_ff_7_qn), .Q(go_Int), .Qn(d_ff_7_qn));  // open: preset, en, reset
  // Probe on Count
  // Probe on \无条件分支指令数 
  // Probe on \有条件分支成功跳转 
  Multiplexer #(.width(32), .enable("false")) multiplexer_6 (
    .in0(multiplexer_8_out), .in1(multiplexer_9_out), .out(multiplexer_6_out), .sel(control_signal[9]));
  // Probe on multiplexer_7_out
  Multiplexer #(.width(32), .enable("false")) multiplexer_7 (
    .in0(multiplexer_4_out), .in1(multiplexer_5_out), .out(multiplexer_7_out), .sel(go_Int));
  not not_1 (not_1_out, halt);
  Multiplexer #(.width(32), .enable("false")) multiplexer_8 (
    .in0(PC_1), .in1(branch_addr), .out(multiplexer_8_out), .sel(branch));
  Multiplexer #(.width(32), .enable("false")) multiplexer_9 (
    .in0({PC_1[31:28], rom_1_data_2, rom_1_data, rom_1_data_6[4:2], rd_1, rom_1_data_6[0], rom_1_data_5, rom_1_data_4, 2'b00}),
    .in1(RF_A), .out(multiplexer_9_out), .sel(control_signal[8]));
  Register #(.width(32)) PC (.D(multiplexer_7_out), .en(not_1_out), .Q(PC_q), .clk(clk), .clr(RST));
  D_Flip_Flop d_ff_8 (.clk(clk), .D(stop), .Qn(d_ff_8_qn), .reset(RST));  // open: Q, preset, en
  PC_1 pc_1_1 (.PC(PC_q), .PC_4(PC_1));
  Counter #(.width(16), .max('hffff), .trigger("falling")) \u_总周期计数  (
    .count(d_ff_8_qn), .Q(Count), .clk(clk), .clr(RST));  // open: load, D, carry
  Register #(.width(32)) \u_数码管锁存  (.D(RF_B), .en(display__a0), .Q(SyscallOut), .clk(clk), .clr(RST));
  Controller controller_1 (
    .OP(rom_1_data_3), .Funct(rom_1_data_4),
    .\控制信号 ({ALUOP, control_signal[23:8], beq, bne, bltz, control_signal[4:0]}), .RS(rom_1_data_2));
  ROM #(.addrWidth(10), .dataWidth(32)) rom_1 (
    .addr(PC_q[11:2]),
    .data({rom_1_data_3, rom_1_data_2, rom_1_data, rom_1_data_6[4:2], rd_1, rom_1_data_6[0], rom_1_data_5, rom_1_data_4}));  // open: sel
  Multiplexer #(.width(32), .enable("false")) multiplexer_10 (
    .in0({Status[31:13], IM3, Status[11:9], IM2, Status[7:5], IM1, Status[3:2], EXL, IE}), .in1(EPC),
    .out(multiplexer_10_out), .sel(rd_1));
  Multiplexer #(.width(5), .enable("false")) multiplexer_11 (
    .in0(rom_1_data), .in1({rom_1_data_6[4:2], rd_1, rom_1_data_6[0]}), .out(multiplexer_11_out),
    .sel(control_signal[21]));
  Counter #(.width(16), .max('hffff), .trigger("falling")) \u_无条件分支指令计数  (
    .count(control_signal[9]), .Q(\无条件分支指令数 ), .clk(clk), .clr(RST));  // open: load, D, carry
  Multiplexer #(.width(32), .enable("false")) multiplexer_12 (
    .in0(multiplexer_20_out), .in1(multiplexer_10_out), .out(multiplexer_12_out), .sel(control_signal[2]));
  Multiplexer #(.width(5), .enable("false")) multiplexer_13 (
    .in0(rom_1_data_2), .in1(5'b00010), .out(multiplexer_13_out), .sel(control_signal[23]));
  Multiplexer #(.width(5), .enable("false")) multiplexer_14 (
    .in0(rom_1_data), .in1(5'b00100), .out(multiplexer_14_out), .sel(control_signal[22]));
  Multiplexer #(.width(5), .enable("false")) multiplexer_15 (
    .in0(multiplexer_11_out), .in1({5{1'b1}}), .out(multiplexer_15_out), .sel(control_signal[20]));
  Multiplexer #(.width(17), .enable("false")) multiplexer_16 (
    .in0(17'ha), .in1({{12{1'b0}}, rom_1_data_5}), .out(multiplexer_16_out), .sel(control_signal[12]));
  Multiplexer #(.width(17), .enable("false")) multiplexer_17 (
    .in0(multiplexer_16_out), .in1(multiplexer_18_out), .out(multiplexer_17_out), .sel(control_signal[11]));
  Multiplexer #(.width(17), .enable("false")) multiplexer_18 (
    .in0({{2{rom_1_data_6[4]}}, rom_1_data_6[3:2], rd_1, rom_1_data_6[0], rom_1_data_5, rom_1_data_4}),
    .in1({1'b0, rom_1_data_6[4:2], rd_1, rom_1_data_6[0], rom_1_data_5, rom_1_data_4}),
    .out(multiplexer_18_out), .sel(control_signal[10]));
  Multiplexer #(.width(32), .enable("false")) multiplexer_19 (
    .in0({alu_1_result, ALU_R_0}), .in1(PC_1), .out(multiplexer_19_out), .sel(control_signal[18]));
  Multiplexer #(.width(32), .enable("false")) multiplexer_20 (
    .in0(multiplexer_19_out), .in1(multiplexer_21_out), .out(multiplexer_20_out), .sel(control_signal[17]));
  Multiplexer #(.width(32), .enable("false")) multiplexer_21 (
    .in0(mips_ram_1_p6), .in1({{16{1'b0}}, multiplexer_25_out}), .out(multiplexer_21_out),
    .sel(control_signal[16]));
  // Probe on multiplexer_15_out
  assign {bit_extender_1_out, bit_extender_1_out_2} = {{15{multiplexer_17_out[16]}}, multiplexer_17_out};  // Bit_Extender bit_extender_1
  // RegisterFile registerfile_1: pin names not known; wires that end beside it: multiplexer_12_out, clk, control_signal[19], multiplexer_15_out, multiplexer_13_out, multiplexer_14_out, RF_A, RF_B
  // Probe on multiplexer_14_out
  // Probe on multiplexer_13_out
  Counter #(.width(16), .max('hffff), .trigger("falling")) \u_有条件分支成功跳转计数  (
    .count(branch), .Q(\有条件分支成功跳转 ), .clk(clk), .clr(RST));  // open: load, D, carry
  Multiplexer #(.width(32), .enable("false")) multiplexer_22 (
    .in0(RF_A), .in1(RF_B), .out(multiplexer_22_out), .sel(control_signal[15]));
  Multiplexer #(.width(32), .enable("false")) multiplexer_23 (
    .in0(RF_B), .in1(RF_A), .out(multiplexer_23_out), .sel(control_signal[14]));
  Multiplexer #(.width(32), .enable("false")) multiplexer_24 (
    .in0(multiplexer_23_out), .in1({bit_extender_1_out, bit_extender_1_out_2}), .out(multiplexer_24_out),
    .sel(control_signal[13]));
  // MIPS_RAM mips_ram_1: pin names not known; wires that end beside it: alu_1_result[25:2], RF_B, control_signal[3], clk, RST, mips_ram_1_p6
  Adder #(.width(32)) adder_1 (.a(PC_1), .b({bit_extender_1_out_2, 2'b00}), .out(branch_addr));  // open: cin, cout
  ALU alu_1 (
    .X(multiplexer_22_out), .Y(multiplexer_24_out), .AluOP(ALUOP), .Equal(ALU_Equal),
    .Result({alu_1_result, ALU_R_0}));  // open: Signed_Overflow, UnSigned_Overflow, Result_2
  Multiplexer #(.width(16), .enable("false")) multiplexer_25 (
    .in0(mips_ram_1_p6[15:0]), .in1(mips_ram_1_p6[31:16]), .out(multiplexer_25_out), .sel(alu_1_result[1]));
  not not_2 (not_2_out, ALU_Equal);
  and and_10 (halt, control_signal[4], ~not_2_out);  // AND_Gate
  and and_11 (display__a0, control_signal[4], not_2_out);
  and and_12 (and_12_out, ALU_Equal, beq);
  and and_13 (and_13_out, ~ALU_Equal, bne);  // AND_Gate
  and and_14 (and_14_out, ALU_R_0, bltz);
  or or_10 (branch, and_12_out, and_13_out, and_14_out);

  // Other names for the same wires on the sheet: eret = control_signal[0]; mtc0 = control_signal[1];
  //   mfc0 = control_signal[2]; DM_WE = control_signal[3]; syscall = control_signal[4];
  //   control_signal (some bits) = {ALUOP, beq, bne, bltz}; jump_register = control_signal[8];
  //   jump = control_signal[9]; zero_ext_IMM = control_signal[10]; extend_IMM = control_signal[11];
  //   extend_shamt = control_signal[12]; Y__S_EXT = control_signal[13]; Y__RF_A = control_signal[14];
  //   X__RF_B = control_signal[15]; Din__DM_half = control_signal[16]; Din__DM = control_signal[17];
  //   Din__PC_1 = control_signal[18]; RF_WE = control_signal[19]; rW__GPR_31 = control_signal[20];
  //   rW__rd = control_signal[21]; rB___a0 = control_signal[22]; rA___v0 = control_signal[23];
  //   Status (some bits) = {IM3, IM2, IM1, EXL, IE}; 总周期数[15:0] = Count

  // Notes on the sheet:
  //   中断源
  //   中断等待指示
  //   数码管输出
  //   指令存储器
  //   contents of rom_1 (hex, n*v repeats v):
  //   0 201dffff 201b1111 409b6000 20110001 8000c09 20110001 20120002 20130003 8000c0d 20110001 20120002
  //   20130003 8000c11 20110001 20120002 20130003 8000c15 20110001 20120002 20130003 c000cbc 20100001
  //   20110001 118fc0 112020 20020022 c 118882 12200001 8000c19 112020 20020022 c 20110001 118880 112020
  //   20020022 c 12200001 8000c23 20110001 118fc0 112020 20020022 c 1188c3 112020 20020022 c 118903 112020
  //   20020022 c 118903 112020 20020022 c 118903 112020 20020022 c 118903 112020 20020022 c 118903 112020
  //   20020022 c 118903 112020 20020022 c 118903 112020 20020022 c 20100001 109fc0 139fc3 8021 2012000c
  //   24160003 26100001 3210000f 20080008 20090001 139900 2709825 132020 20020022 c 1094022 1500fff9
  //   22100001 2018000f 2188024 108700 20080008 20090001 139902 2709825 132021 20020022 c 1094022 1500fff9
  //   108702 2c9b022 12c00001 8000c54 4020 1084027 84400 3508ffff 82021 20020022 c 2010ffff 20110000
  //   ae300000 22100001 22310004 ae300000 22100001 22310004 ae300000 22100001 22310004 ae300000 22100001
  //   22310004 ae300000 22100001 22310004 ae300000 22100001 22310004 ae300000 22100001 22310004 ae300000
  //   22100001 22310004 ae300000 22100001 22310004 ae300000 22100001 22310004 ae300000 22100001 22310004
  //   ae300000 22100001 22310004 ae300000 22100001 22310004 ae300000 22100001 22310004 ae300000 22100001
  //   22310004 ae300000 22100001 22310004 22100001 8020 2011003c 8e130000 8e340000 274402a 11000002
  //   ae330000 ae140000 2231fffc 1611fff8 102020 20020022 c 22100004 2011003c 1611fff2 2002000a c 20100000
  //   22100001 102020 20020022 c 22100002 102020 20020022 c 22100003 102020 20020022 c 22100004 102020
  //   20020022 c 22100005 102020 20020022 c 22100006 102020 20020022 c 22100007 102020 20020022 c 22100008
  //   102020 20020022 20020022 c 3e00008 23bdffe0 afa40000 afa20004 afb00008 afb3000c afb40010 afb50014
  //   afb60018 401a7000 afba001c 401a6000 afba0020 201b1101 409b6000 20160001 20140006 20150001 168020
  //   108100 2149825 132020 20020022 c 1600fffa 295a022 1680fff7 40806000 8fa40000 8fa20004 8fb00008
  //   8fb3000c 8fb40010 8fb50014 8fb60018 8fba001c 409a7000 8fba0020 409a6000 23bd0020 201b1103 409b6000
  //   42000018 23bdffe0 afa40000 afa20004 afb00008 afb3000c afb40010 afb50014 afb60018 401a7000 afba001c
  //   401a6000 afba0020 201b1001 409b6000 20160002 20140006 20150001 168020 108100 2149825 132020 20020022
  //   c 1600fffa 295a022 1680fff7 40806000 8fa40000 8fa20004 8fb00008 8fb3000c 8fb40010 8fb50014 8fb60018
  //   8fba001c 409a7000 8fba0020 409a6000 23bd0020 201b1003 409b6000 42000018 23bdffe0 afa40000 afa20004
  //   afb00008 afb3000c afb40010 afb50014 afb60018 401a7000 afba001c 401a6000 afba0020 201b0001 409b6000
  //   20160003 20140006 20150001 168020 108100 2149825 132020 20020022 c 1600fffa 295a022 1680fff7
  //   40806000 8fa40000 8fa20004 8fb00008 8fb3000c 8fb40010 8fb50014 8fb60018 8fba001c 409a7000 8fba0020
  //   409a6000 23bd0020 201b0003 409b6000 42000018
  //   寄存器堆
  //   数据存储器
endmodule

module PC_1 (
  input  [31:0] PC,
  output [31:0] PC_4
);

  Adder #(.width(32)) adder_1 (.a(PC), .b(32'h4), .out(PC_4));  // open: cin, cout
endmodule

// Contorller
module Controller (
  input  [5:0] OP,
  input  [5:0] Funct,
  input  [4:0] RS,
  output [27:0] \控制信号 
);

  wire add, addi, addiu, addu, \and , andi, comparator_1_eq, comparator_16_eq, comparator_17_eq,
       comparator_18_eq, comparator_19_eq, comparator_20_eq, comparator_21_eq, comparator_22_eq,
       comparator_23_eq, comparator_24_eq, comparator_25_eq, comparator_26_eq, comparator_27_eq,
       comparator_28_eq, comparator_29_eq, comparator_30_eq, comparator_31_eq, comparator_32_eq,
       comparator_33_eq, j, lw, \nor , \or , or_2_out, or_3_out, or_4_out, or_5_out, or_6_out, or_7_out,
       or_9_out, or_10_out, or_11_out, or_12_out, or_13_out, or_14_out, or_15_out, or_16_out, or_17_out,
       or_18_out, or_19_out, or_21_out, or_22_out, or_23_out, or_24_out, or_25_out, or_26_out, or_27_out,
       or_28_out, or_30_out, or_31_out, or_32_out, or_33_out, or_34_out, or_35_out, or_36_out, or_37_out,
       or_38_out, or_39_out, or_40_out, or_42_out, or_43_out, or_44_out, or_45_out, or_46_out, or_47_out,
       or_48_out, or_49_out, or_50_out, or_51_out, or_53_out, or_54_out, or_55_out, or_56_out, or_57_out,
       or_58_out, or_59_out, or_60_out, or_61_out, or_62_out, or_63_out, or_65_out, or_66_out, or_67_out,
       or_68_out, or_69_out, or_70_out, or_71_out, or_72_out, or_73_out, or_75_out, or_76_out, or_78_out,
       or_79_out, or_80_out, or_81_out, or_82_out, or_83_out, or_84_out, or_85_out, or_86_out, or_87_out,
       or_88_out, or_90_out, or_92_out, or_93_out, or_94_out, or_95_out, or_96_out, or_97_out, or_98_out,
       or_99_out, or_100_out, or_101_out, or_104_out, ori, sll, slt, slti, sltiu, sltu, sra, srl, sub;

  Comparator #(.width(6)) comparator_1 (.a(OP), .b({6{1'b0}}), .eq(comparator_1_eq));  // open: gt, lt
  Comparator #(.width(6)) comparator_2 (.a(OP), .b(6'b000001), .eq(\控制信号 [5]));  // open: gt, lt
  Comparator #(.width(6)) comparator_3 (.a(OP), .b(6'b000010), .eq(j));  // open: gt, lt
  Comparator #(.width(6)) comparator_4 (.a(OP), .b(6'b000011), .eq(\控制信号 [20]));  // open: gt, lt
  Comparator #(.width(6)) comparator_5 (.a(OP), .b(6'b000100), .eq(\控制信号 [7]));  // open: gt, lt
  Comparator #(.width(6)) comparator_6 (.a(OP), .b(6'b000101), .eq(\控制信号 [6]));  // open: gt, lt
  Comparator #(.width(6)) comparator_7 (.a(OP), .b(6'b001000), .eq(addi));  // open: gt, lt
  Comparator #(.width(6)) comparator_8 (.a(OP), .b(6'b001001), .eq(addiu));  // open: gt, lt
  Comparator #(.width(6)) comparator_9 (.a(OP), .b(6'b001010), .eq(slti));  // open: gt, lt
  Comparator #(.width(6)) comparator_10 (.a(OP), .b(6'b001011), .eq(sltiu));  // open: gt, lt
  Comparator #(.width(6)) comparator_11 (.a(OP), .b(6'b001100), .eq(andi));  // open: gt, lt
  Comparator #(.width(6)) comparator_12 (.a(OP), .b(6'b001101), .eq(ori));  // open: gt, lt
  Comparator #(.width(6)) comparator_13 (.a(OP), .b(6'b100001), .eq(\控制信号 [16]));  // open: gt, lt
  Comparator #(.width(6)) comparator_14 (.a(OP), .b(6'b100011), .eq(lw));  // open: gt, lt
  Comparator #(.width(6)) comparator_15 (.a(OP), .b(6'b101011), .eq(\控制信号 [3]));  // open: gt, lt
  Comparator #(.width(6)) comparator_16 (.a(OP), .b(6'b010000), .eq(comparator_16_eq));  // open: gt, lt
  Comparator #(.width(6)) comparator_17 (.a(Funct), .b({6{1'b0}}), .eq(comparator_17_eq));  // open: gt, lt
  Comparator #(.width(6)) comparator_18 (.a(Funct), .b(6'b000010), .eq(comparator_18_eq));  // open: gt, lt
  Comparator #(.width(6)) comparator_19 (.a(Funct), .b(6'b000011), .eq(comparator_19_eq));  // open: gt, lt
  Comparator #(.width(6)) comparator_20 (.a(Funct), .b(6'b000110), .eq(comparator_20_eq));  // open: gt, lt
  Comparator #(.width(6)) comparator_21 (.a(Funct), .b(6'b001000), .eq(comparator_21_eq));  // open: gt, lt
  Comparator #(.width(6)) comparator_22 (.a(Funct), .b(6'b001100), .eq(comparator_22_eq));  // open: gt, lt
  Comparator #(.width(6)) comparator_23 (.a(Funct), .b(6'b100000), .eq(comparator_23_eq));  // open: gt, lt
  Comparator #(.width(6)) comparator_24 (.a(Funct), .b(6'b100001), .eq(comparator_24_eq));  // open: gt, lt
  Comparator #(.width(6)) comparator_25 (.a(Funct), .b(6'b100010), .eq(comparator_25_eq));  // open: gt, lt
  Comparator #(.width(6)) comparator_26 (.a(Funct), .b(6'b100100), .eq(comparator_26_eq));  // open: gt, lt
  Comparator #(.width(6)) comparator_27 (.a(Funct), .b(6'b100101), .eq(comparator_27_eq));  // open: gt, lt
  Comparator #(.width(6)) comparator_28 (.a(Funct), .b(6'b100111), .eq(comparator_28_eq));  // open: gt, lt
  Comparator #(.width(6)) comparator_29 (.a(Funct), .b(6'b101010), .eq(comparator_29_eq));  // open: gt, lt
  Comparator #(.width(6)) comparator_30 (.a(Funct), .b(6'b101011), .eq(comparator_30_eq));  // open: gt, lt
  Comparator #(.width(6)) comparator_31 (.a(Funct), .b(6'b011000), .eq(comparator_31_eq));  // open: gt, lt
  Comparator #(.width(5)) comparator_32 (.a(RS), .b({5{1'b0}}), .eq(comparator_32_eq));  // open: gt, lt
  Comparator #(.width(5)) comparator_33 (.a(RS), .b(5'b00100), .eq(comparator_33_eq));  // open: gt, lt
  // Probe on {\控制信号 [27:23], \控制信号 [23], \控制信号 [21:19], \控制信号 [20], \控制信号 [17:5], \控制信号 [23], \控制信号 [3:0]}
  and and_1 (sll, comparator_1_eq, comparator_17_eq);
  and and_2 (srl, comparator_1_eq, comparator_18_eq);
  and and_3 (sra, comparator_1_eq, comparator_19_eq);
  and and_4 (\控制信号 [14], comparator_1_eq, comparator_20_eq);
  and and_5 (\控制信号 [8], comparator_1_eq, comparator_21_eq);
  and and_6 (\控制信号 [23], comparator_1_eq, comparator_22_eq);
  and and_7 (add, comparator_1_eq, comparator_23_eq);
  and and_8 (addu, comparator_1_eq, comparator_24_eq);
  and and_9 (sub, comparator_1_eq, comparator_25_eq);
  and and_10 (\and , comparator_1_eq, comparator_26_eq);
  and and_11 (\or , comparator_1_eq, comparator_27_eq);
  and and_12 (\nor , comparator_1_eq, comparator_28_eq);
  and and_13 (slt, comparator_1_eq, comparator_29_eq);
  and and_14 (sltu, comparator_1_eq, comparator_30_eq);
  and and_15 (\控制信号 [0], comparator_16_eq, comparator_31_eq);
  and and_16 (\控制信号 [2], comparator_16_eq, comparator_32_eq);
  and and_17 (\控制信号 [1], comparator_16_eq, comparator_33_eq);
  or or_1 (\控制信号 [27], \or , or_2_out);
  or or_2 (or_2_out, or_3_out, \nor );
  or or_3 (or_3_out, slt, or_4_out);
  or or_4 (or_4_out, or_5_out, sltu);
  or or_5 (or_5_out, \控制信号 [5], or_6_out);
  or or_6 (or_6_out, or_7_out, slti);
  or or_7 (or_7_out, sltiu, ori);
  or or_8 (\控制信号 [26], \控制信号 [23], or_9_out);
  or or_9 (or_9_out, or_10_out, add);
  or or_10 (or_10_out, addu, or_11_out);
  or or_11 (or_11_out, or_12_out, sub);
  or or_12 (or_12_out, \and , or_13_out);
  or or_13 (or_13_out, or_14_out, sltu);
  or or_14 (or_14_out, addi, or_15_out);
  or or_15 (or_15_out, or_16_out, addiu);
  or or_16 (or_16_out, sltiu, or_17_out);
  or or_17 (or_17_out, or_18_out, andi);
  or or_18 (or_18_out, \控制信号 [16], or_19_out);
  or or_19 (or_19_out, lw, \控制信号 [3]);
  or or_20 (\控制信号 [25], srl, or_21_out);
  or or_21 (or_21_out, or_22_out, \控制信号 [14]);
  or or_22 (or_22_out, \控制信号 [23], or_23_out);
  or or_23 (or_23_out, or_24_out, sub);
  or or_24 (or_24_out, \and , or_25_out);
  or or_25 (or_25_out, or_26_out, \nor );
  or or_26 (or_26_out, slt, or_27_out);
  or or_27 (or_27_out, or_28_out, \控制信号 [5]);
  or or_28 (or_28_out, slti, andi);
  or or_29 (\控制信号 [24], sra, or_30_out);
  or or_30 (or_30_out, or_31_out, add);
  or or_31 (or_31_out, addu, or_32_out);
  or or_32 (or_32_out, or_33_out, \and );
  or or_33 (or_33_out, slt, or_34_out);
  or or_34 (or_34_out, or_35_out, \控制信号 [5]);
  or or_35 (or_35_out, addi, or_36_out);
  or or_36 (or_36_out, or_37_out, addiu);
  or or_37 (or_37_out, slti, or_38_out);
  or or_38 (or_38_out, or_39_out, andi);
  or or_39 (or_39_out, \控制信号 [16], or_40_out);
  or or_40 (or_40_out, lw, \控制信号 [3]);
  or or_41 (\控制信号 [21], sll, or_42_out);
  or or_42 (or_42_out, or_43_out, srl);
  or or_43 (or_43_out, sra, or_44_out);
  or or_44 (or_44_out, or_45_out, \控制信号 [14]);
  or or_45 (or_45_out, add, or_46_out);
  or or_46 (or_46_out, or_47_out, addu);
  or or_47 (or_47_out, sub, or_48_out);
  or or_48 (or_48_out, or_49_out, \and );
  or or_49 (or_49_out, \or , or_50_out);
  or or_50 (or_50_out, or_51_out, \nor );
  or or_51 (or_51_out, slt, sltu);
  or or_52 (\控制信号 [19], sll, or_53_out);
  or or_53 (or_53_out, or_54_out, srl);
  or or_54 (or_54_out, sra, or_55_out);
  or or_55 (or_55_out, or_56_out, \控制信号 [14]);
  or or_56 (or_56_out, add, or_57_out);
  or or_57 (or_57_out, or_58_out, addu);
  or or_58 (or_58_out, sub, or_59_out);
  or or_59 (or_59_out, or_60_out, \and );
  or or_60 (or_60_out, \or , or_61_out);
  or or_61 (or_61_out, or_62_out, \nor );
  or or_62 (or_62_out, slt, or_63_out);
  or or_63 (or_63_out, sltu, or_65_out);
  or or_64 (\控制信号 [17], \控制信号 [16], lw);
  or or_65 (or_65_out, \控制信号 [20], or_66_out);
  or or_66 (or_66_out, or_67_out, addi);
  or or_67 (or_67_out, addiu, or_68_out);
  or or_68 (or_68_out, or_69_out, slti);
  or or_69 (or_69_out, sltiu, or_70_out);
  or or_70 (or_70_out, or_71_out, andi);
  or or_71 (or_71_out, ori, or_72_out);
  or or_72 (or_72_out, or_73_out, \控制信号 [16]);
  or or_73 (or_73_out, lw, \控制信号 [2]);
  or or_74 (\控制信号 [15], sll, or_75_out);
  or or_75 (or_75_out, or_76_out, srl);
  or or_76 (or_76_out, sra, \控制信号 [14]);
  or or_77 (\控制信号 [13], sll, or_78_out);
  or or_78 (or_78_out, or_79_out, srl);
  or or_79 (or_79_out, sra, or_80_out);
  or or_80 (or_80_out, or_81_out, \控制信号 [23]);
  or or_81 (or_81_out, addi, or_82_out);
  or or_82 (or_82_out, or_83_out, addiu);
  or or_83 (or_83_out, slti, or_84_out);
  or or_84 (or_84_out, or_85_out, sltiu);
  or or_85 (or_85_out, andi, or_86_out);
  or or_86 (or_86_out, or_87_out, ori);
  or or_87 (or_87_out, \控制信号 [16], or_88_out);
  or or_88 (or_88_out, lw, \控制信号 [3]);
  or or_89 (\控制信号 [12], sll, or_90_out);
  or or_90 (or_90_out, srl, sra);
  or or_91 (\控制信号 [11], \控制信号 [5], or_92_out);
  or or_92 (or_92_out, or_93_out, \控制信号 [7]);
  or or_93 (or_93_out, \控制信号 [6], or_94_out);
  or or_94 (or_94_out, or_95_out, addi);
  or or_95 (or_95_out, addiu, or_96_out);
  or or_96 (or_96_out, or_97_out, slti);
  or or_97 (or_97_out, sltiu, or_98_out);
  or or_98 (or_98_out, or_99_out, andi);
  or or_99 (or_99_out, ori, or_100_out);
  or or_100 (or_100_out, or_101_out, \控制信号 [16]);
  or or_101 (or_101_out, lw, \控制信号 [3]);
  or or_102 (\控制信号 [9], \控制信号 [8], or_104_out);
  or or_103 (\控制信号 [10], andi, ori);
  or or_104 (or_104_out, j, \控制信号 [20]);

  assign {\控制信号 [22], \控制信号 [18], \控制信号 [4]} = {\控制信号 [23], \控制信号 [20], \控制信号 [23]};

  // Other names for the same wires on the sheet: eret = \控制信号 [0]; mtc0 = \控制信号 [1]; mfc0 = \控制信号 [2]; sw = \控制信号 [3];
  //   bltz = \控制信号 [5]; bne = \控制信号 [6]; beq = \控制信号 [7]; jr = \控制信号 [8]; srlv = \控制信号 [14]; lh = \控制信号 [16];
  //   jal = \控制信号 [20]; syscall = \控制信号 [23]
endmodule

module ALU (
  input  [31:0] X,
  input  [31:0] Y,
  input  [3:0] AluOP,
  output Signed_Overflow,
  output UnSigned_Overflow,
  output Equal,
  output [31:0] Result,
  output [31:0] Result_2
);

  wire adder_1_cout, and_2_out, and_3_out, and_5_out, and_6_out, and_7_out, and_8_out, comparator_2_lt,
       or_2_out, or_4_out;
  wire [0:0] comparator_1_lt, xor_2_out;
  wire [31:0] adder_1_out, and_1_out, divider_1_out, divider_1_rem, multiplexer_2_out, multiplier_1_cout,
       multiplier_1_out, not_1_out, not_2_out, or_1_out, shifter_1_out, shifter_2_out, shifter_3_out,
       xor_1_out;

  // Probe on X
  // Probe on X
  // Probe on Y
  // Probe on Y
  Shifter #(.width(32)) shifter_1 (.in(X), .\dist (Y[4:0]), .out(shifter_1_out));
  Shifter #(.width(32), .shift("ar")) shifter_2 (.in(X), .\dist (Y[4:0]), .out(shifter_2_out));
  Shifter #(.width(32), .shift("lr")) shifter_3 (.in(X), .\dist (Y[4:0]), .out(shifter_3_out));
  Multiplier #(.width(32)) multiplier_1 (.a(X), .b(Y), .out(multiplier_1_out), .cout(multiplier_1_cout));  // open: cin
  Divider #(.width(32)) divider_1 (.a(X), .b(Y), .out(divider_1_out), .rem(divider_1_rem));  // open: upper
  assign and_1_out = X & Y;  // AND_Gate and_1, 32 bits wide
  assign or_1_out = X | Y;  // OR_Gate or_1, 32 bits wide
  assign xor_1_out = X ^ Y;  // XOR_Gate xor_1, 32 bits wide
  Comparator #(.width(32), .mode("unsigned")) comparator_1 (
    .a(X), .b(Y), .eq(Equal), .lt(comparator_1_lt[0]));  // open: gt
  Multiplexer #(.select(4), .width(32), .enable("false")) multiplexer_1 (
    .in0(shifter_1_out), .in1(shifter_2_out), .in2(shifter_3_out), .in3(multiplier_1_out),
    .in4(divider_1_out), .in5(adder_1_out), .in6(adder_1_out), .in7(and_1_out), .in8(or_1_out),
    .in9(xor_1_out), .in10(not_1_out), .in11({{31{1'b0}}, xor_2_out[0]}),
    .in12({{31{1'b0}}, comparator_1_lt[0]}), .in13({32{1'b0}}), .in14({32{1'b0}}), .in15({32{1'b0}}),
    .out(Result), .sel(AluOP));
  assign not_1_out = ~or_1_out;  // NOT_Gate not_1, 32 bits wide
  // Probe on AluOP
  xor xor_2 (xor_2_out[0], xor_1_out[31], comparator_1_lt[0]);
  // Probe on Result
  // Probe on Result
  Multiplexer #(.width(32), .enable("false")) multiplexer_2 (
    .in0(Y), .in1(not_2_out), .out(multiplexer_2_out), .sel(AluOP[1]));
  assign not_2_out = ~Y;  // NOT_Gate not_2, 32 bits wide
  // Probe on Result_2
  Adder #(.width(32)) adder_1 (.a(X), .b(multiplexer_2_out), .out(adder_1_out), .cin(AluOP[1]), .cout(adder_1_cout));
  Multiplexer #(.select(4), .width(32), .disabled(0), .enable("false")) multiplexer_3 (
    .in0({32{1'b0}}), .in1({32{1'b0}}), .in2({32{1'b0}}), .in3(multiplier_1_cout), .in4(divider_1_rem),
    .in5({32{1'b0}}), .in6({32{1'b0}}), .in7({32{1'b0}}), .in8({32{1'b0}}), .in9({32{1'b0}}),
    .in10({32{1'b0}}), .in11({32{1'b0}}), .in12({32{1'b0}}), .in13({32{1'b0}}), .in14({32{1'b0}}),
    .in15({32{1'b0}}), .out(Result_2), .sel(AluOP));
  and and_2 (and_2_out, ~adder_1_out[31], multiplexer_2_out[31], X[31]);  // AND_Gate
  or or_2 (or_2_out, and_2_out, and_3_out);
  and and_3 (and_3_out, adder_1_out[31], ~X[31], ~multiplexer_2_out[31]);  // AND_Gate
  Comparator #(.width(32), .mode("unsigned")) comparator_2 (
    .a(X), .b(adder_1_out), .lt(comparator_2_lt));  // open: gt, eq
  and and_4 (Signed_Overflow, or_2_out, or_4_out);
  or or_3 (UnSigned_Overflow, and_6_out, and_5_out);
  and and_5 (and_5_out, comparator_2_lt, and_8_out);
  and and_6 (and_6_out, adder_1_cout, and_7_out);
  or or_4 (or_4_out, and_7_out, and_8_out);
  and and_7 (and_7_out, AluOP[0], ~AluOP[1], AluOP[2], ~AluOP[3]);  // AND_Gate
  and and_8 (and_8_out, ~AluOP[0], AluOP[1], AluOP[2], ~AluOP[3]);  // AND_Gate

  // Other names for the same wires on the sheet: OF = Signed_Overflow; Result2[31:0] = Result_2; S[3:0] = AluOP;
  //   UOF = UnSigned_Overflow

  // Notes on the sheet:
  //   不要改变此引脚区域内容，也不要改变ALU封装形式
  //   输入引脚
  //   请在下方利用上方输入输出引脚的隧道信号构建ALU电路，ctrl+d复制选择部件
  //   华中科技大学计算机学院 计算机组成原理，鸣谢加州大学伯克利CS61C课程
  //   输出引脚
  //   探测区域
endmodule

// IC
module InterruptCatcher (
  input  clk,
  input  Int1,
  input  clear1,
  input  Int2,
  input  clear2,
  input  Int3,
  input  clear3,
  input  reset,
  output \_1号等待 ,
  output \_1号挂起 ,
  output \_2号等待 ,
  output \_2号挂起 ,
  output \_3号等待 ,
  output \_3号挂起 
);

  wire and_1_out, and_2_out, and_3_out, d_ff_1_q, d_ff_2_q, d_ff_3_q, or_1_out, or_2_out, or_3_out;

  D_Flip_Flop d_ff_1 (.clk(Int1), .D(1'b1), .Q(d_ff_1_q), .reset(\_1号挂起 ));  // open: Qn, preset, en
  D_Flip_Flop d_ff_2 (.clk(Int2), .D(1'b1), .Q(d_ff_2_q), .reset(\_2号挂起 ));  // open: Qn, preset, en
  D_Flip_Flop d_ff_3 (.clk(Int3), .D(1'b1), .Q(d_ff_3_q), .reset(\_3号挂起 ));  // open: Qn, preset, en
  or or_1 (or_1_out, d_ff_1_q, \_1号挂起 );
  and and_1 (and_1_out, or_1_out, ~clear1);  // AND_Gate
  or or_2 (or_2_out, d_ff_2_q, \_2号挂起 );
  and and_2 (and_2_out, or_2_out, ~clear2);  // AND_Gate
  or or_3 (or_3_out, d_ff_3_q, \_3号挂起 );
  and and_3 (and_3_out, or_3_out, ~clear3);  // AND_Gate
  D_Flip_Flop IR1 (.clk(clk), .D(and_1_out), .Q(\_1号挂起 ), .reset(reset));  // open: Qn, preset, en
  D_Flip_Flop IR2 (.clk(clk), .D(and_2_out), .Q(\_2号挂起 ), .reset(reset));  // open: Qn, preset, en
  D_Flip_Flop IR3 (.clk(clk), .D(and_3_out), .Q(\_3号挂起 ), .reset(reset));  // open: Qn, preset, en
  or or_4 (\_1号等待 , d_ff_1_q, \_1号挂起 );
  or or_5 (\_2号等待 , d_ff_2_q, \_2号挂起 );
  or or_6 (\_3号等待 , d_ff_3_q, \_3号挂起 );
endmodule
