// Logisim project CS1501_U201514477_华龙_cpu_redirect.circ as structural Verilog: 10 circuits, main circuit MIPS CPU
module MIPS_CPU (
);

  wire alu_1_equal, and_6_out, and_7_out, branch, clk, clock_1_out, d_ff_1_qn, d_ff_2_qn, d_ff_3_qn, Din__DM,
       Din__DM_half, Din__PC_1, display_a0, DM_WE, ex_mem_1_mem_halt, EX_RF_WE, goto, halting, IR1, IR2, IR3,
       jump, Load_Use, lock, MEM_RF_WE, not_1_out, not_2_out, not_3_out, not_4_out, not_5_out, or_3_out,
       pull_resistor_4_node, pull_resistor_6_node, rA___v0, rB___a0, redirecter_1_redirect_rf_a,
       redirecter_1_redirect_rf_b, RST, rW__GPR_31, rW__rd, stop, syscall, W1, W2, W3, WB_RF_WE, X__RF_B,
       Y__RF_A, Y__S_EXT, \单步执行_out ;
  wire [3:0] ALUOP;
  wire [4:0] EX_rW, MEM_rW, multiplexer_2_out, multiplexer_3_out, multiplexer_4_out, multiplexer_5_out, WB_rW;
  wire [5:0] EX_OP;
  wire [11:0] and_1_out, and_2_out, and_3_out, and_4_out, and_5_out;
  wire [15:0] Count, \load_use次数 , multiplexer_12_out, \插入气泡数 , \无条件分支指令数 , \有条件分支成功跳转 ;
  wire [25:0] id_ex_1_ex_ir;
  wire [27:0] id_ex_1_ex_ctrl;
  wire [31:0] \controller_1_控制信号 , EX_Data, ex_mem_1_mem_alu_r, ex_mem_1_mem_ctrl, ex_mem_1_mem_pc_1,
       ex_mem_1_mem_rf_b, EX_PC, extender_1_imm, goto_addr, id_ex_1_ex_imm, id_ex_1_ex_pc_1, id_ex_1_ex_rf_a,
       id_ex_1_ex_rf_b, ID_PC, if_id_1_id_ir, if_id_1_id_pc_1, IF_PC, MEM_Data, MEM_PC, mem_wb_1_wb_alu_r,
       mem_wb_1_wb_ctrl, mem_wb_1_wb_dm_d, mem_wb_1_wb_pc_1, mips_ram_1_p6, multiplexer_1_out,
       multiplexer_6_out, multiplexer_7_out, multiplexer_8_out, multiplexer_9_out, multiplexer_10_out,
       multiplexer_13_out, multiplexer_14_out, pc_1_1_pc_4, redirecter_1_redirected_rf_a,
       redirecter_1_redirected_rf_b, registerfile_1_p7, registerfile_1_p8, RF_W, rom_1_data, SyscallOut,
       WB_PC;

  Button \u_总复位  (.out(RST));
  Button _1 (.out(IR1));
  Button _2 (.out(IR2));
  Button _3 (.out(IR3));
  LED led_1 (.in(W1));
  LED led_2 (.in(W2));
  LED led_3 (.in(W3));
  Multiplexer #(.width(32), .enable("false")) multiplexer_1 (
    .in0(pc_1_1_pc_4), .in1(goto_addr), .out(multiplexer_1_out), .sel(goto));
  // Probe on multiplexer_1_out
  not not_1 (not_1_out, lock);
  Hex_Digit_Display hex_digit_display_1 (.value(SyscallOut[31:28]));  // open: dp
  // Probe on Count
  assign and_1_out = IF_PC[11:0] & {12{1'b1}};  // AND_Gate and_1, 12 bits wide
  // Probe on and_1_out
  assign and_2_out = ID_PC[11:0] & {12{1'b1}};  // AND_Gate and_2, 12 bits wide
  // Probe on and_2_out
  // Probe on and_3_out
  assign and_3_out = EX_PC[11:0] & {12{1'b1}};  // AND_Gate and_3, 12 bits wide
  // Probe on and_4_out
  assign and_4_out = MEM_PC[11:0] & {12{1'b1}};  // AND_Gate and_4, 12 bits wide
  assign and_5_out = WB_PC[11:0] & {12{1'b1}};  // AND_Gate and_5, 12 bits wide
  // Probe on and_5_out
  Register #(.width(32)) PC (.D(multiplexer_1_out), .en(not_1_out), .Q(IF_PC), .clk(clk), .clr(RST));
  and and_6 (and_6_out, ~goto, Load_Use);  // AND_Gate
  Hex_Digit_Display hex_digit_display_2 (.value(SyscallOut[23:20]));  // open: dp
  Hex_Digit_Display hex_digit_display_3 (.value(SyscallOut[27:24]));  // open: dp
  // Probe on IF_PC
  or or_1 (lock, stop, and_6_out);
  Hex_Digit_Display hex_digit_display_4 (.value(SyscallOut[19:16]));  // open: dp
  Hex_Digit_Display hex_digit_display_5 (.value(SyscallOut[15:12]));  // open: dp
  PC_1 pc_1_1 (.PC(IF_PC), .PC_4(pc_1_1_pc_4));
  Hex_Digit_Display hex_digit_display_6 (.value(SyscallOut[7:4]));  // open: dp
  Hex_Digit_Display hex_digit_display_7 (.value(SyscallOut[11:8]));  // open: dp
  IF_ID if_id_1 (
    .IF_PC(IF_PC), .ID_PC(ID_PC), .lock_when_0_stop_transport(not_2_out), .CLK(clk), .\同步清零 (goto),
    .IF_PC_1(pc_1_1_pc_4), .ID_PC_1(if_id_1_id_pc_1), .IF_IR(rom_1_data), .ID_IR(if_id_1_id_ir));
  ROM #(.addrWidth(10), .dataWidth(32)) rom_1 (.addr(IF_PC[11:2]), .data(rom_1_data));  // open: sel
  not not_2 (not_2_out, lock);
  Pull_Resistor #(.pull(1)) pull_resistor_1 (.node(not_2_out));
  Hex_Digit_Display hex_digit_display_8 (.value(SyscallOut[3:0]));  // open: dp
  Pull_Resistor pull_resistor_2 (.node(goto));
  // Probe on RF_W
  Controller controller_1 (
    .OP(if_id_1_id_ir[31:26]), .Funct(if_id_1_id_ir[5:0]),
    .\控制信号 ({\controller_1_控制信号 [31:28], rA___v0, rB___a0, rW__rd, rW__GPR_31, \controller_1_控制信号 [23:0]}));
  Extender extender_1 (
    .extend_IMM(\controller_1_控制信号 [15]), .extend_shamt(\controller_1_控制信号 [16]), .IR(if_id_1_id_ir),
    .zero_extend_IMM(\controller_1_控制信号 [14]), .IMM(extender_1_imm));
  // Probe on Count
  // Probe on \无条件分支指令数 
  // Probe on \有条件分支成功跳转 
  // Probe on \load_use次数 
  // Probe on \插入气泡数 
  // Probe on WB_rW
  Multiplexer #(.width(5), .enable("false")) multiplexer_2 (
    .in0(if_id_1_id_ir[20:16]), .in1(if_id_1_id_ir[15:11]), .out(multiplexer_2_out), .sel(rW__rd));
  Clock clock_1 (.out(clock_1_out));
  Button \u_单步执行  (.out(\单步执行_out ));
  Multiplexer #(.width(5), .enable("false")) multiplexer_3 (
    .in0(if_id_1_id_ir[25:21]), .in1(5'b00010), .out(multiplexer_3_out), .sel(rA___v0));
  Multiplexer #(.width(5), .enable("false")) multiplexer_4 (
    .in0(if_id_1_id_ir[20:16]), .in1(5'b00100), .out(multiplexer_4_out), .sel(rB___a0));
  Multiplexer #(.width(5), .enable("false")) multiplexer_5 (
    .in0(multiplexer_2_out), .in1({5{1'b1}}), .out(multiplexer_5_out), .sel(rW__GPR_31));
  D_Flip_Flop d_ff_1 (.clk(clk), .D(stop), .Qn(d_ff_1_qn), .reset(RST));  // open: Q, preset, en
  xor xor_1 (clk, clock_1_out, \单步执行_out );
  // RegisterFile registerfile_1: pin names not known; wires that end beside it: RF_W, clk, WB_RF_WE, WB_rW, multiplexer_3_out, multiplexer_4_out, registerfile_1_p7, registerfile_1_p8
  Redirecter redirecter_1 (
    .EX_rW(EX_rW), .rA(multiplexer_3_out), .rB(multiplexer_4_out), .MEM_rW(MEM_rW),
    .ID_OP(if_id_1_id_ir[31:26]), .EX_RF_WE(EX_RF_WE), .MEM_RF_WE(MEM_RF_WE), .Load_Use(Load_Use),
    .EX_OP(EX_OP), .ID_Funct(if_id_1_id_ir[5:0]), .redirected_RF_A(redirecter_1_redirected_rf_a),
    .redirected_RF_B(redirecter_1_redirected_rf_b), .EX_Data(EX_Data), .MEM_Data(MEM_Data),
    .redirect_RF_A(redirecter_1_redirect_rf_a), .redirect_RF_B(redirecter_1_redirect_rf_b));
  Counter #(.width(16), .max('hffff), .trigger("falling")) \u_总周期计数  (
    .count(d_ff_1_qn), .Q(Count), .clk(clk), .clr(RST));  // open: load, D, carry
  Counter #(.width(16), .max('hffff), .trigger("falling")) \Load_Use计数  (
    .count(Load_Use), .Q(\load_use次数 ), .clk(clk), .clr(RST));  // open: load, D, carry
  // Probe on ID_PC
  Multiplexer #(.width(32), .enable("false")) multiplexer_6 (
    .in0(registerfile_1_p7), .in1(redirecter_1_redirected_rf_a), .out(multiplexer_6_out),
    .sel(redirecter_1_redirect_rf_a));
  Multiplexer #(.width(32), .enable("false")) multiplexer_7 (
    .in0(registerfile_1_p8), .in1(redirecter_1_redirected_rf_b), .out(multiplexer_7_out),
    .sel(redirecter_1_redirect_rf_b));
  ID_EX id_ex_1 (
    .CLK(clk), .\同步清零 (pull_resistor_4_node), .ID_PC(ID_PC), .EX_PC(EX_PC), .ID_PC_1(if_id_1_id_pc_1),
    .EX_PC_1(id_ex_1_ex_pc_1), .ID_IR(if_id_1_id_ir), .EX_IR({EX_OP, id_ex_1_ex_ir}),
    .lock_when_0_stop_transport(not_3_out),
    .ID_CTRL({\controller_1_控制信号 [31:28], rA___v0, rB___a0, rW__rd, rW__GPR_31, \controller_1_控制信号 [23:0]}),
    .EX_CTRL({ALUOP, id_ex_1_ex_ctrl[27:24], EX_RF_WE, id_ex_1_ex_ctrl[22:20], X__RF_B, Y__RF_A, Y__S_EXT, id_ex_1_ex_ctrl[16:9], syscall, id_ex_1_ex_ctrl[7:0]}),
    .ID_RF_A(multiplexer_6_out), .EX_RF_A(id_ex_1_ex_rf_a), .ID_RF_B(multiplexer_7_out),
    .EX_RF_B(id_ex_1_ex_rf_b), .ID_IMM(extender_1_imm), .EX_IMM(id_ex_1_ex_imm), .ID_rW(multiplexer_5_out),
    .EX_rW(EX_rW));
  not not_3 (not_3_out, stop);
  Pull_Resistor #(.pull(1)) pull_resistor_3 (.node(not_3_out));
  not not_4 (not_4_out, jump);
  // Probe on EX_PC
  Pull_Resistor pull_resistor_4 (.node(pull_resistor_4_node));
  or or_2 (pull_resistor_4_node, halting, goto, Load_Use);
  D_Flip_Flop d_ff_2 (.clk(clk), .D(not_4_out), .Qn(d_ff_2_qn), .preset(RST));  // open: Q, en, reset
  // Probe on EX_rW
  Counter #(.width(16), .max('hffff), .trigger("falling")) \u_无条件分支指令计数  (
    .count(d_ff_2_qn), .Q(\无条件分支指令数 ), .clk(clk), .clr(RST));  // open: load, D, carry
  Counter #(.width(16), .max('hffff), .trigger("falling")) \u_插入气泡计数  (
    .count(Load_Use), .Q(\插入气泡数 ), .clk(clk), .clr(RST));  // open: load, D, carry
  Multiplexer #(.width(32), .enable("false")) multiplexer_8 (
    .in0(id_ex_1_ex_rf_b), .in1(id_ex_1_ex_rf_a), .out(multiplexer_8_out), .sel(Y__RF_A));
  Register #(.width(32)) \u_数码管锁存  (.D(id_ex_1_ex_rf_b), .en(display_a0), .Q(SyscallOut), .clk(clk), .clr(RST));
  // Probe on MEM_PC
  Multiplexer #(.width(32), .enable("false")) multiplexer_9 (
    .in0(id_ex_1_ex_rf_a), .in1(id_ex_1_ex_rf_b), .out(multiplexer_9_out), .sel(X__RF_B));
  Multiplexer #(.width(32), .enable("false")) multiplexer_10 (
    .in0(multiplexer_8_out), .in1(id_ex_1_ex_imm), .out(multiplexer_10_out), .sel(Y__S_EXT));
  not not_5 (not_5_out, branch);
  ALU alu_1 (
    .AluOP(ALUOP), .X(multiplexer_9_out), .Equal(alu_1_equal), .Result(EX_Data), .Y(multiplexer_10_out));  // open: Signed_Overflow, Result_2, UnSigned_Overflow
  D_Flip_Flop d_ff_3 (.clk(clk), .D(not_5_out), .Qn(d_ff_3_qn), .preset(RST));  // open: Q, en, reset
  // Probe on WB_PC
  NPC npc_1 (
    .ALU_R(EX_Data),
    .CTRL({ALUOP, id_ex_1_ex_ctrl[27:24], EX_RF_WE, id_ex_1_ex_ctrl[22:20], X__RF_B, Y__RF_A, Y__S_EXT, id_ex_1_ex_ctrl[16:9], syscall, id_ex_1_ex_ctrl[7:0]}),
    .IMM(id_ex_1_ex_imm), .PC_1(id_ex_1_ex_pc_1), .IR({EX_OP, id_ex_1_ex_ir}), .RF_A(id_ex_1_ex_rf_a),
    .branch(branch), .jump_or_branch(goto), .jump(jump), .new_addr(goto_addr), .ALU_Equal(alu_1_equal));
  and and_7 (and_7_out, alu_1_equal, syscall);
  and and_8 (display_a0, ~alu_1_equal, syscall);  // AND_Gate
  Counter #(.width(16), .max('hffff), .trigger("falling")) \u_有条件分支成功跳转计数  (
    .count(d_ff_3_qn), .Q(\有条件分支成功跳转 ), .clk(clk), .clr(RST));  // open: load, D, carry
  // Probe on EX_Data
  EX_MEM ex_mem_1 (
    .CLK(clk), .\同步清零 (pull_resistor_6_node), .EX_PC(EX_PC), .MEM_PC(MEM_PC), .EX_PC_1(id_ex_1_ex_pc_1),
    .MEM_PC_1(ex_mem_1_mem_pc_1),
    .EX_CTRL({ALUOP, id_ex_1_ex_ctrl[27:24], EX_RF_WE, id_ex_1_ex_ctrl[22:20], X__RF_B, Y__RF_A, Y__S_EXT, id_ex_1_ex_ctrl[16:9], syscall, id_ex_1_ex_ctrl[7:0]}),
    .MEM_CTRL({ex_mem_1_mem_ctrl[31:24], MEM_RF_WE, ex_mem_1_mem_ctrl[22:8], DM_WE, ex_mem_1_mem_ctrl[6:0]}),
    .lock_when_0_stop_transport(not_3_out), .EX_rW(EX_rW), .MEM_rW(MEM_rW), .EX_RF_B(id_ex_1_ex_rf_b),
    .MEM_RF_B(ex_mem_1_mem_rf_b), .EX_ALU_R(EX_Data), .MEM_ALU_R(ex_mem_1_mem_alu_r), .EX_HALT(and_7_out),
    .MEM_HALT(ex_mem_1_mem_halt));
  Pull_Resistor #(.pull(1)) pull_resistor_5 (.node(not_3_out));
  Pull_Resistor pull_resistor_6 (.node(pull_resistor_6_node));
  // Probe on MEM_rW
  or or_3 (or_3_out, ex_mem_1_mem_ctrl[21], ex_mem_1_mem_ctrl[20]);
  // MIPS_RAM mips_ram_1: pin names not known; wires that end beside it: ex_mem_1_mem_alu_r[13:2], ex_mem_1_mem_rf_b, DM_WE, clk, RST, mips_ram_1_p6
  // Probe on MEM_Data
  Multiplexer #(.width(32), .enable("false")) multiplexer_11 (
    .in0(ex_mem_1_mem_alu_r), .in1(mips_ram_1_p6), .out(MEM_Data), .sel(or_3_out));
  MEM_WB mem_wb_1 (
    .CLK(clk), .\同步清零 (pull_resistor_6_node), .MEM_PC(MEM_PC), .WB_PC(WB_PC), .MEM_PC_1(ex_mem_1_mem_pc_1),
    .WB_PC_1(mem_wb_1_wb_pc_1),
    .MEM_CTRL({ex_mem_1_mem_ctrl[31:24], MEM_RF_WE, ex_mem_1_mem_ctrl[22:8], DM_WE, ex_mem_1_mem_ctrl[6:0]}),
    .WB_CTRL({mem_wb_1_wb_ctrl[31:24], WB_RF_WE, Din__PC_1, Din__DM, Din__DM_half, mem_wb_1_wb_ctrl[19:0]}),
    .lock_when_0_stop_transport(not_3_out), .MEM_rW(MEM_rW), .WB_rW(WB_rW), .MEM_ALU_R(ex_mem_1_mem_alu_r),
    .WB_ALU_R(mem_wb_1_wb_alu_r), .MEM_DM_D(mips_ram_1_p6), .WB_DM_D(mem_wb_1_wb_dm_d),
    .MEM_HALT(ex_mem_1_mem_halt), .WB_HALT(halting));
  Multiplexer #(.width(16), .enable("false")) multiplexer_12 (
    .in0(mem_wb_1_wb_dm_d[15:0]), .in1(mem_wb_1_wb_dm_d[31:16]), .out(multiplexer_12_out),
    .sel(mem_wb_1_wb_alu_r[1]));
  D_Flip_Flop #(.trigger("falling")) d_ff_4 (.clk(halting), .D(1'b1), .Q(stop), .reset(RST));  // open: Qn, preset, en
  Multiplexer #(.width(32), .enable("false")) multiplexer_13 (
    .in0(mem_wb_1_wb_alu_r), .in1(mem_wb_1_wb_pc_1), .out(multiplexer_13_out), .sel(Din__PC_1));
  Multiplexer #(.width(32), .enable("false")) multiplexer_14 (
    .in0(mem_wb_1_wb_dm_d), .in1({{16{1'b0}}, multiplexer_12_out}), .out(multiplexer_14_out),
    .sel(Din__DM_half));
  // Probe on RF_W
  Multiplexer #(.width(32), .enable("false")) multiplexer_15 (
    .in0(multiplexer_13_out), .in1(multiplexer_14_out), .out(RF_W), .sel(Din__DM));

  // Other names for the same wires on the sheet: 总周期数[15:0] = Count

  // Notes on the sheet:
  //   中断源
  //   中断等待指示
  //   指令存储器
  //   数码管输出
  //   contents of rom_1 (hex, n*v repeats v):
  //   20110001 8000c05 20110001 20120002 20130003 8000c09 20110001 20120002 20130003 8000c0d 20110001
  //   20120002 20130003 8000c11 20110001 20120002 20130003 c000cb8 20100001 20110001 118fc0 112020
  //   20020022 c 118882 12200001 8000c15 112020 20020022 c 20110001 118880 112020 20020022 c 12200001
  //   8000c1f 20110001 118fc0 112020 20020022 c 1188c3 112020 20020022 c 118903 112020 20020022 c 118903
  //   112020 20020022 c 118903 112020 20020022 c 118903 112020 20020022 c 118903 112020 20020022 c 118903
  //   112020 20020022 c 118903 112020 20020022 c 20100001 109fc0 139fc3 8021 2012000c 24160003 26100001
  //   3210000f 20080008 20090001 139900 2709825 132020 20020022 c 1094022 1500fff9 22100001 2018000f
  //   2188024 108700 20080008 20090001 139902 2709825 132021 20020022 c 1094022 1500fff9 108702 2c9b022
  //   12c00001 8000c50 4020 1084027 84400 3508ffff 82021 20020022 c 2010ffff 20110000 ae300000 22100001
  //   22310004 ae300000 22100001 22310004 ae300000 22100001 22310004 ae300000 22100001 22310004 ae300000
  //   22100001 22310004 ae300000 22100001 22310004 ae300000 22100001 22310004 ae300000 22100001 22310004
  //   ae300000 22100001 22310004 ae300000 22100001 22310004 ae300000 22100001 22310004 ae300000 22100001
  //   22310004 ae300000 22100001 22310004 ae300000 22100001 22310004 ae300000 22100001 22310004 ae300000
  //   22100001 22310004 22100001 8020 2011003c 8e130000 8e340000 274402a 11000002 ae330000 ae140000
  //   2231fffc 1611fff8 102020 20020022 c 22100004 2011003c 1611fff2 2002000a c 20100000 22100001 102020
  //   20020022 c 22100002 102020 20020022 c 22100003 102020 20020022 c 22100004 102020 20020022 c 22100005
  //   102020 20020022 c 22100006 102020 20020022 c 22100007 102020 20020022 c 22100008 102020 20020022
  //   20020022 c 3e00008
  //   寄存器堆
  //   数据存储器
endmodule

module PC_1 (
  input  [31:0] PC,
  output [31:0] PC_4
);

  Adder #(.width(32)) adder_1 (.a(PC), .b(32'h4), .out(PC_4));  // open: cin, cout
endmodule

// Contorller
module Controller (
  input  [5:0] OP,
  input  [5:0] Funct,
  output [31:0] \控制信号 
);

  wire add, addi, addiu, addu, \and , andi, comparator_1_eq, comparator_16_eq, comparator_17_eq,
       comparator_18_eq, comparator_19_eq, comparator_20_eq, comparator_21_eq, comparator_22_eq,
       comparator_23_eq, comparator_24_eq, comparator_25_eq, comparator_26_eq, comparator_27_eq,
       comparator_28_eq, comparator_29_eq, j, lw, \nor , \or , or_2_out, or_3_out, or_4_out, or_5_out,
       or_6_out, or_7_out, or_9_out, or_10_out, or_11_out, or_12_out, or_13_out, or_14_out, or_15_out,
       or_16_out, or_17_out, or_18_out, or_19_out, or_21_out, or_22_out, or_23_out, or_24_out, or_25_out,
       or_26_out, or_27_out, or_28_out, or_30_out, or_31_out, or_32_out, or_33_out, or_34_out, or_35_out,
       or_36_out, or_37_out, or_38_out, or_39_out, or_40_out, or_42_out, or_43_out, or_44_out, or_45_out,
       or_46_out, or_47_out, or_48_out, or_49_out, or_50_out, or_51_out, or_53_out, or_54_out, or_55_out,
       or_56_out, or_57_out, or_58_out, or_59_out, or_60_out, or_61_out, or_62_out, or_63_out, or_65_out,
       or_66_out, or_67_out, or_68_out, or_69_out, or_70_out, or_71_out, or_72_out, or_74_out, or_75_out,
       or_77_out, or_78_out, or_79_out, or_80_out, or_81_out, or_82_out, or_83_out, or_84_out, or_85_out,
       or_86_out, or_87_out, or_89_out, or_91_out, or_92_out, or_93_out, or_94_out, or_95_out, or_96_out,
       or_97_out, or_98_out, or_99_out, or_100_out, or_103_out, ori, sll, slt, slti, sltiu, sltu, sra, srl,
       sub;

  Comparator #(.width(6)) comparator_1 (.a(OP), .b({6{1'b0}}), .eq(comparator_1_eq));  // open: gt, lt
  Comparator #(.width(6)) comparator_2 (.a(OP), .b(6'b000001), .eq(\控制信号 [9]));  // open: gt, lt
  Comparator #(.width(6)) comparator_3 (.a(OP), .b(6'b000010), .eq(j));  // open: gt, lt
  Comparator #(.width(6)) comparator_4 (.a(OP), .b(6'b000011), .eq(\控制信号 [24]));  // open: gt, lt
  Comparator #(.width(6)) comparator_5 (.a(OP), .b(6'b000100), .eq(\控制信号 [11]));  // open: gt, lt
  Comparator #(.width(6)) comparator_6 (.a(OP), .b(6'b000101), .eq(\控制信号 [10]));  // open: gt, lt
  Comparator #(.width(6)) comparator_7 (.a(OP), .b(6'b001000), .eq(addi));  // open: gt, lt
  Comparator #(.width(6)) comparator_8 (.a(OP), .b(6'b001001), .eq(addiu));  // open: gt, lt
  Comparator #(.width(6)) comparator_9 (.a(OP), .b(6'b001010), .eq(slti));  // open: gt, lt
  Comparator #(.width(6)) comparator_10 (.a(OP), .b(6'b001011), .eq(sltiu));  // open: gt, lt
  Comparator #(.width(6)) comparator_11 (.a(OP), .b(6'b001100), .eq(andi));  // open: gt, lt
  Comparator #(.width(6)) comparator_12 (.a(OP), .b(6'b001101), .eq(ori));  // open: gt, lt
  Comparator #(.width(6)) comparator_13 (.a(OP), .b(6'b100001), .eq(\控制信号 [20]));  // open: gt, lt
  Comparator #(.width(6)) comparator_14 (.a(OP), .b(6'b100011), .eq(lw));  // open: gt, lt
  Comparator #(.width(6)) comparator_15 (.a(OP), .b(6'b101011), .eq(\控制信号 [7]));  // open: gt, lt
  Comparator #(.width(6)) comparator_16 (.a(Funct), .b({6{1'b0}}), .eq(comparator_16_eq));  // open: gt, lt
  Comparator #(.width(6)) comparator_17 (.a(Funct), .b(6'b000010), .eq(comparator_17_eq));  // open: gt, lt
  Comparator #(.width(6)) comparator_18 (.a(Funct), .b(6'b000011), .eq(comparator_18_eq));  // open: gt, lt
  Comparator #(.width(6)) comparator_19 (.a(Funct), .b(6'b000110), .eq(comparator_19_eq));  // open: gt, lt
  Comparator #(.width(6)) comparator_20 (.a(Funct), .b(6'b001000), .eq(comparator_20_eq));  // open: gt, lt
  Comparator #(.width(6)) comparator_21 (.a(Funct), .b(6'b001100), .eq(comparator_21_eq));  // open: gt, lt
  Comparator #(.width(6)) comparator_22 (.a(Funct), .b(6'b100000), .eq(comparator_22_eq));  // open: gt, lt
  Comparator #(.width(6)) comparator_23 (.a(Funct), .b(6'b100001), .eq(comparator_23_eq));  // open: gt, lt
  Comparator #(.width(6)) comparator_24 (.a(Funct), .b(6'b100010), .eq(comparator_24_eq));  // open: gt, lt
  Comparator #(.width(6)) comparator_25 (.a(Funct), .b(6'b100100), .eq(comparator_25_eq));  // open: gt, lt
  Comparator #(.width(6)) comparator_26 (.a(Funct), .b(6'b100101), .eq(comparator_26_eq));  // open: gt, lt
  Comparator #(.width(6)) comparator_27 (.a(Funct), .b(6'b100111), .eq(comparator_27_eq));  // open: gt, lt
  Comparator #(.width(6)) comparator_28 (.a(Funct), .b(6'b101010), .eq(comparator_28_eq));  // open: gt, lt
  Comparator #(.width(6)) comparator_29 (.a(Funct), .b(6'b101011), .eq(comparator_29_eq));  // open: gt, lt
  and and_1 (sll, comparator_1_eq, comparator_16_eq);
  and and_2 (srl, comparator_1_eq, comparator_17_eq);
  and and_3 (sra, comparator_1_eq, comparator_18_eq);
  and and_4 (\控制信号 [18], comparator_1_eq, comparator_19_eq);
  and and_5 (\控制信号 [12], comparator_1_eq, comparator_20_eq);
  and and_6 (\控制信号 [27], comparator_1_eq, comparator_21_eq);
  and and_7 (add, comparator_1_eq, comparator_22_eq);
  and and_8 (addu, comparator_1_eq, comparator_23_eq);
  and and_9 (sub, comparator_1_eq, comparator_24_eq);
  and and_10 (\and , comparator_1_eq, comparator_25_eq);
  and and_11 (\or , comparator_1_eq, comparator_26_eq);
  and and_12 (\nor , comparator_1_eq, comparator_27_eq);
  and and_13 (slt, comparator_1_eq, comparator_28_eq);
  and and_14 (sltu, comparator_1_eq, comparator_29_eq);
  or or_1 (\控制信号 [31], \or , or_2_out);
  or or_2 (or_2_out, or_3_out, \nor );
  or or_3 (or_3_out, slt, or_4_out);
  or or_4 (or_4_out, or_5_out, sltu);
  or or_5 (or_5_out, \控制信号 [9], or_6_out);
  or or_6 (or_6_out, or_7_out, slti);
  or or_7 (or_7_out, sltiu, ori);
  // Probe on {\控制信号 [31:27], \控制信号 [27], \控制信号 [25:23], \控制信号 [24], \控制信号 [21:9], \控制信号 [27], \控制信号 [7], {7{1'b0}}}
  or or_8 (\控制信号 [30], \控制信号 [27], or_9_out);
  or or_9 (or_9_out, or_10_out, add);
  or or_10 (or_10_out, addu, or_11_out);
  or or_11 (or_11_out, or_12_out, sub);
  or or_12 (or_12_out, \and , or_13_out);
  or or_13 (or_13_out, or_14_out, sltu);
  or or_14 (or_14_out, addi, or_15_out);
  or or_15 (or_15_out, or_16_out, addiu);
  or or_16 (or_16_out, sltiu, or_17_out);
  or or_17 (or_17_out, or_18_out, andi);
  or or_18 (or_18_out, \控制信号 [20], or_19_out);
  or or_19 (or_19_out, lw, \控制信号 [7]);
  or or_20 (\控制信号 [29], srl, or_21_out);
  or or_21 (or_21_out, or_22_out, \控制信号 [18]);
  or or_22 (or_22_out, \控制信号 [27], or_23_out);
  or or_23 (or_23_out, or_24_out, sub);
  or or_24 (or_24_out, \and , or_25_out);
  or or_25 (or_25_out, or_26_out, \nor );
  or or_26 (or_26_out, slt, or_27_out);
  or or_27 (or_27_out, or_28_out, \控制信号 [9]);
  or or_28 (or_28_out, slti, andi);
  or or_29 (\控制信号 [28], sra, or_30_out);
  or or_30 (or_30_out, or_31_out, add);
  or or_31 (or_31_out, addu, or_32_out);
  or or_32 (or_32_out, or_33_out, \and );
  or or_33 (or_33_out, slt, or_34_out);
  or or_34 (or_34_out, or_35_out, \控制信号 [9]);
  or or_35 (or_35_out, addi, or_36_out);
  or or_36 (or_36_out, or_37_out, addiu);
  or or_37 (or_37_out, slti, or_38_out);
  or or_38 (or_38_out, or_39_out, andi);
  or or_39 (or_39_out, \控制信号 [20], or_40_out);
  or or_40 (or_40_out, lw, \控制信号 [7]);
  or or_41 (\控制信号 [25], sll, or_42_out);
  or or_42 (or_42_out, or_43_out, srl);
  or or_43 (or_43_out, sra, or_44_out);
  or or_44 (or_44_out, or_45_out, \控制信号 [18]);
  or or_45 (or_45_out, add, or_46_out);
  or or_46 (or_46_out, or_47_out, addu);
  or or_47 (or_47_out, sub, or_48_out);
  or or_48 (or_48_out, or_49_out, \and );
  or or_49 (or_49_out, \or , or_50_out);
  or or_50 (or_50_out, or_51_out, \nor );
  or or_51 (or_51_out, slt, sltu);
  or or_52 (\控制信号 [23], sll, or_53_out);
  or or_53 (or_53_out, or_54_out, srl);
  or or_54 (or_54_out, sra, or_55_out);
  or or_55 (or_55_out, or_56_out, \控制信号 [18]);
  or or_56 (or_56_out, add, or_57_out);
  or or_57 (or_57_out, or_58_out, addu);
  or or_58 (or_58_out, sub, or_59_out);
  or or_59 (or_59_out, or_60_out, \and );
  or or_60 (or_60_out, \or , or_61_out);
  or or_61 (or_61_out, or_62_out, \nor );
  or or_62 (or_62_out, slt, or_63_out);
  or or_63 (or_63_out, sltu, or_65_out);
  or or_64 (\控制信号 [21], \控制信号 [20], lw);
  or or_65 (or_65_out, \控制信号 [24], or_66_out);
  or or_66 (or_66_out, or_67_out, addi);
  or or_67 (or_67_out, addiu, or_68_out);
  or or_68 (or_68_out, or_69_out, slti);
  or or_69 (or_69_out, sltiu, or_70_out);
  or or_70 (or_70_out, or_71_out, andi);
  or or_71 (or_71_out, ori, or_72_out);
  or or_72 (or_72_out, \控制信号 [20], lw);
  or or_73 (\控制信号 [19], sll, or_74_out);
  or or_74 (or_74_out, or_75_out, srl);
  or or_75 (or_75_out, sra, \控制信号 [18]);
  or or_76 (\控制信号 [17], sll, or_77_out);
  or or_77 (or_77_out, or_78_out, srl);
  or or_78 (or_78_out, sra, or_79_out);
  or or_79 (or_79_out, or_80_out, \控制信号 [27]);
  or or_80 (or_80_out, addi, or_81_out);
  or or_81 (or_81_out, or_82_out, addiu);
  or or_82 (or_82_out, slti, or_83_out);
  or or_83 (or_83_out, or_84_out, sltiu);
  or or_84 (or_84_out, andi, or_85_out);
  or or_85 (or_85_out, or_86_out, ori);
  or or_86 (or_86_out, \控制信号 [20], or_87_out);
  or or_87 (or_87_out, lw, \控制信号 [7]);
  or or_88 (\控制信号 [16], sll, or_89_out);
  or or_89 (or_89_out, srl, sra);
  or or_90 (\控制信号 [15], \控制信号 [9], or_91_out);
  or or_91 (or_91_out, or_92_out, \控制信号 [11]);
  or or_92 (or_92_out, \控制信号 [10], or_93_out);
  or or_93 (or_93_out, or_94_out, addi);
  or or_94 (or_94_out, addiu, or_95_out);
  or or_95 (or_95_out, or_96_out, slti);
  or or_96 (or_96_out, sltiu, or_97_out);
  or or_97 (or_97_out, or_98_out, andi);
  or or_98 (or_98_out, ori, or_99_out);
  or or_99 (or_99_out, or_100_out, \控制信号 [20]);
  or or_100 (or_100_out, lw, \控制信号 [7]);
  or or_101 (\控制信号 [14], andi, ori);
  or or_102 (\控制信号 [13], \控制信号 [12], or_103_out);
  or or_103 (or_103_out, j, \控制信号 [24]);

  assign {\控制信号 [26], \控制信号 [22], \控制信号 [8], \控制信号 [6:0]} = {\控制信号 [27], \控制信号 [24], \控制信号 [27], {7{1'b0}}};

  // Other names for the same wires on the sheet: sw = \控制信号 [7]; bltz = \控制信号 [9]; bne = \控制信号 [10]; beq = \控制信号 [11];
  //   jr = \控制信号 [12]; srlv = \控制信号 [18]; lh = \控制信号 [20]; jal = \控制信号 [24]; syscall = \控制信号 [27]
endmodule

module IF_ID (
  input  CLK,
  input  lock_when_0_stop_transport,
  input  \同步清零 ,
  input  [31:0] IF_PC,
  input  [31:0] IF_PC_1,
  input  [31:0] IF_IR,
  output [31:0] ID_PC,
  output [31:0] ID_PC_1,
  output [31:0] ID_IR
);

  wire [31:0] multiplexer_1_out, multiplexer_2_out, multiplexer_3_out;

  Multiplexer #(.width(32), .enable("false")) multiplexer_1 (
    .in0(IF_PC), .in1({32{1'b0}}), .out(multiplexer_1_out), .sel(\同步清零 ));
  Multiplexer #(.width(32), .enable("false")) multiplexer_2 (
    .in0(IF_PC_1), .in1({32{1'b0}}), .out(multiplexer_2_out), .sel(\同步清零 ));
  Multiplexer #(.width(32), .enable("false")) multiplexer_3 (
    .in0(IF_IR), .in1({32{1'b0}}), .out(multiplexer_3_out), .sel(\同步清零 ));
  Register #(.width(32)) register_1 (
    .D(multiplexer_1_out), .en(lock_when_0_stop_transport), .Q(ID_PC), .clk(CLK));  // open: clr
  Register #(.width(32)) register_2 (
    .D(multiplexer_2_out), .en(lock_when_0_stop_transport), .Q(ID_PC_1), .clk(CLK));  // open: clr
  Register #(.width(32)) register_3 (
    .D(multiplexer_3_out), .en(lock_when_0_stop_transport), .Q(ID_IR), .clk(CLK));  // open: clr
endmodule

module ID_EX (
  input  CLK,
  input  lock_when_0_stop_transport,
  input  \同步清零 ,
  input  [31:0] ID_PC,
  input  [31:0] ID_PC_1,
  input  [31:0] ID_IR,
  input  [31:0] ID_CTRL,
  input  [31:0] ID_RF_A,
  input  [31:0] ID_RF_B,
  input  [4:0] ID_rW,
  input  [31:0] ID_IMM,
  output [31:0] EX_PC,
  output [31:0] EX_PC_1,
  output [31:0] EX_IR,
  output [31:0] EX_CTRL,
  output [31:0] EX_RF_A,
  output [31:0] EX_RF_B,
  output [4:0] EX_rW,
  output [31:0] EX_IMM
);

  wire [4:0] multiplexer_7_out;
  wire [31:0] multiplexer_1_out, multiplexer_2_out, multiplexer_3_out, multiplexer_4_out, multiplexer_5_out,
       multiplexer_6_out, multiplexer_8_out;

  Multiplexer #(.width(32), .enable("false")) multiplexer_1 (
    .in0(ID_PC), .in1({32{1'b0}}), .out(multiplexer_1_out), .sel(\同步清零 ));
  Multiplexer #(.width(32), .enable("false")) multiplexer_2 (
    .in0(ID_PC_1), .in1({32{1'b0}}), .out(multiplexer_2_out), .sel(\同步清零 ));
  Multiplexer #(.width(32), .enable("false")) multiplexer_3 (
    .in0(ID_IR), .in1({32{1'b0}}), .out(multiplexer_3_out), .sel(\同步清零 ));
  Multiplexer #(.width(32), .enable("false")) multiplexer_4 (
    .in0(ID_CTRL), .in1({32{1'b0}}), .out(multiplexer_4_out), .sel(\同步清零 ));
  Multiplexer #(.width(32), .enable("false")) multiplexer_5 (
    .in0(ID_RF_A), .in1({32{1'b0}}), .out(multiplexer_5_out), .sel(\同步清零 ));
  Multiplexer #(.width(32), .enable("false")) multiplexer_6 (
    .in0(ID_RF_B), .in1({32{1'b0}}), .out(multiplexer_6_out), .sel(\同步清零 ));
  Multiplexer #(.width(5), .enable("false")) multiplexer_7 (
    .in0(ID_rW), .in1({5{1'b0}}), .out(multiplexer_7_out), .sel(\同步清零 ));
  Multiplexer #(.width(32), .enable("false")) multiplexer_8 (
    .in0(ID_IMM), .in1({32{1'b0}}), .out(multiplexer_8_out), .sel(\同步清零 ));
  Register #(.width(32)) register_1 (
    .D(multiplexer_1_out), .en(lock_when_0_stop_transport), .Q(EX_PC), .clk(CLK));  // open: clr
  Register #(.width(32)) register_2 (
    .D(multiplexer_2_out), .en(lock_when_0_stop_transport), .Q(EX_PC_1), .clk(CLK));  // open: clr
  Register #(.width(32)) register_3 (
    .D(multiplexer_3_out), .en(lock_when_0_stop_transport), .Q(EX_IR), .clk(CLK));  // open: clr
  Register #(.width(32)) register_4 (
    .D(multiplexer_4_out), .en(lock_when_0_stop_transport), .Q(EX_CTRL), .clk(CLK));  // open: clr
  Register #(.width(32)) register_5 (
    .D(multiplexer_5_out), .en(lock_when_0_stop_transport), .Q(EX_RF_A), .clk(CLK));  // open: clr
  Register #(.width(32)) register_6 (
    .D(multiplexer_6_out), .en(lock_when_0_stop_transport), .Q(EX_RF_B), .clk(CLK));  // open: clr
  Register #(.width(5)) register_7 (
    .D(multiplexer_7_out), .en(lock_when_0_stop_transport), .Q(EX_rW), .clk(CLK));  // open: clr
  Register #(.width(32)) register_8 (
    .D(multiplexer_8_out), .en(lock_when_0_stop_transport), .Q(EX_IMM), .clk(CLK));  // open: clr
endmodule

module EX_MEM (
  input  CLK,
  input  lock_when_0_stop_transport,
  input  \同步清零 ,
  input  [31:0] EX_PC,
  input  [31:0] EX_PC_1,
  input  [31:0] EX_CTRL,
  input  [4:0] EX_rW,
  input  [31:0] EX_RF_B,
  input  [31:0] EX_ALU_R,
  input  EX_HALT,
  output [31:0] MEM_PC,
  output [31:0] MEM_PC_1,
  output [31:0] MEM_CTRL,
  output [4:0] MEM_rW,
  output [31:0] MEM_RF_B,
  output [31:0] MEM_ALU_R,
  output MEM_HALT
);

  wire multiplexer_7_out;
  wire [4:0] multiplexer_4_out;
  wire [31:0] multiplexer_1_out, multiplexer_2_out, multiplexer_3_out, multiplexer_5_out, multiplexer_6_out;

  Multiplexer #(.width(32), .enable("false")) multiplexer_1 (
    .in0(EX_PC), .in1({32{1'b0}}), .out(multiplexer_1_out), .sel(\同步清零 ));
  Multiplexer #(.width(32), .enable("false")) multiplexer_2 (
    .in0(EX_PC_1), .in1({32{1'b0}}), .out(multiplexer_2_out), .sel(\同步清零 ));
  Multiplexer #(.width(32), .enable("false")) multiplexer_3 (
    .in0(EX_CTRL), .in1({32{1'b0}}), .out(multiplexer_3_out), .sel(\同步清零 ));
  Multiplexer #(.width(5), .enable("false")) multiplexer_4 (
    .in0(EX_rW), .in1({5{1'b0}}), .out(multiplexer_4_out), .sel(\同步清零 ));
  Multiplexer #(.width(32), .enable("false")) multiplexer_5 (
    .in0(EX_RF_B), .in1({32{1'b0}}), .out(multiplexer_5_out), .sel(\同步清零 ));
  Multiplexer #(.width(32), .enable("false")) multiplexer_6 (
    .in0(EX_ALU_R), .in1({32{1'b0}}), .out(multiplexer_6_out), .sel(\同步清零 ));
  Multiplexer #(.enable("false")) multiplexer_7 (.in0(EX_HALT), .in1(1'b0), .out(multiplexer_7_out), .sel(\同步清零 ));
  Register #(.width(32)) register_1 (
    .D(multiplexer_1_out), .en(lock_when_0_stop_transport), .Q(MEM_PC), .clk(CLK));  // open: clr
  Register #(.width(32)) register_2 (
    .D(multiplexer_2_out), .en(lock_when_0_stop_transport), .Q(MEM_PC_1), .clk(CLK));  // open: clr
  Register #(.width(32)) register_3 (
    .D(multiplexer_3_out), .en(lock_when_0_stop_transport), .Q(MEM_CTRL), .clk(CLK));  // open: clr
  Register #(.width(5)) register_4 (
    .D(multiplexer_4_out), .en(lock_when_0_stop_transport), .Q(MEM_rW), .clk(CLK));  // open: clr
  Register #(.width(32)) register_5 (
    .D(multiplexer_5_out), .en(lock_when_0_stop_transport), .Q(MEM_RF_B), .clk(CLK));  // open: clr
  Register #(.width(32)) register_6 (
    .D(multiplexer_6_out), .en(lock_when_0_stop_transport), .Q(MEM_ALU_R), .clk(CLK));  // open: clr
  Register #(.width(1)) register_7 (
    .D(multiplexer_7_out), .en(lock_when_0_stop_transport), .Q(MEM_HALT), .clk(CLK));  // open: clr
endmodule

// MEM//WB
module MEM_WB (
  input  CLK,
  input  lock_when_0_stop_transport,
  input  \同步清零 ,
  input  [31:0] MEM_PC,
  input  [31:0] MEM_PC_1,
  input  [31:0] MEM_CTRL,
  input  [4:0] MEM_rW,
  input  [31:0] MEM_ALU_R,
  input  [31:0] MEM_DM_D,
  input  MEM_HALT,
  output [31:0] WB_PC,
  output [31:0] WB_PC_1,
  output [31:0] WB_CTRL,
  output [4:0] WB_rW,
  output [31:0] WB_ALU_R,
  output [31:0] WB_DM_D,
  output WB_HALT
);

  wire multiplexer_7_out;
  wire [4:0] multiplexer_4_out;
  wire [31:0] multiplexer_1_out, multiplexer_2_out, multiplexer_3_out, multiplexer_5_out, multiplexer_6_out;

  Multiplexer #(.width(32), .enable("false")) multiplexer_1 (
    .in0(MEM_PC), .in1({32{1'b0}}), .out(multiplexer_1_out), .sel(\同步清零 ));
  Multiplexer #(.width(32), .enable("false")) multiplexer_2 (
    .in0(MEM_PC_1), .in1({32{1'b0}}), .out(multiplexer_2_out), .sel(\同步清零 ));
  Multiplexer #(.width(32), .enable("false")) multiplexer_3 (
    .in0(MEM_CTRL), .in1({32{1'b0}}), .out(multiplexer_3_out), .sel(\同步清零 ));
  Multiplexer #(.width(5), .enable("false")) multiplexer_4 (
    .in0(MEM_rW), .in1({5{1'b0}}), .out(multiplexer_4_out), .sel(\同步清零 ));
  Multiplexer #(.width(32), .enable("false")) multiplexer_5 (
    .in0(MEM_ALU_R), .in1({32{1'b0}}), .out(multiplexer_5_out), .sel(\同步清零 ));
  Multiplexer #(.width(32), .enable("false")) multiplexer_6 (
    .in0(MEM_DM_D), .in1({32{1'b0}}), .out(multiplexer_6_out), .sel(\同步清零 ));
  Multiplexer #(.enable("false")) multiplexer_7 (.in0(MEM_HALT), .in1(1'b0), .out(multiplexer_7_out), .sel(\同步清零 ));
  Register #(.width(32)) register_1 (
    .D(multiplexer_1_out), .en(lock_when_0_stop_transport), .Q(WB_PC), .clk(CLK));  // open: clr
  Register #(.width(32)) register_2 (
    .D(multiplexer_2_out), .en(lock_when_0_stop_transport), .Q(WB_PC_1), .clk(CLK));  // open: clr
  Register #(.width(32)) register_3 (
    .D(multiplexer_3_out), .en(lock_when_0_stop_transport), .Q(WB_CTRL), .clk(CLK));  // open: clr
  Register #(.width(5)) register_4 (
    .D(multiplexer_4_out), .en(lock_when_0_stop_transport), .Q(WB_rW), .clk(CLK));  // open: clr
  Register #(.width(32)) register_5 (
    .D(multiplexer_5_out), .en(lock_when_0_stop_transport), .Q(WB_ALU_R), .clk(CLK));  // open: clr
  Register #(.width(32)) register_6 (
    .D(multiplexer_6_out), .en(lock_when_0_stop_transport), .Q(WB_DM_D), .clk(CLK));  // open: clr
  Register #(.width(1)) register_7 (
    .D(multiplexer_7_out), .en(lock_when_0_stop_transport), .Q(WB_HALT), .clk(CLK));  // open: clr
endmodule

module Redirecter (
  input  [5:0] ID_OP,
  input  [5:0] ID_Funct,
  input  [5:0] EX_OP,
  input  [4:0] EX_rW,
  input  EX_RF_WE,
  input  [4:0] rA,
  input  [4:0] rB,
  input  [31:0] EX_Data,
  input  [4:0] MEM_rW,
  input  [31:0] MEM_Data,
  input  MEM_RF_WE,
  output redirect_RF_A,
  output [31:0] redirected_RF_A,
  output Load_Use,
  output [31:0] redirected_RF_B,
  output redirect_RF_B
);

  wire add, addi, addiu, addu, \and , and_15_out, and_16_out, and_17_out, and_18_out, and_19_out, and_20_out,
       and_21_out, and_22_out, and_23_out, and_24_out, and_25_out, and_26_out, and_27_out, and_28_out,
       and_30_out, and_31_out, and_32_out, andi, beq, bltz, bne, comparator_1_eq, comparator_16_eq,
       comparator_17_eq, comparator_18_eq, comparator_19_eq, comparator_20_eq, comparator_21_eq,
       comparator_22_eq, comparator_23_eq, comparator_24_eq, comparator_25_eq, comparator_26_eq,
       comparator_27_eq, comparator_28_eq, comparator_29_eq, comparator_33_eq, comparator_34_eq,
       comparator_35_eq, comparator_36_eq, comparator_37_eq, comparator_38_eq, comparator_39_eq,
       comparator_40_eq, comparator_41_eq, comparator_42_eq, EX_lh, EX_lw, EX_sw, \EX段冲突 , j, jal, jr, lh,
       lw, \MEM段冲突 , \nor , not_1_out, not_2_out, \or , or_5_out, or_6_out, or_7_out, or_8_out, or_12_out,
       or_14_out, or_15_out, or_16_out, ori, \rA在EX段冲突 , \rA在MEM段冲突 , \rB在EX段冲突 , \rB在MEM段冲突 , read_rA,
       read_rB, sll, slt, slti, sltiu, sltu, sra, srl, srlv, sub, sw, syscall;

  Comparator #(.width(6)) comparator_1 (.a(ID_OP), .b({6{1'b0}}), .eq(comparator_1_eq));  // open: gt, lt
  Comparator #(.width(6)) comparator_2 (.a(ID_OP), .b(6'b000001), .eq(bltz));  // open: gt, lt
  Comparator #(.width(6)) comparator_3 (.a(ID_OP), .b(6'b000010), .eq(j));  // open: gt, lt
  Comparator #(.width(6)) comparator_4 (.a(ID_OP), .b(6'b000011), .eq(jal));  // open: gt, lt
  Comparator #(.width(6)) comparator_5 (.a(ID_OP), .b(6'b000100), .eq(beq));  // open: gt, lt
  Comparator #(.width(6)) comparator_6 (.a(ID_OP), .b(6'b000101), .eq(bne));  // open: gt, lt
  Comparator #(.width(6)) comparator_7 (.a(ID_OP), .b(6'b001000), .eq(addi));  // open: gt, lt
  Comparator #(.width(6)) comparator_8 (.a(ID_OP), .b(6'b001001), .eq(addiu));  // open: gt, lt
  Comparator #(.width(6)) comparator_9 (.a(ID_OP), .b(6'b001010), .eq(slti));  // open: gt, lt
  Comparator #(.width(6)) comparator_10 (.a(ID_OP), .b(6'b001011), .eq(sltiu));  // open: gt, lt
  Comparator #(.width(6)) comparator_11 (.a(ID_OP), .b(6'b001100), .eq(andi));  // open: gt, lt
  Comparator #(.width(6)) comparator_12 (.a(ID_OP), .b(6'b001101), .eq(ori));  // open: gt, lt
  Comparator #(.width(6)) comparator_13 (.a(ID_OP), .b(6'b100001), .eq(lh));  // open: gt, lt
  Comparator #(.width(6)) comparator_14 (.a(ID_OP), .b(6'b100011), .eq(lw));  // open: gt, lt
  Comparator #(.width(6)) comparator_15 (.a(ID_OP), .b(6'b101011), .eq(sw));  // open: gt, lt
  Comparator #(.width(6)) comparator_16 (.a(ID_Funct), .b({6{1'b0}}), .eq(comparator_16_eq));  // open: gt, lt
  Comparator #(.width(6)) comparator_17 (.a(ID_Funct), .b(6'b000010), .eq(comparator_17_eq));  // open: gt, lt
  Comparator #(.width(6)) comparator_18 (.a(ID_Funct), .b(6'b000011), .eq(comparator_18_eq));  // open: gt, lt
  Comparator #(.width(6)) comparator_19 (.a(ID_Funct), .b(6'b000110), .eq(comparator_19_eq));  // open: gt, lt
  Comparator #(.width(6)) comparator_20 (.a(ID_Funct), .b(6'b001000), .eq(comparator_20_eq));  // open: gt, lt
  Comparator #(.width(6)) comparator_21 (.a(ID_Funct), .b(6'b001100), .eq(comparator_21_eq));  // open: gt, lt
  Comparator #(.width(6)) comparator_22 (.a(ID_Funct), .b(6'b100000), .eq(comparator_22_eq));  // open: gt, lt
  Comparator #(.width(6)) comparator_23 (.a(ID_Funct), .b(6'b100001), .eq(comparator_23_eq));  // open: gt, lt
  Comparator #(.width(6)) comparator_24 (.a(ID_Funct), .b(6'b100010), .eq(comparator_24_eq));  // open: gt, lt
  Comparator #(.width(6)) comparator_25 (.a(ID_Funct), .b(6'b100100), .eq(comparator_25_eq));  // open: gt, lt
  Comparator #(.width(6)) comparator_26 (.a(ID_Funct), .b(6'b100101), .eq(comparator_26_eq));  // open: gt, lt
  Comparator #(.width(6)) comparator_27 (.a(ID_Funct), .b(6'b100111), .eq(comparator_27_eq));  // open: gt, lt
  Comparator #(.width(6)) comparator_28 (.a(ID_Funct), .b(6'b101010), .eq(comparator_28_eq));  // open: gt, lt
  Comparator #(.width(6)) comparator_29 (.a(ID_Funct), .b(6'b101011), .eq(comparator_29_eq));  // open: gt, lt
  and and_1 (sll, comparator_1_eq, comparator_16_eq);
  and and_2 (srl, comparator_1_eq, comparator_17_eq);
  and and_3 (sra, comparator_1_eq, comparator_18_eq);
  and and_4 (srlv, comparator_1_eq, comparator_19_eq);
  and and_5 (jr, comparator_1_eq, comparator_20_eq);
  and and_6 (syscall, comparator_1_eq, comparator_21_eq);
  and and_7 (add, comparator_1_eq, comparator_22_eq);
  and and_8 (addu, comparator_1_eq, comparator_23_eq);
  and and_9 (sub, comparator_1_eq, comparator_24_eq);
  and and_10 (\and , comparator_1_eq, comparator_25_eq);
  and and_11 (\or , comparator_1_eq, comparator_26_eq);
  and and_12 (\nor , comparator_1_eq, comparator_27_eq);
  and and_13 (slt, comparator_1_eq, comparator_28_eq);
  and and_14 (sltu, comparator_1_eq, comparator_29_eq);
  Comparator #(.width(6)) comparator_30 (.a(EX_OP), .b(6'b100001), .eq(EX_lh));  // open: gt, lt
  Comparator #(.width(6)) comparator_31 (.a(EX_OP), .b(6'b100011), .eq(EX_lw));  // open: gt, lt
  Comparator #(.width(6)) comparator_32 (.a(EX_OP), .b(6'b101011), .eq(EX_sw));  // open: gt, lt
  or or_1 (read_rA, bltz, beq, srlv, bne, jr, addi, addiu, add, slti, addu, sltiu, sub, andi, \and , ori, \or , lh, \nor , lw, slt, sw, sltu);
  or or_2 (read_rB, bne, sll, srl, sra, add, sw, addu, sltu, sub, slt, \and , srlv, \or , bltz, \nor , beq);
  Comparator #(.width(5)) comparator_33 (.a(EX_rW), .b(rA), .eq(comparator_33_eq));  // open: gt, lt
  Comparator #(.width(5)) comparator_34 (.a(EX_rW), .b(rB), .eq(comparator_34_eq));  // open: gt, lt
  Comparator #(.width(5)) comparator_35 (.a(EX_rW), .b({5{1'b0}}), .eq(comparator_35_eq));  // open: gt, lt
  Comparator #(.width(5)) comparator_36 (.a(EX_rW), .b(5'b00010), .eq(comparator_36_eq));  // open: gt, lt
  Comparator #(.width(5)) comparator_37 (.a(EX_rW), .b(5'b00100), .eq(comparator_37_eq));  // open: gt, lt
  Comparator #(.width(5)) comparator_38 (.a(MEM_rW), .b(rA), .eq(comparator_38_eq));  // open: gt, lt
  Comparator #(.width(5)) comparator_39 (.a(MEM_rW), .b(rB), .eq(comparator_39_eq));  // open: gt, lt
  Comparator #(.width(5)) comparator_40 (.a(MEM_rW), .b({5{1'b0}}), .eq(comparator_40_eq));  // open: gt, lt
  Comparator #(.width(5)) comparator_41 (.a(MEM_rW), .b(5'b00010), .eq(comparator_41_eq));  // open: gt, lt
  Comparator #(.width(5)) comparator_42 (.a(MEM_rW), .b(5'b00100), .eq(comparator_42_eq));  // open: gt, lt
  and and_15 (and_15_out, comparator_33_eq, read_rA);
  and and_16 (and_16_out, comparator_34_eq, read_rB);
  and and_17 (and_17_out, comparator_36_eq, syscall);
  and and_18 (and_18_out, comparator_37_eq, syscall);
  and and_19 (and_19_out, comparator_38_eq, read_rA);
  and and_20 (and_20_out, comparator_39_eq, read_rB);
  and and_21 (and_21_out, comparator_41_eq, syscall);
  and and_22 (and_22_out, comparator_42_eq, syscall);
  or or_3 (\rA在EX段冲突 , and_15_out, and_17_out);
  or or_4 (\rA在MEM段冲突 , and_19_out, and_21_out);
  or or_5 (or_5_out, and_15_out, and_16_out);
  not not_1 (not_1_out, comparator_35_eq);
  or or_6 (or_6_out, and_17_out, and_18_out);
  or or_7 (or_7_out, and_19_out, and_20_out);
  not not_2 (not_2_out, comparator_40_eq);
  or or_8 (or_8_out, and_21_out, and_22_out);
  or or_9 (\rB在MEM段冲突 , and_22_out, and_20_out);
  or or_10 (\rB在EX段冲突 , and_18_out, and_16_out);
  and and_23 (and_23_out, or_5_out, not_1_out, EX_RF_WE);
  and and_24 (and_24_out, EX_RF_WE, or_6_out);
  and and_25 (and_25_out, or_7_out, not_2_out, MEM_RF_WE);
  and and_26 (and_26_out, MEM_RF_WE, or_8_out);
  or or_11 (\EX段冲突 , and_23_out, and_24_out);
  or or_12 (or_12_out, EX_sw, EX_lw, EX_lh);
  or or_13 (\MEM段冲突 , and_25_out, and_26_out);
  and and_27 (and_27_out, \rA在EX段冲突 , \EX段冲突 );
  or or_14 (or_14_out, and_27_out, and_28_out);
  and and_28 (and_28_out, \rA在MEM段冲突 , \MEM段冲突 );
  and and_29 (Load_Use, \EX段冲突 , or_12_out);
  and and_30 (and_30_out, ~or_12_out, \EX段冲突 );  // AND_Gate
  and and_31 (and_31_out, \MEM段冲突 , \rB在MEM段冲突 );
  or or_15 (or_15_out, and_31_out, and_32_out);
  and and_32 (and_32_out, \EX段冲突 , \rB在EX段冲突 );
  or or_16 (or_16_out, and_30_out, \MEM段冲突 );
  and and_33 (redirect_RF_A, or_14_out, or_16_out);
  and and_34 (redirect_RF_B, or_16_out, or_15_out);
  Multiplexer #(.width(32), .enable("false")) multiplexer_1 (
    .in0(MEM_Data), .in1(EX_Data), .out(redirected_RF_A), .sel(and_27_out));
  Multiplexer #(.width(32), .enable("false")) multiplexer_2 (
    .in0(MEM_Data), .in1(EX_Data), .out(redirected_RF_B), .sel(and_32_out));
endmodule

module NPC (
  input  ALU_Equal,
  input  [31:0] ALU_R,
  input  [31:0] CTRL,
  input  [31:0] IMM,
  input  [31:0] PC_1,
  input  [31:0] IR,
  input  [31:0] RF_A,
  output branch,
  output jump_or_branch,
  output jump,
  output [31:0] new_addr
);

  wire and_1_out, and_2_out, and_3_out;
  wire [31:0] adder_1_out, multiplexer_1_out;

  Adder #(.width(32)) adder_1 (.a({IMM[29:0], 2'b00}), .b(PC_1), .out(adder_1_out));  // open: cin, cout
  and and_1 (and_1_out, ALU_R[0], CTRL[9]);
  and and_2 (and_2_out, ALU_Equal, CTRL[11]);
  or or_1 (branch, and_1_out, and_2_out, and_3_out);
  and and_3 (and_3_out, ~ALU_Equal, CTRL[10]);  // AND_Gate
  Multiplexer #(.width(32), .enable("false")) multiplexer_1 (
    .in0({PC_1[31:28], IR[25:0], 2'b00}), .in1(RF_A), .out(multiplexer_1_out), .sel(CTRL[12]));
  or or_2 (jump_or_branch, branch, CTRL[13]);
  Multiplexer #(.width(32), .enable("false")) multiplexer_2 (
    .in0(adder_1_out), .in1(multiplexer_1_out), .out(new_addr), .sel(CTRL[13]));

  assign jump = CTRL[13];

  // Other names for the same wires on the sheet: bltz = CTRL[9]; bne = CTRL[10]; beq = CTRL[11];
  //   jump_register = CTRL[12]
endmodule

// 扩展
module Extender (
  input  extend_IMM,
  input  extend_shamt,
  input  [31:0] IR,
  input  zero_extend_IMM,
  output [31:0] IMM
);

  wire [16:0] multiplexer_1_out, multiplexer_2_out, multiplexer_3_out;

  Multiplexer #(.width(17), .enable("false")) multiplexer_1 (
    .in0(17'ha), .in1({{12{1'b0}}, IR[10:6]}), .out(multiplexer_1_out), .sel(extend_shamt));
  Multiplexer #(.width(17), .enable("false")) multiplexer_2 (
    .in0({{2{IR[15]}}, IR[14:0]}), .in1({1'b0, IR[15:0]}), .out(multiplexer_2_out), .sel(zero_extend_IMM));
  Multiplexer #(.width(17), .enable("false")) multiplexer_3 (
    .in0(multiplexer_1_out), .in1(multiplexer_2_out), .out(multiplexer_3_out), .sel(extend_IMM));
  assign IMM = {{15{multiplexer_3_out[16]}}, multiplexer_3_out};  // Bit_Extender bit_extender_1

  // Other names for the same wires on the sheet: zero_ext_IMM = zero_extend_IMM
endmodule
