// Logisim project CS1501_U201514477_华龙_alu.circ as structural Verilog
// FA
module L_FA_1_cfbc2c13 (
  input  Input_1,
  input  Input_2,
  input  Input_3,
  output Output_1,
  output Output_2
);

  wire and_2_out, AND_out, xor_2_out;

  or OR (Output_1, AND_out, and_2_out);
  and AND (AND_out, Input_2, Input_3);
  and and_2 (and_2_out, Input_1, xor_2_out);
  xor XOR (Output_2, Input_1, xor_2_out);
  xor xor_2 (xor_2_out, Input_2, Input_3);

  // Notes on the sheet:
  //   Si = Xi ^ Yi ^ Cin
  //   Cout = Xi Yi + Cin (Xi ^ Yi)
endmodule

module L_FA_2_f89faf23 (
  input  Cin,
  input  Xi,
  input  Yi,
  output Cout,
  output Si
);

  wire AND_2_out, AND_out, XOR_2_out;

  or OR (Cout, AND_out, AND_2_out);
  and AND (AND_out, Xi, Yi);
  and AND_2 (AND_2_out, Cin, XOR_2_out);
  xor XOR (Si, Cin, XOR_2_out);
  xor XOR_2 (XOR_2_out, Xi, Yi);

  // Notes on the sheet:
  //   Si = Xi ^ Yi ^ Cin
  //   Cout = Xi Yi + Cin (Xi ^ Yi)
endmodule

module L_FA_3_9ee01b69 (
  input  Cin,
  input  Xi,
  input  Yi,
  output Cout,
  output Si
);

  wire AND_2_out, AND_out, XOR_2_out;

  or OR (Cout, AND_out, AND_2_out);
  and AND (AND_out, Xi, Yi);
  and AND_2 (AND_2_out, Cin, XOR_2_out);
  xor XOR (Si, Cin, XOR_2_out);
  xor XOR_2 (XOR_2_out, Xi, Yi);

  // Notes on the sheet:
  //   Si = Xi ^ Yi ^ Cin
  //   Cout = Xi Yi + Cin (Xi ^ Yi)
endmodule

// ADD
module L_8_39a60a46 (
  input  [7:0] X,
  input  [7:0] Y,
  input  Cin,
  output [7:0] S,
  output Cout,
  output Overflow
);

  wire l_fa_1_cfbc2c13_2_output_1, l_fa_1_cfbc2c13_3_output_1, l_fa_1_cfbc2c13_4_output_1,
       l_fa_1_cfbc2c13_5_output_1, l_fa_1_cfbc2c13_6_output_1, l_fa_1_cfbc2c13_7_output_1,
       l_fa_1_cfbc2c13_8_output_1;

  xor xor_1 (Overflow, Cout, l_fa_1_cfbc2c13_2_output_1);
  L_FA_1_cfbc2c13 l_fa_1_cfbc2c13_1 (
    .Output_1(Cout), .Output_2(S[7]), .Input_1(l_fa_1_cfbc2c13_2_output_1), .Input_2(X[7]), .Input_3(Y[7]));
  L_FA_1_cfbc2c13 l_fa_1_cfbc2c13_2 (
    .Output_1(l_fa_1_cfbc2c13_2_output_1), .Output_2(S[6]), .Input_1(l_fa_1_cfbc2c13_3_output_1),
    .Input_2(X[6]), .Input_3(Y[6]));
  L_FA_1_cfbc2c13 l_fa_1_cfbc2c13_3 (
    .Output_1(l_fa_1_cfbc2c13_3_output_1), .Output_2(S[5]), .Input_1(l_fa_1_cfbc2c13_4_output_1),
    .Input_2(X[5]), .Input_3(Y[5]));
  L_FA_1_cfbc2c13 l_fa_1_cfbc2c13_4 (
    .Output_1(l_fa_1_cfbc2c13_4_output_1), .Output_2(S[4]), .Input_1(l_fa_1_cfbc2c13_5_output_1),
    .Input_2(X[4]), .Input_3(Y[4]));
  L_FA_1_cfbc2c13 l_fa_1_cfbc2c13_5 (
    .Output_1(l_fa_1_cfbc2c13_5_output_1), .Output_2(S[3]), .Input_1(l_fa_1_cfbc2c13_6_output_1),
    .Input_2(X[3]), .Input_3(Y[3]));
  L_FA_1_cfbc2c13 l_fa_1_cfbc2c13_6 (
    .Output_1(l_fa_1_cfbc2c13_6_output_1), .Output_2(S[2]), .Input_1(l_fa_1_cfbc2c13_7_output_1),
    .Input_2(X[2]), .Input_3(Y[2]));
  // Probe on X
  // Probe on Y
  // Probe on S
  L_FA_1_cfbc2c13 l_fa_1_cfbc2c13_7 (
    .Output_1(l_fa_1_cfbc2c13_7_output_1), .Output_2(S[1]), .Input_1(l_fa_1_cfbc2c13_8_output_1),
    .Input_2(X[1]), .Input_3(Y[1]));
  // Probe on X
  // Probe on Y
  // Probe on S
  L_FA_1_cfbc2c13 l_fa_1_cfbc2c13_8 (
    .Output_1(l_fa_1_cfbc2c13_8_output_1), .Output_2(S[0]), .Input_1(Cin), .Input_2(X[0]), .Input_3(Y[0]));

  // Other names for the same wires on the sheet: OF = Overflow

  // Notes on the sheet:
  //   输入引脚区
  //   符号位
  //   输出引脚区
  //   +
  //   =
  //   有符号加法
  //   +
  //   =
  //   无符号加法
endmodule

// CAS
module L_8_60805474 (
  input  [7:0] X,
  input  [7:0] Y,
  input  Cin,
  input  Sub,
  output [7:0] S,
  output Cout,
  output Overflow
);

  wire l_fa_1_cfbc2c13_2_output_1, l_fa_1_cfbc2c13_3_output_1, l_fa_1_cfbc2c13_4_output_1,
       l_fa_1_cfbc2c13_5_output_1, l_fa_1_cfbc2c13_6_output_1, l_fa_1_cfbc2c13_7_output_1,
       l_fa_1_cfbc2c13_8_output_1, or_1_out, xor_2_out, xor_3_out, xor_4_out, xor_5_out, xor_6_out,
       xor_7_out, xor_8_out, xor_9_out;
  wire [8:0] C;

  xor xor_1 (Overflow, Cout, l_fa_1_cfbc2c13_2_output_1);
  L_FA_1_cfbc2c13 l_fa_1_cfbc2c13_1 (
    .Output_1(Cout), .Output_2(S[7]), .Input_1(l_fa_1_cfbc2c13_2_output_1), .Input_2(X[7]),
    .Input_3(xor_2_out));
  xor xor_2 (xor_2_out, Y[7], Sub);
  L_FA_1_cfbc2c13 l_fa_1_cfbc2c13_2 (
    .Output_1(l_fa_1_cfbc2c13_2_output_1), .Output_2(S[6]), .Input_1(l_fa_1_cfbc2c13_3_output_1),
    .Input_2(X[6]), .Input_3(xor_3_out));
  xor xor_3 (xor_3_out, Y[6], Sub);
  L_FA_1_cfbc2c13 l_fa_1_cfbc2c13_3 (
    .Output_1(l_fa_1_cfbc2c13_3_output_1), .Output_2(S[5]), .Input_1(l_fa_1_cfbc2c13_4_output_1),
    .Input_2(X[5]), .Input_3(xor_4_out));
  xor xor_4 (xor_4_out, Y[5], Sub);
  L_FA_1_cfbc2c13 l_fa_1_cfbc2c13_4 (
    .Output_1(l_fa_1_cfbc2c13_4_output_1), .Output_2(S[4]), .Input_1(l_fa_1_cfbc2c13_5_output_1),
    .Input_2(X[4]), .Input_3(xor_5_out));
  xor xor_5 (xor_5_out, Y[4], Sub);
  L_FA_1_cfbc2c13 l_fa_1_cfbc2c13_5 (
    .Output_1(l_fa_1_cfbc2c13_5_output_1), .Output_2(S[3]), .Input_1(l_fa_1_cfbc2c13_6_output_1),
    .Input_2(X[3]), .Input_3(xor_6_out));
  xor xor_6 (xor_6_out, Y[3], Sub);
  L_FA_1_cfbc2c13 l_fa_1_cfbc2c13_6 (
    .Output_1(l_fa_1_cfbc2c13_6_output_1), .Output_2(S[2]), .Input_1(l_fa_1_cfbc2c13_7_output_1),
    .Input_2(X[2]), .Input_3(xor_7_out));
  xor xor_7 (xor_7_out, Y[2], Sub);
  // Probe on X
  // Probe on Y
  // Probe on S
  L_FA_1_cfbc2c13 l_fa_1_cfbc2c13_7 (
    .Output_1(l_fa_1_cfbc2c13_7_output_1), .Output_2(S[1]), .Input_1(l_fa_1_cfbc2c13_8_output_1),
    .Input_2(X[1]), .Input_3(xor_8_out));
  xor xor_8 (xor_8_out, Y[1], Sub);
  or or_1 (or_1_out, Cin, Sub);
  L_FA_1_cfbc2c13 l_fa_1_cfbc2c13_8 (
    .Output_1(l_fa_1_cfbc2c13_8_output_1), .Output_2(S[0]), .Input_1(or_1_out), .Input_2(X[0]),
    .Input_3(xor_9_out));
  xor xor_9 (xor_9_out, Y[0], Sub);
  // Probe on X
  // Probe on Y
  // Probe on S
  Multiplexer #(.width(9), .enable("false")) multiplexer_1 (.in0(9'hba), .in1(9'h92), .out(C), .sel(Sub));

  // Other names for the same wires on the sheet: OF = Overflow

  // Notes on the sheet:
  //   输入引脚区
  //   符号位
  //   输出引脚区
  //   =
  //   有符号
  //   =
  //   无符号
endmodule

// CLA74182
module L_CLA74182_1d5d366e (
  input  Input_1,
  input  Input_2,
  input  Input_3,
  input  Input_4,
  input  Input_5,
  input  Input_6,
  input  Input_7,
  input  Input_8,
  input  Input_9,
  output Output_1,
  output Output_2,
  output Output_3,
  output Output_4,
  output Output_5,
  output Output_6
);

  wire and_1_out, and_2_out, and_3_out, and_4_out, and_5_out, and_6_out, and_7_out, and_8_out, and_9_out,
       and_10_out, and_11_out, and_12_out, and_13_out, and_14_out, and_15_out, and_16_out, and_17_out,
       and_18_out, and_19_out, and_20_out, and_21_out, and_22_out, and_23_out, and_24_out, and_25_out,
       and_26_out, and_27_out, and_28_out, and_29_out, or_1_out, or_3_out, or_4_out, or_5_out, or_6_out,
       or_8_out, or_10_out, or_12_out;

  and and_1 (and_1_out, Input_2, Input_4);
  and and_2 (and_2_out, Input_4, Input_6);
  and and_3 (and_3_out, Input_4, Input_6);
  and and_4 (and_4_out, Input_8, Input_9);
  and and_5 (and_5_out, Input_6, Input_7);
  and and_6 (and_6_out, Input_6, Input_8);
  and and_7 (and_7_out, Input_8, Input_9);
  and and_8 (and_8_out, Input_2, Input_4);
  and and_9 (and_9_out, Input_2, Input_4);
  and and_10 (and_10_out, Input_6, Input_7);
  and and_11 (and_11_out, Input_2, Input_4);
  and and_12 (and_12_out, Input_2, Input_3);
  and and_13 (and_13_out, Input_2, Input_4);
  and and_14 (and_14_out, Input_2, Input_4);
  and and_15 (and_15_out, Input_6, Input_7);
  and and_16 (and_16_out, and_1_out, Input_6);
  and and_17 (and_17_out, Input_8, Input_9);
  and and_18 (and_18_out, Input_4, Input_5);
  and and_19 (and_19_out, and_2_out, Input_7);
  and and_20 (and_20_out, and_3_out, and_4_out);
  or or_1 (or_1_out, Input_5, and_5_out);
  and and_21 (and_21_out, and_6_out, Input_9);
  or or_2 (Output_4, Input_7, and_7_out);
  and and_22 (and_22_out, Input_2, Input_3);
  and and_23 (and_23_out, and_8_out, Input_5);
  and and_24 (and_24_out, and_9_out, and_10_out);
  and and_25 (and_25_out, and_11_out, Input_6);
  and and_26 (and_26_out, Input_8, Input_9);
  or or_3 (or_3_out, Input_1, and_12_out);
  or or_4 (or_4_out, or_3_out, and_27_out);
  and and_27 (and_27_out, and_13_out, Input_5);
  and and_28 (and_28_out, and_14_out, and_15_out);
  or or_5 (or_5_out, and_28_out, and_29_out);
  and and_29 (and_29_out, and_16_out, and_17_out);
  or or_6 (or_6_out, Input_3, and_18_out);
  or or_7 (Output_2, or_6_out, or_8_out);
  or or_8 (or_8_out, and_19_out, and_20_out);
  or or_9 (Output_3, or_1_out, and_21_out);
  or or_10 (or_10_out, Input_1, and_22_out);
  or or_11 (Output_5, or_10_out, or_12_out);
  or or_12 (or_12_out, and_23_out, and_24_out);
  and and_30 (Output_6, and_25_out, and_26_out);
  or or_13 (Output_1, or_4_out, or_5_out);

  // Other names for the same wires on the sheet: C1 = Output_4; C2 = Output_3; C3 = Output_2; C4 = Output_1;
  //   Cin = Input_9; G1 = Input_7; G2 = Input_5; G3 = Input_3; G4 = Input_1; G_b34ae9e7 = Output_5; P1 = Input_8;
  //   P2 = Input_6; P3 = Input_4; P4 = Input_2; P_95817e72 = Output_6

  // Notes on the sheet:
  //   输入引脚区
  //   请根据以上引脚以及隧道信号设计完成74LS182先行进位电路
  //   输出引脚区
  //   请勿增改引脚定义
endmodule

// 4位快速加法器
module L_4_25000c3a (
  input  [3:0] Input_bus_1,
  input  [3:0] Input_bus_2,
  input  Input_1,
  output [3:0] Output_bus_1,
  output Output_1,
  output Output_2,
  output Output_3
);

  wire and_1_out, and_2_out, and_3_out, and_4_out, L_CLA74182_1d5d366e_1_output_2,
       L_CLA74182_1d5d366e_1_output_3, L_CLA74182_1d5d366e_1_output_4, or_1_out, or_2_out, or_3_out, or_4_out;

  L_CLA74182_1d5d366e L_CLA74182_1d5d366e_1 (
    .Input_1(and_1_out), .Input_2(or_1_out), .Input_3(and_2_out), .Input_4(or_2_out), .Input_5(and_3_out),
    .Input_6(or_3_out), .Input_7(and_4_out), .Input_8(or_4_out), .Input_9(Input_1), .Output_1(Output_1),
    .Output_2(L_CLA74182_1d5d366e_1_output_2), .Output_3(L_CLA74182_1d5d366e_1_output_3),
    .Output_4(L_CLA74182_1d5d366e_1_output_4), .Output_5(Output_2), .Output_6(Output_3));
  or or_1 (or_1_out, Input_bus_1[3], Input_bus_2[3]);
  and and_1 (and_1_out, Input_bus_1[3], Input_bus_2[3]);
  L_FA_1_cfbc2c13 L_FA_1_cfbc2c13_1 (
    .Output_2(Output_bus_1[3]), .Input_1(L_CLA74182_1d5d366e_1_output_2), .Input_2(Input_bus_1[3]),
    .Input_3(Input_bus_2[3]));  // open: Output_1
  or or_2 (or_2_out, Input_bus_1[2], Input_bus_2[2]);
  and and_2 (and_2_out, Input_bus_1[2], Input_bus_2[2]);
  L_FA_1_cfbc2c13 L_FA_1_cfbc2c13_2 (
    .Output_2(Output_bus_1[2]), .Input_1(L_CLA74182_1d5d366e_1_output_3), .Input_2(Input_bus_1[2]),
    .Input_3(Input_bus_2[2]));  // open: Output_1
  or or_3 (or_3_out, Input_bus_1[1], Input_bus_2[1]);
  and and_3 (and_3_out, Input_bus_1[1], Input_bus_2[1]);
  L_FA_1_cfbc2c13 L_FA_1_cfbc2c13_3 (
    .Output_2(Output_bus_1[1]), .Input_1(L_CLA74182_1d5d366e_1_output_4), .Input_2(Input_bus_1[1]),
    .Input_3(Input_bus_2[1]));  // open: Output_1
  and and_4 (and_4_out, Input_bus_1[0], Input_bus_2[0]);
  or or_4 (or_4_out, Input_bus_1[0], Input_bus_2[0]);
  L_FA_1_cfbc2c13 L_FA_1_cfbc2c13_4 (
    .Output_2(Output_bus_1[0]), .Input_1(Input_1), .Input_2(Input_bus_1[0]), .Input_3(Input_bus_2[0]));  // open: Output_1
  // Probe on Input_bus_1
  // Probe on Input_bus_2
  // Probe on Output_bus_1
  // Probe on Input_bus_1
  // Probe on Input_bus_2
  // Probe on Output_bus_1

  // Other names for the same wires on the sheet: Cin = Input_1; Cout = Output_1; G_b34ae9e7 = Output_2;
  //   P_95817e72 = Output_3; S[3:0] = Output_bus_1; S0 = Output_bus_1[0]; S1 = Output_bus_1[1]; S2 = Output_bus_1[2];
  //   S3 = Output_bus_1[3]; X[3:0] = Input_bus_1; X0 = Input_bus_1[0]; X1 = Input_bus_1[1]; X2 = Input_bus_1[2];
  //   X3 = Input_bus_1[3]; Y[3:0] = Input_bus_2; Y0 = Input_bus_2[0]; Y1 = Input_bus_2[1]; Y2 = Input_bus_2[2];
  //   Y3 = Input_bus_2[3]

  // Notes on the sheet:
  //   输入引脚区
  //   输出引脚区
  //   +
  //   =
  //   有符号加法
  //   +
  //   =
  //   无符号加法
endmodule

// 16位快速加法器
module L_16_436a7a6f (
  input  [15:0] Input_bus_1,
  input  [15:0] Input_bus_2,
  input  Input_1,
  output [15:0] Output_bus_1,
  output Output_1,
  output Output_2,
  output Output_3
);

  wire L_4_25000c3a_1_output_2, L_4_25000c3a_1_output_3, L_4_25000c3a_2_output_2, L_4_25000c3a_2_output_3,
       L_4_25000c3a_3_output_2, L_4_25000c3a_3_output_3, L_4_25000c3a_4_output_2, L_4_25000c3a_4_output_3,
       L_CLA74182_1d5d366e_1_output_2, L_CLA74182_1d5d366e_1_output_3, L_CLA74182_1d5d366e_1_output_4;

  L_CLA74182_1d5d366e L_CLA74182_1d5d366e_1 (
    .Input_1(L_4_25000c3a_1_output_2), .Input_2(L_4_25000c3a_1_output_3), .Input_3(L_4_25000c3a_2_output_2),
    .Input_4(L_4_25000c3a_2_output_3), .Input_5(L_4_25000c3a_3_output_2), .Input_6(L_4_25000c3a_3_output_3),
    .Input_7(L_4_25000c3a_4_output_2), .Input_8(L_4_25000c3a_4_output_3), .Input_9(Input_1),
    .Output_1(Output_1), .Output_2(L_CLA74182_1d5d366e_1_output_2),
    .Output_3(L_CLA74182_1d5d366e_1_output_3), .Output_4(L_CLA74182_1d5d366e_1_output_4),
    .Output_5(Output_2), .Output_6(Output_3));
  L_4_25000c3a L_4_25000c3a_1 (
    .Input_bus_1(Input_bus_1[15:12]), .Input_bus_2(Input_bus_2[15:12]),
    .Input_1(L_CLA74182_1d5d366e_1_output_2), .Output_bus_1(Output_bus_1[15:12]),
    .Output_2(L_4_25000c3a_1_output_2), .Output_3(L_4_25000c3a_1_output_3));  // open: Output_1
  L_4_25000c3a L_4_25000c3a_2 (
    .Input_bus_1(Input_bus_1[11:8]), .Input_bus_2(Input_bus_2[11:8]),
    .Input_1(L_CLA74182_1d5d366e_1_output_3), .Output_bus_1(Output_bus_1[11:8]),
    .Output_2(L_4_25000c3a_2_output_2), .Output_3(L_4_25000c3a_2_output_3));  // open: Output_1
  L_4_25000c3a L_4_25000c3a_3 (
    .Input_bus_1(Input_bus_1[7:4]), .Input_bus_2(Input_bus_2[7:4]), .Input_1(L_CLA74182_1d5d366e_1_output_4),
    .Output_bus_1(Output_bus_1[7:4]), .Output_2(L_4_25000c3a_3_output_2), .Output_3(L_4_25000c3a_3_output_3));  // open: Output_1
  // Probe on Input_bus_1
  // Probe on Input_bus_2
  // Probe on Output_bus_1
  L_4_25000c3a L_4_25000c3a_4 (
    .Input_bus_1(Input_bus_1[3:0]), .Input_bus_2(Input_bus_2[3:0]), .Input_1(Input_1),
    .Output_bus_1(Output_bus_1[3:0]), .Output_2(L_4_25000c3a_4_output_2), .Output_3(L_4_25000c3a_4_output_3));  // open: Output_1
  // Probe on Input_bus_1
  // Probe on Input_bus_2
  // Probe on Output_bus_1

  // Other names for the same wires on the sheet: Cin = Input_1; Cout = Output_1; G_b34ae9e7 = Output_2;
  //   P_95817e72 = Output_3; S[15:0] = Output_bus_1; S0[3:0] = Output_bus_1[3:0]; S1[3:0] = Output_bus_1[7:4];
  //   S2[3:0] = Output_bus_1[11:8]; S3[3:0] = Output_bus_1[15:12]; X[15:0] = Input_bus_1; X0[3:0] = Input_bus_1[3:0];
  //   X1[3:0] = Input_bus_1[7:4]; X2[3:0] = Input_bus_1[11:8]; X3[3:0] = Input_bus_1[15:12]; Y[15:0] = Input_bus_2;
  //   Y0[3:0] = Input_bus_2[3:0]; Y1[3:0] = Input_bus_2[7:4]; Y2[3:0] = Input_bus_2[11:8];
  //   Y3[3:0] = Input_bus_2[15:12]

  // Notes on the sheet:
  //   输入引脚区
  //   输出引脚区
  //   +
  //   =
  //   有符号加法
  //   +
  //   =
  //   无符号加法
endmodule

module Adder_32_bit (
  input  Cin,
  input  [31:0] X,
  input  [31:0] Y,
  output Cout,
  output [31:0] S,
  output Overflow
);

  // Probe on X
  // Probe on Y
  // Probe on S
  // Probe on X
  // Probe on Y
  // Probe on S

  // Other names for the same wires on the sheet: S0[15:0] = S[15:0]; S1[15:0] = S[31:16]; X0[15:0] = X[15:0];
  //   X1[15:0] = X[31:16]; Y0[15:0] = Y[15:0]; Y1[15:0] = Y[31:16]

  // Notes on the sheet:
  //   输入引脚区
  //   输出引脚区
  //   +
  //   =
  //   有符号加法
  //   +
  //   =
  //   无符号加法
endmodule

module L_6045bfdb (
  input  [7:0] X,
  input  [7:0] Y,
  output [15:0] L_ed793cec
);

  wire ALU_R0_9e22f50a, and_1_out, and_2_out, and_3_out, Clear, CLK, counter_1_carry, counter_2_carry,
       decoder_1_out1, decoder_1_out2, En_38cdd5e1, L_887469d5, LoadData, not_3_out, not_4_out,
       NOT_Yn_1_69aa92c6, NOT_Yn_826f67aa, R0_ALU_5576953a, Yn_1_7c33830c, Yn_Yn_1_bd1425a1;
  wire [1:0] counter_1_q;
  wire [3:0] counter_2_q;
  wire [7:0] controlled_buffer_1_out, l_8_39a60a46_1_s, multiplexer_1_out, multiplexer_2_out, register_1_q,
       register_2_q, X_q;

  Button Start (.out(Clear));
  Clock clock_1 (.out(CLK));
  Multiplexer #(.width(8), .enable("false")) multiplexer_1 (
    .in0(register_1_q), .in1({{2{L_ed793cec[15]}}, L_ed793cec[14:9]}), .out(multiplexer_1_out),
    .sel(L_887469d5));
  Register L_9386c242 (.D(multiplexer_1_out), .en(En_38cdd5e1), .Q(L_ed793cec[15:8]), .clk(CLK), .clr(Clear));
  Register register_1 (.D(l_8_39a60a46_1_s), .en(ALU_R0_9e22f50a), .Q(register_1_q), .clk(CLK), .clr(Clear));
  L_8_39a60a46 l_8_39a60a46_1 (
    .X(register_2_q), .Y(controlled_buffer_1_out), .Cin(and_2_out), .S(l_8_39a60a46_1_s));  // open: Cout, Overflow
  Register register_2 (.D(L_ed793cec[15:8]), .en(R0_ALU_5576953a), .Q(register_2_q), .clk(CLK), .clr(Clear));
  assign controlled_buffer_1_out = and_1_out ? X_q : 8'bz;  // Controlled_Buffer controlled_buffer_1
  and and_1 (and_1_out, NOT_Yn_826f67aa, Yn_1_7c33830c);
  // Probe on X
  // Probe on L_ed793cec[15:8]
  Multiplexer #(.width(8), .enable("false")) multiplexer_2 (
    .in0(L_ed793cec[8:1]), .in1(Y), .out(multiplexer_2_out), .sel(LoadData));
  assign controlled_buffer_1_out = and_2_out ? ~X_q : 8'bz;  // Controlled_Inverter L_f83231a3
  and and_2 (and_2_out, L_ed793cec[0], NOT_Yn_1_69aa92c6);
  Register u_X (.D(X), .en(LoadData), .Q(X_q), .clk(CLK));  // open: clr
  // Probe on Y
  // Probe on L_ed793cec[7:0]
  Register Y_2 (.D(multiplexer_2_out), .en(L_887469d5), .Q(L_ed793cec[7:0]), .clk(CLK));  // open: clr
  // Probe on L_ed793cec
  // Probe on Yn_1_7c33830c
  not not_1 (NOT_Yn_826f67aa, L_ed793cec[0]);
  Register #(.width(1)) Yn_1_7c33830c_2 (
    .D(L_ed793cec[0]), .en(L_887469d5), .Q(Yn_1_7c33830c), .clk(CLK), .clr(LoadData));
  Counter #(.width(2), .max('h3)) counter_1 (
    .Q(counter_1_q), .carry(counter_1_carry), .clk(CLK), .clr(Clear));  // open: load, D, count
  Counter #(.width(4), .max('h9), .ongoal("stay")) counter_2 (
    .Q(counter_2_q), .carry(counter_2_carry), .clk(counter_1_carry), .clr(Clear));  // open: load, D, count
  xnor xnor_1 (Yn_Yn_1_bd1425a1, L_ed793cec[0], Yn_1_7c33830c);
  not not_2 (NOT_Yn_1_69aa92c6, Yn_1_7c33830c);
  Decoder #(.select(2)) decoder_1 (
    .out0(ALU_R0_9e22f50a), .out1(decoder_1_out1), .out2(decoder_1_out2), .out3(R0_ALU_5576953a),
    .sel(counter_1_q), .en(not_3_out));
  not not_3 (not_3_out, counter_2_carry);
  nor nor_1 (LoadData, counter_2_q[0], counter_2_q[1], counter_2_q[2], counter_2_q[3]);
  not not_4 (not_4_out, Yn_Yn_1_bd1425a1);
  and and_3 (and_3_out, not_4_out, decoder_1_out1);
  or or_1 (L_887469d5, decoder_1_out2, LoadData);
  or or_2 (En_38cdd5e1, and_3_out, L_887469d5);

  // Other names for the same wires on the sheet: Yn = L_ed793cec[0]
endmodule

// 与门阵列
module L_8_aa5564b8 (
  input  [7:0] X,
  input  [7:0] Y,
  output [7:0] XY0,
  output [7:0] XY1,
  output [7:0] XY2,
  output [7:0] XY3,
  output [7:0] XY4,
  output [7:0] XY5,
  output [7:0] XY6,
  output [7:0] XY7
);

  and and_1 (XY0[7], X[7], Y[0]);
  and and_2 (XY1[7], X[7], Y[1]);
  and and_3 (XY2[7], X[7], Y[2]);
  and and_4 (XY3[7], X[7], Y[3]);
  and and_5 (XY4[7], X[7], Y[4]);
  and and_6 (XY5[7], X[7], Y[5]);
  and and_7 (XY6[7], X[7], Y[6]);
  and and_8 (XY7[7], X[7], Y[7]);
  and and_9 (XY0[6], X[6], Y[0]);
  and and_10 (XY1[6], X[6], Y[1]);
  and and_11 (XY2[6], X[6], Y[2]);
  and and_12 (XY3[6], X[6], Y[3]);
  and and_13 (XY4[6], X[6], Y[4]);
  and and_14 (XY5[6], X[6], Y[5]);
  and and_15 (XY6[6], X[6], Y[6]);
  and and_16 (XY7[6], X[6], Y[7]);
  and and_17 (XY0[5], X[5], Y[0]);
  and and_18 (XY1[5], X[5], Y[1]);
  and and_19 (XY2[5], X[5], Y[2]);
  and and_20 (XY3[5], X[5], Y[3]);
  and and_21 (XY4[5], X[5], Y[4]);
  and and_22 (XY5[5], X[5], Y[5]);
  and and_23 (XY6[5], X[5], Y[6]);
  and and_24 (XY7[5], X[5], Y[7]);
  and and_25 (XY0[3], X[3], Y[0]);
  and and_26 (XY0[4], X[4], Y[0]);
  and and_27 (XY1[3], X[3], Y[1]);
  and and_28 (XY1[4], X[4], Y[1]);
  and and_29 (XY2[3], X[3], Y[2]);
  and and_30 (XY2[4], X[4], Y[2]);
  and and_31 (XY3[3], X[3], Y[3]);
  and and_32 (XY3[4], X[4], Y[3]);
  and and_33 (XY4[3], X[3], Y[4]);
  and and_34 (XY4[4], X[4], Y[4]);
  and and_35 (XY5[3], X[3], Y[5]);
  and and_36 (XY5[4], X[4], Y[5]);
  and and_37 (XY6[4], X[4], Y[6]);
  and and_38 (XY6[3], X[3], Y[6]);
  and and_39 (XY7[3], X[3], Y[7]);
  and and_40 (XY7[4], X[4], Y[7]);
  and and_41 (XY0[2], X[2], Y[0]);
  and and_42 (XY1[2], X[2], Y[1]);
  and and_43 (XY2[2], X[2], Y[2]);
  and and_44 (XY3[2], X[2], Y[3]);
  and and_45 (XY4[2], X[2], Y[4]);
  and and_46 (XY5[2], X[2], Y[5]);
  and and_47 (XY6[2], X[2], Y[6]);
  and and_48 (XY7[2], X[2], Y[7]);
  and and_49 (XY0[1], X[1], Y[0]);
  and and_50 (XY1[1], X[1], Y[1]);
  and and_51 (XY2[1], X[1], Y[2]);
  and and_52 (XY3[1], X[1], Y[3]);
  and and_53 (XY4[1], X[1], Y[4]);
  and and_54 (XY5[1], X[1], Y[5]);
  and and_55 (XY6[1], X[1], Y[6]);
  and and_56 (XY7[1], X[1], Y[7]);
  and and_57 (XY0[0], X[0], Y[0]);
  and and_58 (XY1[0], X[0], Y[1]);
  and and_59 (XY2[0], X[0], Y[2]);
  and and_60 (XY3[0], X[0], Y[3]);
  and and_61 (XY4[0], X[0], Y[4]);
  and and_62 (XY5[0], X[0], Y[5]);
  and and_63 (XY6[0], X[0], Y[6]);
  and and_64 (XY7[0], X[0], Y[7]);

  // Other names for the same wires on the sheet: X0Y0 = XY0[0]; X1Y0 = XY0[1]; X2Y0 = XY0[2]; X3Y0 = XY0[3];
  //   X4Y0 = XY0[4]; X5Y0 = XY0[5]; X6Y0 = XY0[6]; X7Y0 = XY0[7]; X0Y1 = XY1[0]; X1Y1 = XY1[1]; X2Y1 = XY1[2];
  //   X3Y1 = XY1[3]; X4Y1 = XY1[4]; X5Y1 = XY1[5]; X6Y1 = XY1[6]; X7Y1 = XY1[7]; X0Y2 = XY2[0]; X1Y2 = XY2[1];
  //   X2Y2 = XY2[2]; X3Y2 = XY2[3]; X4Y2 = XY2[4]; X5Y2 = XY2[5]; X6Y2 = XY2[6]; X7Y2 = XY2[7]; X0Y3 = XY3[0];
  //   X1Y3 = XY3[1]; X2Y3 = XY3[2]; X3Y3 = XY3[3]; X4Y3 = XY3[4]; X5Y3 = XY3[5]; X6Y3 = XY3[6]; X7Y3 = XY3[7];
  //   X0Y4 = XY4[0]; X1Y4 = XY4[1]; X2Y4 = XY4[2]; X3Y4 = XY4[3]; X4Y4 = XY4[4]; X5Y4 = XY4[5]; X6Y4 = XY4[6];
  //   X7Y4 = XY4[7]; X0Y5 = XY5[0]; X1Y5 = XY5[1]; X2Y5 = XY5[2]; X3Y5 = XY5[3]; X4Y5 = XY5[4]; X5Y5 = XY5[5];
  //   X6Y5 = XY5[6]; X7Y5 = XY5[7]; X0Y6 = XY6[0]; X1Y6 = XY6[1]; X2Y6 = XY6[2]; X3Y6 = XY6[3]; X4Y6 = XY6[4];
  //   X5Y6 = XY6[5]; X6Y6 = XY6[6]; X7Y6 = XY6[7]; X0Y7 = XY7[0]; X1Y7 = XY7[1]; X2Y7 = XY7[2]; X3Y7 = XY7[3];
  //   X4Y7 = XY7[4]; X5Y7 = XY7[5]; X6Y7 = XY7[6]; X7Y7 = XY7[7]
endmodule

module L_8_32a76294 (
  input  [7:0] X,
  input  [7:0] Y,
  output [15:0] L_ed793cec
);

  wire l_fa_3_9ee01b69_2_cout, l_fa_3_9ee01b69_2_si, l_fa_3_9ee01b69_3_cout, l_fa_3_9ee01b69_4_cout,
       l_fa_3_9ee01b69_4_si, l_fa_3_9ee01b69_5_cout, l_fa_3_9ee01b69_5_si, l_fa_3_9ee01b69_6_cout,
       l_fa_3_9ee01b69_7_cout, l_fa_3_9ee01b69_7_si, l_fa_3_9ee01b69_8_cout, l_fa_3_9ee01b69_8_si,
       l_fa_3_9ee01b69_9_cout, l_fa_3_9ee01b69_9_si, l_fa_3_9ee01b69_10_cout, l_fa_3_9ee01b69_11_cout,
       l_fa_3_9ee01b69_11_si, l_fa_3_9ee01b69_12_cout, l_fa_3_9ee01b69_12_si, l_fa_3_9ee01b69_13_cout,
       l_fa_3_9ee01b69_13_si, l_fa_3_9ee01b69_14_cout, l_fa_3_9ee01b69_14_si, l_fa_3_9ee01b69_15_cout,
       l_fa_3_9ee01b69_16_cout, l_fa_3_9ee01b69_16_si, l_fa_3_9ee01b69_17_cout, l_fa_3_9ee01b69_17_si,
       l_fa_3_9ee01b69_18_cout, l_fa_3_9ee01b69_18_si, l_fa_3_9ee01b69_19_cout, l_fa_3_9ee01b69_19_si,
       l_fa_3_9ee01b69_20_cout, l_fa_3_9ee01b69_20_si, l_fa_3_9ee01b69_21_cout, l_fa_3_9ee01b69_22_cout,
       l_fa_3_9ee01b69_22_si, l_fa_3_9ee01b69_23_cout, l_fa_3_9ee01b69_23_si, l_fa_3_9ee01b69_24_cout,
       l_fa_3_9ee01b69_24_si, l_fa_3_9ee01b69_25_cout, l_fa_3_9ee01b69_25_si, l_fa_3_9ee01b69_26_cout,
       l_fa_3_9ee01b69_26_si, l_fa_3_9ee01b69_27_cout, l_fa_3_9ee01b69_27_si, l_fa_3_9ee01b69_28_cout,
       l_fa_3_9ee01b69_29_cout, l_fa_3_9ee01b69_29_si, l_fa_3_9ee01b69_30_cout, l_fa_3_9ee01b69_30_si,
       l_fa_3_9ee01b69_31_cout, l_fa_3_9ee01b69_31_si, l_fa_3_9ee01b69_32_cout, l_fa_3_9ee01b69_32_si,
       l_fa_3_9ee01b69_33_cout, l_fa_3_9ee01b69_33_si, l_fa_3_9ee01b69_34_cout, l_fa_3_9ee01b69_34_si,
       l_fa_3_9ee01b69_35_cout, l_fa_3_9ee01b69_36_cout, l_fa_3_9ee01b69_36_si, l_fa_3_9ee01b69_37_cout,
       l_fa_3_9ee01b69_37_si, l_fa_3_9ee01b69_38_cout, l_fa_3_9ee01b69_38_si, l_fa_3_9ee01b69_39_cout,
       l_fa_3_9ee01b69_39_si, l_fa_3_9ee01b69_40_cout, l_fa_3_9ee01b69_40_si, l_fa_3_9ee01b69_41_cout,
       l_fa_3_9ee01b69_42_cout, l_fa_3_9ee01b69_42_si, l_fa_3_9ee01b69_43_cout, l_fa_3_9ee01b69_43_si,
       l_fa_3_9ee01b69_44_cout, l_fa_3_9ee01b69_44_si, l_fa_3_9ee01b69_45_cout, l_fa_3_9ee01b69_45_si,
       l_fa_3_9ee01b69_46_cout, l_fa_3_9ee01b69_47_cout, l_fa_3_9ee01b69_47_si, l_fa_3_9ee01b69_48_cout,
       l_fa_3_9ee01b69_48_si, l_fa_3_9ee01b69_49_cout, l_fa_3_9ee01b69_49_si, l_fa_3_9ee01b69_50_cout,
       l_fa_3_9ee01b69_51_cout, l_fa_3_9ee01b69_51_si, l_fa_3_9ee01b69_52_cout, l_fa_3_9ee01b69_52_si,
       l_fa_3_9ee01b69_53_cout, l_fa_3_9ee01b69_54_cout, l_fa_3_9ee01b69_54_si, l_fa_3_9ee01b69_55_cout,
       l_fa_3_9ee01b69_56_cout, X0Y1, X0Y2, X0Y3, X0Y4, X0Y5, X0Y6, X0Y7, X1Y0, X1Y1, X1Y2, X1Y3, X1Y4, X1Y5,
       X1Y6, X1Y7, X2Y0, X2Y1, X2Y2, X2Y3, X2Y4, X2Y5, X2Y6, X2Y7, X3Y0, X3Y1, X3Y2, X3Y3, X3Y4, X3Y5, X3Y6,
       X3Y7, X4Y0, X4Y1, X4Y2, X4Y3, X4Y4, X4Y5, X4Y6, X4Y7, X5Y0, X5Y1, X5Y2, X5Y3, X5Y4, X5Y5, X5Y6, X5Y7,
       X6Y0, X6Y1, X6Y2, X6Y3, X6Y4, X6Y5, X6Y6, X6Y7, X7Y0, X7Y1, X7Y2, X7Y3, X7Y4, X7Y5, X7Y6, X7Y7;

  L_FA_3_9ee01b69 l_fa_3_9ee01b69_1 (
    .Cout(L_ed793cec[15]), .Si(L_ed793cec[14]), .Cin(l_fa_3_9ee01b69_2_cout), .Xi(l_fa_3_9ee01b69_3_cout),
    .Yi(X7Y7));
  // Probe on X
  // Probe on L_ed793cec
  L_FA_3_9ee01b69 l_fa_3_9ee01b69_2 (
    .Cout(l_fa_3_9ee01b69_2_cout), .Si(l_fa_3_9ee01b69_2_si), .Cin(l_fa_3_9ee01b69_4_cout), .Xi(X6Y7),
    .Yi(X7Y6));
  L_FA_3_9ee01b69 l_fa_3_9ee01b69_3 (
    .Cout(l_fa_3_9ee01b69_3_cout), .Si(L_ed793cec[13]), .Cin(l_fa_3_9ee01b69_5_cout),
    .Xi(l_fa_3_9ee01b69_6_cout), .Yi(l_fa_3_9ee01b69_2_si));
  L_FA_3_9ee01b69 l_fa_3_9ee01b69_4 (
    .Cout(l_fa_3_9ee01b69_4_cout), .Si(l_fa_3_9ee01b69_4_si), .Cin(l_fa_3_9ee01b69_7_cout), .Xi(X6Y6),
    .Yi(X7Y5));
  L_FA_3_9ee01b69 l_fa_3_9ee01b69_5 (
    .Cout(l_fa_3_9ee01b69_5_cout), .Si(l_fa_3_9ee01b69_5_si), .Cin(l_fa_3_9ee01b69_8_cout), .Xi(X5Y7),
    .Yi(l_fa_3_9ee01b69_4_si));
  L_FA_3_9ee01b69 l_fa_3_9ee01b69_6 (
    .Cout(l_fa_3_9ee01b69_6_cout), .Si(L_ed793cec[12]), .Cin(l_fa_3_9ee01b69_9_cout),
    .Xi(l_fa_3_9ee01b69_10_cout), .Yi(l_fa_3_9ee01b69_5_si));
  // Probe on Y
  L_FA_3_9ee01b69 l_fa_3_9ee01b69_7 (
    .Cout(l_fa_3_9ee01b69_7_cout), .Si(l_fa_3_9ee01b69_7_si), .Cin(l_fa_3_9ee01b69_11_cout), .Xi(X6Y5),
    .Yi(X7Y4));
  L_FA_3_9ee01b69 l_fa_3_9ee01b69_8 (
    .Cout(l_fa_3_9ee01b69_8_cout), .Si(l_fa_3_9ee01b69_8_si), .Cin(l_fa_3_9ee01b69_12_cout), .Xi(X5Y6),
    .Yi(l_fa_3_9ee01b69_7_si));
  L_FA_3_9ee01b69 l_fa_3_9ee01b69_9 (
    .Cout(l_fa_3_9ee01b69_9_cout), .Si(l_fa_3_9ee01b69_9_si), .Cin(l_fa_3_9ee01b69_13_cout), .Xi(X4Y7),
    .Yi(l_fa_3_9ee01b69_8_si));
  L_FA_3_9ee01b69 l_fa_3_9ee01b69_10 (
    .Cout(l_fa_3_9ee01b69_10_cout), .Si(L_ed793cec[11]), .Cin(l_fa_3_9ee01b69_14_cout),
    .Xi(l_fa_3_9ee01b69_15_cout), .Yi(l_fa_3_9ee01b69_9_si));
  L_FA_3_9ee01b69 l_fa_3_9ee01b69_11 (
    .Cout(l_fa_3_9ee01b69_11_cout), .Si(l_fa_3_9ee01b69_11_si), .Cin(l_fa_3_9ee01b69_16_cout), .Xi(X6Y4),
    .Yi(X7Y3));
  L_FA_3_9ee01b69 l_fa_3_9ee01b69_12 (
    .Cout(l_fa_3_9ee01b69_12_cout), .Si(l_fa_3_9ee01b69_12_si), .Cin(l_fa_3_9ee01b69_17_cout), .Xi(X5Y5),
    .Yi(l_fa_3_9ee01b69_11_si));
  L_FA_3_9ee01b69 l_fa_3_9ee01b69_13 (
    .Cout(l_fa_3_9ee01b69_13_cout), .Si(l_fa_3_9ee01b69_13_si), .Cin(l_fa_3_9ee01b69_18_cout), .Xi(X4Y6),
    .Yi(l_fa_3_9ee01b69_12_si));
  L_FA_3_9ee01b69 l_fa_3_9ee01b69_14 (
    .Cout(l_fa_3_9ee01b69_14_cout), .Si(l_fa_3_9ee01b69_14_si), .Cin(l_fa_3_9ee01b69_19_cout), .Xi(X3Y7),
    .Yi(l_fa_3_9ee01b69_13_si));
  L_FA_3_9ee01b69 l_fa_3_9ee01b69_15 (
    .Cout(l_fa_3_9ee01b69_15_cout), .Si(L_ed793cec[10]), .Cin(l_fa_3_9ee01b69_20_cout),
    .Xi(l_fa_3_9ee01b69_21_cout), .Yi(l_fa_3_9ee01b69_14_si));
  L_FA_3_9ee01b69 l_fa_3_9ee01b69_16 (
    .Cout(l_fa_3_9ee01b69_16_cout), .Si(l_fa_3_9ee01b69_16_si), .Cin(l_fa_3_9ee01b69_22_cout), .Xi(X6Y3),
    .Yi(X7Y2));
  L_FA_3_9ee01b69 l_fa_3_9ee01b69_17 (
    .Cout(l_fa_3_9ee01b69_17_cout), .Si(l_fa_3_9ee01b69_17_si), .Cin(l_fa_3_9ee01b69_23_cout), .Xi(X5Y4),
    .Yi(l_fa_3_9ee01b69_16_si));
  L_FA_3_9ee01b69 l_fa_3_9ee01b69_18 (
    .Cout(l_fa_3_9ee01b69_18_cout), .Si(l_fa_3_9ee01b69_18_si), .Cin(l_fa_3_9ee01b69_24_cout), .Xi(X4Y5),
    .Yi(l_fa_3_9ee01b69_17_si));
  L_FA_3_9ee01b69 l_fa_3_9ee01b69_19 (
    .Cout(l_fa_3_9ee01b69_19_cout), .Si(l_fa_3_9ee01b69_19_si), .Cin(l_fa_3_9ee01b69_25_cout), .Xi(X3Y6),
    .Yi(l_fa_3_9ee01b69_18_si));
  L_FA_3_9ee01b69 l_fa_3_9ee01b69_20 (
    .Cout(l_fa_3_9ee01b69_20_cout), .Si(l_fa_3_9ee01b69_20_si), .Cin(l_fa_3_9ee01b69_26_cout), .Xi(X2Y7),
    .Yi(l_fa_3_9ee01b69_19_si));
  L_FA_3_9ee01b69 l_fa_3_9ee01b69_21 (
    .Cout(l_fa_3_9ee01b69_21_cout), .Si(L_ed793cec[9]), .Cin(l_fa_3_9ee01b69_27_cout),
    .Xi(l_fa_3_9ee01b69_28_cout), .Yi(l_fa_3_9ee01b69_20_si));
  L_FA_3_9ee01b69 l_fa_3_9ee01b69_22 (
    .Cout(l_fa_3_9ee01b69_22_cout), .Si(l_fa_3_9ee01b69_22_si), .Cin(l_fa_3_9ee01b69_29_cout), .Xi(X6Y2),
    .Yi(X7Y1));
  L_FA_3_9ee01b69 l_fa_3_9ee01b69_23 (
    .Cout(l_fa_3_9ee01b69_23_cout), .Si(l_fa_3_9ee01b69_23_si), .Cin(l_fa_3_9ee01b69_30_cout), .Xi(X5Y3),
    .Yi(l_fa_3_9ee01b69_22_si));
  L_FA_3_9ee01b69 l_fa_3_9ee01b69_24 (
    .Cout(l_fa_3_9ee01b69_24_cout), .Si(l_fa_3_9ee01b69_24_si), .Cin(l_fa_3_9ee01b69_31_cout), .Xi(X4Y4),
    .Yi(l_fa_3_9ee01b69_23_si));
  L_FA_3_9ee01b69 l_fa_3_9ee01b69_25 (
    .Cout(l_fa_3_9ee01b69_25_cout), .Si(l_fa_3_9ee01b69_25_si), .Cin(l_fa_3_9ee01b69_32_cout), .Xi(X3Y5),
    .Yi(l_fa_3_9ee01b69_24_si));
  L_FA_3_9ee01b69 l_fa_3_9ee01b69_26 (
    .Cout(l_fa_3_9ee01b69_26_cout), .Si(l_fa_3_9ee01b69_26_si), .Cin(l_fa_3_9ee01b69_33_cout), .Xi(X2Y6),
    .Yi(l_fa_3_9ee01b69_25_si));
  L_FA_3_9ee01b69 l_fa_3_9ee01b69_27 (
    .Cout(l_fa_3_9ee01b69_27_cout), .Si(l_fa_3_9ee01b69_27_si), .Cin(l_fa_3_9ee01b69_34_cout), .Xi(X1Y7),
    .Yi(l_fa_3_9ee01b69_26_si));
  L_FA_3_9ee01b69 l_fa_3_9ee01b69_28 (
    .Cout(l_fa_3_9ee01b69_28_cout), .Si(L_ed793cec[8]), .Cin(l_fa_3_9ee01b69_35_cout), .Xi(1'b0),
    .Yi(l_fa_3_9ee01b69_27_si));
  L_FA_3_9ee01b69 l_fa_3_9ee01b69_29 (
    .Cout(l_fa_3_9ee01b69_29_cout), .Si(l_fa_3_9ee01b69_29_si), .Cin(1'b0), .Xi(X6Y1), .Yi(X7Y0));
  L_FA_3_9ee01b69 l_fa_3_9ee01b69_30 (
    .Cout(l_fa_3_9ee01b69_30_cout), .Si(l_fa_3_9ee01b69_30_si), .Cin(l_fa_3_9ee01b69_36_cout), .Xi(X5Y2),
    .Yi(l_fa_3_9ee01b69_29_si));
  L_FA_3_9ee01b69 l_fa_3_9ee01b69_31 (
    .Cout(l_fa_3_9ee01b69_31_cout), .Si(l_fa_3_9ee01b69_31_si), .Cin(l_fa_3_9ee01b69_37_cout), .Xi(X4Y3),
    .Yi(l_fa_3_9ee01b69_30_si));
  L_FA_3_9ee01b69 l_fa_3_9ee01b69_32 (
    .Cout(l_fa_3_9ee01b69_32_cout), .Si(l_fa_3_9ee01b69_32_si), .Cin(l_fa_3_9ee01b69_38_cout), .Xi(X3Y4),
    .Yi(l_fa_3_9ee01b69_31_si));
  L_FA_3_9ee01b69 l_fa_3_9ee01b69_33 (
    .Cout(l_fa_3_9ee01b69_33_cout), .Si(l_fa_3_9ee01b69_33_si), .Cin(l_fa_3_9ee01b69_39_cout), .Xi(X2Y5),
    .Yi(l_fa_3_9ee01b69_32_si));
  L_FA_3_9ee01b69 l_fa_3_9ee01b69_34 (
    .Cout(l_fa_3_9ee01b69_34_cout), .Si(l_fa_3_9ee01b69_34_si), .Cin(l_fa_3_9ee01b69_40_cout), .Xi(X1Y6),
    .Yi(l_fa_3_9ee01b69_33_si));
  L_FA_3_9ee01b69 l_fa_3_9ee01b69_35 (
    .Cout(l_fa_3_9ee01b69_35_cout), .Si(L_ed793cec[7]), .Cin(l_fa_3_9ee01b69_41_cout), .Xi(X0Y7),
    .Yi(l_fa_3_9ee01b69_34_si));
  L_FA_3_9ee01b69 l_fa_3_9ee01b69_36 (
    .Cout(l_fa_3_9ee01b69_36_cout), .Si(l_fa_3_9ee01b69_36_si), .Cin(1'b0), .Xi(X5Y1), .Yi(X6Y0));
  L_FA_3_9ee01b69 l_fa_3_9ee01b69_37 (
    .Cout(l_fa_3_9ee01b69_37_cout), .Si(l_fa_3_9ee01b69_37_si), .Cin(l_fa_3_9ee01b69_42_cout), .Xi(X4Y2),
    .Yi(l_fa_3_9ee01b69_36_si));
  L_FA_3_9ee01b69 l_fa_3_9ee01b69_38 (
    .Cout(l_fa_3_9ee01b69_38_cout), .Si(l_fa_3_9ee01b69_38_si), .Cin(l_fa_3_9ee01b69_43_cout), .Xi(X3Y3),
    .Yi(l_fa_3_9ee01b69_37_si));
  L_FA_3_9ee01b69 l_fa_3_9ee01b69_39 (
    .Cout(l_fa_3_9ee01b69_39_cout), .Si(l_fa_3_9ee01b69_39_si), .Cin(l_fa_3_9ee01b69_44_cout), .Xi(X2Y4),
    .Yi(l_fa_3_9ee01b69_38_si));
  L_FA_3_9ee01b69 l_fa_3_9ee01b69_40 (
    .Cout(l_fa_3_9ee01b69_40_cout), .Si(l_fa_3_9ee01b69_40_si), .Cin(l_fa_3_9ee01b69_45_cout), .Xi(X1Y5),
    .Yi(l_fa_3_9ee01b69_39_si));
  L_FA_3_9ee01b69 l_fa_3_9ee01b69_41 (
    .Cout(l_fa_3_9ee01b69_41_cout), .Si(L_ed793cec[6]), .Cin(l_fa_3_9ee01b69_46_cout), .Xi(X0Y6),
    .Yi(l_fa_3_9ee01b69_40_si));
  L_FA_3_9ee01b69 l_fa_3_9ee01b69_42 (
    .Cout(l_fa_3_9ee01b69_42_cout), .Si(l_fa_3_9ee01b69_42_si), .Cin(1'b0), .Xi(X4Y1), .Yi(X5Y0));
  L_FA_3_9ee01b69 l_fa_3_9ee01b69_43 (
    .Cout(l_fa_3_9ee01b69_43_cout), .Si(l_fa_3_9ee01b69_43_si), .Cin(l_fa_3_9ee01b69_47_cout), .Xi(X3Y2),
    .Yi(l_fa_3_9ee01b69_42_si));
  L_FA_3_9ee01b69 l_fa_3_9ee01b69_44 (
    .Cout(l_fa_3_9ee01b69_44_cout), .Si(l_fa_3_9ee01b69_44_si), .Cin(l_fa_3_9ee01b69_48_cout), .Xi(X2Y3),
    .Yi(l_fa_3_9ee01b69_43_si));
  L_FA_3_9ee01b69 l_fa_3_9ee01b69_45 (
    .Cout(l_fa_3_9ee01b69_45_cout), .Si(l_fa_3_9ee01b69_45_si), .Cin(l_fa_3_9ee01b69_49_cout), .Xi(X1Y4),
    .Yi(l_fa_3_9ee01b69_44_si));
  L_FA_3_9ee01b69 l_fa_3_9ee01b69_46 (
    .Cout(l_fa_3_9ee01b69_46_cout), .Si(L_ed793cec[5]), .Cin(l_fa_3_9ee01b69_50_cout), .Xi(X0Y5),
    .Yi(l_fa_3_9ee01b69_45_si));
  L_FA_3_9ee01b69 l_fa_3_9ee01b69_47 (
    .Cout(l_fa_3_9ee01b69_47_cout), .Si(l_fa_3_9ee01b69_47_si), .Cin(1'b0), .Xi(X3Y1), .Yi(X4Y0));
  L_FA_3_9ee01b69 l_fa_3_9ee01b69_48 (
    .Cout(l_fa_3_9ee01b69_48_cout), .Si(l_fa_3_9ee01b69_48_si), .Cin(l_fa_3_9ee01b69_51_cout), .Xi(X2Y2),
    .Yi(l_fa_3_9ee01b69_47_si));
  L_FA_3_9ee01b69 l_fa_3_9ee01b69_49 (
    .Cout(l_fa_3_9ee01b69_49_cout), .Si(l_fa_3_9ee01b69_49_si), .Cin(l_fa_3_9ee01b69_52_cout), .Xi(X1Y3),
    .Yi(l_fa_3_9ee01b69_48_si));
  L_FA_3_9ee01b69 l_fa_3_9ee01b69_50 (
    .Cout(l_fa_3_9ee01b69_50_cout), .Si(L_ed793cec[4]), .Cin(l_fa_3_9ee01b69_53_cout), .Xi(X0Y4),
    .Yi(l_fa_3_9ee01b69_49_si));
  L_FA_3_9ee01b69 l_fa_3_9ee01b69_51 (
    .Cout(l_fa_3_9ee01b69_51_cout), .Si(l_fa_3_9ee01b69_51_si), .Cin(1'b0), .Xi(X2Y1), .Yi(X3Y0));
  L_FA_3_9ee01b69 l_fa_3_9ee01b69_52 (
    .Cout(l_fa_3_9ee01b69_52_cout), .Si(l_fa_3_9ee01b69_52_si), .Cin(l_fa_3_9ee01b69_54_cout), .Xi(X1Y2),
    .Yi(l_fa_3_9ee01b69_51_si));
  L_FA_3_9ee01b69 l_fa_3_9ee01b69_53 (
    .Cout(l_fa_3_9ee01b69_53_cout), .Si(L_ed793cec[3]), .Cin(l_fa_3_9ee01b69_55_cout), .Xi(X0Y3),
    .Yi(l_fa_3_9ee01b69_52_si));
  L_FA_3_9ee01b69 l_fa_3_9ee01b69_54 (
    .Cout(l_fa_3_9ee01b69_54_cout), .Si(l_fa_3_9ee01b69_54_si), .Cin(1'b0), .Xi(X1Y1), .Yi(X2Y0));
  L_FA_3_9ee01b69 l_fa_3_9ee01b69_55 (
    .Cout(l_fa_3_9ee01b69_55_cout), .Si(L_ed793cec[2]), .Cin(l_fa_3_9ee01b69_56_cout), .Xi(X0Y2),
    .Yi(l_fa_3_9ee01b69_54_si));
  L_FA_3_9ee01b69 l_fa_3_9ee01b69_56 (
    .Cout(l_fa_3_9ee01b69_56_cout), .Si(L_ed793cec[1]), .Cin(1'b0), .Xi(X0Y1), .Yi(X1Y0));
  L_8_aa5564b8 l_8_aa5564b8_1 (
    .X(X), .Y(Y), .XY7({X7Y7, X6Y7, X5Y7, X4Y7, X3Y7, X2Y7, X1Y7, X0Y7}),
    .XY6({X7Y6, X6Y6, X5Y6, X4Y6, X3Y6, X2Y6, X1Y6, X0Y6}),
    .XY5({X7Y5, X6Y5, X5Y5, X4Y5, X3Y5, X2Y5, X1Y5, X0Y5}),
    .XY4({X7Y4, X6Y4, X5Y4, X4Y4, X3Y4, X2Y4, X1Y4, X0Y4}),
    .XY3({X7Y3, X6Y3, X5Y3, X4Y3, X3Y3, X2Y3, X1Y3, X0Y3}),
    .XY2({X7Y2, X6Y2, X5Y2, X4Y2, X3Y2, X2Y2, X1Y2, X0Y2}),
    .XY1({X7Y1, X6Y1, X5Y1, X4Y1, X3Y1, X2Y1, X1Y1, X0Y1}),
    .XY0({X7Y0, X6Y0, X5Y0, X4Y0, X3Y0, X2Y0, X1Y0, L_ed793cec[0]}));

  // Other names for the same wires on the sheet: P[15:0] = L_ed793cec; P0 = L_ed793cec[0]; X0Y0 = L_ed793cec[0];
  //   XY0[7:0] = {X7Y0, X6Y0, X5Y0, X4Y0, X3Y0, X2Y0, X1Y0, L_ed793cec[0]}; P1 = L_ed793cec[1]; P2 = L_ed793cec[2];
  //   P3 = L_ed793cec[3]; P4 = L_ed793cec[4]; P5 = L_ed793cec[5]; P6 = L_ed793cec[6]; P7 = L_ed793cec[7];
  //   P8 = L_ed793cec[8]; P9 = L_ed793cec[9]; P10 = L_ed793cec[10]; P11 = L_ed793cec[11]; P12 = L_ed793cec[12];
  //   P13 = L_ed793cec[13]; P14 = L_ed793cec[14]; P15 = L_ed793cec[15];
  //   XY1[7:0] = {X7Y1, X6Y1, X5Y1, X4Y1, X3Y1, X2Y1, X1Y1, X0Y1};
  //   XY2[7:0] = {X7Y2, X6Y2, X5Y2, X4Y2, X3Y2, X2Y2, X1Y2, X0Y2};
  //   XY3[7:0] = {X7Y3, X6Y3, X5Y3, X4Y3, X3Y3, X2Y3, X1Y3, X0Y3};
  //   XY4[7:0] = {X7Y4, X6Y4, X5Y4, X4Y4, X3Y4, X2Y4, X1Y4, X0Y4};
  //   XY5[7:0] = {X7Y5, X6Y5, X5Y5, X4Y5, X3Y5, X2Y5, X1Y5, X0Y5};
  //   XY6[7:0] = {X7Y6, X6Y6, X5Y6, X4Y6, X3Y6, X2Y6, X1Y6, X0Y6};
  //   XY7[7:0] = {X7Y7, X6Y7, X5Y7, X4Y7, X3Y7, X2Y7, X1Y7, X0Y7}
endmodule

module ALU (
  input  [3:0] S,
  input  X,
  input  Y,
  output Result,
  output Result2,
  output UOF,
  output Overflow,
  output Equal
);

  wire Adder_32_bit_1_cout, Adder_32_bit_1_overflow, AND2_out, AND3_out, AND_4_INPUTS_1_out,
       AND_4_INPUTS_2_out, comparator_2_gt, OR1_out;
  wire [0:0] comparator_1_lt, XOR1_out;
  wire [4:1] undriven;
  wire [31:0] Adder_32_bit_1_s, AND_32_BIT_out, Divider_output_bus_1, Divider_output_bus_2,
       multiplexer_2_out, mutiplier_output_bus_1, mutiplier_output_bus_2, not_1_out, not_2_out,
       OR_32_BIT_out, shifter_1_out, shifter_2_out, shifter_3_out, XOR_32_BIT_out;
  wire [31:1] multiplexer_1_out, multiplexer_3_out, undriven_3;
  wire [31:5] undriven_2;

  Shifter #(.width(32)) shifter_1 (.in({undriven_3, X}), .\dist ({undriven, Y}), .out(shifter_1_out));
  Shifter #(.width(32), .shift("ar")) shifter_2 (.in({undriven_3, X}), .\dist ({undriven, Y}), .out(shifter_2_out));
  Shifter #(.width(32), .shift("lr")) shifter_3 (.in({undriven_3, X}), .\dist ({undriven, Y}), .out(shifter_3_out));
  empty mutiplier (
    .Output_bus_2(mutiplier_output_bus_2), .Output_bus_1(mutiplier_output_bus_1),
    .Input_bus_2({undriven_2, undriven, Y}), .Input_bus_1({undriven_3, X}));
  empty Divider (
    .Output_bus_2(Divider_output_bus_2), .Output_bus_1(Divider_output_bus_1),
    .Input_bus_2({undriven_2, undriven, Y}), .Input_bus_1({undriven_3, X}));
  assign AND_32_BIT_out = {undriven_3, X} & {undriven_2, undriven, Y};  // AND_Gate AND_32_BIT, 32 bits wide
  assign OR_32_BIT_out = {undriven_3, X} | {undriven_2, undriven, Y};  // OR_Gate OR_32_BIT, 32 bits wide
  assign XOR_32_BIT_out = {undriven_3, X} ^ {undriven_2, undriven, Y};  // XOR_Gate XOR_32_BIT, 32 bits wide
  Comparator #(.width(32), .mode("unsigned")) comparator_1 (
    .a({undriven_3, X}), .b({undriven_2, undriven, Y}), .eq(Equal), .lt(comparator_1_lt[0]));  // open: gt
  Multiplexer #(.select(4), .width(32), .enable("false")) multiplexer_1 (
    .in0(shifter_1_out), .in1(shifter_2_out), .in2(shifter_3_out), .in3(mutiplier_output_bus_2),
    .in4(Divider_output_bus_2), .in5(Adder_32_bit_1_s), .in6(Adder_32_bit_1_s), .in7(AND_32_BIT_out),
    .in8(OR_32_BIT_out), .in9(XOR_32_BIT_out), .in10(not_1_out), .in11({{31{1'b0}}, XOR1_out[0]}),
    .in12({{31{1'b0}}, comparator_1_lt[0]}), .in13({32{1'b0}}), .in14({32{1'b0}}), .in15({32{1'b0}}),
    .out({multiplexer_1_out, Result}), .sel(S));
  assign not_1_out = ~OR_32_BIT_out;  // NOT_Gate not_1, 32 bits wide
  xor XOR1 (XOR1_out[0], XOR_32_BIT_out[31], comparator_1_lt[0]);
  Adder_32_bit Adder_32_bit_1 (
    .X({undriven_3, X}), .Y(multiplexer_2_out), .Cin(S[1]), .S(Adder_32_bit_1_s), .Cout(Adder_32_bit_1_cout),
    .Overflow(Adder_32_bit_1_overflow));
  Multiplexer #(.width(32), .enable("false")) multiplexer_2 (
    .in0({undriven_2, undriven, Y}), .in1(not_2_out), .out(multiplexer_2_out), .sel(S[1]));
  assign not_2_out = ~{undriven_2, undriven, Y};  // NOT_Gate not_2, 32 bits wide
  Multiplexer #(.select(4), .width(32), .enable("false")) multiplexer_3 (
    .in0({32{1'b0}}), .in1({32{1'b0}}), .in2({32{1'b0}}), .in3(mutiplier_output_bus_1),
    .in4(Divider_output_bus_1), .in5({32{1'b0}}), .in6({32{1'b0}}), .in7({32{1'b0}}), .in8({32{1'b0}}),
    .in9({32{1'b0}}), .in10({32{1'b0}}), .in11({32{1'b0}}), .in12({32{1'b0}}), .in13({32{1'b0}}),
    .in14({32{1'b0}}), .in15({32{1'b0}}), .out({multiplexer_3_out, Result2}), .sel(S));
  Comparator #(.width(32), .mode("unsigned")) comparator_2 (
    .a(Adder_32_bit_1_s), .b({undriven_3, X}), .gt(comparator_2_gt));  // open: eq, lt
  and AND1 (Overflow, Adder_32_bit_1_overflow, OR1_out);
  or OR2 (UOF, AND2_out, AND3_out);
  and AND2 (AND2_out, Adder_32_bit_1_cout, AND_4_INPUTS_1_out);
  and AND3 (AND3_out, comparator_2_gt, AND_4_INPUTS_2_out);
  or OR1 (OR1_out, AND_4_INPUTS_1_out, AND_4_INPUTS_2_out);
  and AND_4_INPUTS_1 (AND_4_INPUTS_1_out, S[0], ~S[1], S[2], ~S[3]);  // AND_Gate
  and AND_4_INPUTS_2 (AND_4_INPUTS_2_out, ~S[0], S[1], S[2], ~S[3]);  // AND_Gate
  // Pins of 1 and 32 bits meet at {undriven_2, undriven, Y}
  // Pins of 1 and 32 bits meet at {multiplexer_3_out, Result2}
  // Pins of 1 and 32 bits meet at {undriven_3, X}
  // Pins of 1 and 32 bits meet at {multiplexer_1_out, Result}
endmodule

module L_965effb8 (
  input  [31:0] X,
  input  [31:0] Y,
  input  [3:0] ALUOP,
  output Signed_Overflow_3b60ffbb,
  output Unsigned_overflow_34c64657,
  output [31:0] Result,
  output [31:0] Result_2_5283d6eb,
  output Equal
);

  // Probe on X
  // Probe on X
  // ALU alu_1: pin names not known; wires that end beside it: X, Y, Signed_Overflow_3b60ffbb, ALUOP, Unsigned_overflow_34c64657, Equal, Result, Result_2_5283d6eb
  // Probe on ALUOP
  // Probe on Y
  // Probe on Y
  // Probe on Result
  // Probe on Result
  // Probe on Result_2_5283d6eb

  // Notes on the sheet:
  //   ALu电路无需调整位置即可连接在该电路中，并且不能出现蓝色线缆和三态输出
endmodule

module L_04c43cf7 (
);

  wire l_fa_2_f89faf23_2_cout, l_fa_2_f89faf23_2_si, l_fa_2_f89faf23_3_si, l_fa_2_f89faf23_4_cout,
       l_fa_2_f89faf23_4_si, l_fa_2_f89faf23_5_si, l_fa_2_f89faf23_6_si, l_fa_2_f89faf23_7_si,
       l_fa_2_f89faf23_8_si, l_fa_2_f89faf23_10_si, l_fa_2_f89faf23_11_cout, l_fa_2_f89faf23_11_si,
       l_fa_2_f89faf23_12_si, l_fa_2_f89faf23_13_cout, l_fa_2_f89faf23_13_si, l_fa_2_f89faf23_14_si,
       l_fa_2_f89faf23_15_si, l_fa_2_f89faf23_17_si, l_fa_2_f89faf23_18_cout, l_fa_2_f89faf23_18_si,
       l_fa_2_f89faf23_19_si, l_fa_2_f89faf23_20_cout, l_fa_2_f89faf23_20_si, l_fa_2_f89faf23_21_si,
       l_fa_2_f89faf23_22_si, l_fa_2_f89faf23_23_si, l_fa_2_f89faf23_24_si, l_fa_2_f89faf23_26_si,
       l_fa_2_f89faf23_27_cout, l_fa_2_f89faf23_27_si, l_fa_2_f89faf23_28_si, l_fa_2_f89faf23_29_cout,
       l_fa_2_f89faf23_29_si, l_fa_2_f89faf23_30_si, l_fa_2_f89faf23_31_si, l_fa_2_f89faf23_32_si,
       l_fa_2_f89faf23_34_cout, l_fa_2_f89faf23_34_si, l_fa_2_f89faf23_35_si, l_fa_2_f89faf23_36_cout,
       l_fa_2_f89faf23_36_si, l_fa_2_f89faf23_37_si, l_fa_2_f89faf23_38_si, l_fa_2_f89faf23_39_si,
       l_fa_2_f89faf23_40_si, l_fa_2_f89faf23_42_si, l_fa_2_f89faf23_43_cout, l_fa_2_f89faf23_43_si,
       l_fa_2_f89faf23_44_si, l_fa_2_f89faf23_45_si, l_fa_2_f89faf23_46_cout, l_fa_2_f89faf23_46_si,
       l_fa_2_f89faf23_47_si, l_fa_2_f89faf23_49_si, l_fa_2_f89faf23_50_cout, l_fa_2_f89faf23_50_si,
       l_fa_2_f89faf23_51_si, l_fa_2_f89faf23_52_cout, l_fa_2_f89faf23_52_si, l_fa_2_f89faf23_53_si,
       l_fa_2_f89faf23_54_si, l_fa_2_f89faf23_55_si, l_fa_2_f89faf23_56_si, l_fa_2_f89faf23_58_si,
       l_fa_2_f89faf23_59_cout, l_fa_2_f89faf23_59_si, l_fa_2_f89faf23_60_si, l_fa_2_f89faf23_61_cout,
       l_fa_2_f89faf23_61_si, l_fa_2_f89faf23_62_si, l_fa_2_f89faf23_63_si, l_fa_2_f89faf23_64_si,
       l_fa_2_f89faf23_66_cout, l_fa_2_f89faf23_66_si, l_fa_2_f89faf23_67_si, l_fa_2_f89faf23_68_cout,
       l_fa_2_f89faf23_68_si, l_fa_2_f89faf23_69_si, l_fa_2_f89faf23_70_si, l_fa_2_f89faf23_71_si,
       l_fa_2_f89faf23_72_si, l_fa_2_f89faf23_74_si, l_fa_2_f89faf23_75_cout, l_fa_2_f89faf23_75_si,
       l_fa_2_f89faf23_76_si, l_fa_2_f89faf23_77_si, l_fa_2_f89faf23_78_cout, l_fa_2_f89faf23_78_si,
       l_fa_2_f89faf23_79_si, l_fa_2_f89faf23_81_si, l_fa_2_f89faf23_82_cout, l_fa_2_f89faf23_82_si,
       l_fa_2_f89faf23_83_si, l_fa_2_f89faf23_84_cout, l_fa_2_f89faf23_84_si, l_fa_2_f89faf23_85_si,
       l_fa_2_f89faf23_86_si, l_fa_2_f89faf23_87_si, l_fa_2_f89faf23_88_si, l_fa_2_f89faf23_90_si,
       l_fa_2_f89faf23_91_cout, l_fa_2_f89faf23_91_si, l_fa_2_f89faf23_92_si, l_fa_2_f89faf23_93_cout,
       l_fa_2_f89faf23_93_si, l_fa_2_f89faf23_94_si, l_fa_2_f89faf23_95_si, l_fa_2_f89faf23_96_si,
       l_fa_2_f89faf23_98_cout, l_fa_2_f89faf23_98_si, l_fa_2_f89faf23_99_si, l_fa_2_f89faf23_100_cout,
       l_fa_2_f89faf23_100_si, l_fa_2_f89faf23_101_si, l_fa_2_f89faf23_102_si, l_fa_2_f89faf23_103_si,
       l_fa_2_f89faf23_104_si, l_fa_2_f89faf23_106_si, l_fa_2_f89faf23_107_cout, l_fa_2_f89faf23_107_si,
       l_fa_2_f89faf23_108_si, l_fa_2_f89faf23_109_si, l_fa_2_f89faf23_110_cout, l_fa_2_f89faf23_110_si,
       l_fa_2_f89faf23_111_si, l_fa_2_f89faf23_113_si, l_fa_2_f89faf23_114_cout, l_fa_2_f89faf23_114_si,
       l_fa_2_f89faf23_115_si, l_fa_2_f89faf23_116_cout, l_fa_2_f89faf23_116_si, l_fa_2_f89faf23_117_si,
       l_fa_2_f89faf23_118_si, l_fa_2_f89faf23_119_si, l_fa_2_f89faf23_120_si, l_fa_2_f89faf23_122_si,
       l_fa_2_f89faf23_123_cout, l_fa_2_f89faf23_123_si, l_fa_2_f89faf23_124_si, l_fa_2_f89faf23_125_cout,
       l_fa_2_f89faf23_125_si, l_fa_2_f89faf23_126_si, l_fa_2_f89faf23_127_si, l_fa_2_f89faf23_128_si,
       undriven, undriven_2, undriven_3, undriven_4, undriven_5, undriven_6, undriven_7, undriven_8,
       undriven_9, undriven_10, undriven_11, undriven_12, undriven_13, undriven_14, undriven_15, undriven_16,
       undriven_17, undriven_18, undriven_19, undriven_20, undriven_21, undriven_22, undriven_23,
       undriven_24, undriven_25, undriven_26, undriven_27, undriven_28, undriven_29, undriven_30,
       undriven_31, undriven_32, undriven_33, undriven_34, undriven_35, undriven_36, undriven_37,
       undriven_38, undriven_39, undriven_40, undriven_41, undriven_42, undriven_43, undriven_44,
       undriven_45, undriven_46, undriven_47, undriven_48, undriven_49, undriven_50, undriven_51,
       undriven_52, undriven_53, undriven_54, undriven_55, undriven_56, undriven_57, undriven_58,
       undriven_59, undriven_60, undriven_61, undriven_62, undriven_63, undriven_64, undriven_65,
       undriven_66, undriven_67, undriven_68, undriven_69, undriven_70, undriven_71, undriven_72,
       undriven_73, undriven_74, undriven_75, undriven_76, undriven_77, undriven_78, undriven_79,
       undriven_80, undriven_81, undriven_82, undriven_83, undriven_84, undriven_85, undriven_86,
       undriven_87, undriven_88, undriven_89, undriven_90, undriven_91, undriven_92, undriven_93,
       undriven_94, undriven_95, undriven_96, undriven_97, undriven_98, undriven_99, undriven_100,
       undriven_101, undriven_102, undriven_103, undriven_104, undriven_105, undriven_106, undriven_107,
       undriven_108, undriven_109, undriven_110, undriven_111, undriven_112, undriven_113, undriven_114,
       undriven_115, undriven_116, undriven_117, undriven_118, undriven_119, undriven_120, undriven_121,
       undriven_122, undriven_123, undriven_124, undriven_125, undriven_126, undriven_127, undriven_128,
       undriven_130;
  wire [1:0] l_fa_2_f89faf23_5_cout, l_fa_2_f89faf23_12_cout, l_fa_2_f89faf23_19_cout,
       l_fa_2_f89faf23_26_cout, l_fa_2_f89faf23_37_cout, l_fa_2_f89faf23_44_cout, l_fa_2_f89faf23_51_cout,
       l_fa_2_f89faf23_58_cout, l_fa_2_f89faf23_69_cout, l_fa_2_f89faf23_76_cout, l_fa_2_f89faf23_83_cout,
       l_fa_2_f89faf23_90_cout, l_fa_2_f89faf23_101_cout, l_fa_2_f89faf23_108_cout, l_fa_2_f89faf23_115_cout,
       l_fa_2_f89faf23_122_cout, undriven_131;
  wire [2:0] l_fa_2_f89faf23_7_cout, l_fa_2_f89faf23_17_cout, l_fa_2_f89faf23_24_cout,
       l_fa_2_f89faf23_31_cout, l_fa_2_f89faf23_40_cout, l_fa_2_f89faf23_49_cout, l_fa_2_f89faf23_56_cout,
       l_fa_2_f89faf23_64_cout, l_fa_2_f89faf23_71_cout, l_fa_2_f89faf23_81_cout, l_fa_2_f89faf23_88_cout,
       l_fa_2_f89faf23_95_cout, l_fa_2_f89faf23_103_cout, l_fa_2_f89faf23_113_cout, l_fa_2_f89faf23_120_cout,
       l_fa_2_f89faf23_128_cout, undriven_129;

  shape shape_1 ();
  L_FA_2_f89faf23 l_fa_2_f89faf23_1 ();  // open: Cout, Si, Cin, Xi, Yi
  L_FA_2_f89faf23 l_fa_2_f89faf23_2 (
    .Cout(l_fa_2_f89faf23_2_cout), .Si(l_fa_2_f89faf23_2_si), .Cin(l_fa_2_f89faf23_7_si),
    .Xi(l_fa_2_f89faf23_3_si), .Yi(l_fa_2_f89faf23_8_si));
  L_FA_2_f89faf23 l_fa_2_f89faf23_3 (
    .Cout(l_fa_2_f89faf23_7_cout[2]), .Si(l_fa_2_f89faf23_3_si), .Cin(undriven_3), .Xi(undriven),
    .Yi(undriven_2));
  L_FA_2_f89faf23 l_fa_2_f89faf23_4 (
    .Cout(l_fa_2_f89faf23_4_cout), .Si(l_fa_2_f89faf23_4_si), .Cin(l_fa_2_f89faf23_12_cout[0]),
    .Xi(l_fa_2_f89faf23_5_si), .Yi(l_fa_2_f89faf23_12_cout[1]));
  L_FA_2_f89faf23 l_fa_2_f89faf23_5 (
    .Cout(l_fa_2_f89faf23_5_cout[0]), .Si(l_fa_2_f89faf23_5_si), .Cin(l_fa_2_f89faf23_13_cout),
    .Xi(l_fa_2_f89faf23_2_si), .Yi(l_fa_2_f89faf23_6_si));
  L_FA_2_f89faf23 l_fa_2_f89faf23_6 (
    .Cout(l_fa_2_f89faf23_5_cout[1]), .Si(l_fa_2_f89faf23_6_si), .Cin(l_fa_2_f89faf23_17_cout[0]),
    .Xi(l_fa_2_f89faf23_17_cout[2]), .Yi(l_fa_2_f89faf23_17_cout[1]));
  L_FA_2_f89faf23 l_fa_2_f89faf23_7 (
    .Cout(l_fa_2_f89faf23_7_cout[0]), .Si(l_fa_2_f89faf23_7_si), .Cin(1'b0), .Xi(undriven_7), .Yi(undriven_8));
  L_FA_2_f89faf23 l_fa_2_f89faf23_8 (
    .Cout(l_fa_2_f89faf23_7_cout[1]), .Si(l_fa_2_f89faf23_8_si), .Cin(undriven_6), .Xi(undriven_4),
    .Yi(undriven_5));
  L_FA_2_f89faf23 l_fa_2_f89faf23_9 ();  // open: Cout, Si, Cin, Xi, Yi
  L_FA_2_f89faf23 l_fa_2_f89faf23_10 (
    .Cout(l_fa_2_f89faf23_17_cout[2]), .Si(l_fa_2_f89faf23_10_si), .Cin(undriven_11), .Xi(undriven_9),
    .Yi(undriven_10));
  L_FA_2_f89faf23 l_fa_2_f89faf23_11 (
    .Cout(l_fa_2_f89faf23_11_cout), .Si(l_fa_2_f89faf23_11_si), .Cin(l_fa_2_f89faf23_19_cout[0]),
    .Xi(l_fa_2_f89faf23_12_si), .Yi(l_fa_2_f89faf23_19_cout[1]));
  L_FA_2_f89faf23 l_fa_2_f89faf23_12 (
    .Cout(l_fa_2_f89faf23_12_cout[0]), .Si(l_fa_2_f89faf23_12_si), .Cin(l_fa_2_f89faf23_20_cout),
    .Xi(l_fa_2_f89faf23_13_si), .Yi(l_fa_2_f89faf23_14_si));
  L_FA_2_f89faf23 l_fa_2_f89faf23_13 (
    .Cout(l_fa_2_f89faf23_13_cout), .Si(l_fa_2_f89faf23_13_si), .Cin(l_fa_2_f89faf23_17_si),
    .Xi(l_fa_2_f89faf23_10_si), .Yi(l_fa_2_f89faf23_15_si));
  L_FA_2_f89faf23 l_fa_2_f89faf23_14 (
    .Cout(l_fa_2_f89faf23_12_cout[1]), .Si(l_fa_2_f89faf23_14_si), .Cin(l_fa_2_f89faf23_24_cout[0]),
    .Xi(l_fa_2_f89faf23_24_cout[2]), .Yi(l_fa_2_f89faf23_24_cout[1]));
  L_FA_2_f89faf23 l_fa_2_f89faf23_15 (
    .Cout(l_fa_2_f89faf23_17_cout[1]), .Si(l_fa_2_f89faf23_15_si), .Cin(undriven_14), .Xi(undriven_12),
    .Yi(undriven_13));
  L_FA_2_f89faf23 l_fa_2_f89faf23_16 ();  // open: Cout, Si, Cin, Xi, Yi
  shape shape_2 ();
  L_FA_2_f89faf23 l_fa_2_f89faf23_17 (
    .Cout(l_fa_2_f89faf23_17_cout[0]), .Si(l_fa_2_f89faf23_17_si), .Cin(1'b0), .Xi(undriven_15),
    .Yi(undriven_16));
  L_FA_2_f89faf23 l_fa_2_f89faf23_18 (
    .Cout(l_fa_2_f89faf23_18_cout), .Si(l_fa_2_f89faf23_18_si), .Cin(l_fa_2_f89faf23_26_cout[0]),
    .Xi(l_fa_2_f89faf23_19_si), .Yi(l_fa_2_f89faf23_26_cout[1]));
  L_FA_2_f89faf23 l_fa_2_f89faf23_19 (
    .Cout(l_fa_2_f89faf23_19_cout[0]), .Si(l_fa_2_f89faf23_19_si), .Cin(l_fa_2_f89faf23_27_cout),
    .Xi(l_fa_2_f89faf23_20_si), .Yi(l_fa_2_f89faf23_23_si));
  L_FA_2_f89faf23 l_fa_2_f89faf23_20 (
    .Cout(l_fa_2_f89faf23_20_cout), .Si(l_fa_2_f89faf23_20_si), .Cin(l_fa_2_f89faf23_24_si),
    .Xi(l_fa_2_f89faf23_21_si), .Yi(l_fa_2_f89faf23_22_si));
  L_FA_2_f89faf23 l_fa_2_f89faf23_21 (
    .Cout(l_fa_2_f89faf23_24_cout[2]), .Si(l_fa_2_f89faf23_21_si), .Cin(undriven_19), .Xi(undriven_17),
    .Yi(undriven_18));
  L_FA_2_f89faf23 l_fa_2_f89faf23_22 (
    .Cout(l_fa_2_f89faf23_24_cout[1]), .Si(l_fa_2_f89faf23_22_si), .Cin(undriven_22), .Xi(undriven_20),
    .Yi(undriven_21));
  L_FA_2_f89faf23 l_fa_2_f89faf23_23 (
    .Cout(l_fa_2_f89faf23_19_cout[1]), .Si(l_fa_2_f89faf23_23_si), .Cin(l_fa_2_f89faf23_31_cout[0]),
    .Xi(l_fa_2_f89faf23_31_cout[2]), .Yi(l_fa_2_f89faf23_31_cout[1]));
  L_FA_2_f89faf23 l_fa_2_f89faf23_24 (
    .Cout(l_fa_2_f89faf23_24_cout[0]), .Si(l_fa_2_f89faf23_24_si), .Cin(1'b0), .Xi(undriven_23),
    .Yi(undriven_24));
  L_FA_2_f89faf23 l_fa_2_f89faf23_25 ();  // open: Cout, Si, Cin, Xi, Yi
  L_FA_2_f89faf23 l_fa_2_f89faf23_26 (
    .Cout(l_fa_2_f89faf23_26_cout[0]), .Si(l_fa_2_f89faf23_26_si), .Cin(l_fa_2_f89faf23_34_cout),
    .Xi(l_fa_2_f89faf23_27_si), .Yi(l_fa_2_f89faf23_30_si));
  L_FA_2_f89faf23 l_fa_2_f89faf23_27 (
    .Cout(l_fa_2_f89faf23_27_cout), .Si(l_fa_2_f89faf23_27_si), .Cin(l_fa_2_f89faf23_31_si),
    .Xi(l_fa_2_f89faf23_28_si), .Yi(l_fa_2_f89faf23_32_si));
  L_FA_2_f89faf23 l_fa_2_f89faf23_28 (
    .Cout(l_fa_2_f89faf23_31_cout[2]), .Si(l_fa_2_f89faf23_28_si), .Cin(undriven_27), .Xi(undriven_25),
    .Yi(undriven_26));
  shape shape_3 ();
  L_FA_2_f89faf23 l_fa_2_f89faf23_29 (
    .Cout(l_fa_2_f89faf23_29_cout), .Si(l_fa_2_f89faf23_29_si), .Cin(l_fa_2_f89faf23_37_cout[0]),
    .Xi(l_fa_2_f89faf23_26_si), .Yi(l_fa_2_f89faf23_37_cout[1]));
  L_FA_2_f89faf23 l_fa_2_f89faf23_30 (
    .Cout(l_fa_2_f89faf23_26_cout[1]), .Si(l_fa_2_f89faf23_30_si), .Cin(l_fa_2_f89faf23_40_cout[0]),
    .Xi(l_fa_2_f89faf23_40_cout[2]), .Yi(l_fa_2_f89faf23_40_cout[1]));
  L_FA_2_f89faf23 l_fa_2_f89faf23_31 (
    .Cout(l_fa_2_f89faf23_31_cout[0]), .Si(l_fa_2_f89faf23_31_si), .Cin(1'b0), .Xi(undriven_31),
    .Yi(undriven_32));
  L_FA_2_f89faf23 l_fa_2_f89faf23_32 (
    .Cout(l_fa_2_f89faf23_31_cout[1]), .Si(l_fa_2_f89faf23_32_si), .Cin(undriven_30), .Xi(undriven_28),
    .Yi(undriven_29));
  L_FA_2_f89faf23 l_fa_2_f89faf23_33 ();  // open: Cout, Si, Cin, Xi, Yi
  L_FA_2_f89faf23 l_fa_2_f89faf23_34 (
    .Cout(l_fa_2_f89faf23_34_cout), .Si(l_fa_2_f89faf23_34_si), .Cin(l_fa_2_f89faf23_40_si),
    .Xi(l_fa_2_f89faf23_35_si), .Yi(l_fa_2_f89faf23_39_si));
  L_FA_2_f89faf23 l_fa_2_f89faf23_35 (
    .Cout(l_fa_2_f89faf23_40_cout[2]), .Si(l_fa_2_f89faf23_35_si), .Cin(undriven_35), .Xi(undriven_33),
    .Yi(undriven_34));
  L_FA_2_f89faf23 l_fa_2_f89faf23_36 (
    .Cout(l_fa_2_f89faf23_36_cout), .Si(l_fa_2_f89faf23_36_si), .Cin(l_fa_2_f89faf23_44_cout[0]),
    .Xi(l_fa_2_f89faf23_37_si), .Yi(l_fa_2_f89faf23_44_cout[1]));
  L_FA_2_f89faf23 l_fa_2_f89faf23_37 (
    .Cout(l_fa_2_f89faf23_37_cout[0]), .Si(l_fa_2_f89faf23_37_si), .Cin(l_fa_2_f89faf23_46_cout),
    .Xi(l_fa_2_f89faf23_34_si), .Yi(l_fa_2_f89faf23_38_si));
  L_FA_2_f89faf23 l_fa_2_f89faf23_38 (
    .Cout(l_fa_2_f89faf23_37_cout[1]), .Si(l_fa_2_f89faf23_38_si), .Cin(l_fa_2_f89faf23_49_cout[0]),
    .Xi(l_fa_2_f89faf23_49_cout[2]), .Yi(l_fa_2_f89faf23_49_cout[1]));
  L_FA_2_f89faf23 l_fa_2_f89faf23_39 (
    .Cout(l_fa_2_f89faf23_40_cout[1]), .Si(l_fa_2_f89faf23_39_si), .Cin(undriven_38), .Xi(undriven_36),
    .Yi(undriven_37));
  L_FA_2_f89faf23 l_fa_2_f89faf23_40 (
    .Cout(l_fa_2_f89faf23_40_cout[0]), .Si(l_fa_2_f89faf23_40_si), .Cin(1'b0), .Xi(undriven_39),
    .Yi(undriven_40));
  L_FA_2_f89faf23 l_fa_2_f89faf23_41 ();  // open: Cout, Si, Cin, Xi, Yi
  L_FA_2_f89faf23 l_fa_2_f89faf23_42 (
    .Cout(l_fa_2_f89faf23_49_cout[2]), .Si(l_fa_2_f89faf23_42_si), .Cin(undriven_43), .Xi(undriven_41),
    .Yi(undriven_42));
  L_FA_2_f89faf23 l_fa_2_f89faf23_43 (
    .Cout(l_fa_2_f89faf23_43_cout), .Si(l_fa_2_f89faf23_43_si), .Cin(l_fa_2_f89faf23_51_cout[0]),
    .Xi(l_fa_2_f89faf23_44_si), .Yi(l_fa_2_f89faf23_51_cout[1]));
  L_FA_2_f89faf23 l_fa_2_f89faf23_44 (
    .Cout(l_fa_2_f89faf23_44_cout[0]), .Si(l_fa_2_f89faf23_44_si), .Cin(l_fa_2_f89faf23_52_cout),
    .Xi(l_fa_2_f89faf23_46_si), .Yi(l_fa_2_f89faf23_45_si));
  L_FA_2_f89faf23 l_fa_2_f89faf23_45 (
    .Cout(l_fa_2_f89faf23_44_cout[1]), .Si(l_fa_2_f89faf23_45_si), .Cin(l_fa_2_f89faf23_56_cout[0]),
    .Xi(l_fa_2_f89faf23_56_cout[2]), .Yi(l_fa_2_f89faf23_56_cout[1]));
  L_FA_2_f89faf23 l_fa_2_f89faf23_46 (
    .Cout(l_fa_2_f89faf23_46_cout), .Si(l_fa_2_f89faf23_46_si), .Cin(l_fa_2_f89faf23_49_si),
    .Xi(l_fa_2_f89faf23_42_si), .Yi(l_fa_2_f89faf23_47_si));
  L_FA_2_f89faf23 l_fa_2_f89faf23_47 (
    .Cout(l_fa_2_f89faf23_49_cout[1]), .Si(l_fa_2_f89faf23_47_si), .Cin(undriven_46), .Xi(undriven_44),
    .Yi(undriven_45));
  L_FA_2_f89faf23 l_fa_2_f89faf23_48 ();  // open: Cout, Si, Cin, Xi, Yi
  shape shape_4 ();
  L_FA_2_f89faf23 l_fa_2_f89faf23_49 (
    .Cout(l_fa_2_f89faf23_49_cout[0]), .Si(l_fa_2_f89faf23_49_si), .Cin(1'b0), .Xi(undriven_47),
    .Yi(undriven_48));
  L_FA_2_f89faf23 l_fa_2_f89faf23_50 (
    .Cout(l_fa_2_f89faf23_50_cout), .Si(l_fa_2_f89faf23_50_si), .Cin(l_fa_2_f89faf23_58_cout[0]),
    .Xi(l_fa_2_f89faf23_51_si), .Yi(l_fa_2_f89faf23_58_cout[1]));
  L_FA_2_f89faf23 l_fa_2_f89faf23_51 (
    .Cout(l_fa_2_f89faf23_51_cout[0]), .Si(l_fa_2_f89faf23_51_si), .Cin(l_fa_2_f89faf23_59_cout),
    .Xi(l_fa_2_f89faf23_52_si), .Yi(l_fa_2_f89faf23_55_si));
  L_FA_2_f89faf23 l_fa_2_f89faf23_52 (
    .Cout(l_fa_2_f89faf23_52_cout), .Si(l_fa_2_f89faf23_52_si), .Cin(l_fa_2_f89faf23_56_si),
    .Xi(l_fa_2_f89faf23_54_si), .Yi(l_fa_2_f89faf23_53_si));
  L_FA_2_f89faf23 l_fa_2_f89faf23_53 (
    .Cout(l_fa_2_f89faf23_56_cout[1]), .Si(l_fa_2_f89faf23_53_si), .Cin(undriven_54), .Xi(undriven_52),
    .Yi(undriven_53));
  L_FA_2_f89faf23 l_fa_2_f89faf23_54 (
    .Cout(l_fa_2_f89faf23_56_cout[2]), .Si(l_fa_2_f89faf23_54_si), .Cin(undriven_51), .Xi(undriven_49),
    .Yi(undriven_50));
  L_FA_2_f89faf23 l_fa_2_f89faf23_55 (
    .Cout(l_fa_2_f89faf23_51_cout[1]), .Si(l_fa_2_f89faf23_55_si), .Cin(l_fa_2_f89faf23_64_cout[0]),
    .Xi(l_fa_2_f89faf23_64_cout[2]), .Yi(l_fa_2_f89faf23_64_cout[1]));
  L_FA_2_f89faf23 l_fa_2_f89faf23_56 (
    .Cout(l_fa_2_f89faf23_56_cout[0]), .Si(l_fa_2_f89faf23_56_si), .Cin(1'b0), .Xi(undriven_55),
    .Yi(undriven_56));
  L_FA_2_f89faf23 l_fa_2_f89faf23_57 ();  // open: Cout, Si, Cin, Xi, Yi
  L_FA_2_f89faf23 l_fa_2_f89faf23_58 (
    .Cout(l_fa_2_f89faf23_58_cout[0]), .Si(l_fa_2_f89faf23_58_si), .Cin(l_fa_2_f89faf23_66_cout),
    .Xi(l_fa_2_f89faf23_59_si), .Yi(l_fa_2_f89faf23_62_si));
  L_FA_2_f89faf23 l_fa_2_f89faf23_59 (
    .Cout(l_fa_2_f89faf23_59_cout), .Si(l_fa_2_f89faf23_59_si), .Cin(l_fa_2_f89faf23_64_si),
    .Xi(l_fa_2_f89faf23_60_si), .Yi(l_fa_2_f89faf23_63_si));
  L_FA_2_f89faf23 l_fa_2_f89faf23_60 (
    .Cout(l_fa_2_f89faf23_64_cout[2]), .Si(l_fa_2_f89faf23_60_si), .Cin(undriven_59), .Xi(undriven_57),
    .Yi(undriven_58));
  shape shape_5 ();
  L_FA_2_f89faf23 l_fa_2_f89faf23_61 (
    .Cout(l_fa_2_f89faf23_61_cout), .Si(l_fa_2_f89faf23_61_si), .Cin(l_fa_2_f89faf23_69_cout[0]),
    .Xi(l_fa_2_f89faf23_58_si), .Yi(l_fa_2_f89faf23_69_cout[1]));
  L_FA_2_f89faf23 l_fa_2_f89faf23_62 (
    .Cout(l_fa_2_f89faf23_58_cout[1]), .Si(l_fa_2_f89faf23_62_si), .Cin(l_fa_2_f89faf23_71_cout[0]),
    .Xi(l_fa_2_f89faf23_71_cout[2]), .Yi(l_fa_2_f89faf23_71_cout[1]));
  L_FA_2_f89faf23 l_fa_2_f89faf23_63 (
    .Cout(l_fa_2_f89faf23_64_cout[1]), .Si(l_fa_2_f89faf23_63_si), .Cin(undriven_62), .Xi(undriven_60),
    .Yi(undriven_61));
  L_FA_2_f89faf23 l_fa_2_f89faf23_64 (
    .Cout(l_fa_2_f89faf23_64_cout[0]), .Si(l_fa_2_f89faf23_64_si), .Cin(1'b0), .Xi(undriven_63),
    .Yi(undriven_64));
  L_FA_2_f89faf23 l_fa_2_f89faf23_65 ();  // open: Cout, Si, Cin, Xi, Yi
  L_FA_2_f89faf23 l_fa_2_f89faf23_66 (
    .Cout(l_fa_2_f89faf23_66_cout), .Si(l_fa_2_f89faf23_66_si), .Cin(l_fa_2_f89faf23_71_si),
    .Xi(l_fa_2_f89faf23_67_si), .Yi(l_fa_2_f89faf23_72_si));
  L_FA_2_f89faf23 l_fa_2_f89faf23_67 (
    .Cout(l_fa_2_f89faf23_71_cout[2]), .Si(l_fa_2_f89faf23_67_si), .Cin(undriven_67), .Xi(undriven_65),
    .Yi(undriven_66));
  L_FA_2_f89faf23 l_fa_2_f89faf23_68 (
    .Cout(l_fa_2_f89faf23_68_cout), .Si(l_fa_2_f89faf23_68_si), .Cin(l_fa_2_f89faf23_76_cout[0]),
    .Xi(l_fa_2_f89faf23_69_si), .Yi(l_fa_2_f89faf23_76_cout[1]));
  L_FA_2_f89faf23 l_fa_2_f89faf23_69 (
    .Cout(l_fa_2_f89faf23_69_cout[0]), .Si(l_fa_2_f89faf23_69_si), .Cin(l_fa_2_f89faf23_78_cout),
    .Xi(l_fa_2_f89faf23_66_si), .Yi(l_fa_2_f89faf23_70_si));
  L_FA_2_f89faf23 l_fa_2_f89faf23_70 (
    .Cout(l_fa_2_f89faf23_69_cout[1]), .Si(l_fa_2_f89faf23_70_si), .Cin(l_fa_2_f89faf23_81_cout[0]),
    .Xi(l_fa_2_f89faf23_81_cout[2]), .Yi(l_fa_2_f89faf23_81_cout[1]));
  L_FA_2_f89faf23 l_fa_2_f89faf23_71 (
    .Cout(l_fa_2_f89faf23_71_cout[0]), .Si(l_fa_2_f89faf23_71_si), .Cin(1'b0), .Xi(undriven_71),
    .Yi(undriven_72));
  L_FA_2_f89faf23 l_fa_2_f89faf23_72 (
    .Cout(l_fa_2_f89faf23_71_cout[1]), .Si(l_fa_2_f89faf23_72_si), .Cin(undriven_70), .Xi(undriven_68),
    .Yi(undriven_69));
  L_FA_2_f89faf23 l_fa_2_f89faf23_73 ();  // open: Cout, Si, Cin, Xi, Yi
  L_FA_2_f89faf23 l_fa_2_f89faf23_74 (
    .Cout(l_fa_2_f89faf23_81_cout[2]), .Si(l_fa_2_f89faf23_74_si), .Cin(undriven_75), .Xi(undriven_73),
    .Yi(undriven_74));
  L_FA_2_f89faf23 l_fa_2_f89faf23_75 (
    .Cout(l_fa_2_f89faf23_75_cout), .Si(l_fa_2_f89faf23_75_si), .Cin(l_fa_2_f89faf23_83_cout[0]),
    .Xi(l_fa_2_f89faf23_76_si), .Yi(l_fa_2_f89faf23_83_cout[1]));
  L_FA_2_f89faf23 l_fa_2_f89faf23_76 (
    .Cout(l_fa_2_f89faf23_76_cout[0]), .Si(l_fa_2_f89faf23_76_si), .Cin(l_fa_2_f89faf23_84_cout),
    .Xi(l_fa_2_f89faf23_78_si), .Yi(l_fa_2_f89faf23_77_si));
  L_FA_2_f89faf23 l_fa_2_f89faf23_77 (
    .Cout(l_fa_2_f89faf23_76_cout[1]), .Si(l_fa_2_f89faf23_77_si), .Cin(l_fa_2_f89faf23_88_cout[0]),
    .Xi(l_fa_2_f89faf23_88_cout[2]), .Yi(l_fa_2_f89faf23_88_cout[1]));
  L_FA_2_f89faf23 l_fa_2_f89faf23_78 (
    .Cout(l_fa_2_f89faf23_78_cout), .Si(l_fa_2_f89faf23_78_si), .Cin(l_fa_2_f89faf23_81_si),
    .Xi(l_fa_2_f89faf23_74_si), .Yi(l_fa_2_f89faf23_79_si));
  L_FA_2_f89faf23 l_fa_2_f89faf23_79 (
    .Cout(l_fa_2_f89faf23_81_cout[1]), .Si(l_fa_2_f89faf23_79_si), .Cin(undriven_78), .Xi(undriven_76),
    .Yi(undriven_77));
  L_FA_2_f89faf23 l_fa_2_f89faf23_80 ();  // open: Cout, Si, Cin, Xi, Yi
  shape shape_6 ();
  L_FA_2_f89faf23 l_fa_2_f89faf23_81 (
    .Cout(l_fa_2_f89faf23_81_cout[0]), .Si(l_fa_2_f89faf23_81_si), .Cin(1'b0), .Xi(undriven_79),
    .Yi(undriven_80));
  L_FA_2_f89faf23 l_fa_2_f89faf23_82 (
    .Cout(l_fa_2_f89faf23_82_cout), .Si(l_fa_2_f89faf23_82_si), .Cin(l_fa_2_f89faf23_90_cout[0]),
    .Xi(l_fa_2_f89faf23_83_si), .Yi(l_fa_2_f89faf23_90_cout[1]));
  L_FA_2_f89faf23 l_fa_2_f89faf23_83 (
    .Cout(l_fa_2_f89faf23_83_cout[0]), .Si(l_fa_2_f89faf23_83_si), .Cin(l_fa_2_f89faf23_91_cout),
    .Xi(l_fa_2_f89faf23_84_si), .Yi(l_fa_2_f89faf23_87_si));
  L_FA_2_f89faf23 l_fa_2_f89faf23_84 (
    .Cout(l_fa_2_f89faf23_84_cout), .Si(l_fa_2_f89faf23_84_si), .Cin(l_fa_2_f89faf23_88_si),
    .Xi(l_fa_2_f89faf23_86_si), .Yi(l_fa_2_f89faf23_85_si));
  L_FA_2_f89faf23 l_fa_2_f89faf23_85 (
    .Cout(l_fa_2_f89faf23_88_cout[1]), .Si(l_fa_2_f89faf23_85_si), .Cin(undriven_86), .Xi(undriven_84),
    .Yi(undriven_85));
  L_FA_2_f89faf23 l_fa_2_f89faf23_86 (
    .Cout(l_fa_2_f89faf23_88_cout[2]), .Si(l_fa_2_f89faf23_86_si), .Cin(undriven_83), .Xi(undriven_81),
    .Yi(undriven_82));
  L_FA_2_f89faf23 l_fa_2_f89faf23_87 (
    .Cout(l_fa_2_f89faf23_83_cout[1]), .Si(l_fa_2_f89faf23_87_si), .Cin(l_fa_2_f89faf23_95_cout[0]),
    .Xi(l_fa_2_f89faf23_95_cout[2]), .Yi(l_fa_2_f89faf23_95_cout[1]));
  L_FA_2_f89faf23 l_fa_2_f89faf23_88 (
    .Cout(l_fa_2_f89faf23_88_cout[0]), .Si(l_fa_2_f89faf23_88_si), .Cin(1'b0), .Xi(undriven_87),
    .Yi(undriven_88));
  L_FA_2_f89faf23 l_fa_2_f89faf23_89 ();  // open: Cout, Si, Cin, Xi, Yi
  L_FA_2_f89faf23 l_fa_2_f89faf23_90 (
    .Cout(l_fa_2_f89faf23_90_cout[0]), .Si(l_fa_2_f89faf23_90_si), .Cin(l_fa_2_f89faf23_98_cout),
    .Xi(l_fa_2_f89faf23_91_si), .Yi(l_fa_2_f89faf23_94_si));
  L_FA_2_f89faf23 l_fa_2_f89faf23_91 (
    .Cout(l_fa_2_f89faf23_91_cout), .Si(l_fa_2_f89faf23_91_si), .Cin(l_fa_2_f89faf23_95_si),
    .Xi(l_fa_2_f89faf23_92_si), .Yi(l_fa_2_f89faf23_96_si));
  L_FA_2_f89faf23 l_fa_2_f89faf23_92 (
    .Cout(l_fa_2_f89faf23_95_cout[2]), .Si(l_fa_2_f89faf23_92_si), .Cin(undriven_91), .Xi(undriven_89),
    .Yi(undriven_90));
  shape shape_7 ();
  L_FA_2_f89faf23 l_fa_2_f89faf23_93 (
    .Cout(l_fa_2_f89faf23_93_cout), .Si(l_fa_2_f89faf23_93_si), .Cin(l_fa_2_f89faf23_101_cout[0]),
    .Xi(l_fa_2_f89faf23_90_si), .Yi(l_fa_2_f89faf23_101_cout[1]));
  L_FA_2_f89faf23 l_fa_2_f89faf23_94 (
    .Cout(l_fa_2_f89faf23_90_cout[1]), .Si(l_fa_2_f89faf23_94_si), .Cin(l_fa_2_f89faf23_103_cout[0]),
    .Xi(l_fa_2_f89faf23_103_cout[2]), .Yi(l_fa_2_f89faf23_103_cout[1]));
  L_FA_2_f89faf23 l_fa_2_f89faf23_95 (
    .Cout(l_fa_2_f89faf23_95_cout[0]), .Si(l_fa_2_f89faf23_95_si), .Cin(1'b0), .Xi(undriven_95),
    .Yi(undriven_96));
  L_FA_2_f89faf23 l_fa_2_f89faf23_96 (
    .Cout(l_fa_2_f89faf23_95_cout[1]), .Si(l_fa_2_f89faf23_96_si), .Cin(undriven_94), .Xi(undriven_92),
    .Yi(undriven_93));
  L_FA_2_f89faf23 l_fa_2_f89faf23_97 ();  // open: Cout, Si, Cin, Xi, Yi
  L_FA_2_f89faf23 l_fa_2_f89faf23_98 (
    .Cout(l_fa_2_f89faf23_98_cout), .Si(l_fa_2_f89faf23_98_si), .Cin(l_fa_2_f89faf23_103_si),
    .Xi(l_fa_2_f89faf23_99_si), .Yi(l_fa_2_f89faf23_104_si));
  L_FA_2_f89faf23 l_fa_2_f89faf23_99 (
    .Cout(l_fa_2_f89faf23_103_cout[2]), .Si(l_fa_2_f89faf23_99_si), .Cin(undriven_99), .Xi(undriven_97),
    .Yi(undriven_98));
  L_FA_2_f89faf23 l_fa_2_f89faf23_100 (
    .Cout(l_fa_2_f89faf23_100_cout), .Si(l_fa_2_f89faf23_100_si), .Cin(l_fa_2_f89faf23_108_cout[0]),
    .Xi(l_fa_2_f89faf23_101_si), .Yi(l_fa_2_f89faf23_108_cout[1]));
  L_FA_2_f89faf23 l_fa_2_f89faf23_101 (
    .Cout(l_fa_2_f89faf23_101_cout[0]), .Si(l_fa_2_f89faf23_101_si), .Cin(l_fa_2_f89faf23_110_cout),
    .Xi(l_fa_2_f89faf23_98_si), .Yi(l_fa_2_f89faf23_102_si));
  L_FA_2_f89faf23 l_fa_2_f89faf23_102 (
    .Cout(l_fa_2_f89faf23_101_cout[1]), .Si(l_fa_2_f89faf23_102_si), .Cin(l_fa_2_f89faf23_113_cout[0]),
    .Xi(l_fa_2_f89faf23_113_cout[2]), .Yi(l_fa_2_f89faf23_113_cout[1]));
  L_FA_2_f89faf23 l_fa_2_f89faf23_103 (
    .Cout(l_fa_2_f89faf23_103_cout[0]), .Si(l_fa_2_f89faf23_103_si), .Cin(1'b0), .Xi(undriven_103),
    .Yi(undriven_104));
  L_FA_2_f89faf23 l_fa_2_f89faf23_104 (
    .Cout(l_fa_2_f89faf23_103_cout[1]), .Si(l_fa_2_f89faf23_104_si), .Cin(undriven_102), .Xi(undriven_100),
    .Yi(undriven_101));
  L_FA_2_f89faf23 l_fa_2_f89faf23_105 ();  // open: Cout, Si, Cin, Xi, Yi
  L_FA_2_f89faf23 l_fa_2_f89faf23_106 (
    .Cout(l_fa_2_f89faf23_113_cout[2]), .Si(l_fa_2_f89faf23_106_si), .Cin(undriven_107), .Xi(undriven_105),
    .Yi(undriven_106));
  L_FA_2_f89faf23 l_fa_2_f89faf23_107 (
    .Cout(l_fa_2_f89faf23_107_cout), .Si(l_fa_2_f89faf23_107_si), .Cin(l_fa_2_f89faf23_115_cout[0]),
    .Xi(l_fa_2_f89faf23_108_si), .Yi(l_fa_2_f89faf23_115_cout[1]));
  L_FA_2_f89faf23 l_fa_2_f89faf23_108 (
    .Cout(l_fa_2_f89faf23_108_cout[0]), .Si(l_fa_2_f89faf23_108_si), .Cin(l_fa_2_f89faf23_116_cout),
    .Xi(l_fa_2_f89faf23_110_si), .Yi(l_fa_2_f89faf23_109_si));
  L_FA_2_f89faf23 l_fa_2_f89faf23_109 (
    .Cout(l_fa_2_f89faf23_108_cout[1]), .Si(l_fa_2_f89faf23_109_si), .Cin(l_fa_2_f89faf23_120_cout[0]),
    .Xi(l_fa_2_f89faf23_120_cout[2]), .Yi(l_fa_2_f89faf23_120_cout[1]));
  L_FA_2_f89faf23 l_fa_2_f89faf23_110 (
    .Cout(l_fa_2_f89faf23_110_cout), .Si(l_fa_2_f89faf23_110_si), .Cin(l_fa_2_f89faf23_113_si),
    .Xi(l_fa_2_f89faf23_106_si), .Yi(l_fa_2_f89faf23_111_si));
  L_FA_2_f89faf23 l_fa_2_f89faf23_111 (
    .Cout(l_fa_2_f89faf23_113_cout[1]), .Si(l_fa_2_f89faf23_111_si), .Cin(undriven_110), .Xi(undriven_108),
    .Yi(undriven_109));
  L_FA_2_f89faf23 l_fa_2_f89faf23_112 ();  // open: Cout, Si, Cin, Xi, Yi
  shape shape_8 ();
  L_FA_2_f89faf23 l_fa_2_f89faf23_113 (
    .Cout(l_fa_2_f89faf23_113_cout[0]), .Si(l_fa_2_f89faf23_113_si), .Cin(1'b0), .Xi(undriven_111),
    .Yi(undriven_112));
  L_FA_2_f89faf23 l_fa_2_f89faf23_114 (
    .Cout(l_fa_2_f89faf23_114_cout), .Si(l_fa_2_f89faf23_114_si), .Cin(l_fa_2_f89faf23_122_cout[0]),
    .Xi(l_fa_2_f89faf23_115_si), .Yi(l_fa_2_f89faf23_122_cout[1]));
  L_FA_2_f89faf23 l_fa_2_f89faf23_115 (
    .Cout(l_fa_2_f89faf23_115_cout[0]), .Si(l_fa_2_f89faf23_115_si), .Cin(l_fa_2_f89faf23_123_cout),
    .Xi(l_fa_2_f89faf23_116_si), .Yi(l_fa_2_f89faf23_119_si));
  L_FA_2_f89faf23 l_fa_2_f89faf23_116 (
    .Cout(l_fa_2_f89faf23_116_cout), .Si(l_fa_2_f89faf23_116_si), .Cin(l_fa_2_f89faf23_120_si),
    .Xi(l_fa_2_f89faf23_117_si), .Yi(l_fa_2_f89faf23_118_si));
  L_FA_2_f89faf23 l_fa_2_f89faf23_117 (
    .Cout(l_fa_2_f89faf23_120_cout[2]), .Si(l_fa_2_f89faf23_117_si), .Cin(undriven_115), .Xi(undriven_113),
    .Yi(undriven_114));
  L_FA_2_f89faf23 l_fa_2_f89faf23_118 (
    .Cout(l_fa_2_f89faf23_120_cout[1]), .Si(l_fa_2_f89faf23_118_si), .Cin(undriven_118), .Xi(undriven_116),
    .Yi(undriven_117));
  L_FA_2_f89faf23 l_fa_2_f89faf23_119 (
    .Cout(l_fa_2_f89faf23_115_cout[1]), .Si(l_fa_2_f89faf23_119_si), .Cin(l_fa_2_f89faf23_128_cout[0]),
    .Xi(l_fa_2_f89faf23_128_cout[2]), .Yi(l_fa_2_f89faf23_128_cout[1]));
  L_FA_2_f89faf23 l_fa_2_f89faf23_120 (
    .Cout(l_fa_2_f89faf23_120_cout[0]), .Si(l_fa_2_f89faf23_120_si), .Cin(1'b0), .Xi(undriven_119),
    .Yi(undriven_120));
  L_FA_2_f89faf23 l_fa_2_f89faf23_121 ();  // open: Cout, Si, Cin, Xi, Yi
  L_FA_2_f89faf23 l_fa_2_f89faf23_122 (
    .Cout(l_fa_2_f89faf23_122_cout[0]), .Si(l_fa_2_f89faf23_122_si), .Cin(undriven_125),
    .Xi(l_fa_2_f89faf23_123_si), .Yi(l_fa_2_f89faf23_126_si));
  L_FA_2_f89faf23 l_fa_2_f89faf23_123 (
    .Cout(l_fa_2_f89faf23_123_cout), .Si(l_fa_2_f89faf23_123_si), .Cin(l_fa_2_f89faf23_128_si),
    .Xi(l_fa_2_f89faf23_124_si), .Yi(l_fa_2_f89faf23_127_si));
  L_FA_2_f89faf23 l_fa_2_f89faf23_124 (
    .Cout(l_fa_2_f89faf23_128_cout[2]), .Si(l_fa_2_f89faf23_124_si), .Cin(undriven_123), .Xi(undriven_121),
    .Yi(undriven_122));
  L_FA_2_f89faf23 l_fa_2_f89faf23_125 (
    .Cout(l_fa_2_f89faf23_125_cout), .Si(l_fa_2_f89faf23_125_si), .Cin(undriven_131[0]),
    .Xi(l_fa_2_f89faf23_122_si), .Yi(undriven_131[1]));
  L_FA_2_f89faf23 l_fa_2_f89faf23_126 (
    .Cout(l_fa_2_f89faf23_122_cout[1]), .Si(l_fa_2_f89faf23_126_si), .Cin(undriven_129[0]),
    .Xi(undriven_129[2]), .Yi(undriven_129[1]));
  L_FA_2_f89faf23 l_fa_2_f89faf23_127 (
    .Cout(l_fa_2_f89faf23_128_cout[1]), .Si(l_fa_2_f89faf23_127_si), .Cin(undriven_127), .Xi(undriven_124),
    .Yi(undriven_126));
  L_FA_2_f89faf23 l_fa_2_f89faf23_128 (
    .Cout(l_fa_2_f89faf23_128_cout[0]), .Si(l_fa_2_f89faf23_128_si), .Cin(1'b0), .Xi(undriven_128),
    .Yi(undriven_130));

  // Notes on the sheet:
  //   16
  //   15
  //   14
  //   13
  //   12
  //   11
  //   10
  //   9
  //   8
  //   7
  //   6
  //   5
  //   2^4
  //   2^2
  //   2^3
  //   2^2
  //   2^2
  //   2^1
  //   2^1
  //   2^1
  //   2^1
  //   2^1
  //   2^0
  //   2^0
  //   2^0
endmodule

module empty (
  input  [31:0] Input_bus_1,
  input  [31:0] Input_bus_2,
  output [31:0] Output_bus_1,
  output [31:0] Output_bus_2
);
endmodule
