// Logisim project cpu_redirect.circ as structural Verilog: 12 circuits, main circuit MIPS_CPU_dc0b7d01
module MIPS_CPU_dc0b7d01 (
);

  wire alu_1_equal, and_6_out, and_7_out, branch, clk, clock_1_out, d_ff_1_qn, Din_DM_1c5ae605,
       Din_DM_half_bec5fb0f, Din_PC_1_4b7f8d88, display_a0_a04d6dcc, DM_WE, ex_mem_44939670_1_mem_halt,
       EX_RF_WE, goto, halting, IR1, IR2, IR3, jump, L_151b31bd_out, Load_Use, lock, MEM_RF_WE, not_1_out,
       not_2_out, not_3_out, or_3_out, pull_resistor_4_node, pull_resistor_5_node, rA_v0_3c73e1bd,
       rB_a0_8069dfbc, redirecter_1_redirect_rf_a, redirecter_1_redirect_rf_b, RST, rW_GPR_31_da4e8e18,
       rW_rd_b899f4bf, stop, syscall, W1, W2, W3, WB_RF_WE_2cc8db04, X_RF_B_d533957b, Y_RF_A_4287b89d,
       Y_S_EXT_58f9bb5c;
  wire [3:0] ALUOP;
  wire [4:0] EX_rW, MEM_rW, multiplexer_2_out, multiplexer_3_out, multiplexer_4_out, multiplexer_5_out, WB_rW;
  wire [5:0] EX_OP;
  wire [11:0] and_1_out, and_2_out, and_3_out, and_4_out, and_5_out;
  wire [15:0] Count, L_57ecc1e4, L_1266ec10, L_d909b624, load_use_ba48eafd, multiplexer_12_out;
  wire [25:0] id_ex_924e70ce_1_ex_ir;
  wire [27:0] id_ex_924e70ce_1_ex_ctrl;
  wire [31:0] controller_1_l_5c51f2f3, EX_Data, ex_mem_44939670_1_mem_alu_r, ex_mem_44939670_1_mem_ctrl,
       ex_mem_44939670_1_mem_pc_1_ae2eaadc, ex_mem_44939670_1_mem_rf_b, EX_PC, extender_1_imm, goto_addr,
       id_ex_924e70ce_1_ex_imm, id_ex_924e70ce_1_ex_pc_plus_1, id_ex_924e70ce_1_ex_rf_a,
       id_ex_924e70ce_1_ex_rf_b, ID_PC, IF_PC, if_to_id_1_id_ir, if_to_id_1_id_pc_plus_1, MEM_Data, MEM_PC,
       mem_wb_f3e5a8a4_1_wb_alu_r, mem_wb_f3e5a8a4_1_wb_ctrl, mem_wb_f3e5a8a4_1_wb_dm_d,
       mem_wb_f3e5a8a4_1_wb_pc_1_ce54614b, mips_ram_1_p6, multiplexer_1_out, multiplexer_6_out,
       multiplexer_7_out, multiplexer_8_out, multiplexer_9_out, multiplexer_10_out, multiplexer_13_out,
       multiplexer_14_out, pc_1_35941c9d_1_pc_4_1ec677fa, redirecter_1_redirected_rf_a,
       redirecter_1_redirected_rf_b, registerfile_1_p7, registerfile_1_p8, RF_W, rom_1_data, SyscallOut,
       WB_PC;

  Button L_57da1777 (.out(RST));
  Button L_1_2f1a01df (.out(IR1));
  Button L_2_8760bd1e (.out(IR2));
  Button L_3_165848fd (.out(IR3));
  LED led_1 (.in(W1));
  LED led_2 (.in(W2));
  LED led_3 (.in(W3));
  Multiplexer #(.width(32), .enable("false")) multiplexer_1 (
    .in0(pc_1_35941c9d_1_pc_4_1ec677fa), .in1(goto_addr), .out(multiplexer_1_out), .sel(goto));
  // Probe on multiplexer_1_out
  not not_1 (not_1_out, lock);
  Hex_Digit_Display hex_digit_display_1 (.value(SyscallOut[31:28]));  // open: dp
  // Probe on Count
  // Probe on and_1_out
  assign and_1_out = IF_PC[11:0] & {12{1'b1}};  // AND_Gate and_1, 12 bits wide
  assign and_2_out = ID_PC[11:0] & {12{1'b1}};  // AND_Gate and_2, 12 bits wide
  // Probe on and_2_out
  assign and_3_out = EX_PC[11:0] & {12{1'b1}};  // AND_Gate and_3, 12 bits wide
  // Probe on and_3_out
  // Probe on and_4_out
  assign and_4_out = MEM_PC[11:0] & {12{1'b1}};  // AND_Gate and_4, 12 bits wide
  // Probe on and_5_out
  assign and_5_out = WB_PC[11:0] & {12{1'b1}};  // AND_Gate and_5, 12 bits wide
  Register #(.width(32)) PC (.D(multiplexer_1_out), .en(not_1_out), .Q(IF_PC), .clk(clk), .clr(RST));
  and and_6 (and_6_out, ~goto, Load_Use);  // AND_Gate
  Hex_Digit_Display hex_digit_display_2 (.value(SyscallOut[27:24]));  // open: dp
  Hex_Digit_Display hex_digit_display_3 (.value(SyscallOut[23:20]));  // open: dp
  // Probe on IF_PC
  or or_1 (lock, stop, and_6_out);
  Hex_Digit_Display hex_digit_display_4 (.value(SyscallOut[19:16]));  // open: dp
  Hex_Digit_Display hex_digit_display_5 (.value(SyscallOut[15:12]));  // open: dp
  PC_1_35941c9d pc_1_35941c9d_1 (.PC(IF_PC), .PC_4_1ec677fa(pc_1_35941c9d_1_pc_4_1ec677fa));
  Hex_Digit_Display hex_digit_display_6 (.value(SyscallOut[7:4]));  // open: dp
  Hex_Digit_Display hex_digit_display_7 (.value(SyscallOut[11:8]));  // open: dp
  IF_to_ID if_to_id_1 (
    .IF_PC(IF_PC), .ID_PC(ID_PC), .CLK(clk), .clear(goto), .IF_PC_plus_1(pc_1_35941c9d_1_pc_4_1ec677fa),
    .ID_PC_plus_1(if_to_id_1_id_pc_plus_1), .IF_IR(rom_1_data), .ID_IR(if_to_id_1_id_ir), .lock(clk));
  ROM #(.addrWidth(10), .dataWidth(32)) rom_1 (.addr(IF_PC[11:2]), .data(rom_1_data));
  not not_2 (not_2_out, lock);
  Pull_Resistor #(.pull(1)) pull_resistor_1 (.node(not_2_out));
  Hex_Digit_Display hex_digit_display_8 (.value(SyscallOut[3:0]));  // open: dp
  Pull_Resistor pull_resistor_2 (.node(goto));
  // Probe on RF_W
  Controller controller_1 (
    .OP(if_to_id_1_id_ir[31:26]), .Funct(if_to_id_1_id_ir[5:0]),
    .L_5c51f2f3({controller_1_l_5c51f2f3[31:28], rA_v0_3c73e1bd, rB_a0_8069dfbc, rW_rd_b899f4bf, rW_GPR_31_da4e8e18, controller_1_l_5c51f2f3[23:0]}));
  Extender extender_1 (
    .extend_IMM(controller_1_l_5c51f2f3[15]), .extend_shamt(controller_1_l_5c51f2f3[16]),
    .IR(if_to_id_1_id_ir), .zero_extend_IMM(controller_1_l_5c51f2f3[14]), .IMM(extender_1_imm));
  // Probe on Count
  // Probe on L_1266ec10
  // Probe on L_d909b624
  // Probe on load_use_ba48eafd
  // Probe on L_57ecc1e4
  // Probe on WB_rW
  Multiplexer #(.width(5), .enable("false")) multiplexer_2 (
    .in0(if_to_id_1_id_ir[20:16]), .in1(if_to_id_1_id_ir[15:11]), .out(multiplexer_2_out),
    .sel(rW_rd_b899f4bf));
  Clock clock_1 (.out(clock_1_out));
  Button L_151b31bd (.out(L_151b31bd_out));
  Multiplexer #(.width(5), .enable("false")) multiplexer_3 (
    .in0(if_to_id_1_id_ir[25:21]), .in1(5'b00010), .out(multiplexer_3_out), .sel(rA_v0_3c73e1bd));
  Multiplexer #(.width(5), .enable("false")) multiplexer_4 (
    .in0(if_to_id_1_id_ir[20:16]), .in1(5'b00100), .out(multiplexer_4_out), .sel(rB_a0_8069dfbc));
  Multiplexer #(.width(5), .enable("false")) multiplexer_5 (
    .in0(multiplexer_2_out), .in1({5{1'b1}}), .out(multiplexer_5_out), .sel(rW_GPR_31_da4e8e18));
  D_Flip_Flop d_ff_1 (.clk(clk), .D(stop), .Qn(d_ff_1_qn), .reset(RST));  // open: Q, preset
  xor xor_1 (clk, clock_1_out, L_151b31bd_out);
  // RegisterFile registerfile_1: pin names not known; wires that end beside it: RF_W, clk, WB_RF_WE_2cc8db04, WB_rW, multiplexer_3_out, multiplexer_4_out, registerfile_1_p7, registerfile_1_p8
  Redirecter redirecter_1 (
    .EX_rW(EX_rW), .rA(multiplexer_3_out), .rB(multiplexer_4_out), .MEM_rW(MEM_rW), .EX_RF_WE(EX_RF_WE),
    .MEM_RF_WE(MEM_RF_WE), .Load_Use(Load_Use), .EX_OP(EX_OP),
    .Control_signals({controller_1_l_5c51f2f3[31:28], rA_v0_3c73e1bd, rB_a0_8069dfbc, rW_rd_b899f4bf, rW_GPR_31_da4e8e18, controller_1_l_5c51f2f3[23:0]}),
    .redirected_RF_A(redirecter_1_redirected_rf_a), .redirected_RF_B(redirecter_1_redirected_rf_b),
    .EX_Data(EX_Data), .MEM_Data(MEM_Data), .redirect_RF_A(redirecter_1_redirect_rf_a),
    .redirect_RF_B(redirecter_1_redirect_rf_b));
  Counter #(.width(16), .max('hffff), .trigger("falling")) L_54e97544 (
    .count(d_ff_1_qn), .Q(Count), .clk(clk), .clr(RST));  // open: load, D, carry
  Counter #(.width(16), .max('hffff), .trigger("falling")) Load_Use_56f41de5 (
    .count(Load_Use), .Q(load_use_ba48eafd), .clk(clk), .clr(RST));  // open: load, D, carry
  // Probe on ID_PC
  Multiplexer #(.width(32), .enable("false")) multiplexer_6 (
    .in0(registerfile_1_p7), .in1(redirecter_1_redirected_rf_a), .out(multiplexer_6_out),
    .sel(redirecter_1_redirect_rf_a));
  Multiplexer #(.width(32), .enable("false")) multiplexer_7 (
    .in0(registerfile_1_p8), .in1(redirecter_1_redirected_rf_b), .out(multiplexer_7_out),
    .sel(redirecter_1_redirect_rf_b));
  ID_EX_924e70ce id_ex_924e70ce_1 (
    .ID_PC(ID_PC), .EX_PC(EX_PC), .ID_PC_plus_1(if_to_id_1_id_pc_plus_1),
    .EX_PC_plus_1(id_ex_924e70ce_1_ex_pc_plus_1), .ID_IR(if_to_id_1_id_ir),
    .EX_IR({EX_OP, id_ex_924e70ce_1_ex_ir}),
    .ID_CTRL({controller_1_l_5c51f2f3[31:28], rA_v0_3c73e1bd, rB_a0_8069dfbc, rW_rd_b899f4bf, rW_GPR_31_da4e8e18, controller_1_l_5c51f2f3[23:0]}),
    .EX_CTRL({ALUOP, id_ex_924e70ce_1_ex_ctrl[27:24], EX_RF_WE, id_ex_924e70ce_1_ex_ctrl[22:20], X_RF_B_d533957b, Y_RF_A_4287b89d, Y_S_EXT_58f9bb5c, id_ex_924e70ce_1_ex_ctrl[16:9], syscall, id_ex_924e70ce_1_ex_ctrl[7:0]}),
    .ID_RF_A(multiplexer_6_out), .EX_RF_A(id_ex_924e70ce_1_ex_rf_a), .ID_RF_B(multiplexer_7_out),
    .EX_RF_B(id_ex_924e70ce_1_ex_rf_b), .ID_IMM(extender_1_imm), .EX_IMM(id_ex_924e70ce_1_ex_imm),
    .ID_rW(multiplexer_5_out), .EX_rW(EX_rW), .lock(not_3_out), .clear(not_3_out));  // open: CLK
  not not_3 (not_3_out, stop);
  Pull_Resistor #(.pull(1)) pull_resistor_3 (.node(not_3_out));
  // Probe on EX_PC
  Pull_Resistor pull_resistor_4 (.node(pull_resistor_4_node));
  or or_2 (pull_resistor_4_node, halting, goto, Load_Use);
  Counter #(.width(16), .max('hffff), .trigger("falling")) L_5fc3c42a (
    .count(jump), .Q(L_1266ec10), .clk(clk), .clr(RST));  // open: load, D, carry
  Counter #(.width(16), .max('hffff), .trigger("falling")) L_8bdb9b71 (
    .count(Load_Use), .Q(L_57ecc1e4), .clk(clk), .clr(RST));  // open: load, D, carry
  // Probe on EX_rW
  Multiplexer #(.width(32), .enable("false")) multiplexer_8 (
    .in0(id_ex_924e70ce_1_ex_rf_b), .in1(id_ex_924e70ce_1_ex_rf_a), .out(multiplexer_8_out),
    .sel(Y_RF_A_4287b89d));
  Register #(.width(32)) L_5ace57c3 (
    .D(id_ex_924e70ce_1_ex_rf_b), .en(display_a0_a04d6dcc), .Q(SyscallOut), .clk(clk), .clr(RST));
  // Probe on MEM_PC
  Multiplexer #(.width(32), .enable("false")) multiplexer_9 (
    .in0(id_ex_924e70ce_1_ex_rf_a), .in1(id_ex_924e70ce_1_ex_rf_b), .out(multiplexer_9_out),
    .sel(X_RF_B_d533957b));
  Multiplexer #(.width(32), .enable("false")) multiplexer_10 (
    .in0(multiplexer_8_out), .in1(id_ex_924e70ce_1_ex_imm), .out(multiplexer_10_out), .sel(Y_S_EXT_58f9bb5c));
  Counter #(.width(16), .max('hffff), .trigger("falling")) L_7d5bc005 (
    .count(branch), .Q(L_d909b624), .clk(clk), .clr(RST));  // open: load, D, carry
  ALU alu_1 (
    .X(multiplexer_9_out), .Y(multiplexer_10_out), .AluOP(ALUOP), .Equal(alu_1_equal), .Result(EX_Data));  // open: Signed_Overflow_9e58537c, UnSigned_Overflow_f391286f, Result_2_87641da0
  // Probe on WB_PC
  NPC npc_1 (
    .ALU_R(EX_Data),
    .CTRL({ALUOP, id_ex_924e70ce_1_ex_ctrl[27:24], EX_RF_WE, id_ex_924e70ce_1_ex_ctrl[22:20], X_RF_B_d533957b, Y_RF_A_4287b89d, Y_S_EXT_58f9bb5c, id_ex_924e70ce_1_ex_ctrl[16:9], syscall, id_ex_924e70ce_1_ex_ctrl[7:0]}),
    .IMM(id_ex_924e70ce_1_ex_imm), .PC_1_507ea4d3(id_ex_924e70ce_1_ex_pc_plus_1),
    .IR({EX_OP, id_ex_924e70ce_1_ex_ir}), .RF_A(id_ex_924e70ce_1_ex_rf_a), .branch(branch),
    .jump_or_branch_b511ffd3(goto), .jump(jump), .new_addr(goto_addr), .ALU_Equal(alu_1_equal));
  and and_7 (and_7_out, alu_1_equal, syscall);
  and and_8 (display_a0_a04d6dcc, ~alu_1_equal, syscall);  // AND_Gate
  // Probe on EX_Data
  EX_MEM_44939670 ex_mem_44939670_1 (
    .CLK(clk), .L_58cf2f01(pull_resistor_5_node), .EX_PC(EX_PC), .MEM_PC(MEM_PC),
    .EX_PC_1_98e5f4a5(id_ex_924e70ce_1_ex_pc_plus_1),
    .MEM_PC_1_ae2eaadc(ex_mem_44939670_1_mem_pc_1_ae2eaadc),
    .EX_CTRL({ALUOP, id_ex_924e70ce_1_ex_ctrl[27:24], EX_RF_WE, id_ex_924e70ce_1_ex_ctrl[22:20], X_RF_B_d533957b, Y_RF_A_4287b89d, Y_S_EXT_58f9bb5c, id_ex_924e70ce_1_ex_ctrl[16:9], syscall, id_ex_924e70ce_1_ex_ctrl[7:0]}),
    .MEM_CTRL({ex_mem_44939670_1_mem_ctrl[31:24], MEM_RF_WE, ex_mem_44939670_1_mem_ctrl[22:8], DM_WE, ex_mem_44939670_1_mem_ctrl[6:0]}),
    .lock_when_0_stop_transport_5efc0fcd(not_3_out), .EX_rW(EX_rW), .MEM_rW(MEM_rW),
    .EX_RF_B(id_ex_924e70ce_1_ex_rf_b), .MEM_RF_B(ex_mem_44939670_1_mem_rf_b), .EX_ALU_R(EX_Data),
    .MEM_ALU_R(ex_mem_44939670_1_mem_alu_r), .EX_HALT(and_7_out), .MEM_HALT(ex_mem_44939670_1_mem_halt));
  Pull_Resistor pull_resistor_5 (.node(pull_resistor_5_node));
  Pull_Resistor #(.pull(1)) pull_resistor_6 (.node(not_3_out));
  // Probe on MEM_rW
  or or_3 (or_3_out, ex_mem_44939670_1_mem_ctrl[21], ex_mem_44939670_1_mem_ctrl[20]);
  // MIPS_RAM mips_ram_1: pin names not known; wires that end beside it: ex_mem_44939670_1_mem_alu_r[13:2], ex_mem_44939670_1_mem_rf_b, DM_WE, clk, RST, mips_ram_1_p6
  // Probe on MEM_Data
  Multiplexer #(.width(32), .enable("false")) multiplexer_11 (
    .in0(ex_mem_44939670_1_mem_alu_r), .in1(mips_ram_1_p6), .out(MEM_Data), .sel(or_3_out));
  MEM_WB_f3e5a8a4 mem_wb_f3e5a8a4_1 (
    .CLK(clk), .L_58cf2f01(pull_resistor_5_node), .MEM_PC(MEM_PC), .WB_PC(WB_PC),
    .MEM_PC_1_ae2eaadc(ex_mem_44939670_1_mem_pc_1_ae2eaadc),
    .WB_PC_1_ce54614b(mem_wb_f3e5a8a4_1_wb_pc_1_ce54614b),
    .MEM_CTRL({ex_mem_44939670_1_mem_ctrl[31:24], MEM_RF_WE, ex_mem_44939670_1_mem_ctrl[22:8], DM_WE, ex_mem_44939670_1_mem_ctrl[6:0]}),
    .WB_CTRL({mem_wb_f3e5a8a4_1_wb_ctrl[31:24], WB_RF_WE_2cc8db04, Din_PC_1_4b7f8d88, Din_DM_1c5ae605, Din_DM_half_bec5fb0f, mem_wb_f3e5a8a4_1_wb_ctrl[19:0]}),
    .lock_when_0_stop_transport_5efc0fcd(not_3_out), .MEM_rW(MEM_rW), .WB_rW(WB_rW),
    .MEM_ALU_R(ex_mem_44939670_1_mem_alu_r), .WB_ALU_R(mem_wb_f3e5a8a4_1_wb_alu_r), .MEM_DM_D(mips_ram_1_p6),
    .WB_DM_D(mem_wb_f3e5a8a4_1_wb_dm_d), .MEM_HALT(ex_mem_44939670_1_mem_halt), .WB_HALT(halting));
  Multiplexer #(.width(16), .enable("false")) multiplexer_12 (
    .in0(mem_wb_f3e5a8a4_1_wb_dm_d[15:0]), .in1(mem_wb_f3e5a8a4_1_wb_dm_d[31:16]), .out(multiplexer_12_out),
    .sel(mem_wb_f3e5a8a4_1_wb_alu_r[1]));
  D_Flip_Flop #(.trigger("falling")) d_ff_2 (.clk(halting), .D(1'b1), .Q(stop), .reset(RST));  // open: Qn, preset
  Multiplexer #(.width(32), .enable("false")) multiplexer_13 (
    .in0(mem_wb_f3e5a8a4_1_wb_alu_r), .in1(mem_wb_f3e5a8a4_1_wb_pc_1_ce54614b), .out(multiplexer_13_out),
    .sel(Din_PC_1_4b7f8d88));
  Multiplexer #(.width(32), .enable("false")) multiplexer_14 (
    .in0(mem_wb_f3e5a8a4_1_wb_dm_d), .in1({{16{1'b0}}, multiplexer_12_out}), .out(multiplexer_14_out),
    .sel(Din_DM_half_bec5fb0f));
  // Probe on RF_W
  Multiplexer #(.width(32), .enable("false")) multiplexer_15 (
    .in0(multiplexer_13_out), .in1(multiplexer_14_out), .out(RF_W), .sel(Din_DM_1c5ae605));

  // Other names for the same wires on the sheet: L_35e5ca7f[15:0] = Count

  // Notes on the sheet:
  //   中断源
  //   中断等待指示
  //   指令存储器
  //   数码管输出
  //   contents of rom_1 (hex, n*v repeats v):
  //   20110001 8000c05 20110001 20120002 20130003 8000c09 20110001 20120002 20130003 8000c0d 20110001
  //   20120002 20130003 8000c11 20110001 20120002 20130003 c000cb8 20100001 20110001 118fc0 112020
  //   20020022 c 118882 12200001 8000c15 112020 20020022 c 20110001 118880 112020 20020022 c 12200001
  //   8000c1f 20110001 118fc0 112020 20020022 c 1188c3 112020 20020022 c 118903 112020 20020022 c 118903
  //   112020 20020022 c 118903 112020 20020022 c 118903 112020 20020022 c 118903 112020 20020022 c 118903
  //   112020 20020022 c 118903 112020 20020022 c 20100001 109fc0 139fc3 8021 2012000c 24160003 26100001
  //   3210000f 20080008 20090001 139900 2709825 132020 20020022 c 1094022 1500fff9 22100001 2018000f
  //   2188024 108700 20080008 20090001 139902 2709825 132021 20020022 c 1094022 1500fff9 108702 2c9b022
  //   12c00001 8000c50 4020 1084027 84400 3508ffff 82021 20020022 c 2010ffff 20110000 ae300000 22100001
  //   22310004 ae300000 22100001 22310004 ae300000 22100001 22310004 ae300000 22100001 22310004 ae300000
  //   22100001 22310004 ae300000 22100001 22310004 ae300000 22100001 22310004 ae300000 22100001 22310004
  //   ae300000 22100001 22310004 ae300000 22100001 22310004 ae300000 22100001 22310004 ae300000 22100001
  //   22310004 ae300000 22100001 22310004 ae300000 22100001 22310004 ae300000 22100001 22310004 ae300000
  //   22100001 22310004 22100001 8020 2011003c 8e130000 8e340000 274402a 11000002 ae330000 ae140000
  //   2231fffc 1611fff8 102020 20020022 c 22100004 2011003c 1611fff2 2002000a c 20100000 22100001 102020
  //   20020022 c 22100002 102020 20020022 c 22100003 102020 20020022 c 22100004 102020 20020022 c 22100005
  //   102020 20020022 c 22100006 102020 20020022 c 22100007 102020 20020022 c 22100008 102020 20020022
  //   20020022 c 3e00008
  //   寄存器堆
  //   数据存储器
endmodule

module PC_1_35941c9d (
  input  [31:0] PC,
  output [31:0] PC_4_1ec677fa
);

  Adder #(.width(32)) adder_1 (.a(PC), .b(32'h4), .out(PC_4_1ec677fa));  // open: cin, cout
endmodule

// Contorller
module Controller (
  input  [5:0] OP,
  input  [5:0] Funct,
  output [31:0] L_5c51f2f3
);

  wire add, addi, addiu, addu, \and , andi, comparator_1_eq, comparator_16_eq, comparator_17_eq,
       comparator_18_eq, comparator_19_eq, comparator_20_eq, comparator_21_eq, comparator_22_eq,
       comparator_23_eq, comparator_24_eq, comparator_25_eq, comparator_26_eq, comparator_27_eq,
       comparator_28_eq, comparator_29_eq, j, lw, \nor , \or , or_2_out, or_3_out, or_4_out, or_5_out,
       or_6_out, or_7_out, or_9_out, or_10_out, or_11_out, or_12_out, or_13_out, or_14_out, or_15_out,
       or_16_out, or_17_out, or_18_out, or_19_out, or_21_out, or_22_out, or_23_out, or_24_out, or_25_out,
       or_26_out, or_27_out, or_28_out, or_30_out, or_31_out, or_32_out, or_33_out, or_34_out, or_35_out,
       or_36_out, or_37_out, or_38_out, or_39_out, or_40_out, or_42_out, or_43_out, or_44_out, or_45_out,
       or_46_out, or_47_out, or_48_out, or_49_out, or_50_out, or_51_out, or_53_out, or_54_out, or_55_out,
       or_56_out, or_57_out, or_58_out, or_59_out, or_60_out, or_61_out, or_62_out, or_63_out, or_65_out,
       or_66_out, or_67_out, or_68_out, or_69_out, or_70_out, or_71_out, or_72_out, or_74_out, or_75_out,
       or_77_out, or_78_out, or_79_out, or_80_out, or_81_out, or_82_out, or_83_out, or_84_out, or_85_out,
       or_86_out, or_87_out, or_89_out, or_91_out, or_92_out, or_93_out, or_94_out, or_95_out, or_96_out,
       or_97_out, or_98_out, or_99_out, or_100_out, or_103_out, ori, sll, slt, slti, sltiu, sltu, sra, srl,
       sub;

  Comparator #(.width(6)) comparator_1 (.a(OP), .b({6{1'b0}}), .eq(comparator_1_eq));  // open: gt, lt
  Comparator #(.width(6)) comparator_2 (.a(OP), .b(6'b000001), .eq(L_5c51f2f3[9]));  // open: gt, lt
  Comparator #(.width(6)) comparator_3 (.a(OP), .b(6'b000010), .eq(j));  // open: gt, lt
  Comparator #(.width(6)) comparator_4 (.a(OP), .b(6'b000011), .eq(L_5c51f2f3[24]));  // open: gt, lt
  Comparator #(.width(6)) comparator_5 (.a(OP), .b(6'b000100), .eq(L_5c51f2f3[11]));  // open: gt, lt
  Comparator #(.width(6)) comparator_6 (.a(OP), .b(6'b000101), .eq(L_5c51f2f3[10]));  // open: gt, lt
  Comparator #(.width(6)) comparator_7 (.a(OP), .b(6'b001000), .eq(addi));  // open: gt, lt
  Comparator #(.width(6)) comparator_8 (.a(OP), .b(6'b001001), .eq(addiu));  // open: gt, lt
  Comparator #(.width(6)) comparator_9 (.a(OP), .b(6'b001010), .eq(slti));  // open: gt, lt
  Comparator #(.width(6)) comparator_10 (.a(OP), .b(6'b001011), .eq(sltiu));  // open: gt, lt
  Comparator #(.width(6)) comparator_11 (.a(OP), .b(6'b001100), .eq(andi));  // open: gt, lt
  Comparator #(.width(6)) comparator_12 (.a(OP), .b(6'b001101), .eq(ori));  // open: gt, lt
  Comparator #(.width(6)) comparator_13 (.a(OP), .b(6'b100001), .eq(L_5c51f2f3[20]));  // open: gt, lt
  Comparator #(.width(6)) comparator_14 (.a(OP), .b(6'b100011), .eq(lw));  // open: gt, lt
  Comparator #(.width(6)) comparator_15 (.a(OP), .b(6'b101011), .eq(L_5c51f2f3[7]));  // open: gt, lt
  Comparator #(.width(6)) comparator_16 (.a(Funct), .b({6{1'b0}}), .eq(comparator_16_eq));  // open: gt, lt
  Comparator #(.width(6)) comparator_17 (.a(Funct), .b(6'b000010), .eq(comparator_17_eq));  // open: gt, lt
  Comparator #(.width(6)) comparator_18 (.a(Funct), .b(6'b000011), .eq(comparator_18_eq));  // open: gt, lt
  Comparator #(.width(6)) comparator_19 (.a(Funct), .b(6'b000110), .eq(comparator_19_eq));  // open: gt, lt
  Comparator #(.width(6)) comparator_20 (.a(Funct), .b(6'b001000), .eq(comparator_20_eq));  // open: gt, lt
  Comparator #(.width(6)) comparator_21 (.a(Funct), .b(6'b001100), .eq(comparator_21_eq));  // open: gt, lt
  Comparator #(.width(6)) comparator_22 (.a(Funct), .b(6'b100000), .eq(comparator_22_eq));  // open: gt, lt
  Comparator #(.width(6)) comparator_23 (.a(Funct), .b(6'b100001), .eq(comparator_23_eq));  // open: gt, lt
  Comparator #(.width(6)) comparator_24 (.a(Funct), .b(6'b100010), .eq(comparator_24_eq));  // open: gt, lt
  Comparator #(.width(6)) comparator_25 (.a(Funct), .b(6'b100100), .eq(comparator_25_eq));  // open: gt, lt
  Comparator #(.width(6)) comparator_26 (.a(Funct), .b(6'b100101), .eq(comparator_26_eq));  // open: gt, lt
  Comparator #(.width(6)) comparator_27 (.a(Funct), .b(6'b100111), .eq(comparator_27_eq));  // open: gt, lt
  Comparator #(.width(6)) comparator_28 (.a(Funct), .b(6'b101010), .eq(comparator_28_eq));  // open: gt, lt
  Comparator #(.width(6)) comparator_29 (.a(Funct), .b(6'b101011), .eq(comparator_29_eq));  // open: gt, lt
  and and_1 (sll, comparator_1_eq, comparator_16_eq);
  and and_2 (srl, comparator_1_eq, comparator_17_eq);
  and and_3 (sra, comparator_1_eq, comparator_18_eq);
  and and_4 (L_5c51f2f3[18], comparator_1_eq, comparator_19_eq);
  and and_5 (L_5c51f2f3[12], comparator_1_eq, comparator_20_eq);
  and and_6 (L_5c51f2f3[27], comparator_1_eq, comparator_21_eq);
  and and_7 (add, comparator_1_eq, comparator_22_eq);
  and and_8 (addu, comparator_1_eq, comparator_23_eq);
  and and_9 (sub, comparator_1_eq, comparator_24_eq);
  and and_10 (\and , comparator_1_eq, comparator_25_eq);
  and and_11 (\or , comparator_1_eq, comparator_26_eq);
  and and_12 (\nor , comparator_1_eq, comparator_27_eq);
  and and_13 (slt, comparator_1_eq, comparator_28_eq);
  and and_14 (sltu, comparator_1_eq, comparator_29_eq);
  or or_1 (L_5c51f2f3[31], \or , or_2_out);
  or or_2 (or_2_out, or_3_out, \nor );
  or or_3 (or_3_out, slt, or_4_out);
  or or_4 (or_4_out, or_5_out, sltu);
  or or_5 (or_5_out, L_5c51f2f3[9], or_6_out);
  or or_6 (or_6_out, or_7_out, slti);
  or or_7 (or_7_out, sltiu, ori);
  // Probe on {L_5c51f2f3[31:27], L_5c51f2f3[27], L_5c51f2f3[25:23], L_5c51f2f3[24], L_5c51f2f3[21:9], L_5c51f2f3[27], L_5c51f2f3[7:5], {5{1'b0}}}
  or or_8 (L_5c51f2f3[30], L_5c51f2f3[27], or_9_out);
  or or_9 (or_9_out, or_10_out, add);
  or or_10 (or_10_out, addu, or_11_out);
  or or_11 (or_11_out, or_12_out, sub);
  or or_12 (or_12_out, \and , or_13_out);
  or or_13 (or_13_out, or_14_out, sltu);
  or or_14 (or_14_out, addi, or_15_out);
  or or_15 (or_15_out, or_16_out, addiu);
  or or_16 (or_16_out, sltiu, or_17_out);
  or or_17 (or_17_out, or_18_out, andi);
  or or_18 (or_18_out, L_5c51f2f3[20], or_19_out);
  or or_19 (or_19_out, lw, L_5c51f2f3[7]);
  or or_20 (L_5c51f2f3[29], srl, or_21_out);
  or or_21 (or_21_out, or_22_out, L_5c51f2f3[18]);
  or or_22 (or_22_out, L_5c51f2f3[27], or_23_out);
  or or_23 (or_23_out, or_24_out, sub);
  or or_24 (or_24_out, \and , or_25_out);
  or or_25 (or_25_out, or_26_out, \nor );
  or or_26 (or_26_out, slt, or_27_out);
  or or_27 (or_27_out, or_28_out, L_5c51f2f3[9]);
  or or_28 (or_28_out, slti, andi);
  or or_29 (L_5c51f2f3[28], sra, or_30_out);
  or or_30 (or_30_out, or_31_out, add);
  or or_31 (or_31_out, addu, or_32_out);
  or or_32 (or_32_out, or_33_out, \and );
  or or_33 (or_33_out, slt, or_34_out);
  or or_34 (or_34_out, or_35_out, L_5c51f2f3[9]);
  or or_35 (or_35_out, addi, or_36_out);
  or or_36 (or_36_out, or_37_out, addiu);
  or or_37 (or_37_out, slti, or_38_out);
  or or_38 (or_38_out, or_39_out, andi);
  or or_39 (or_39_out, L_5c51f2f3[20], or_40_out);
  or or_40 (or_40_out, lw, L_5c51f2f3[7]);
  or or_41 (L_5c51f2f3[25], sll, or_42_out);
  or or_42 (or_42_out, or_43_out, srl);
  or or_43 (or_43_out, sra, or_44_out);
  or or_44 (or_44_out, or_45_out, L_5c51f2f3[18]);
  or or_45 (or_45_out, add, or_46_out);
  or or_46 (or_46_out, or_47_out, addu);
  or or_47 (or_47_out, sub, or_48_out);
  or or_48 (or_48_out, or_49_out, \and );
  or or_49 (or_49_out, \or , or_50_out);
  or or_50 (or_50_out, or_51_out, \nor );
  or or_51 (or_51_out, slt, sltu);
  or or_52 (L_5c51f2f3[23], sll, or_53_out);
  or or_53 (or_53_out, or_54_out, srl);
  or or_54 (or_54_out, sra, or_55_out);
  or or_55 (or_55_out, or_56_out, L_5c51f2f3[18]);
  or or_56 (or_56_out, add, or_57_out);
  or or_57 (or_57_out, or_58_out, addu);
  or or_58 (or_58_out, sub, or_59_out);
  or or_59 (or_59_out, or_60_out, \and );
  or or_60 (or_60_out, \or , or_61_out);
  or or_61 (or_61_out, or_62_out, \nor );
  or or_62 (or_62_out, slt, or_63_out);
  or or_63 (or_63_out, sltu, or_65_out);
  or or_64 (L_5c51f2f3[21], L_5c51f2f3[20], lw);
  or or_65 (or_65_out, L_5c51f2f3[24], or_66_out);
  or or_66 (or_66_out, or_67_out, addi);
  or or_67 (or_67_out, addiu, or_68_out);
  or or_68 (or_68_out, or_69_out, slti);
  or or_69 (or_69_out, sltiu, or_70_out);
  or or_70 (or_70_out, or_71_out, andi);
  or or_71 (or_71_out, ori, or_72_out);
  or or_72 (or_72_out, L_5c51f2f3[20], lw);
  or or_73 (L_5c51f2f3[19], sll, or_74_out);
  or or_74 (or_74_out, or_75_out, srl);
  or or_75 (or_75_out, sra, L_5c51f2f3[18]);
  or or_76 (L_5c51f2f3[17], sll, or_77_out);
  or or_77 (or_77_out, or_78_out, srl);
  or or_78 (or_78_out, sra, or_79_out);
  or or_79 (or_79_out, or_80_out, L_5c51f2f3[27]);
  or or_80 (or_80_out, addi, or_81_out);
  or or_81 (or_81_out, or_82_out, addiu);
  or or_82 (or_82_out, slti, or_83_out);
  or or_83 (or_83_out, or_84_out, sltiu);
  or or_84 (or_84_out, andi, or_85_out);
  or or_85 (or_85_out, or_86_out, ori);
  or or_86 (or_86_out, L_5c51f2f3[20], or_87_out);
  or or_87 (or_87_out, lw, L_5c51f2f3[7]);
  or or_88 (L_5c51f2f3[16], sll, or_89_out);
  or or_89 (or_89_out, srl, sra);
  or or_90 (L_5c51f2f3[15], L_5c51f2f3[9], or_91_out);
  or or_91 (or_91_out, or_92_out, L_5c51f2f3[11]);
  or or_92 (or_92_out, L_5c51f2f3[10], or_93_out);
  or or_93 (or_93_out, or_94_out, addi);
  or or_94 (or_94_out, addiu, or_95_out);
  or or_95 (or_95_out, or_96_out, slti);
  or or_96 (or_96_out, sltiu, or_97_out);
  or or_97 (or_97_out, or_98_out, andi);
  or or_98 (or_98_out, ori, or_99_out);
  or or_99 (or_99_out, or_100_out, L_5c51f2f3[20]);
  or or_100 (or_100_out, lw, L_5c51f2f3[7]);
  or or_101 (L_5c51f2f3[13], L_5c51f2f3[12], or_103_out);
  or or_102 (L_5c51f2f3[14], andi, ori);
  or or_103 (or_103_out, j, L_5c51f2f3[24]);
  or or_104 (L_5c51f2f3[6], L_5c51f2f3[9], L_5c51f2f3[11], L_5c51f2f3[18], L_5c51f2f3[10], L_5c51f2f3[12], addi, addiu, add, slti, addu, sltiu, sub, andi, \and , ori, \or , L_5c51f2f3[20], \nor , lw, slt, L_5c51f2f3[7], sltu);
  or or_105 (L_5c51f2f3[5], L_5c51f2f3[10], sll, srl, sra, add, L_5c51f2f3[7], addu, sltu, sub, slt, \and , L_5c51f2f3[18], \or , L_5c51f2f3[9], \nor , L_5c51f2f3[11]);

  assign {L_5c51f2f3[26], L_5c51f2f3[22], L_5c51f2f3[8], L_5c51f2f3[4:0]} = {L_5c51f2f3[27], L_5c51f2f3[24], L_5c51f2f3[27], {5{1'b0}}};

  // Other names for the same wires on the sheet: read_rB = L_5c51f2f3[5]; read_rA = L_5c51f2f3[6]; sw = L_5c51f2f3[7];
  //   bltz = L_5c51f2f3[9]; bne = L_5c51f2f3[10]; beq = L_5c51f2f3[11]; jr = L_5c51f2f3[12]; srlv = L_5c51f2f3[18];
  //   lh = L_5c51f2f3[20]; jal = L_5c51f2f3[24]; syscall = L_5c51f2f3[27]
endmodule

// 扩展
module Extender (
  input  extend_IMM,
  input  extend_shamt,
  input  [31:0] IR,
  input  zero_extend_IMM,
  output [31:0] IMM
);

  wire [16:0] multiplexer_1_out, multiplexer_2_out, multiplexer_3_out;

  Multiplexer #(.width(17), .enable("false")) multiplexer_1 (
    .in0(17'ha), .in1({{12{1'b0}}, IR[10:6]}), .out(multiplexer_1_out), .sel(extend_shamt));
  Multiplexer #(.width(17), .enable("false")) multiplexer_2 (
    .in0({{2{IR[15]}}, IR[14:0]}), .in1({1'b0, IR[15:0]}), .out(multiplexer_2_out), .sel(zero_extend_IMM));
  Multiplexer #(.width(17), .enable("false")) multiplexer_3 (
    .in0(multiplexer_1_out), .in1(multiplexer_2_out), .out(multiplexer_3_out), .sel(extend_IMM));
  assign IMM = {{15{multiplexer_3_out[16]}}, multiplexer_3_out};  // Bit_Extender bit_extender_1

  // Other names for the same wires on the sheet: extend_IMM_27a03817 = extend_IMM;
  //   extend_shamt_c0141e9d = extend_shamt; zero_ext_IMM_054c79ed = zero_extend_IMM
endmodule

module ALU (
  input  [31:0] X,
  input  [31:0] Y,
  input  [3:0] AluOP,
  output Signed_Overflow_9e58537c,
  output UnSigned_Overflow_f391286f,
  output Equal,
  output [31:0] Result,
  output [31:0] Result_2_87641da0
);

  wire adder_1_cout, and_2_out, and_3_out, and_5_out, and_6_out, and_7_out, and_8_out, comparator_2_lt,
       or_2_out, or_4_out;
  wire [0:0] comparator_1_lt, xor_2_out;
  wire [31:0] adder_1_out, and_1_out, divider_1_out, divider_1_rem, multiplexer_2_out, multiplier_1_cout,
       multiplier_1_out, not_1_out, not_2_out, or_1_out, shifter_1_out, shifter_2_out, shifter_3_out,
       xor_1_out;

  // Probe on X
  // Probe on X
  // Probe on Y
  // Probe on Y
  Shifter #(.width(32)) shifter_1 (.in(X), .\dist (Y[4:0]), .out(shifter_1_out));
  Shifter #(.width(32), .shift("ar")) shifter_2 (.in(X), .\dist (Y[4:0]), .out(shifter_2_out));
  Shifter #(.width(32), .shift("lr")) shifter_3 (.in(X), .\dist (Y[4:0]), .out(shifter_3_out));
  Multiplier #(.width(32)) multiplier_1 (.a(X), .b(Y), .out(multiplier_1_out), .cout(multiplier_1_cout));  // open: cin
  Divider #(.width(32)) divider_1 (.a(X), .b(Y), .out(divider_1_out), .rem(divider_1_rem));  // open: upper
  assign and_1_out = X & Y;  // AND_Gate and_1, 32 bits wide
  assign or_1_out = X | Y;  // OR_Gate or_1, 32 bits wide
  assign xor_1_out = X ^ Y;  // XOR_Gate xor_1, 32 bits wide
  Comparator #(.width(32), .mode("unsigned")) comparator_1 (
    .a(X), .b(Y), .eq(Equal), .lt(comparator_1_lt[0]));  // open: gt
  Multiplexer #(.select(4), .width(32), .enable("false")) multiplexer_1 (
    .in0(shifter_1_out), .in1(shifter_2_out), .in2(shifter_3_out), .in3(multiplier_1_out),
    .in4(divider_1_out), .in5(adder_1_out), .in6(adder_1_out), .in7(and_1_out), .in8(or_1_out),
    .in9(xor_1_out), .in10(not_1_out), .in11({{31{1'b0}}, xor_2_out[0]}),
    .in12({{31{1'b0}}, comparator_1_lt[0]}), .in13({32{1'b0}}), .in14({32{1'b0}}), .in15({32{1'b0}}),
    .out(Result), .sel(AluOP));
  assign not_1_out = ~or_1_out;  // NOT_Gate not_1, 32 bits wide
  // Probe on AluOP
  xor xor_2 (xor_2_out[0], xor_1_out[31], comparator_1_lt[0]);
  // Probe on Result
  // Probe on Result
  Multiplexer #(.width(32), .enable("false")) multiplexer_2 (
    .in0(Y), .in1(not_2_out), .out(multiplexer_2_out), .sel(AluOP[1]));
  assign not_2_out = ~Y;  // NOT_Gate not_2, 32 bits wide
  // Probe on Result_2_87641da0
  Adder #(.width(32)) adder_1 (.a(X), .b(multiplexer_2_out), .out(adder_1_out), .cin(AluOP[1]), .cout(adder_1_cout));
  Multiplexer #(.select(4), .width(32), .enable("false")) multiplexer_3 (
    .in0({32{1'b0}}), .in1({32{1'b0}}), .in2({32{1'b0}}), .in3(multiplier_1_cout), .in4(divider_1_rem),
    .in5({32{1'b0}}), .in6({32{1'b0}}), .in7({32{1'b0}}), .in8({32{1'b0}}), .in9({32{1'b0}}),
    .in10({32{1'b0}}), .in11({32{1'b0}}), .in12({32{1'b0}}), .in13({32{1'b0}}), .in14({32{1'b0}}),
    .in15({32{1'b0}}), .out(Result_2_87641da0), .sel(AluOP));
  and and_2 (and_2_out, ~adder_1_out[31], multiplexer_2_out[31], X[31]);  // AND_Gate
  or or_2 (or_2_out, and_2_out, and_3_out);
  and and_3 (and_3_out, adder_1_out[31], ~X[31], ~multiplexer_2_out[31]);  // AND_Gate
  Comparator #(.width(32), .mode("unsigned")) comparator_2 (
    .a(X), .b(adder_1_out), .lt(comparator_2_lt));  // open: gt, eq
  and and_4 (Signed_Overflow_9e58537c, or_2_out, or_4_out);
  or or_3 (UnSigned_Overflow_f391286f, and_6_out, and_5_out);
  and and_5 (and_5_out, comparator_2_lt, and_8_out);
  and and_6 (and_6_out, adder_1_cout, and_7_out);
  or or_4 (or_4_out, and_7_out, and_8_out);
  and and_7 (and_7_out, AluOP[0], ~AluOP[1], AluOP[2], ~AluOP[3]);  // AND_Gate
  and and_8 (and_8_out, ~AluOP[0], AluOP[1], AluOP[2], ~AluOP[3]);  // AND_Gate

  // Other names for the same wires on the sheet: OF = Signed_Overflow_9e58537c; Result2[31:0] = Result_2_87641da0;
  //   S[3:0] = AluOP; UOF = UnSigned_Overflow_f391286f

  // Notes on the sheet:
  //   不要改变此引脚区域内容，也不要改变ALU封装形式
  //   输入引脚
  //   请在下方利用上方输入输出引脚的隧道信号构建ALU电路，ctrl+d复制选择部件
  //   华中科技大学计算机学院 计算机组成原理，鸣谢加州大学伯克利CS61C课程
  //   输出引脚
  //   探测区域
endmodule

module NPC (
  input  ALU_Equal,
  input  [31:0] ALU_R,
  input  [31:0] CTRL,
  input  [31:0] IMM,
  input  [31:0] PC_1_507ea4d3,
  input  [31:0] IR,
  input  [31:0] RF_A,
  output branch,
  output jump_or_branch_b511ffd3,
  output jump,
  output [31:0] new_addr
);

  wire and_1_out, and_2_out, and_3_out;
  wire [31:0] adder_1_out, multiplexer_1_out;

  Adder #(.width(32)) adder_1 (.a({IMM[29:0], 2'b00}), .b(PC_1_507ea4d3), .out(adder_1_out));  // open: cin, cout
  and and_1 (and_1_out, ALU_R[0], CTRL[9]);
  and and_2 (and_2_out, ALU_Equal, CTRL[11]);
  or or_1 (branch, and_1_out, and_2_out, and_3_out);
  and and_3 (and_3_out, ~ALU_Equal, CTRL[10]);  // AND_Gate
  Multiplexer #(.width(32), .enable("false")) multiplexer_1 (
    .in0({PC_1_507ea4d3[31:28], IR[25:0], 2'b00}), .in1(RF_A), .out(multiplexer_1_out), .sel(CTRL[12]));
  or or_2 (jump_or_branch_b511ffd3, branch, CTRL[13]);
  Multiplexer #(.width(32), .enable("false")) multiplexer_2 (
    .in0(adder_1_out), .in1(multiplexer_1_out), .out(new_addr), .sel(CTRL[13]));

  assign jump = CTRL[13];

  // Other names for the same wires on the sheet: bltz = CTRL[9]; bne = CTRL[10]; beq = CTRL[11];
  //   jump_register_420d251f = CTRL[12]
endmodule

module IF_to_ID (
  input  CLK,
  input  lock,
  input  clear,
  input  [31:0] IF_PC,
  input  [31:0] IF_PC_plus_1,
  input  [31:0] IF_IR,
  output [31:0] ID_PC,
  output [31:0] ID_PC_plus_1,
  output [31:0] ID_IR
);

  wire [31:0] multiplexer_1_out, multiplexer_2_out, multiplexer_3_out;

  Multiplexer #(.width(32), .enable("false")) multiplexer_1 (
    .in0(IF_PC), .in1({32{1'b0}}), .out(multiplexer_1_out), .sel(clear));
  Multiplexer #(.width(32), .enable("false")) multiplexer_2 (
    .in0(IF_PC_plus_1), .in1({32{1'b0}}), .out(multiplexer_2_out), .sel(clear));
  Multiplexer #(.width(32), .enable("false")) multiplexer_3 (
    .in0(IF_IR), .in1({32{1'b0}}), .out(multiplexer_3_out), .sel(clear));
  Register #(.width(32)) register_1 (.D(multiplexer_1_out), .en(lock), .Q(ID_PC), .clk(CLK));  // open: clr
  Register #(.width(32)) register_2 (.D(multiplexer_2_out), .en(lock), .Q(ID_PC_plus_1), .clk(CLK));  // open: clr
  Register #(.width(32)) register_3 (.D(multiplexer_3_out), .en(lock), .Q(ID_IR), .clk(CLK));  // open: clr
endmodule

// ID/EX
module ID_EX_924e70ce (
  input  CLK,
  input  lock,
  input  clear,
  input  [31:0] ID_PC,
  input  [31:0] ID_PC_plus_1,
  input  [31:0] ID_IR,
  input  [31:0] ID_CTRL,
  input  [31:0] ID_RF_A,
  input  [31:0] ID_RF_B,
  input  [4:0] ID_rW,
  input  [31:0] ID_IMM,
  output [31:0] EX_PC,
  output [31:0] EX_PC_plus_1,
  output [31:0] EX_IR,
  output [31:0] EX_CTRL,
  output [31:0] EX_RF_A,
  output [31:0] EX_RF_B,
  output [4:0] EX_rW,
  output [31:0] EX_IMM
);

  wire [4:0] multiplexer_7_out;
  wire [31:0] multiplexer_1_out, multiplexer_2_out, multiplexer_3_out, multiplexer_4_out, multiplexer_5_out,
       multiplexer_6_out, multiplexer_8_out;

  Multiplexer #(.width(32), .enable("false")) multiplexer_1 (
    .in0(ID_PC), .in1({32{1'b0}}), .out(multiplexer_1_out), .sel(clear));
  Multiplexer #(.width(32), .enable("false")) multiplexer_2 (
    .in0(ID_PC_plus_1), .in1({32{1'b0}}), .out(multiplexer_2_out), .sel(clear));
  Multiplexer #(.width(32), .enable("false")) multiplexer_3 (
    .in0(ID_IR), .in1({32{1'b0}}), .out(multiplexer_3_out), .sel(clear));
  Multiplexer #(.width(32), .enable("false")) multiplexer_4 (
    .in0(ID_CTRL), .in1({32{1'b0}}), .out(multiplexer_4_out), .sel(clear));
  Multiplexer #(.width(32), .enable("false")) multiplexer_5 (
    .in0(ID_RF_A), .in1({32{1'b0}}), .out(multiplexer_5_out), .sel(clear));
  Multiplexer #(.width(32), .enable("false")) multiplexer_6 (
    .in0(ID_RF_B), .in1({32{1'b0}}), .out(multiplexer_6_out), .sel(clear));
  Multiplexer #(.width(5), .enable("false")) multiplexer_7 (
    .in0(ID_rW), .in1({5{1'b0}}), .out(multiplexer_7_out), .sel(clear));
  Multiplexer #(.width(32), .enable("false")) multiplexer_8 (
    .in0(ID_IMM), .in1({32{1'b0}}), .out(multiplexer_8_out), .sel(clear));
  Register #(.width(32)) register_1 (.D(multiplexer_1_out), .en(lock), .Q(EX_PC), .clk(CLK));  // open: clr
  Register #(.width(32)) register_2 (.D(multiplexer_2_out), .en(lock), .Q(EX_PC_plus_1), .clk(CLK));  // open: clr
  Register #(.width(32)) register_3 (.D(multiplexer_3_out), .en(lock), .Q(EX_IR), .clk(CLK));  // open: clr
  Register #(.width(32)) register_4 (.D(multiplexer_4_out), .en(lock), .Q(EX_CTRL), .clk(CLK));  // open: clr
  Register #(.width(32)) register_5 (.D(multiplexer_5_out), .en(lock), .Q(EX_RF_A), .clk(CLK));  // open: clr
  Register #(.width(32)) register_6 (.D(multiplexer_6_out), .en(lock), .Q(EX_RF_B), .clk(CLK));  // open: clr
  Register #(.width(5)) register_7 (.D(multiplexer_7_out), .en(lock), .Q(EX_rW), .clk(CLK));  // open: clr
  Register #(.width(32)) register_8 (.D(multiplexer_8_out), .en(lock), .Q(EX_IMM), .clk(CLK));  // open: clr
endmodule

// EX/MEM
module EX_MEM_44939670 (
  input  CLK,
  input  lock_when_0_stop_transport_5efc0fcd,
  input  L_58cf2f01,
  input  [31:0] EX_PC,
  input  [31:0] EX_PC_1_98e5f4a5,
  input  [31:0] EX_CTRL,
  input  [4:0] EX_rW,
  input  [31:0] EX_RF_B,
  input  [31:0] EX_ALU_R,
  input  EX_HALT,
  output [31:0] MEM_PC,
  output [31:0] MEM_PC_1_ae2eaadc,
  output [31:0] MEM_CTRL,
  output [4:0] MEM_rW,
  output [31:0] MEM_RF_B,
  output [31:0] MEM_ALU_R,
  output MEM_HALT
);

  wire multiplexer_7_out;
  wire [4:0] multiplexer_4_out;
  wire [31:0] multiplexer_1_out, multiplexer_2_out, multiplexer_3_out, multiplexer_5_out, multiplexer_6_out;

  Multiplexer #(.width(32), .enable("false")) multiplexer_1 (
    .in0(EX_PC), .in1({32{1'b0}}), .out(multiplexer_1_out), .sel(L_58cf2f01));
  Multiplexer #(.width(32), .enable("false")) multiplexer_2 (
    .in0(EX_PC_1_98e5f4a5), .in1({32{1'b0}}), .out(multiplexer_2_out), .sel(L_58cf2f01));
  Multiplexer #(.width(32), .enable("false")) multiplexer_3 (
    .in0(EX_CTRL), .in1({32{1'b0}}), .out(multiplexer_3_out), .sel(L_58cf2f01));
  Multiplexer #(.width(5), .enable("false")) multiplexer_4 (
    .in0(EX_rW), .in1({5{1'b0}}), .out(multiplexer_4_out), .sel(L_58cf2f01));
  Multiplexer #(.width(32), .enable("false")) multiplexer_5 (
    .in0(EX_RF_B), .in1({32{1'b0}}), .out(multiplexer_5_out), .sel(L_58cf2f01));
  Multiplexer #(.width(32), .enable("false")) multiplexer_6 (
    .in0(EX_ALU_R), .in1({32{1'b0}}), .out(multiplexer_6_out), .sel(L_58cf2f01));
  Multiplexer #(.enable("false")) multiplexer_7 (.in0(EX_HALT), .in1(1'b0), .out(multiplexer_7_out), .sel(L_58cf2f01));
  Register #(.width(32)) register_1 (
    .D(multiplexer_1_out), .en(lock_when_0_stop_transport_5efc0fcd), .Q(MEM_PC), .clk(CLK));  // open: clr
  Register #(.width(32)) register_2 (
    .D(multiplexer_2_out), .en(lock_when_0_stop_transport_5efc0fcd), .Q(MEM_PC_1_ae2eaadc), .clk(CLK));  // open: clr
  Register #(.width(32)) register_3 (
    .D(multiplexer_3_out), .en(lock_when_0_stop_transport_5efc0fcd), .Q(MEM_CTRL), .clk(CLK));  // open: clr
  Register #(.width(5)) register_4 (
    .D(multiplexer_4_out), .en(lock_when_0_stop_transport_5efc0fcd), .Q(MEM_rW), .clk(CLK));  // open: clr
  Register #(.width(32)) register_5 (
    .D(multiplexer_5_out), .en(lock_when_0_stop_transport_5efc0fcd), .Q(MEM_RF_B), .clk(CLK));  // open: clr
  Register #(.width(32)) register_6 (
    .D(multiplexer_6_out), .en(lock_when_0_stop_transport_5efc0fcd), .Q(MEM_ALU_R), .clk(CLK));  // open: clr
  Register #(.width(1)) register_7 (
    .D(multiplexer_7_out), .en(lock_when_0_stop_transport_5efc0fcd), .Q(MEM_HALT), .clk(CLK));  // open: clr
endmodule

// MEM//WB
module MEM_WB_f3e5a8a4 (
  input  CLK,
  input  lock_when_0_stop_transport_5efc0fcd,
  input  L_58cf2f01,
  input  [31:0] MEM_PC,
  input  [31:0] MEM_PC_1_ae2eaadc,
  input  [31:0] MEM_CTRL,
  input  [4:0] MEM_rW,
  input  [31:0] MEM_ALU_R,
  input  [31:0] MEM_DM_D,
  input  MEM_HALT,
  output [31:0] WB_PC,
  output [31:0] WB_PC_1_ce54614b,
  output [31:0] WB_CTRL,
  output [4:0] WB_rW,
  output [31:0] WB_ALU_R,
  output [31:0] WB_DM_D,
  output WB_HALT
);

  wire multiplexer_7_out;
  wire [4:0] multiplexer_4_out;
  wire [31:0] multiplexer_2_out, multiplexer_3_out, multiplexer_5_out, multiplexer_6_out;

  Multiplexer #(.width(32), .enable("false")) multiplexer_1 (
    .in0(MEM_PC), .in1({32{1'b0}}), .out(WB_PC), .sel(L_58cf2f01));
  Multiplexer #(.width(32), .enable("false")) multiplexer_2 (
    .in0(MEM_PC_1_ae2eaadc), .in1({32{1'b0}}), .out(multiplexer_2_out), .sel(L_58cf2f01));
  Multiplexer #(.width(32), .enable("false")) multiplexer_3 (
    .in0(MEM_CTRL), .in1({32{1'b0}}), .out(multiplexer_3_out), .sel(L_58cf2f01));
  Multiplexer #(.width(5), .enable("false")) multiplexer_4 (
    .in0(MEM_rW), .in1({5{1'b0}}), .out(multiplexer_4_out), .sel(L_58cf2f01));
  Multiplexer #(.width(32), .enable("false")) multiplexer_5 (
    .in0(MEM_ALU_R), .in1({32{1'b0}}), .out(multiplexer_5_out), .sel(L_58cf2f01));
  Multiplexer #(.width(32), .enable("false")) multiplexer_6 (
    .in0(MEM_DM_D), .in1({32{1'b0}}), .out(multiplexer_6_out), .sel(L_58cf2f01));
  Multiplexer #(.enable("false")) multiplexer_7 (.in0(MEM_HALT), .in1(1'b0), .out(multiplexer_7_out), .sel(L_58cf2f01));
  // Register #(.width(32)) register_1: pin names not known; wires that end beside it: lock_when_0_stop_transport_5efc0fcd, CLK
  Register #(.width(32)) register_2 (
    .D(multiplexer_2_out), .en(lock_when_0_stop_transport_5efc0fcd), .Q(WB_PC_1_ce54614b), .clk(CLK));  // open: clr
  Register #(.width(32)) register_3 (
    .D(multiplexer_3_out), .en(lock_when_0_stop_transport_5efc0fcd), .Q(WB_CTRL), .clk(CLK));  // open: clr
  Register #(.width(5)) register_4 (
    .D(multiplexer_4_out), .en(lock_when_0_stop_transport_5efc0fcd), .Q(WB_rW), .clk(CLK));  // open: clr
  Register #(.width(32)) register_5 (
    .D(multiplexer_5_out), .en(lock_when_0_stop_transport_5efc0fcd), .Q(WB_ALU_R), .clk(CLK));  // open: clr
  Register #(.width(32)) register_6 (
    .D(multiplexer_6_out), .en(lock_when_0_stop_transport_5efc0fcd), .Q(WB_DM_D), .clk(CLK));  // open: clr
  Register #(.width(1)) register_7 (
    .D(multiplexer_7_out), .en(lock_when_0_stop_transport_5efc0fcd), .Q(WB_HALT), .clk(CLK));  // open: clr
endmodule

module Redirecter (
  input  [31:0] Control_signals,
  input  [5:0] EX_OP,
  input  [4:0] EX_rW,
  input  EX_RF_WE,
  input  [4:0] rA,
  input  [4:0] rB,
  input  [31:0] EX_Data,
  input  [4:0] MEM_rW,
  input  [31:0] MEM_Data,
  input  MEM_RF_WE,
  output redirect_RF_A,
  output [31:0] redirected_RF_A,
  output Load_Use,
  output [31:0] redirected_RF_B,
  output redirect_RF_B
);

  wire and_1_out, and_2_out, and_3_out, and_4_out, and_5_out, and_6_out, and_7_out, and_8_out, and_9_out,
       and_10_out, and_11_out, and_12_out, and_13_out, and_14_out, and_16_out, and_17_out, and_18_out,
       comparator_1_eq, comparator_2_eq, comparator_3_eq, comparator_4_eq, comparator_5_eq, comparator_6_eq,
       comparator_7_eq, comparator_8_eq, comparator_9_eq, comparator_10_eq, EX_d42e9320, EX_lh, EX_lw, EX_sw,
       MEM_548fd6b1, not_1_out, not_2_out, or_3_out, or_4_out, or_5_out, or_6_out, or_10_out, or_12_out,
       or_13_out, or_14_out, rA_EX_9beee9a5, rA_MEM_90c9f4d8, rB_EX_edc59a79, rB_MEM_d8009108;

  Comparator #(.width(5)) comparator_1 (.a(EX_rW), .b(rA), .eq(comparator_1_eq));  // open: gt, lt
  Comparator #(.width(5)) comparator_2 (.a(EX_rW), .b(rB), .eq(comparator_2_eq));  // open: gt, lt
  Comparator #(.width(5)) comparator_3 (.a(EX_rW), .b({5{1'b0}}), .eq(comparator_3_eq));  // open: gt, lt
  Comparator #(.width(5)) comparator_4 (.a(EX_rW), .b(5'b00010), .eq(comparator_4_eq));  // open: gt, lt
  Comparator #(.width(5)) comparator_5 (.a(EX_rW), .b(5'b00100), .eq(comparator_5_eq));  // open: gt, lt
  Comparator #(.width(5)) comparator_6 (.a(MEM_rW), .b(rA), .eq(comparator_6_eq));  // open: gt, lt
  Comparator #(.width(5)) comparator_7 (.a(MEM_rW), .b(rB), .eq(comparator_7_eq));  // open: gt, lt
  Comparator #(.width(5)) comparator_8 (.a(MEM_rW), .b({5{1'b0}}), .eq(comparator_8_eq));  // open: gt, lt
  Comparator #(.width(5)) comparator_9 (.a(MEM_rW), .b(5'b00010), .eq(comparator_9_eq));  // open: gt, lt
  Comparator #(.width(5)) comparator_10 (.a(MEM_rW), .b(5'b00100), .eq(comparator_10_eq));  // open: gt, lt
  and and_1 (and_1_out, comparator_1_eq, Control_signals[6]);
  and and_2 (and_2_out, comparator_2_eq, Control_signals[5]);
  and and_3 (and_3_out, comparator_4_eq, Control_signals[8]);
  and and_4 (and_4_out, comparator_5_eq, Control_signals[8]);
  and and_5 (and_5_out, comparator_6_eq, Control_signals[6]);
  and and_6 (and_6_out, comparator_7_eq, Control_signals[5]);
  and and_7 (and_7_out, comparator_9_eq, Control_signals[8]);
  and and_8 (and_8_out, comparator_10_eq, Control_signals[8]);
  Comparator #(.width(6)) comparator_11 (.a(EX_OP), .b(6'b100001), .eq(EX_lh));  // open: gt, lt
  Comparator #(.width(6)) comparator_12 (.a(EX_OP), .b(6'b100011), .eq(EX_lw));  // open: gt, lt
  Comparator #(.width(6)) comparator_13 (.a(EX_OP), .b(6'b101011), .eq(EX_sw));  // open: gt, lt
  or or_1 (rA_EX_9beee9a5, and_1_out, and_3_out);
  or or_2 (rA_MEM_90c9f4d8, and_5_out, and_7_out);
  or or_3 (or_3_out, and_1_out, and_2_out);
  not not_1 (not_1_out, comparator_3_eq);
  or or_4 (or_4_out, and_3_out, and_4_out);
  or or_5 (or_5_out, and_5_out, and_6_out);
  not not_2 (not_2_out, comparator_8_eq);
  or or_6 (or_6_out, and_7_out, and_8_out);
  or or_7 (rB_MEM_d8009108, and_8_out, and_6_out);
  or or_8 (rB_EX_edc59a79, and_4_out, and_2_out);
  and and_9 (and_9_out, or_3_out, not_1_out, EX_RF_WE);
  and and_10 (and_10_out, EX_RF_WE, or_4_out);
  and and_11 (and_11_out, or_5_out, not_2_out, MEM_RF_WE);
  and and_12 (and_12_out, MEM_RF_WE, or_6_out);
  or or_9 (EX_d42e9320, and_9_out, and_10_out);
  or or_10 (or_10_out, EX_sw, EX_lw, EX_lh);
  or or_11 (MEM_548fd6b1, and_11_out, and_12_out);
  and and_13 (and_13_out, rA_EX_9beee9a5, EX_d42e9320);
  and and_14 (and_14_out, rA_MEM_90c9f4d8, MEM_548fd6b1);
  and and_15 (Load_Use, EX_d42e9320, or_10_out);
  and and_16 (and_16_out, ~or_10_out, EX_d42e9320);  // AND_Gate
  and and_17 (and_17_out, MEM_548fd6b1, rB_MEM_d8009108);
  and and_18 (and_18_out, EX_d42e9320, rB_EX_edc59a79);
  or or_12 (or_12_out, and_13_out, and_14_out);
  or or_13 (or_13_out, and_16_out, MEM_548fd6b1);
  or or_14 (or_14_out, and_17_out, and_18_out);
  and and_19 (redirect_RF_A, or_12_out, or_13_out);
  and and_20 (redirect_RF_B, or_13_out, or_14_out);
  Multiplexer #(.width(32), .enable("false")) multiplexer_1 (
    .in0(MEM_Data), .in1(EX_Data), .out(redirected_RF_A), .sel(and_13_out));
  Multiplexer #(.width(32), .enable("false")) multiplexer_2 (
    .in0(MEM_Data), .in1(EX_Data), .out(redirected_RF_B), .sel(and_18_out));

  // Other names for the same wires on the sheet: read_rB = Control_signals[5]; read_rA = Control_signals[6];
  //   syscall = Control_signals[8]
endmodule

module TEST (
  input  Input_1,
  output Output_1
);

  Redirecter Redirecter_1 (
    .EX_RF_WE(Input_1), .Load_Use(Output_1));  // open: EX_rW, rA, rB, MEM_rW, MEM_RF_WE, EX_OP, Control_signals, redirected_RF_A, redirected_RF_B, EX_Data, MEM_Data, redirect_RF_A, redirect_RF_B
  IF_to_ID IF_ID ();  // open: IF_PC, ID_PC, CLK, clear, IF_PC_plus_1, ID_PC_plus_1, IF_IR, ID_IR, lock
endmodule
