// Logisim project cpu_redirect_FPGA.circ as structural Verilog: 9 circuits, main circuit Controller
module TEST (
  input  Input_1,
  output Output_1
);

  wire [4:0] EX_MEM_1_mem_rw;
  wire [31:0] Controller_1_l_5c51f2f3, EX_MEM_1_mem_alu_r, EX_MEM_1_mem_ctrl, EX_MEM_1_mem_pc,
       EX_MEM_1_mem_pc_plus_1, EX_MEM_1_mem_rf_b, Extender_1_imm, ID_EX_1_ex_ir, ID_EX_1_ex_pc,
       ID_EX_1_ex_pc_plus_1, ID_EX_1_ex_rf_a, ID_EX_1_ex_rf_b, NPC_1_new_addr, undriven, undriven_2;

  NPC NPC_1 (
    .PC_plus_1(undriven), .new_addr(NPC_1_new_addr));  // open: ALU_R, CTRL, IMM, IR, RF_A, branch, goto, jump, ALU_Equal
  Extender Extender_1 (.IR(NPC_1_new_addr), .IMM(Extender_1_imm));  // open: extend_IMM, extend_shamt, zero_ext_IMM
  Controller Controller_1 (.L_5c51f2f3(Controller_1_l_5c51f2f3));  // open: OP, Funct
  Redirecter Redirecter_1 (
    .EX_RF_WE(Input_1), .Load_Use(Output_1), .Control_signals(Extender_1_imm),
    .EX_Data(Controller_1_l_5c51f2f3), .MEM_Data(undriven_2));  // open: EX_rW, rA, rB, MEM_rW, MEM_RF_WE, EX_OP, redirected_RF_A, redirected_RF_B, redirect_RF_A, redirect_RF_B
  IF_ID IF_ID_1 (.IF_IR(undriven_2));  // open: IF_PC, ID_PC, CLK, clear, IF_PC_plus_1, ID_PC_plus_1, ID_IR, lock
  ID_EX ID_EX_1 (
    .ID_PC(undriven), .EX_PC(ID_EX_1_ex_pc), .EX_PC_plus_1(ID_EX_1_ex_pc_plus_1), .EX_IR(ID_EX_1_ex_ir),
    .EX_RF_A(ID_EX_1_ex_rf_a), .EX_RF_B(ID_EX_1_ex_rf_b));  // open: ID_PC_plus_1, ID_IR, ID_CTRL, EX_CTRL, ID_RF_A, ID_RF_B, ID_IMM, EX_IMM, ID_rW, EX_rW, lock, clear, CLK
  EX_MEM EX_MEM_1 (
    .EX_PC(ID_EX_1_ex_pc), .MEM_PC(EX_MEM_1_mem_pc), .EX_PC_plus_1(ID_EX_1_ex_pc_plus_1),
    .MEM_PC_plus_1(EX_MEM_1_mem_pc_plus_1), .EX_CTRL(ID_EX_1_ex_ir), .MEM_CTRL(EX_MEM_1_mem_ctrl),
    .MEM_rW(EX_MEM_1_mem_rw), .EX_RF_B(ID_EX_1_ex_rf_a), .MEM_RF_B(EX_MEM_1_mem_rf_b),
    .EX_ALU_R(ID_EX_1_ex_rf_b), .MEM_ALU_R(EX_MEM_1_mem_alu_r));  // open: CLK, clear, lock, EX_rW, EX_HALT, MEM_HALT
  // MEM_WB MEM_WB_1: pin names not known; wires that end beside it: EX_MEM_1_mem_alu_r, EX_MEM_1_mem_ctrl, EX_MEM_1_mem_rw, EX_MEM_1_mem_pc, EX_MEM_1_mem_pc_plus_1, EX_MEM_1_mem_rf_b
endmodule

// Contorller
module Controller (
  input  [5:0] OP,
  input  [5:0] Funct,
  output [31:0] L_5c51f2f3
);

  wire add, addi, addiu, addu, \and , andi, comparator_1_eq, comparator_16_eq, comparator_17_eq,
       comparator_18_eq, comparator_19_eq, comparator_20_eq, comparator_21_eq, comparator_22_eq,
       comparator_23_eq, comparator_24_eq, comparator_25_eq, comparator_26_eq, comparator_27_eq,
       comparator_28_eq, comparator_29_eq, j, lw, \nor , \or , or_2_out, or_3_out, or_4_out, or_5_out,
       or_6_out, or_7_out, or_9_out, or_10_out, or_11_out, or_12_out, or_13_out, or_14_out, or_15_out,
       or_16_out, or_17_out, or_18_out, or_19_out, or_21_out, or_22_out, or_23_out, or_24_out, or_25_out,
       or_26_out, or_27_out, or_28_out, or_30_out, or_31_out, or_32_out, or_33_out, or_34_out, or_35_out,
       or_36_out, or_37_out, or_38_out, or_39_out, or_40_out, or_42_out, or_43_out, or_44_out, or_45_out,
       or_46_out, or_47_out, or_48_out, or_49_out, or_50_out, or_51_out, or_53_out, or_54_out, or_55_out,
       or_56_out, or_57_out, or_58_out, or_59_out, or_60_out, or_61_out, or_62_out, or_63_out, or_65_out,
       or_66_out, or_67_out, or_68_out, or_69_out, or_70_out, or_71_out, or_72_out, or_74_out, or_75_out,
       or_77_out, or_78_out, or_79_out, or_80_out, or_81_out, or_82_out, or_83_out, or_84_out, or_85_out,
       or_86_out, or_87_out, or_89_out, or_91_out, or_92_out, or_93_out, or_94_out, or_95_out, or_96_out,
       or_97_out, or_98_out, or_99_out, or_100_out, or_103_out, ori, sll, slt, slti, sltiu, sltu, sra, srl,
       sub;

  Comparator #(.width(6)) comparator_1 (.a(OP), .b({6{1'b0}}), .eq(comparator_1_eq));  // open: gt, lt
  Comparator #(.width(6)) comparator_2 (.a(OP), .b(6'b000001), .eq(L_5c51f2f3[9]));  // open: gt, lt
  Comparator #(.width(6)) comparator_3 (.a(OP), .b(6'b000010), .eq(j));  // open: gt, lt
  Comparator #(.width(6)) comparator_4 (.a(OP), .b(6'b000011), .eq(L_5c51f2f3[24]));  // open: gt, lt
  Comparator #(.width(6)) comparator_5 (.a(OP), .b(6'b000100), .eq(L_5c51f2f3[11]));  // open: gt, lt
  Comparator #(.width(6)) comparator_6 (.a(OP), .b(6'b000101), .eq(L_5c51f2f3[10]));  // open: gt, lt
  Comparator #(.width(6)) comparator_7 (.a(OP), .b(6'b001000), .eq(addi));  // open: gt, lt
  Comparator #(.width(6)) comparator_8 (.a(OP), .b(6'b001001), .eq(addiu));  // open: gt, lt
  Comparator #(.width(6)) comparator_9 (.a(OP), .b(6'b001010), .eq(slti));  // open: gt, lt
  Comparator #(.width(6)) comparator_10 (.a(OP), .b(6'b001011), .eq(sltiu));  // open: gt, lt
  Comparator #(.width(6)) comparator_11 (.a(OP), .b(6'b001100), .eq(andi));  // open: gt, lt
  Comparator #(.width(6)) comparator_12 (.a(OP), .b(6'b001101), .eq(ori));  // open: gt, lt
  Comparator #(.width(6)) comparator_13 (.a(OP), .b(6'b100001), .eq(L_5c51f2f3[20]));  // open: gt, lt
  Comparator #(.width(6)) comparator_14 (.a(OP), .b(6'b100011), .eq(lw));  // open: gt, lt
  Comparator #(.width(6)) comparator_15 (.a(OP), .b(6'b101011), .eq(L_5c51f2f3[7]));  // open: gt, lt
  Comparator #(.width(6)) comparator_16 (.a(Funct), .b({6{1'b0}}), .eq(comparator_16_eq));  // open: gt, lt
  Comparator #(.width(6)) comparator_17 (.a(Funct), .b(6'b000010), .eq(comparator_17_eq));  // open: gt, lt
  Comparator #(.width(6)) comparator_18 (.a(Funct), .b(6'b000011), .eq(comparator_18_eq));  // open: gt, lt
  Comparator #(.width(6)) comparator_19 (.a(Funct), .b(6'b000110), .eq(comparator_19_eq));  // open: gt, lt
  Comparator #(.width(6)) comparator_20 (.a(Funct), .b(6'b001000), .eq(comparator_20_eq));  // open: gt, lt
  Comparator #(.width(6)) comparator_21 (.a(Funct), .b(6'b001100), .eq(comparator_21_eq));  // open: gt, lt
  Comparator #(.width(6)) comparator_22 (.a(Funct), .b(6'b100000), .eq(comparator_22_eq));  // open: gt, lt
  Comparator #(.width(6)) comparator_23 (.a(Funct), .b(6'b100001), .eq(comparator_23_eq));  // open: gt, lt
  Comparator #(.width(6)) comparator_24 (.a(Funct), .b(6'b100010), .eq(comparator_24_eq));  // open: gt, lt
  Comparator #(.width(6)) comparator_25 (.a(Funct), .b(6'b100100), .eq(comparator_25_eq));  // open: gt, lt
  Comparator #(.width(6)) comparator_26 (.a(Funct), .b(6'b100101), .eq(comparator_26_eq));  // open: gt, lt
  Comparator #(.width(6)) comparator_27 (.a(Funct), .b(6'b100111), .eq(comparator_27_eq));  // open: gt, lt
  Comparator #(.width(6)) comparator_28 (.a(Funct), .b(6'b101010), .eq(comparator_28_eq));  // open: gt, lt
  Comparator #(.width(6)) comparator_29 (.a(Funct), .b(6'b101011), .eq(comparator_29_eq));  // open: gt, lt
  and and_1 (sll, comparator_1_eq, comparator_16_eq);
  and and_2 (srl, comparator_1_eq, comparator_17_eq);
  and and_3 (sra, comparator_1_eq, comparator_18_eq);
  and and_4 (L_5c51f2f3[18], comparator_1_eq, comparator_19_eq);
  and and_5 (L_5c51f2f3[12], comparator_1_eq, comparator_20_eq);
  and and_6 (L_5c51f2f3[27], comparator_1_eq, comparator_21_eq);
  and and_7 (add, comparator_1_eq, comparator_22_eq);
  and and_8 (addu, comparator_1_eq, comparator_23_eq);
  and and_9 (sub, comparator_1_eq, comparator_24_eq);
  and and_10 (\and , comparator_1_eq, comparator_25_eq);
  and and_11 (\or , comparator_1_eq, comparator_26_eq);
  and and_12 (\nor , comparator_1_eq, comparator_27_eq);
  and and_13 (slt, comparator_1_eq, comparator_28_eq);
  and and_14 (sltu, comparator_1_eq, comparator_29_eq);
  or or_1 (L_5c51f2f3[31], \or , or_2_out);
  or or_2 (or_2_out, or_3_out, \nor );
  or or_3 (or_3_out, slt, or_4_out);
  or or_4 (or_4_out, or_5_out, sltu);
  or or_5 (or_5_out, L_5c51f2f3[9], or_6_out);
  or or_6 (or_6_out, or_7_out, slti);
  or or_7 (or_7_out, sltiu, ori);
  // Probe on {L_5c51f2f3[31:27], L_5c51f2f3[27], L_5c51f2f3[25:23], L_5c51f2f3[24], L_5c51f2f3[21:9], L_5c51f2f3[27], L_5c51f2f3[7:5], {5{1'b0}}}
  or or_8 (L_5c51f2f3[30], L_5c51f2f3[27], or_9_out);
  or or_9 (or_9_out, or_10_out, add);
  or or_10 (or_10_out, addu, or_11_out);
  or or_11 (or_11_out, or_12_out, sub);
  or or_12 (or_12_out, \and , or_13_out);
  or or_13 (or_13_out, or_14_out, sltu);
  or or_14 (or_14_out, addi, or_15_out);
  or or_15 (or_15_out, or_16_out, addiu);
  or or_16 (or_16_out, sltiu, or_17_out);
  or or_17 (or_17_out, or_18_out, andi);
  or or_18 (or_18_out, L_5c51f2f3[20], or_19_out);
  or or_19 (or_19_out, lw, L_5c51f2f3[7]);
  or or_20 (L_5c51f2f3[29], srl, or_21_out);
  or or_21 (or_21_out, or_22_out, L_5c51f2f3[18]);
  or or_22 (or_22_out, L_5c51f2f3[27], or_23_out);
  or or_23 (or_23_out, or_24_out, sub);
  or or_24 (or_24_out, \and , or_25_out);
  or or_25 (or_25_out, or_26_out, \nor );
  or or_26 (or_26_out, slt, or_27_out);
  or or_27 (or_27_out, or_28_out, L_5c51f2f3[9]);
  or or_28 (or_28_out, slti, andi);
  or or_29 (L_5c51f2f3[28], sra, or_30_out);
  or or_30 (or_30_out, or_31_out, add);
  or or_31 (or_31_out, addu, or_32_out);
  or or_32 (or_32_out, or_33_out, \and );
  or or_33 (or_33_out, slt, or_34_out);
  or or_34 (or_34_out, or_35_out, L_5c51f2f3[9]);
  or or_35 (or_35_out, addi, or_36_out);
  or or_36 (or_36_out, or_37_out, addiu);
  or or_37 (or_37_out, slti, or_38_out);
  or or_38 (or_38_out, or_39_out, andi);
  or or_39 (or_39_out, L_5c51f2f3[20], or_40_out);
  or or_40 (or_40_out, lw, L_5c51f2f3[7]);
  or or_41 (L_5c51f2f3[25], sll, or_42_out);
  or or_42 (or_42_out, or_43_out, srl);
  or or_43 (or_43_out, sra, or_44_out);
  or or_44 (or_44_out, or_45_out, L_5c51f2f3[18]);
  or or_45 (or_45_out, add, or_46_out);
  or or_46 (or_46_out, or_47_out, addu);
  or or_47 (or_47_out, sub, or_48_out);
  or or_48 (or_48_out, or_49_out, \and );
  or or_49 (or_49_out, \or , or_50_out);
  or or_50 (or_50_out, or_51_out, \nor );
  or or_51 (or_51_out, slt, sltu);
  or or_52 (L_5c51f2f3[23], sll, or_53_out);
  or or_53 (or_53_out, or_54_out, srl);
  or or_54 (or_54_out, sra, or_55_out);
  or or_55 (or_55_out, or_56_out, L_5c51f2f3[18]);
  or or_56 (or_56_out, add, or_57_out);
  or or_57 (or_57_out, or_58_out, addu);
  or or_58 (or_58_out, sub, or_59_out);
  or or_59 (or_59_out, or_60_out, \and );
  or or_60 (or_60_out, \or , or_61_out);
  or or_61 (or_61_out, or_62_out, \nor );
  or or_62 (or_62_out, slt, or_63_out);
  or or_63 (or_63_out, sltu, or_65_out);
  or or_64 (L_5c51f2f3[21], L_5c51f2f3[20], lw);
  or or_65 (or_65_out, L_5c51f2f3[24], or_66_out);
  or or_66 (or_66_out, or_67_out, addi);
  or or_67 (or_67_out, addiu, or_68_out);
  or or_68 (or_68_out, or_69_out, slti);
  or or_69 (or_69_out, sltiu, or_70_out);
  or or_70 (or_70_out, or_71_out, andi);
  or or_71 (or_71_out, ori, or_72_out);
  or or_72 (or_72_out, L_5c51f2f3[20], lw);
  or or_73 (L_5c51f2f3[19], sll, or_74_out);
  or or_74 (or_74_out, or_75_out, srl);
  or or_75 (or_75_out, sra, L_5c51f2f3[18]);
  or or_76 (L_5c51f2f3[17], sll, or_77_out);
  or or_77 (or_77_out, or_78_out, srl);
  or or_78 (or_78_out, sra, or_79_out);
  or or_79 (or_79_out, or_80_out, L_5c51f2f3[27]);
  or or_80 (or_80_out, addi, or_81_out);
  or or_81 (or_81_out, or_82_out, addiu);
  or or_82 (or_82_out, slti, or_83_out);
  or or_83 (or_83_out, or_84_out, sltiu);
  or or_84 (or_84_out, andi, or_85_out);
  or or_85 (or_85_out, or_86_out, ori);
  or or_86 (or_86_out, L_5c51f2f3[20], or_87_out);
  or or_87 (or_87_out, lw, L_5c51f2f3[7]);
  or or_88 (L_5c51f2f3[16], sll, or_89_out);
  or or_89 (or_89_out, srl, sra);
  or or_90 (L_5c51f2f3[15], L_5c51f2f3[9], or_91_out);
  or or_91 (or_91_out, or_92_out, L_5c51f2f3[11]);
  or or_92 (or_92_out, L_5c51f2f3[10], or_93_out);
  or or_93 (or_93_out, or_94_out, addi);
  or or_94 (or_94_out, addiu, or_95_out);
  or or_95 (or_95_out, or_96_out, slti);
  or or_96 (or_96_out, sltiu, or_97_out);
  or or_97 (or_97_out, or_98_out, andi);
  or or_98 (or_98_out, ori, or_99_out);
  or or_99 (or_99_out, or_100_out, L_5c51f2f3[20]);
  or or_100 (or_100_out, lw, L_5c51f2f3[7]);
  or or_101 (L_5c51f2f3[14], andi, ori);
  or or_102 (L_5c51f2f3[13], L_5c51f2f3[12], or_103_out);
  or or_103 (or_103_out, j, L_5c51f2f3[24]);
  or or_104 (L_5c51f2f3[6], L_5c51f2f3[9], L_5c51f2f3[11], L_5c51f2f3[18], L_5c51f2f3[10], L_5c51f2f3[12], addi, addiu, add, slti, addu, sltiu, sub, andi, \and , ori, \or , L_5c51f2f3[20], \nor , lw, slt, L_5c51f2f3[7], sltu);
  or or_105 (L_5c51f2f3[5], L_5c51f2f3[10], sll, srl, sra, add, L_5c51f2f3[7], addu, sltu, sub, slt, \and , L_5c51f2f3[18], \or , L_5c51f2f3[9], \nor , L_5c51f2f3[11]);

  assign {L_5c51f2f3[26], L_5c51f2f3[22], L_5c51f2f3[8], L_5c51f2f3[4:0]} = {L_5c51f2f3[27], L_5c51f2f3[24], L_5c51f2f3[27], {5{1'b0}}};

  // Other names for the same wires on the sheet: read_rB = L_5c51f2f3[5]; read_rA = L_5c51f2f3[6]; sw = L_5c51f2f3[7];
  //   bltz = L_5c51f2f3[9]; bne = L_5c51f2f3[10]; beq = L_5c51f2f3[11]; jr = L_5c51f2f3[12]; srlv = L_5c51f2f3[18];
  //   lh = L_5c51f2f3[20]; jal = L_5c51f2f3[24]; syscall = L_5c51f2f3[27]
endmodule

// 扩展
module Extender (
  input  extend_IMM,
  input  extend_shamt,
  input  [31:0] IR,
  input  zero_ext_IMM,
  output [31:0] IMM
);

  wire [16:0] multiplexer_1_out, multiplexer_2_out, multiplexer_3_out;

  Multiplexer #(.width(17), .enable("false")) multiplexer_1 (
    .in0(17'ha), .in1({{12{1'b0}}, IR[10:6]}), .out(multiplexer_1_out), .sel(extend_shamt));
  Multiplexer #(.width(17), .enable("false")) multiplexer_2 (
    .in0({{2{IR[15]}}, IR[14:0]}), .in1({1'b0, IR[15:0]}), .out(multiplexer_2_out), .sel(zero_ext_IMM));
  assign IMM = {{15{multiplexer_3_out[16]}}, multiplexer_3_out};  // Bit_Extender bit_extender_1
  Multiplexer #(.width(17), .enable("false")) multiplexer_3 (
    .in0(multiplexer_1_out), .in1(multiplexer_2_out), .out(multiplexer_3_out), .sel(extend_IMM));
endmodule

module NPC (
  input  ALU_Equal,
  input  [31:0] ALU_R,
  input  [31:0] CTRL,
  input  [31:0] IMM,
  input  [31:0] PC_plus_1,
  input  [31:0] IR,
  input  [31:0] RF_A,
  output branch,
  output goto,
  output jump,
  output [31:0] new_addr
);

  wire and_1_out, and_2_out, and_3_out;
  wire [31:0] adder_1_out, multiplexer_1_out;

  Adder #(.width(32)) adder_1 (.a({IMM[29:0], 2'b00}), .b(PC_plus_1), .out(adder_1_out));  // open: cin, cout
  and and_1 (and_1_out, ALU_R[0], CTRL[9]);
  or or_1 (branch, and_1_out, and_2_out, and_3_out);
  and and_2 (and_2_out, ALU_Equal, CTRL[11]);
  and and_3 (and_3_out, ~ALU_Equal, CTRL[10]);  // AND_Gate
  Multiplexer #(.width(32), .enable("false")) multiplexer_1 (
    .in0({PC_plus_1[31:28], IR[25:0], 2'b00}), .in1(RF_A), .out(multiplexer_1_out), .sel(CTRL[12]));
  Multiplexer #(.width(32), .enable("false")) multiplexer_2 (
    .in0(adder_1_out), .in1(multiplexer_1_out), .out(new_addr), .sel(CTRL[13]));
  or or_2 (goto, branch, CTRL[13]);

  assign jump = CTRL[13];

  // Other names for the same wires on the sheet: bltz = CTRL[9]; bne = CTRL[10]; beq = CTRL[11];
  //   jump_register = CTRL[12]
endmodule

module IF_ID (
  input  CLK,
  input  lock,
  input  clear,
  input  [31:0] IF_PC,
  input  [31:0] IF_PC_plus_1,
  input  [31:0] IF_IR,
  output [31:0] ID_PC,
  output [31:0] ID_PC_plus_1,
  output [31:0] ID_IR
);

  wire [31:0] multiplexer_1_out, multiplexer_2_out, multiplexer_3_out;

  Multiplexer #(.width(32), .enable("false")) multiplexer_1 (
    .in0(IF_PC), .in1({32{1'b0}}), .out(multiplexer_1_out), .sel(clear));
  Multiplexer #(.width(32), .enable("false")) multiplexer_2 (
    .in0(IF_PC_plus_1), .in1({32{1'b0}}), .out(multiplexer_2_out), .sel(clear));
  Multiplexer #(.width(32), .enable("false")) multiplexer_3 (
    .in0(IF_IR), .in1({32{1'b0}}), .out(multiplexer_3_out), .sel(clear));
  Register #(.width(32)) register_1 (.D(multiplexer_1_out), .en(lock), .clk(CLK), .Q(ID_PC));  // open: clr
  Register #(.width(32)) register_2 (.D(multiplexer_2_out), .en(lock), .clk(CLK), .Q(ID_PC_plus_1));  // open: clr
  Register #(.width(32)) register_3 (.D(multiplexer_3_out), .en(lock), .clk(CLK), .Q(ID_IR));  // open: clr
endmodule

module ID_EX (
  input  CLK,
  input  lock,
  input  clear,
  input  [31:0] ID_PC,
  input  [31:0] ID_PC_plus_1,
  input  [31:0] ID_IR,
  input  [31:0] ID_CTRL,
  input  [31:0] ID_RF_A,
  input  [31:0] ID_RF_B,
  input  [4:0] ID_rW,
  input  [31:0] ID_IMM,
  output [31:0] EX_PC,
  output [31:0] EX_PC_plus_1,
  output [31:0] EX_IR,
  output [31:0] EX_CTRL,
  output [31:0] EX_RF_A,
  output [31:0] EX_RF_B,
  output [4:0] EX_rW,
  output [31:0] EX_IMM
);

  wire [4:0] multiplexer_7_out;
  wire [31:0] multiplexer_1_out, multiplexer_2_out, multiplexer_3_out, multiplexer_4_out, multiplexer_5_out,
       multiplexer_6_out, multiplexer_8_out;

  Multiplexer #(.width(32), .enable("false")) multiplexer_1 (
    .in0(ID_PC), .in1({32{1'b0}}), .out(multiplexer_1_out), .sel(clear));
  Multiplexer #(.width(32), .enable("false")) multiplexer_2 (
    .in0(ID_PC_plus_1), .in1({32{1'b0}}), .out(multiplexer_2_out), .sel(clear));
  Multiplexer #(.width(32), .enable("false")) multiplexer_3 (
    .in0(ID_IR), .in1({32{1'b0}}), .out(multiplexer_3_out), .sel(clear));
  Multiplexer #(.width(32), .enable("false")) multiplexer_4 (
    .in0(ID_CTRL), .in1({32{1'b0}}), .out(multiplexer_4_out), .sel(clear));
  Multiplexer #(.width(32), .enable("false")) multiplexer_5 (
    .in0(ID_RF_A), .in1({32{1'b0}}), .out(multiplexer_5_out), .sel(clear));
  Multiplexer #(.width(32), .enable("false")) multiplexer_6 (
    .in0(ID_RF_B), .in1({32{1'b0}}), .out(multiplexer_6_out), .sel(clear));
  Multiplexer #(.width(5), .enable("false")) multiplexer_7 (
    .in0(ID_rW), .in1({5{1'b0}}), .out(multiplexer_7_out), .sel(clear));
  Multiplexer #(.width(32), .enable("false")) multiplexer_8 (
    .in0(ID_IMM), .in1({32{1'b0}}), .out(multiplexer_8_out), .sel(clear));
  Register #(.width(32)) register_1 (.D(multiplexer_1_out), .en(lock), .clk(CLK), .Q(EX_PC));  // open: clr
  Register #(.width(32)) register_2 (.D(multiplexer_2_out), .en(lock), .clk(CLK), .Q(EX_PC_plus_1));  // open: clr
  Register #(.width(32)) register_3 (.D(multiplexer_3_out), .en(lock), .clk(CLK), .Q(EX_IR));  // open: clr
  Register #(.width(32)) register_4 (.D(multiplexer_4_out), .en(lock), .clk(CLK), .Q(EX_CTRL));  // open: clr
  Register #(.width(32)) register_5 (.D(multiplexer_5_out), .en(lock), .clk(CLK), .Q(EX_RF_A));  // open: clr
  Register #(.width(32)) register_6 (.D(multiplexer_6_out), .en(lock), .clk(CLK), .Q(EX_RF_B));  // open: clr
  Register #(.width(5)) register_7 (.D(multiplexer_7_out), .en(lock), .clk(CLK), .Q(EX_rW));  // open: clr
  Register #(.width(32)) register_8 (.D(multiplexer_8_out), .en(lock), .clk(CLK), .Q(EX_IMM));  // open: clr
endmodule

module EX_MEM (
  input  CLK,
  input  lock,
  input  clear,
  input  [31:0] EX_PC,
  input  [31:0] EX_PC_plus_1,
  input  [31:0] EX_CTRL,
  input  [4:0] EX_rW,
  input  [31:0] EX_RF_B,
  input  [31:0] EX_ALU_R,
  input  EX_HALT,
  output [31:0] MEM_PC,
  output [31:0] MEM_PC_plus_1,
  output [31:0] MEM_CTRL,
  output [4:0] MEM_rW,
  output [31:0] MEM_RF_B,
  output [31:0] MEM_ALU_R,
  output MEM_HALT
);

  wire multiplexer_7_out;
  wire [4:0] multiplexer_4_out;
  wire [31:0] multiplexer_1_out, multiplexer_2_out, multiplexer_3_out, multiplexer_5_out, multiplexer_6_out;

  Multiplexer #(.width(32), .enable("false")) multiplexer_1 (
    .in0(EX_PC), .in1({32{1'b0}}), .out(multiplexer_1_out), .sel(clear));
  Multiplexer #(.width(32), .enable("false")) multiplexer_2 (
    .in0(EX_PC_plus_1), .in1({32{1'b0}}), .out(multiplexer_2_out), .sel(clear));
  Multiplexer #(.width(32), .enable("false")) multiplexer_3 (
    .in0(EX_CTRL), .in1({32{1'b0}}), .out(multiplexer_3_out), .sel(clear));
  Multiplexer #(.width(5), .enable("false")) multiplexer_4 (
    .in0(EX_rW), .in1({5{1'b0}}), .out(multiplexer_4_out), .sel(clear));
  Multiplexer #(.width(32), .enable("false")) multiplexer_5 (
    .in0(EX_RF_B), .in1({32{1'b0}}), .out(multiplexer_5_out), .sel(clear));
  Multiplexer #(.width(32), .enable("false")) multiplexer_6 (
    .in0(EX_ALU_R), .in1({32{1'b0}}), .out(multiplexer_6_out), .sel(clear));
  Multiplexer #(.enable("false")) multiplexer_7 (.in0(EX_HALT), .in1(1'b0), .out(multiplexer_7_out), .sel(clear));
  Register #(.width(32)) register_1 (.D(multiplexer_1_out), .en(lock), .clk(CLK), .Q(MEM_PC));  // open: clr
  Register #(.width(32)) register_2 (.D(multiplexer_2_out), .en(lock), .clk(CLK), .Q(MEM_PC_plus_1));  // open: clr
  Register #(.width(32)) register_3 (.D(multiplexer_3_out), .en(lock), .clk(CLK), .Q(MEM_CTRL));  // open: clr
  Register #(.width(5)) register_4 (.D(multiplexer_4_out), .en(lock), .clk(CLK), .Q(MEM_rW));  // open: clr
  Register #(.width(32)) register_5 (.D(multiplexer_5_out), .en(lock), .clk(CLK), .Q(MEM_RF_B));  // open: clr
  Register #(.width(32)) register_6 (.D(multiplexer_6_out), .en(lock), .clk(CLK), .Q(MEM_ALU_R));  // open: clr
  Register #(.width(1)) register_7 (.D(multiplexer_7_out), .en(lock), .clk(CLK), .Q(MEM_HALT));  // open: clr
endmodule

module MEM_WB (
  input  CLK,
  input  lock,
  input  clear,
  input  [31:0] MEM_PC,
  input  [31:0] MEM_PC_plus_1,
  input  [31:0] MEM_CTRL,
  input  [4:0] MEM_rW,
  input  [31:0] MEM_ALU_R,
  input  [31:0] MEM_DM_D,
  input  MEM_HALT,
  output [31:0] WB_PC,
  output [31:0] WB_PC_plus_1,
  output [31:0] WB_CTRL,
  output [4:0] WB_rW,
  output [31:0] WB_ALU_R,
  output [31:0] WB_DM_D,
  output WB_HALT
);

  wire multiplexer_7_out;
  wire [4:0] multiplexer_4_out;
  wire [31:0] multiplexer_1_out, multiplexer_2_out, multiplexer_3_out, multiplexer_5_out, multiplexer_6_out;

  Multiplexer #(.width(32), .enable("false")) multiplexer_1 (
    .in0(MEM_PC), .in1({32{1'b0}}), .out(multiplexer_1_out), .sel(clear));
  Multiplexer #(.width(32), .enable("false")) multiplexer_2 (
    .in0(MEM_PC_plus_1), .in1({32{1'b0}}), .out(multiplexer_2_out), .sel(clear));
  Multiplexer #(.width(32), .enable("false")) multiplexer_3 (
    .in0(MEM_CTRL), .in1({32{1'b0}}), .out(multiplexer_3_out), .sel(clear));
  Multiplexer #(.width(5), .enable("false")) multiplexer_4 (
    .in0(MEM_rW), .in1({5{1'b0}}), .out(multiplexer_4_out), .sel(clear));
  Multiplexer #(.width(32), .enable("false")) multiplexer_5 (
    .in0(MEM_ALU_R), .in1({32{1'b0}}), .out(multiplexer_5_out), .sel(clear));
  Multiplexer #(.width(32), .enable("false")) multiplexer_6 (
    .in0(MEM_DM_D), .in1({32{1'b0}}), .out(multiplexer_6_out), .sel(clear));
  Multiplexer #(.enable("false")) multiplexer_7 (.in0(MEM_HALT), .in1(1'b0), .out(multiplexer_7_out), .sel(clear));
  Register #(.width(32)) register_1 (.D(multiplexer_1_out), .en(lock), .clk(CLK), .Q(WB_PC));  // open: clr
  Register #(.width(32)) register_2 (.D(multiplexer_2_out), .en(lock), .clk(CLK), .Q(WB_PC_plus_1));  // open: clr
  Register #(.width(32)) register_3 (.D(multiplexer_3_out), .en(lock), .clk(CLK), .Q(WB_CTRL));  // open: clr
  Register #(.width(5)) register_4 (.D(multiplexer_4_out), .en(lock), .clk(CLK), .Q(WB_rW));  // open: clr
  Register #(.width(32)) register_5 (.D(multiplexer_5_out), .en(lock), .clk(CLK), .Q(WB_ALU_R));  // open: clr
  Register #(.width(32)) register_6 (.D(multiplexer_6_out), .en(lock), .clk(CLK), .Q(WB_DM_D));  // open: clr
  Register #(.width(1)) register_7 (.D(multiplexer_7_out), .en(lock), .clk(CLK), .Q(WB_HALT));  // open: clr
endmodule

module Redirecter (
  input  [31:0] Control_signals,
  input  [5:0] EX_OP,
  input  [4:0] EX_rW,
  input  EX_RF_WE,
  input  [4:0] rA,
  input  [4:0] rB,
  input  [31:0] EX_Data,
  input  [4:0] MEM_rW,
  input  [31:0] MEM_Data,
  input  MEM_RF_WE,
  output redirect_RF_A,
  output [31:0] redirected_RF_A,
  output Load_Use,
  output [31:0] redirected_RF_B,
  output redirect_RF_B
);

  wire and_1_out, and_2_out, and_3_out, and_4_out, and_5_out, and_6_out, and_7_out, and_8_out, and_9_out,
       and_10_out, and_11_out, and_12_out, and_13_out, and_14_out, and_16_out, and_17_out, and_18_out,
       comparator_1_eq, comparator_2_eq, comparator_3_eq, comparator_4_eq, comparator_5_eq, comparator_6_eq,
       comparator_7_eq, comparator_8_eq, comparator_9_eq, comparator_10_eq, EX_d42e9320, EX_lh, EX_lw, EX_sw,
       MEM_548fd6b1, not_1_out, not_2_out, or_3_out, or_4_out, or_5_out, or_6_out, or_10_out, or_12_out,
       or_13_out, or_14_out, rA_EX, rA_MEM, rB_EX_edc59a79, rB_MEM_d8009108;

  Comparator #(.width(5)) comparator_1 (.a(EX_rW), .b(rA), .eq(comparator_1_eq));  // open: gt, lt
  Comparator #(.width(5)) comparator_2 (.a(EX_rW), .b(rB), .eq(comparator_2_eq));  // open: gt, lt
  Comparator #(.width(5)) comparator_3 (.a(EX_rW), .b({5{1'b0}}), .eq(comparator_3_eq));  // open: gt, lt
  Comparator #(.width(5)) comparator_4 (.a(EX_rW), .b(5'b00010), .eq(comparator_4_eq));  // open: gt, lt
  Comparator #(.width(5)) comparator_5 (.a(EX_rW), .b(5'b00100), .eq(comparator_5_eq));  // open: gt, lt
  Comparator #(.width(5)) comparator_6 (.a(MEM_rW), .b(rA), .eq(comparator_6_eq));  // open: gt, lt
  Comparator #(.width(5)) comparator_7 (.a(MEM_rW), .b(rB), .eq(comparator_7_eq));  // open: gt, lt
  Comparator #(.width(5)) comparator_8 (.a(MEM_rW), .b({5{1'b0}}), .eq(comparator_8_eq));  // open: gt, lt
  Comparator #(.width(5)) comparator_9 (.a(MEM_rW), .b(5'b00010), .eq(comparator_9_eq));  // open: gt, lt
  Comparator #(.width(5)) comparator_10 (.a(MEM_rW), .b(5'b00100), .eq(comparator_10_eq));  // open: gt, lt
  and and_1 (and_1_out, comparator_1_eq, Control_signals[6]);
  and and_2 (and_2_out, comparator_2_eq, Control_signals[5]);
  and and_3 (and_3_out, comparator_4_eq, Control_signals[8]);
  and and_4 (and_4_out, comparator_5_eq, Control_signals[8]);
  and and_5 (and_5_out, comparator_6_eq, Control_signals[6]);
  and and_6 (and_6_out, comparator_7_eq, Control_signals[5]);
  and and_7 (and_7_out, comparator_9_eq, Control_signals[8]);
  and and_8 (and_8_out, comparator_10_eq, Control_signals[8]);
  Comparator #(.width(6)) comparator_11 (.a(EX_OP), .b(6'b100001), .eq(EX_lh));  // open: gt, lt
  Comparator #(.width(6)) comparator_12 (.a(EX_OP), .b(6'b100011), .eq(EX_lw));  // open: gt, lt
  Comparator #(.width(6)) comparator_13 (.a(EX_OP), .b(6'b101011), .eq(EX_sw));  // open: gt, lt
  or or_1 (rA_EX, and_1_out, and_3_out);
  or or_2 (rA_MEM, and_5_out, and_7_out);
  or or_3 (or_3_out, and_1_out, and_2_out);
  not not_1 (not_1_out, comparator_3_eq);
  or or_4 (or_4_out, and_3_out, and_4_out);
  or or_5 (or_5_out, and_5_out, and_6_out);
  not not_2 (not_2_out, comparator_8_eq);
  or or_6 (or_6_out, and_7_out, and_8_out);
  or or_7 (rB_MEM_d8009108, and_8_out, and_6_out);
  or or_8 (rB_EX_edc59a79, and_4_out, and_2_out);
  and and_9 (and_9_out, or_3_out, not_1_out, EX_RF_WE);
  and and_10 (and_10_out, EX_RF_WE, or_4_out);
  and and_11 (and_11_out, or_5_out, not_2_out, MEM_RF_WE);
  and and_12 (and_12_out, MEM_RF_WE, or_6_out);
  or or_9 (EX_d42e9320, and_9_out, and_10_out);
  or or_10 (or_10_out, EX_sw, EX_lw, EX_lh);
  or or_11 (MEM_548fd6b1, and_11_out, and_12_out);
  and and_13 (and_13_out, rA_EX, EX_d42e9320);
  and and_14 (and_14_out, rA_MEM, MEM_548fd6b1);
  and and_15 (Load_Use, EX_d42e9320, or_10_out);
  and and_16 (and_16_out, ~or_10_out, EX_d42e9320);  // AND_Gate
  and and_17 (and_17_out, MEM_548fd6b1, rB_MEM_d8009108);
  and and_18 (and_18_out, EX_d42e9320, rB_EX_edc59a79);
  or or_12 (or_12_out, and_13_out, and_14_out);
  or or_13 (or_13_out, and_16_out, MEM_548fd6b1);
  or or_14 (or_14_out, and_17_out, and_18_out);
  and and_19 (redirect_RF_A, or_12_out, or_13_out);
  and and_20 (redirect_RF_B, or_13_out, or_14_out);
  Multiplexer #(.width(32), .enable("false")) multiplexer_1 (
    .in0(MEM_Data), .in1(EX_Data), .out(redirected_RF_A), .sel(and_13_out));
  Multiplexer #(.width(32), .enable("false")) multiplexer_2 (
    .in0(MEM_Data), .in1(EX_Data), .out(redirected_RF_B), .sel(and_18_out));

  // Other names for the same wires on the sheet: read_rB = Control_signals[5]; read_rA = Control_signals[6];
  //   syscall = Control_signals[8]
endmodule
