// Logisim project alu.circ as structural Verilog
// FA
module \一位全加器FA封装1  (
  input  Cin,
  input  Xi,
  input  Yi,
  output Cout,
  output Si
);

  wire AND_2_out, AND_out, XOR_2_out;

  or OR (Cout, AND_out, AND_2_out);
  and AND (AND_out, Xi, Yi);
  and AND_2 (AND_2_out, Cin, XOR_2_out);
  xor XOR (Si, Cin, XOR_2_out);
  xor XOR_2 (XOR_2_out, Xi, Yi);

  // Notes on the sheet:
  //   Si = Xi ^ Yi ^ Cin
  //   Cout = Xi Yi + Cin (Xi ^ Yi)
endmodule

module \一位全加器FA封装2  (
  input  Cin,
  input  Xi,
  input  Yi,
  output Cout,
  output Si
);

  wire AND_2_out, AND_out, XOR_2_out;

  or OR (Cout, AND_out, AND_2_out);
  and AND (AND_out, Xi, Yi);
  and AND_2 (AND_2_out, Cin, XOR_2_out);
  xor XOR (Si, Cin, XOR_2_out);
  xor XOR_2 (XOR_2_out, Xi, Yi);

  // Notes on the sheet:
  //   Si = Xi ^ Yi ^ Cin
  //   Cout = Xi Yi + Cin (Xi ^ Yi)
endmodule

module \一位全加器FA封装3  (
  input  Cin,
  input  Xi,
  input  Yi,
  output Cout,
  output Si
);

  wire AND_2_out, AND_out, XOR_2_out;

  or OR (Cout, AND_out, AND_2_out);
  and AND (AND_out, Xi, Yi);
  and AND_2 (AND_2_out, Cin, XOR_2_out);
  xor XOR (Si, Cin, XOR_2_out);
  xor XOR_2 (XOR_2_out, Xi, Yi);

  // Notes on the sheet:
  //   Si = Xi ^ Yi ^ Cin
  //   Cout = Xi Yi + Cin (Xi ^ Yi)
endmodule

// ADD
module \_8位串行加法器  (
  input  [7:0] X,
  input  [7:0] Y,
  input  Cin,
  output [7:0] S,
  output Cout,
  output Overflow
);

  wire \一位全加器fa封装1_2_cout , \一位全加器fa封装1_3_cout , \一位全加器fa封装1_4_cout , \一位全加器fa封装1_5_cout ,
       \一位全加器fa封装1_6_cout , \一位全加器fa封装1_7_cout , \一位全加器fa封装1_8_cout ;

  xor xor_1 (Overflow, Cout, \一位全加器fa封装1_2_cout );
  \一位全加器FA封装1  \u_一位全加器fa封装1_1  (.Cout(Cout), .Si(S[7]), .Cin(\一位全加器fa封装1_2_cout ), .Xi(X[7]), .Yi(Y[7]));
  \一位全加器FA封装1  \u_一位全加器fa封装1_2  (
    .Cout(\一位全加器fa封装1_2_cout ), .Si(S[6]), .Cin(\一位全加器fa封装1_3_cout ), .Xi(X[6]), .Yi(Y[6]));
  \一位全加器FA封装1  \u_一位全加器fa封装1_3  (
    .Cout(\一位全加器fa封装1_3_cout ), .Si(S[5]), .Cin(\一位全加器fa封装1_4_cout ), .Xi(X[5]), .Yi(Y[5]));
  \一位全加器FA封装1  \u_一位全加器fa封装1_4  (
    .Cout(\一位全加器fa封装1_4_cout ), .Si(S[4]), .Cin(\一位全加器fa封装1_5_cout ), .Xi(X[4]), .Yi(Y[4]));
  \一位全加器FA封装1  \u_一位全加器fa封装1_5  (
    .Cout(\一位全加器fa封装1_5_cout ), .Si(S[3]), .Cin(\一位全加器fa封装1_6_cout ), .Xi(X[3]), .Yi(Y[3]));
  \一位全加器FA封装1  \u_一位全加器fa封装1_6  (
    .Cout(\一位全加器fa封装1_6_cout ), .Si(S[2]), .Cin(\一位全加器fa封装1_7_cout ), .Xi(X[2]), .Yi(Y[2]));
  // Probe on X
  // Probe on Y
  // Probe on S
  \一位全加器FA封装1  \u_一位全加器fa封装1_7  (
    .Cout(\一位全加器fa封装1_7_cout ), .Si(S[1]), .Cin(\一位全加器fa封装1_8_cout ), .Xi(X[1]), .Yi(Y[1]));
  // Probe on X
  // Probe on Y
  // Probe on S
  \一位全加器FA封装1  \u_一位全加器fa封装1_8  (.Cout(\一位全加器fa封装1_8_cout ), .Si(S[0]), .Cin(Cin), .Xi(X[0]), .Yi(Y[0]));

  // Other names for the same wires on the sheet: OF = Overflow

  // Notes on the sheet:
  //   输入引脚区
  //   符号位
  //   输出引脚区
  //   +
  //   =
  //   有符号加法
  //   +
  //   =
  //   无符号加法
endmodule

// CAS
module \_8位可控加减法器  (
  input  [7:0] X,
  input  [7:0] Y,
  input  Cin,
  input  Sub,
  output [7:0] S,
  output Cout,
  output Overflow
);

  wire or_1_out, xor_2_out, xor_3_out, xor_4_out, xor_5_out, xor_6_out, xor_7_out, xor_8_out, xor_9_out,
       \一位全加器fa封装1_2_cout , \一位全加器fa封装1_3_cout , \一位全加器fa封装1_4_cout , \一位全加器fa封装1_5_cout ,
       \一位全加器fa封装1_6_cout , \一位全加器fa封装1_7_cout , \一位全加器fa封装1_8_cout ;
  wire [8:0] C;

  xor xor_1 (Overflow, Cout, \一位全加器fa封装1_2_cout );
  \一位全加器FA封装1  \u_一位全加器fa封装1_1  (.Cout(Cout), .Si(S[7]), .Cin(\一位全加器fa封装1_2_cout ), .Xi(X[7]), .Yi(xor_2_out));
  xor xor_2 (xor_2_out, Y[7], Sub);
  \一位全加器FA封装1  \u_一位全加器fa封装1_2  (
    .Cout(\一位全加器fa封装1_2_cout ), .Si(S[6]), .Cin(\一位全加器fa封装1_3_cout ), .Xi(X[6]), .Yi(xor_3_out));
  xor xor_3 (xor_3_out, Y[6], Sub);
  \一位全加器FA封装1  \u_一位全加器fa封装1_3  (
    .Cout(\一位全加器fa封装1_3_cout ), .Si(S[5]), .Cin(\一位全加器fa封装1_4_cout ), .Xi(X[5]), .Yi(xor_4_out));
  xor xor_4 (xor_4_out, Y[5], Sub);
  \一位全加器FA封装1  \u_一位全加器fa封装1_4  (
    .Cout(\一位全加器fa封装1_4_cout ), .Si(S[4]), .Cin(\一位全加器fa封装1_5_cout ), .Xi(X[4]), .Yi(xor_5_out));
  xor xor_5 (xor_5_out, Y[4], Sub);
  \一位全加器FA封装1  \u_一位全加器fa封装1_5  (
    .Cout(\一位全加器fa封装1_5_cout ), .Si(S[3]), .Cin(\一位全加器fa封装1_6_cout ), .Xi(X[3]), .Yi(xor_6_out));
  xor xor_6 (xor_6_out, Y[3], Sub);
  \一位全加器FA封装1  \u_一位全加器fa封装1_6  (
    .Cout(\一位全加器fa封装1_6_cout ), .Si(S[2]), .Cin(\一位全加器fa封装1_7_cout ), .Xi(X[2]), .Yi(xor_7_out));
  xor xor_7 (xor_7_out, Y[2], Sub);
  // Probe on X
  // Probe on Y
  // Probe on S
  \一位全加器FA封装1  \u_一位全加器fa封装1_7  (
    .Cout(\一位全加器fa封装1_7_cout ), .Si(S[1]), .Cin(\一位全加器fa封装1_8_cout ), .Xi(X[1]), .Yi(xor_8_out));
  xor xor_8 (xor_8_out, Y[1], Sub);
  or or_1 (or_1_out, Cin, Sub);
  \一位全加器FA封装1  \u_一位全加器fa封装1_8  (.Cout(\一位全加器fa封装1_8_cout ), .Si(S[0]), .Cin(or_1_out), .Xi(X[0]), .Yi(xor_9_out));
  xor xor_9 (xor_9_out, Y[0], Sub);
  // Probe on X
  // Probe on Y
  // Probe on S
  Multiplexer #(.width(9), .enable("false")) multiplexer_1 (.in0(9'hba), .in1(9'h92), .out(C), .sel(Sub));

  // Other names for the same wires on the sheet: OF = Overflow

  // Notes on the sheet:
  //   输入引脚区
  //   符号位
  //   输出引脚区
  //   =
  //   有符号
  //   =
  //   无符号
endmodule

// CLA74182
module CLA74182 (
  input  G4,
  input  P4,
  input  G3,
  input  P3,
  input  G2,
  input  P2,
  input  G1,
  input  P1,
  input  Cin,
  output C4,
  output C3,
  output C2,
  output C1,
  output G_star,
  output P_star
);

  wire and_1_out, and_2_out, and_3_out, and_4_out, and_5_out, and_6_out, and_7_out, and_8_out, and_9_out,
       and_10_out, and_11_out, and_12_out, and_13_out, and_14_out, and_15_out, and_16_out, and_17_out,
       and_18_out, and_19_out, and_20_out, and_21_out, and_22_out, and_23_out, and_24_out, and_25_out,
       and_26_out, and_27_out, and_28_out, and_29_out, or_1_out, or_3_out, or_4_out, or_5_out, or_6_out,
       or_8_out, or_10_out, or_12_out;

  and and_1 (and_1_out, P4, P3);
  and and_2 (and_2_out, P3, P2);
  and and_3 (and_3_out, P3, P2);
  and and_4 (and_4_out, P1, Cin);
  and and_5 (and_5_out, P2, G1);
  and and_6 (and_6_out, P2, P1);
  and and_7 (and_7_out, P1, Cin);
  and and_8 (and_8_out, P4, P3);
  and and_9 (and_9_out, P4, P3);
  and and_10 (and_10_out, P2, G1);
  and and_11 (and_11_out, P4, P3);
  and and_12 (and_12_out, P4, G3);
  and and_13 (and_13_out, P4, P3);
  and and_14 (and_14_out, P4, P3);
  and and_15 (and_15_out, P2, G1);
  and and_16 (and_16_out, and_1_out, P2);
  and and_17 (and_17_out, P1, Cin);
  and and_18 (and_18_out, P3, G2);
  and and_19 (and_19_out, and_2_out, G1);
  and and_20 (and_20_out, and_3_out, and_4_out);
  or or_1 (or_1_out, G2, and_5_out);
  and and_21 (and_21_out, and_6_out, Cin);
  or or_2 (C1, G1, and_7_out);
  and and_22 (and_22_out, P4, G3);
  and and_23 (and_23_out, and_8_out, G2);
  and and_24 (and_24_out, and_9_out, and_10_out);
  and and_25 (and_25_out, and_11_out, P2);
  and and_26 (and_26_out, P1, Cin);
  or or_3 (or_3_out, G4, and_12_out);
  or or_4 (or_4_out, or_3_out, and_27_out);
  and and_27 (and_27_out, and_13_out, G2);
  and and_28 (and_28_out, and_14_out, and_15_out);
  or or_5 (or_5_out, and_28_out, and_29_out);
  and and_29 (and_29_out, and_16_out, and_17_out);
  or or_6 (or_6_out, G3, and_18_out);
  or or_7 (C3, or_6_out, or_8_out);
  or or_8 (or_8_out, and_19_out, and_20_out);
  or or_9 (C2, or_1_out, and_21_out);
  or or_10 (or_10_out, G4, and_22_out);
  or or_11 (G_star, or_10_out, or_12_out);
  or or_12 (or_12_out, and_23_out, and_24_out);
  and and_30 (P_star, and_25_out, and_26_out);
  or or_13 (C4, or_4_out, or_5_out);

  // Notes on the sheet:
  //   输入引脚区
  //   请根据以上引脚以及隧道信号设计完成74LS182先行进位电路
  //   输出引脚区
  //   请勿增改引脚定义
endmodule

// 4位快速加法器
module \_4位快速加法器  (
  input  [3:0] X,
  input  [3:0] Y,
  input  Cin,
  output [3:0] S,
  output Cout,
  output G_star,
  output P_star
);

  wire and_1_out, and_2_out, and_3_out, and_4_out, cla74182_1_c1, cla74182_1_c2, cla74182_1_c3, or_1_out,
       or_2_out, or_3_out, or_4_out;

  CLA74182 cla74182_1 (
    .G4(and_1_out), .P4(or_1_out), .G3(and_2_out), .P3(or_2_out), .G2(and_3_out), .P2(or_3_out),
    .G1(and_4_out), .P1(or_4_out), .Cin(Cin), .C4(Cout), .C3(cla74182_1_c3), .C2(cla74182_1_c2),
    .C1(cla74182_1_c1), .G_star(G_star), .P_star(P_star));
  or or_1 (or_1_out, X[3], Y[3]);
  and and_1 (and_1_out, X[3], Y[3]);
  \一位全加器FA封装1  \u_一位全加器fa封装1_1  (.Si(S[3]), .Cin(cla74182_1_c3), .Xi(X[3]), .Yi(Y[3]));  // open: Cout
  or or_2 (or_2_out, X[2], Y[2]);
  and and_2 (and_2_out, X[2], Y[2]);
  \一位全加器FA封装1  \u_一位全加器fa封装1_2  (.Si(S[2]), .Cin(cla74182_1_c2), .Xi(X[2]), .Yi(Y[2]));  // open: Cout
  or or_3 (or_3_out, X[1], Y[1]);
  and and_3 (and_3_out, X[1], Y[1]);
  \一位全加器FA封装1  \u_一位全加器fa封装1_3  (.Si(S[1]), .Cin(cla74182_1_c1), .Xi(X[1]), .Yi(Y[1]));  // open: Cout
  and and_4 (and_4_out, X[0], Y[0]);
  or or_4 (or_4_out, X[0], Y[0]);
  \一位全加器FA封装1  \u_一位全加器fa封装1_4  (.Si(S[0]), .Cin(Cin), .Xi(X[0]), .Yi(Y[0]));  // open: Cout
  // Probe on X
  // Probe on Y
  // Probe on S
  // Probe on X
  // Probe on Y
  // Probe on S

  // Notes on the sheet:
  //   输入引脚区
  //   输出引脚区
  //   +
  //   =
  //   有符号加法
  //   +
  //   =
  //   无符号加法
endmodule

// 16位快速加法器
module \_16位快速加法器  (
  input  [15:0] X,
  input  [15:0] Y,
  input  Cin,
  output [15:0] S,
  output Cout,
  output G_star,
  output P_star
);

  wire cla74182_1_c1, cla74182_1_c2, cla74182_1_c3, \n4位快速加法器_1_g_star , \n4位快速加法器_1_p_star ,
       \n4位快速加法器_2_g_star , \n4位快速加法器_2_p_star , \n4位快速加法器_3_g_star , \n4位快速加法器_3_p_star ,
       \n4位快速加法器_4_g_star , \n4位快速加法器_4_p_star ;

  CLA74182 cla74182_1 (
    .G4(\n4位快速加法器_1_g_star ), .P4(\n4位快速加法器_1_p_star ), .G3(\n4位快速加法器_2_g_star ), .P3(\n4位快速加法器_2_p_star ),
    .G2(\n4位快速加法器_3_g_star ), .P2(\n4位快速加法器_3_p_star ), .G1(\n4位快速加法器_4_g_star ), .P1(\n4位快速加法器_4_p_star ),
    .Cin(Cin), .C4(Cout), .C3(cla74182_1_c3), .C2(cla74182_1_c2), .C1(cla74182_1_c1), .G_star(G_star),
    .P_star(P_star));
  \_4位快速加法器  \u_4位快速加法器_1  (
    .X(X[15:12]), .Y(Y[15:12]), .Cin(cla74182_1_c3), .S(S[15:12]), .G_star(\n4位快速加法器_1_g_star ),
    .P_star(\n4位快速加法器_1_p_star ));  // open: Cout
  \_4位快速加法器  \u_4位快速加法器_2  (
    .X(X[11:8]), .Y(Y[11:8]), .Cin(cla74182_1_c2), .S(S[11:8]), .G_star(\n4位快速加法器_2_g_star ),
    .P_star(\n4位快速加法器_2_p_star ));  // open: Cout
  \_4位快速加法器  \u_4位快速加法器_3  (
    .X(X[7:4]), .Y(Y[7:4]), .Cin(cla74182_1_c1), .S(S[7:4]), .G_star(\n4位快速加法器_3_g_star ),
    .P_star(\n4位快速加法器_3_p_star ));  // open: Cout
  // Probe on X
  // Probe on Y
  // Probe on S
  \_4位快速加法器  \u_4位快速加法器_4  (
    .X(X[3:0]), .Y(Y[3:0]), .Cin(Cin), .S(S[3:0]), .G_star(\n4位快速加法器_4_g_star ), .P_star(\n4位快速加法器_4_p_star ));  // open: Cout
  // Probe on X
  // Probe on Y
  // Probe on S

  // Other names for the same wires on the sheet: S0[3:0] = S[3:0]; S1[3:0] = S[7:4]; S2[3:0] = S[11:8];
  //   S3[3:0] = S[15:12]; X0[3:0] = X[3:0]; X1[3:0] = X[7:4]; X2[3:0] = X[11:8]; X3[3:0] = X[15:12]; Y0[3:0] = Y[3:0];
  //   Y1[3:0] = Y[7:4]; Y2[3:0] = Y[11:8]; Y3[3:0] = Y[15:12]

  // Notes on the sheet:
  //   输入引脚区
  //   输出引脚区
  //   +
  //   =
  //   有符号加法
  //   +
  //   =
  //   无符号加法
endmodule

// 32位加法器
module \_32位快速加法器  (
  input  Cin,
  input  [31:0] X,
  input  [31:0] Y,
  output Cout,
  output [31:0] S,
  output Overflow
);

  wire and_1_out, and_2_out, cla74182_1_c1, \n16位快速加法器_1_g_star , \n16位快速加法器_1_p_star , \n16位快速加法器_2_g_star ,
       \n16位快速加法器_2_p_star ;

  and and_1 (and_1_out, ~S[31], X[31], Y[31]);  // AND_Gate
  or or_1 (Overflow, and_1_out, and_2_out);
  CLA74182 cla74182_1 (
    .G4(1'b0), .P4(1'b1), .G3(1'b0), .P3(1'b1), .G2(\n16位快速加法器_1_g_star ), .P2(\n16位快速加法器_1_p_star ),
    .G1(\n16位快速加法器_2_g_star ), .P1(\n16位快速加法器_2_p_star ), .Cin(Cin), .C2(Cout), .C1(cla74182_1_c1));  // open: C4, C3, G_star, P_star
  and and_2 (and_2_out, S[31], ~X[31], ~Y[31]);  // AND_Gate
  \_16位快速加法器  \u_16位快速加法器_1  (
    .X(X[31:16]), .Y(Y[31:16]), .Cin(cla74182_1_c1), .S(S[31:16]), .G_star(\n16位快速加法器_1_g_star ),
    .P_star(\n16位快速加法器_1_p_star ));  // open: Cout
  // Probe on X
  // Probe on Y
  // Probe on S
  \_16位快速加法器  \u_16位快速加法器_2  (
    .X(X[15:0]), .Y(Y[15:0]), .Cin(Cin), .S(S[15:0]), .G_star(\n16位快速加法器_2_g_star ),
    .P_star(\n16位快速加法器_2_p_star ));  // open: Cout
  // Probe on X
  // Probe on Y
  // Probe on S

  // Other names for the same wires on the sheet: S0[15:0] = S[15:0]; S1[15:0] = S[31:16]; X0[15:0] = X[15:0];
  //   X1[15:0] = X[31:16]; Y0[15:0] = Y[15:0]; Y1[15:0] = Y[31:16]

  // Notes on the sheet:
  //   输入引脚区
  //   输出引脚区
  //   +
  //   =
  //   有符号加法
  //   +
  //   =
  //   无符号加法
endmodule

module \补码一位乘法器  (
  input  [7:0] X,
  input  [7:0] Y,
  output [15:0] \乘积 
);

  wire ALU_R0, and_1_out, and_2_out, and_3_out, Clear, CLK, counter_1_carry, counter_2_carry, decoder_1_out1,
       decoder_1_out2, En, LoadData, not_3_out, not_4_out, nYn, nYn_1, R0_ALU, tunnel, Yn_1, Yn_Yn_1;
  wire [1:0] counter_1_q;
  wire [3:0] counter_2_q;
  wire [7:0] controlled_buffer_1_out, multiplexer_1_out, multiplexer_2_out, \n8位串行加法器_1_s , register_2_q,
       register_3_q, X_q;

  Button Start (.out(Clear));
  Clock clock_1 (.out(CLK));
  Multiplexer #(.width(8), .enable("false")) multiplexer_1 (
    .in0(register_2_q), .in1({{2{\乘积 [15]}}, \乘积 [14:9]}), .out(multiplexer_1_out), .sel(tunnel));
  Register register (.D(multiplexer_1_out), .en(En), .Q(\乘积 [15:8]), .clk(CLK), .clr(Clear));
  Register register_2 (.D(\n8位串行加法器_1_s ), .en(ALU_R0), .Q(register_2_q), .clk(CLK), .clr(Clear));
  \_8位串行加法器  \u_8位串行加法器_1  (
    .X(register_3_q), .Y(controlled_buffer_1_out), .Cin(and_2_out), .S(\n8位串行加法器_1_s ));  // open: Cout, Overflow
  Register register_3 (.D(\乘积 [15:8]), .en(R0_ALU), .Q(register_3_q), .clk(CLK), .clr(Clear));
  assign controlled_buffer_1_out = and_1_out ? X_q : 8'bz;  // Controlled_Buffer controlled_buffer_1
  and and_1 (and_1_out, nYn, Yn_1);
  // Probe on X
  // Probe on \乘积 [15:8]
  Multiplexer #(.width(8), .enable("false")) multiplexer_2 (
    .in0(\乘积 [8:1]), .in1(Y), .out(multiplexer_2_out), .sel(LoadData));
  assign controlled_buffer_1_out = and_2_out ? ~X_q : 8'bz;  // Controlled_Inverter 取反
  and and_2 (and_2_out, \乘积 [0], nYn_1);
  Register u_X (.D(X), .en(LoadData), .Q(X_q), .clk(CLK));  // open: clr
  // Probe on Y
  // Probe on \乘积 [7:0]
  Register Y_2 (.D(multiplexer_2_out), .en(tunnel), .Q(\乘积 [7:0]), .clk(CLK));  // open: clr
  // Probe on \乘积 
  // Probe on Yn_1
  not not_1 (nYn, \乘积 [0]);
  Register #(.width(1)) Yn_1_2 (.D(\乘积 [0]), .en(tunnel), .Q(Yn_1), .clk(CLK), .clr(LoadData));
  Counter #(.width(2), .max('h3)) counter_1 (
    .Q(counter_1_q), .carry(counter_1_carry), .clk(CLK), .clr(Clear));  // open: load, D, count
  Counter #(.width(4), .max('h9), .ongoal("stay")) counter_2 (
    .Q(counter_2_q), .carry(counter_2_carry), .clk(counter_1_carry), .clr(Clear));  // open: load, D, count
  xnor xnor_1 (Yn_Yn_1, \乘积 [0], Yn_1);
  not not_2 (nYn_1, Yn_1);
  Decoder #(.select(2), .disabled(0)) decoder_1 (
    .out0(ALU_R0), .out1(decoder_1_out1), .out2(decoder_1_out2), .out3(R0_ALU), .sel(counter_1_q),
    .en(not_3_out));
  not not_3 (not_3_out, counter_2_carry);
  nor nor_1 (LoadData, counter_2_q[0], counter_2_q[1], counter_2_q[2], counter_2_q[3]);
  not not_4 (not_4_out, Yn_Yn_1);
  and and_3 (and_3_out, not_4_out, decoder_1_out1);
  or or_1 (tunnel, decoder_1_out2, LoadData);
  or or_2 (En, and_3_out, tunnel);

  // Other names for the same wires on the sheet: Yn = \乘积 [0]
endmodule

// 与门阵列
module \_8位乘法与门阵列  (
  input  [7:0] X,
  input  [7:0] Y,
  output [7:0] XY0,
  output [7:0] XY1,
  output [7:0] XY2,
  output [7:0] XY3,
  output [7:0] XY4,
  output [7:0] XY5,
  output [7:0] XY6,
  output [7:0] XY7
);

  and and_1 (XY0[7], X[7], Y[0]);
  and and_2 (XY1[7], X[7], Y[1]);
  and and_3 (XY2[7], X[7], Y[2]);
  and and_4 (XY3[7], X[7], Y[3]);
  and and_5 (XY4[7], X[7], Y[4]);
  and and_6 (XY5[7], X[7], Y[5]);
  and and_7 (XY6[7], X[7], Y[6]);
  and and_8 (XY7[7], X[7], Y[7]);
  and and_9 (XY0[6], X[6], Y[0]);
  and and_10 (XY1[6], X[6], Y[1]);
  and and_11 (XY2[6], X[6], Y[2]);
  and and_12 (XY3[6], X[6], Y[3]);
  and and_13 (XY4[6], X[6], Y[4]);
  and and_14 (XY5[6], X[6], Y[5]);
  and and_15 (XY6[6], X[6], Y[6]);
  and and_16 (XY7[6], X[6], Y[7]);
  and and_17 (XY0[5], X[5], Y[0]);
  and and_18 (XY1[5], X[5], Y[1]);
  and and_19 (XY2[5], X[5], Y[2]);
  and and_20 (XY3[5], X[5], Y[3]);
  and and_21 (XY4[5], X[5], Y[4]);
  and and_22 (XY5[5], X[5], Y[5]);
  and and_23 (XY6[5], X[5], Y[6]);
  and and_24 (XY7[5], X[5], Y[7]);
  and and_25 (XY0[3], X[3], Y[0]);
  and and_26 (XY0[4], X[4], Y[0]);
  and and_27 (XY1[4], X[4], Y[1]);
  and and_28 (XY1[3], X[3], Y[1]);
  and and_29 (XY2[4], X[4], Y[2]);
  and and_30 (XY2[3], X[3], Y[2]);
  and and_31 (XY3[3], X[3], Y[3]);
  and and_32 (XY3[4], X[4], Y[3]);
  and and_33 (XY4[3], X[3], Y[4]);
  and and_34 (XY4[4], X[4], Y[4]);
  and and_35 (XY5[3], X[3], Y[5]);
  and and_36 (XY5[4], X[4], Y[5]);
  and and_37 (XY6[4], X[4], Y[6]);
  and and_38 (XY6[3], X[3], Y[6]);
  and and_39 (XY7[3], X[3], Y[7]);
  and and_40 (XY7[4], X[4], Y[7]);
  and and_41 (XY0[2], X[2], Y[0]);
  and and_42 (XY1[2], X[2], Y[1]);
  and and_43 (XY2[2], X[2], Y[2]);
  and and_44 (XY3[2], X[2], Y[3]);
  and and_45 (XY4[2], X[2], Y[4]);
  and and_46 (XY5[2], X[2], Y[5]);
  and and_47 (XY6[2], X[2], Y[6]);
  and and_48 (XY7[2], X[2], Y[7]);
  and and_49 (XY0[1], X[1], Y[0]);
  and and_50 (XY1[1], X[1], Y[1]);
  and and_51 (XY2[1], X[1], Y[2]);
  and and_52 (XY3[1], X[1], Y[3]);
  and and_53 (XY4[1], X[1], Y[4]);
  and and_54 (XY5[1], X[1], Y[5]);
  and and_55 (XY6[1], X[1], Y[6]);
  and and_56 (XY7[1], X[1], Y[7]);
  and and_57 (XY0[0], X[0], Y[0]);
  and and_58 (XY1[0], X[0], Y[1]);
  and and_59 (XY2[0], X[0], Y[2]);
  and and_60 (XY3[0], X[0], Y[3]);
  and and_61 (XY4[0], X[0], Y[4]);
  and and_62 (XY5[0], X[0], Y[5]);
  and and_63 (XY6[0], X[0], Y[6]);
  and and_64 (XY7[0], X[0], Y[7]);

  // Other names for the same wires on the sheet: X0Y0 = XY0[0]; X1Y0 = XY0[1]; X2Y0 = XY0[2]; X3Y0 = XY0[3];
  //   X4Y0 = XY0[4]; X5Y0 = XY0[5]; X6Y0 = XY0[6]; X7Y0 = XY0[7]; X0Y1 = XY1[0]; X1Y1 = XY1[1]; X2Y1 = XY1[2];
  //   X3Y1 = XY1[3]; X4Y1 = XY1[4]; X5Y1 = XY1[5]; X6Y1 = XY1[6]; X7Y1 = XY1[7]; X0Y2 = XY2[0]; X1Y2 = XY2[1];
  //   X2Y2 = XY2[2]; X3Y2 = XY2[3]; X4Y2 = XY2[4]; X5Y2 = XY2[5]; X6Y2 = XY2[6]; X7Y2 = XY2[7]; X0Y3 = XY3[0];
  //   X1Y3 = XY3[1]; X2Y3 = XY3[2]; X3Y3 = XY3[3]; X4Y3 = XY3[4]; X5Y3 = XY3[5]; X6Y3 = XY3[6]; X7Y3 = XY3[7];
  //   X0Y4 = XY4[0]; X1Y4 = XY4[1]; X2Y4 = XY4[2]; X3Y4 = XY4[3]; X4Y4 = XY4[4]; X5Y4 = XY4[5]; X6Y4 = XY4[6];
  //   X7Y4 = XY4[7]; X0Y5 = XY5[0]; X1Y5 = XY5[1]; X2Y5 = XY5[2]; X3Y5 = XY5[3]; X4Y5 = XY5[4]; X5Y5 = XY5[5];
  //   X6Y5 = XY5[6]; X7Y5 = XY5[7]; X0Y6 = XY6[0]; X1Y6 = XY6[1]; X2Y6 = XY6[2]; X3Y6 = XY6[3]; X4Y6 = XY6[4];
  //   X5Y6 = XY6[5]; X6Y6 = XY6[6]; X7Y6 = XY6[7]; X0Y7 = XY7[0]; X1Y7 = XY7[1]; X2Y7 = XY7[2]; X3Y7 = XY7[3];
  //   X4Y7 = XY7[4]; X5Y7 = XY7[5]; X6Y7 = XY7[6]; X7Y7 = XY7[7]
endmodule

module \_8位斜向进位阵列乘法器  (
  input  [7:0] X,
  input  [7:0] Y,
  output [15:0] \乘积 
);

  wire X0Y1, X0Y2, X0Y3, X0Y4, X0Y5, X0Y6, X0Y7, X1Y0, X1Y1, X1Y2, X1Y3, X1Y4, X1Y5, X1Y6, X1Y7, X2Y0, X2Y1,
       X2Y2, X2Y3, X2Y4, X2Y5, X2Y6, X2Y7, X3Y0, X3Y1, X3Y2, X3Y3, X3Y4, X3Y5, X3Y6, X3Y7, X4Y0, X4Y1, X4Y2,
       X4Y3, X4Y4, X4Y5, X4Y6, X4Y7, X5Y0, X5Y1, X5Y2, X5Y3, X5Y4, X5Y5, X5Y6, X5Y7, X6Y0, X6Y1, X6Y2, X6Y3,
       X6Y4, X6Y5, X6Y6, X6Y7, X7Y0, X7Y1, X7Y2, X7Y3, X7Y4, X7Y5, X7Y6, X7Y7, \一位全加器fa封装3_2_cout ,
       \一位全加器fa封装3_2_si , \一位全加器fa封装3_3_cout , \一位全加器fa封装3_4_cout , \一位全加器fa封装3_4_si , \一位全加器fa封装3_5_cout ,
       \一位全加器fa封装3_5_si , \一位全加器fa封装3_6_cout , \一位全加器fa封装3_7_cout , \一位全加器fa封装3_7_si , \一位全加器fa封装3_8_cout ,
       \一位全加器fa封装3_8_si , \一位全加器fa封装3_9_cout , \一位全加器fa封装3_9_si , \一位全加器fa封装3_10_cout , \一位全加器fa封装3_11_cout ,
       \一位全加器fa封装3_11_si , \一位全加器fa封装3_12_cout , \一位全加器fa封装3_12_si , \一位全加器fa封装3_13_cout ,
       \一位全加器fa封装3_13_si , \一位全加器fa封装3_14_cout , \一位全加器fa封装3_14_si , \一位全加器fa封装3_15_cout ,
       \一位全加器fa封装3_16_cout , \一位全加器fa封装3_16_si , \一位全加器fa封装3_17_cout , \一位全加器fa封装3_17_si ,
       \一位全加器fa封装3_18_cout , \一位全加器fa封装3_18_si , \一位全加器fa封装3_19_cout , \一位全加器fa封装3_19_si ,
       \一位全加器fa封装3_20_cout , \一位全加器fa封装3_20_si , \一位全加器fa封装3_21_cout , \一位全加器fa封装3_22_cout ,
       \一位全加器fa封装3_22_si , \一位全加器fa封装3_23_cout , \一位全加器fa封装3_23_si , \一位全加器fa封装3_24_cout ,
       \一位全加器fa封装3_24_si , \一位全加器fa封装3_25_cout , \一位全加器fa封装3_25_si , \一位全加器fa封装3_26_cout ,
       \一位全加器fa封装3_26_si , \一位全加器fa封装3_27_cout , \一位全加器fa封装3_27_si , \一位全加器fa封装3_28_cout ,
       \一位全加器fa封装3_29_cout , \一位全加器fa封装3_29_si , \一位全加器fa封装3_30_cout , \一位全加器fa封装3_30_si ,
       \一位全加器fa封装3_31_cout , \一位全加器fa封装3_31_si , \一位全加器fa封装3_32_cout , \一位全加器fa封装3_32_si ,
       \一位全加器fa封装3_33_cout , \一位全加器fa封装3_33_si , \一位全加器fa封装3_34_cout , \一位全加器fa封装3_34_si ,
       \一位全加器fa封装3_35_cout , \一位全加器fa封装3_36_cout , \一位全加器fa封装3_36_si , \一位全加器fa封装3_37_cout ,
       \一位全加器fa封装3_37_si , \一位全加器fa封装3_38_cout , \一位全加器fa封装3_38_si , \一位全加器fa封装3_39_cout ,
       \一位全加器fa封装3_39_si , \一位全加器fa封装3_40_cout , \一位全加器fa封装3_40_si , \一位全加器fa封装3_41_cout ,
       \一位全加器fa封装3_42_cout , \一位全加器fa封装3_42_si , \一位全加器fa封装3_43_cout , \一位全加器fa封装3_43_si ,
       \一位全加器fa封装3_44_cout , \一位全加器fa封装3_44_si , \一位全加器fa封装3_45_cout , \一位全加器fa封装3_45_si ,
       \一位全加器fa封装3_46_cout , \一位全加器fa封装3_47_cout , \一位全加器fa封装3_47_si , \一位全加器fa封装3_48_cout ,
       \一位全加器fa封装3_48_si , \一位全加器fa封装3_49_cout , \一位全加器fa封装3_49_si , \一位全加器fa封装3_50_cout ,
       \一位全加器fa封装3_51_cout , \一位全加器fa封装3_51_si , \一位全加器fa封装3_52_cout , \一位全加器fa封装3_52_si ,
       \一位全加器fa封装3_53_cout , \一位全加器fa封装3_54_cout , \一位全加器fa封装3_54_si , \一位全加器fa封装3_55_cout ,
       \一位全加器fa封装3_56_cout ;

  \一位全加器FA封装3  \u_一位全加器fa封装3_1  (
    .Cout(\乘积 [15]), .Si(\乘积 [14]), .Cin(\一位全加器fa封装3_2_cout ), .Xi(\一位全加器fa封装3_3_cout ), .Yi(X7Y7));
  // Probe on X
  // Probe on \乘积 
  \一位全加器FA封装3  \u_一位全加器fa封装3_2  (
    .Cout(\一位全加器fa封装3_2_cout ), .Si(\一位全加器fa封装3_2_si ), .Cin(\一位全加器fa封装3_4_cout ), .Xi(X6Y7), .Yi(X7Y6));
  \一位全加器FA封装3  \u_一位全加器fa封装3_3  (
    .Cout(\一位全加器fa封装3_3_cout ), .Si(\乘积 [13]), .Cin(\一位全加器fa封装3_5_cout ), .Xi(\一位全加器fa封装3_6_cout ),
    .Yi(\一位全加器fa封装3_2_si ));
  \一位全加器FA封装3  \u_一位全加器fa封装3_4  (
    .Cout(\一位全加器fa封装3_4_cout ), .Si(\一位全加器fa封装3_4_si ), .Cin(\一位全加器fa封装3_7_cout ), .Xi(X6Y6), .Yi(X7Y5));
  \一位全加器FA封装3  \u_一位全加器fa封装3_5  (
    .Cout(\一位全加器fa封装3_5_cout ), .Si(\一位全加器fa封装3_5_si ), .Cin(\一位全加器fa封装3_8_cout ), .Xi(X5Y7),
    .Yi(\一位全加器fa封装3_4_si ));
  \一位全加器FA封装3  \u_一位全加器fa封装3_6  (
    .Cout(\一位全加器fa封装3_6_cout ), .Si(\乘积 [12]), .Cin(\一位全加器fa封装3_9_cout ), .Xi(\一位全加器fa封装3_10_cout ),
    .Yi(\一位全加器fa封装3_5_si ));
  // Probe on Y
  \一位全加器FA封装3  \u_一位全加器fa封装3_7  (
    .Cout(\一位全加器fa封装3_7_cout ), .Si(\一位全加器fa封装3_7_si ), .Cin(\一位全加器fa封装3_11_cout ), .Xi(X6Y5), .Yi(X7Y4));
  \一位全加器FA封装3  \u_一位全加器fa封装3_8  (
    .Cout(\一位全加器fa封装3_8_cout ), .Si(\一位全加器fa封装3_8_si ), .Cin(\一位全加器fa封装3_12_cout ), .Xi(X5Y6),
    .Yi(\一位全加器fa封装3_7_si ));
  \一位全加器FA封装3  \u_一位全加器fa封装3_9  (
    .Cout(\一位全加器fa封装3_9_cout ), .Si(\一位全加器fa封装3_9_si ), .Cin(\一位全加器fa封装3_13_cout ), .Xi(X4Y7),
    .Yi(\一位全加器fa封装3_8_si ));
  \一位全加器FA封装3  \u_一位全加器fa封装3_10  (
    .Cout(\一位全加器fa封装3_10_cout ), .Si(\乘积 [11]), .Cin(\一位全加器fa封装3_14_cout ), .Xi(\一位全加器fa封装3_15_cout ),
    .Yi(\一位全加器fa封装3_9_si ));
  \一位全加器FA封装3  \u_一位全加器fa封装3_11  (
    .Cout(\一位全加器fa封装3_11_cout ), .Si(\一位全加器fa封装3_11_si ), .Cin(\一位全加器fa封装3_16_cout ), .Xi(X6Y4), .Yi(X7Y3));
  \一位全加器FA封装3  \u_一位全加器fa封装3_12  (
    .Cout(\一位全加器fa封装3_12_cout ), .Si(\一位全加器fa封装3_12_si ), .Cin(\一位全加器fa封装3_17_cout ), .Xi(X5Y5),
    .Yi(\一位全加器fa封装3_11_si ));
  \一位全加器FA封装3  \u_一位全加器fa封装3_13  (
    .Cout(\一位全加器fa封装3_13_cout ), .Si(\一位全加器fa封装3_13_si ), .Cin(\一位全加器fa封装3_18_cout ), .Xi(X4Y6),
    .Yi(\一位全加器fa封装3_12_si ));
  \一位全加器FA封装3  \u_一位全加器fa封装3_14  (
    .Cout(\一位全加器fa封装3_14_cout ), .Si(\一位全加器fa封装3_14_si ), .Cin(\一位全加器fa封装3_19_cout ), .Xi(X3Y7),
    .Yi(\一位全加器fa封装3_13_si ));
  \一位全加器FA封装3  \u_一位全加器fa封装3_15  (
    .Cout(\一位全加器fa封装3_15_cout ), .Si(\乘积 [10]), .Cin(\一位全加器fa封装3_20_cout ), .Xi(\一位全加器fa封装3_21_cout ),
    .Yi(\一位全加器fa封装3_14_si ));
  \一位全加器FA封装3  \u_一位全加器fa封装3_16  (
    .Cout(\一位全加器fa封装3_16_cout ), .Si(\一位全加器fa封装3_16_si ), .Cin(\一位全加器fa封装3_22_cout ), .Xi(X6Y3), .Yi(X7Y2));
  \一位全加器FA封装3  \u_一位全加器fa封装3_17  (
    .Cout(\一位全加器fa封装3_17_cout ), .Si(\一位全加器fa封装3_17_si ), .Cin(\一位全加器fa封装3_23_cout ), .Xi(X5Y4),
    .Yi(\一位全加器fa封装3_16_si ));
  \一位全加器FA封装3  \u_一位全加器fa封装3_18  (
    .Cout(\一位全加器fa封装3_18_cout ), .Si(\一位全加器fa封装3_18_si ), .Cin(\一位全加器fa封装3_24_cout ), .Xi(X4Y5),
    .Yi(\一位全加器fa封装3_17_si ));
  \一位全加器FA封装3  \u_一位全加器fa封装3_19  (
    .Cout(\一位全加器fa封装3_19_cout ), .Si(\一位全加器fa封装3_19_si ), .Cin(\一位全加器fa封装3_25_cout ), .Xi(X3Y6),
    .Yi(\一位全加器fa封装3_18_si ));
  \一位全加器FA封装3  \u_一位全加器fa封装3_20  (
    .Cout(\一位全加器fa封装3_20_cout ), .Si(\一位全加器fa封装3_20_si ), .Cin(\一位全加器fa封装3_26_cout ), .Xi(X2Y7),
    .Yi(\一位全加器fa封装3_19_si ));
  \一位全加器FA封装3  \u_一位全加器fa封装3_21  (
    .Cout(\一位全加器fa封装3_21_cout ), .Si(\乘积 [9]), .Cin(\一位全加器fa封装3_27_cout ), .Xi(\一位全加器fa封装3_28_cout ),
    .Yi(\一位全加器fa封装3_20_si ));
  \一位全加器FA封装3  \u_一位全加器fa封装3_22  (
    .Cout(\一位全加器fa封装3_22_cout ), .Si(\一位全加器fa封装3_22_si ), .Cin(\一位全加器fa封装3_29_cout ), .Xi(X6Y2), .Yi(X7Y1));
  \一位全加器FA封装3  \u_一位全加器fa封装3_23  (
    .Cout(\一位全加器fa封装3_23_cout ), .Si(\一位全加器fa封装3_23_si ), .Cin(\一位全加器fa封装3_30_cout ), .Xi(X5Y3),
    .Yi(\一位全加器fa封装3_22_si ));
  \一位全加器FA封装3  \u_一位全加器fa封装3_24  (
    .Cout(\一位全加器fa封装3_24_cout ), .Si(\一位全加器fa封装3_24_si ), .Cin(\一位全加器fa封装3_31_cout ), .Xi(X4Y4),
    .Yi(\一位全加器fa封装3_23_si ));
  \一位全加器FA封装3  \u_一位全加器fa封装3_25  (
    .Cout(\一位全加器fa封装3_25_cout ), .Si(\一位全加器fa封装3_25_si ), .Cin(\一位全加器fa封装3_32_cout ), .Xi(X3Y5),
    .Yi(\一位全加器fa封装3_24_si ));
  \一位全加器FA封装3  \u_一位全加器fa封装3_26  (
    .Cout(\一位全加器fa封装3_26_cout ), .Si(\一位全加器fa封装3_26_si ), .Cin(\一位全加器fa封装3_33_cout ), .Xi(X2Y6),
    .Yi(\一位全加器fa封装3_25_si ));
  \一位全加器FA封装3  \u_一位全加器fa封装3_27  (
    .Cout(\一位全加器fa封装3_27_cout ), .Si(\一位全加器fa封装3_27_si ), .Cin(\一位全加器fa封装3_34_cout ), .Xi(X1Y7),
    .Yi(\一位全加器fa封装3_26_si ));
  \一位全加器FA封装3  \u_一位全加器fa封装3_28  (
    .Cout(\一位全加器fa封装3_28_cout ), .Si(\乘积 [8]), .Cin(\一位全加器fa封装3_35_cout ), .Xi(1'b0), .Yi(\一位全加器fa封装3_27_si ));
  \一位全加器FA封装3  \u_一位全加器fa封装3_29  (
    .Cout(\一位全加器fa封装3_29_cout ), .Si(\一位全加器fa封装3_29_si ), .Cin(1'b0), .Xi(X6Y1), .Yi(X7Y0));
  \一位全加器FA封装3  \u_一位全加器fa封装3_30  (
    .Cout(\一位全加器fa封装3_30_cout ), .Si(\一位全加器fa封装3_30_si ), .Cin(\一位全加器fa封装3_36_cout ), .Xi(X5Y2),
    .Yi(\一位全加器fa封装3_29_si ));
  \一位全加器FA封装3  \u_一位全加器fa封装3_31  (
    .Cout(\一位全加器fa封装3_31_cout ), .Si(\一位全加器fa封装3_31_si ), .Cin(\一位全加器fa封装3_37_cout ), .Xi(X4Y3),
    .Yi(\一位全加器fa封装3_30_si ));
  \一位全加器FA封装3  \u_一位全加器fa封装3_32  (
    .Cout(\一位全加器fa封装3_32_cout ), .Si(\一位全加器fa封装3_32_si ), .Cin(\一位全加器fa封装3_38_cout ), .Xi(X3Y4),
    .Yi(\一位全加器fa封装3_31_si ));
  \一位全加器FA封装3  \u_一位全加器fa封装3_33  (
    .Cout(\一位全加器fa封装3_33_cout ), .Si(\一位全加器fa封装3_33_si ), .Cin(\一位全加器fa封装3_39_cout ), .Xi(X2Y5),
    .Yi(\一位全加器fa封装3_32_si ));
  \一位全加器FA封装3  \u_一位全加器fa封装3_34  (
    .Cout(\一位全加器fa封装3_34_cout ), .Si(\一位全加器fa封装3_34_si ), .Cin(\一位全加器fa封装3_40_cout ), .Xi(X1Y6),
    .Yi(\一位全加器fa封装3_33_si ));
  \一位全加器FA封装3  \u_一位全加器fa封装3_35  (
    .Cout(\一位全加器fa封装3_35_cout ), .Si(\乘积 [7]), .Cin(\一位全加器fa封装3_41_cout ), .Xi(X0Y7), .Yi(\一位全加器fa封装3_34_si ));
  \一位全加器FA封装3  \u_一位全加器fa封装3_36  (
    .Cout(\一位全加器fa封装3_36_cout ), .Si(\一位全加器fa封装3_36_si ), .Cin(1'b0), .Xi(X5Y1), .Yi(X6Y0));
  \一位全加器FA封装3  \u_一位全加器fa封装3_37  (
    .Cout(\一位全加器fa封装3_37_cout ), .Si(\一位全加器fa封装3_37_si ), .Cin(\一位全加器fa封装3_42_cout ), .Xi(X4Y2),
    .Yi(\一位全加器fa封装3_36_si ));
  \一位全加器FA封装3  \u_一位全加器fa封装3_38  (
    .Cout(\一位全加器fa封装3_38_cout ), .Si(\一位全加器fa封装3_38_si ), .Cin(\一位全加器fa封装3_43_cout ), .Xi(X3Y3),
    .Yi(\一位全加器fa封装3_37_si ));
  \一位全加器FA封装3  \u_一位全加器fa封装3_39  (
    .Cout(\一位全加器fa封装3_39_cout ), .Si(\一位全加器fa封装3_39_si ), .Cin(\一位全加器fa封装3_44_cout ), .Xi(X2Y4),
    .Yi(\一位全加器fa封装3_38_si ));
  \一位全加器FA封装3  \u_一位全加器fa封装3_40  (
    .Cout(\一位全加器fa封装3_40_cout ), .Si(\一位全加器fa封装3_40_si ), .Cin(\一位全加器fa封装3_45_cout ), .Xi(X1Y5),
    .Yi(\一位全加器fa封装3_39_si ));
  \一位全加器FA封装3  \u_一位全加器fa封装3_41  (
    .Cout(\一位全加器fa封装3_41_cout ), .Si(\乘积 [6]), .Cin(\一位全加器fa封装3_46_cout ), .Xi(X0Y6), .Yi(\一位全加器fa封装3_40_si ));
  \一位全加器FA封装3  \u_一位全加器fa封装3_42  (
    .Cout(\一位全加器fa封装3_42_cout ), .Si(\一位全加器fa封装3_42_si ), .Cin(1'b0), .Xi(X4Y1), .Yi(X5Y0));
  \一位全加器FA封装3  \u_一位全加器fa封装3_43  (
    .Cout(\一位全加器fa封装3_43_cout ), .Si(\一位全加器fa封装3_43_si ), .Cin(\一位全加器fa封装3_47_cout ), .Xi(X3Y2),
    .Yi(\一位全加器fa封装3_42_si ));
  \一位全加器FA封装3  \u_一位全加器fa封装3_44  (
    .Cout(\一位全加器fa封装3_44_cout ), .Si(\一位全加器fa封装3_44_si ), .Cin(\一位全加器fa封装3_48_cout ), .Xi(X2Y3),
    .Yi(\一位全加器fa封装3_43_si ));
  \一位全加器FA封装3  \u_一位全加器fa封装3_45  (
    .Cout(\一位全加器fa封装3_45_cout ), .Si(\一位全加器fa封装3_45_si ), .Cin(\一位全加器fa封装3_49_cout ), .Xi(X1Y4),
    .Yi(\一位全加器fa封装3_44_si ));
  \一位全加器FA封装3  \u_一位全加器fa封装3_46  (
    .Cout(\一位全加器fa封装3_46_cout ), .Si(\乘积 [5]), .Cin(\一位全加器fa封装3_50_cout ), .Xi(X0Y5), .Yi(\一位全加器fa封装3_45_si ));
  \一位全加器FA封装3  \u_一位全加器fa封装3_47  (
    .Cout(\一位全加器fa封装3_47_cout ), .Si(\一位全加器fa封装3_47_si ), .Cin(1'b0), .Xi(X3Y1), .Yi(X4Y0));
  \一位全加器FA封装3  \u_一位全加器fa封装3_48  (
    .Cout(\一位全加器fa封装3_48_cout ), .Si(\一位全加器fa封装3_48_si ), .Cin(\一位全加器fa封装3_51_cout ), .Xi(X2Y2),
    .Yi(\一位全加器fa封装3_47_si ));
  \一位全加器FA封装3  \u_一位全加器fa封装3_49  (
    .Cout(\一位全加器fa封装3_49_cout ), .Si(\一位全加器fa封装3_49_si ), .Cin(\一位全加器fa封装3_52_cout ), .Xi(X1Y3),
    .Yi(\一位全加器fa封装3_48_si ));
  \一位全加器FA封装3  \u_一位全加器fa封装3_50  (
    .Cout(\一位全加器fa封装3_50_cout ), .Si(\乘积 [4]), .Cin(\一位全加器fa封装3_53_cout ), .Xi(X0Y4), .Yi(\一位全加器fa封装3_49_si ));
  \一位全加器FA封装3  \u_一位全加器fa封装3_51  (
    .Cout(\一位全加器fa封装3_51_cout ), .Si(\一位全加器fa封装3_51_si ), .Cin(1'b0), .Xi(X2Y1), .Yi(X3Y0));
  \一位全加器FA封装3  \u_一位全加器fa封装3_52  (
    .Cout(\一位全加器fa封装3_52_cout ), .Si(\一位全加器fa封装3_52_si ), .Cin(\一位全加器fa封装3_54_cout ), .Xi(X1Y2),
    .Yi(\一位全加器fa封装3_51_si ));
  \一位全加器FA封装3  \u_一位全加器fa封装3_53  (
    .Cout(\一位全加器fa封装3_53_cout ), .Si(\乘积 [3]), .Cin(\一位全加器fa封装3_55_cout ), .Xi(X0Y3), .Yi(\一位全加器fa封装3_52_si ));
  \一位全加器FA封装3  \u_一位全加器fa封装3_54  (
    .Cout(\一位全加器fa封装3_54_cout ), .Si(\一位全加器fa封装3_54_si ), .Cin(1'b0), .Xi(X1Y1), .Yi(X2Y0));
  \一位全加器FA封装3  \u_一位全加器fa封装3_55  (
    .Cout(\一位全加器fa封装3_55_cout ), .Si(\乘积 [2]), .Cin(\一位全加器fa封装3_56_cout ), .Xi(X0Y2), .Yi(\一位全加器fa封装3_54_si ));
  \一位全加器FA封装3  \u_一位全加器fa封装3_56  (.Cout(\一位全加器fa封装3_56_cout ), .Si(\乘积 [1]), .Cin(1'b0), .Xi(X0Y1), .Yi(X1Y0));
  \_8位乘法与门阵列  \u_8位乘法与门阵列_1  (
    .X(X), .Y(Y), .XY7({X7Y7, X6Y7, X5Y7, X4Y7, X3Y7, X2Y7, X1Y7, X0Y7}),
    .XY6({X7Y6, X6Y6, X5Y6, X4Y6, X3Y6, X2Y6, X1Y6, X0Y6}),
    .XY5({X7Y5, X6Y5, X5Y5, X4Y5, X3Y5, X2Y5, X1Y5, X0Y5}),
    .XY4({X7Y4, X6Y4, X5Y4, X4Y4, X3Y4, X2Y4, X1Y4, X0Y4}),
    .XY3({X7Y3, X6Y3, X5Y3, X4Y3, X3Y3, X2Y3, X1Y3, X0Y3}),
    .XY2({X7Y2, X6Y2, X5Y2, X4Y2, X3Y2, X2Y2, X1Y2, X0Y2}),
    .XY1({X7Y1, X6Y1, X5Y1, X4Y1, X3Y1, X2Y1, X1Y1, X0Y1}),
    .XY0({X7Y0, X6Y0, X5Y0, X4Y0, X3Y0, X2Y0, X1Y0, \乘积 [0]}));

  // Other names for the same wires on the sheet: P[15:0] = \乘积 ; P0 = \乘积 [0]; X0Y0 = \乘积 [0];
  //   XY0[7:0] = {X7Y0, X6Y0, X5Y0, X4Y0, X3Y0, X2Y0, X1Y0, \乘积 [0]}; P1 = \乘积 [1]; P2 = \乘积 [2]; P3 = \乘积 [3];
  //   P4 = \乘积 [4]; P5 = \乘积 [5]; P6 = \乘积 [6]; P7 = \乘积 [7]; P8 = \乘积 [8]; P9 = \乘积 [9]; P10 = \乘积 [10];
  //   P11 = \乘积 [11]; P12 = \乘积 [12]; P13 = \乘积 [13]; P14 = \乘积 [14]; P15 = \乘积 [15];
  //   XY1[7:0] = {X7Y1, X6Y1, X5Y1, X4Y1, X3Y1, X2Y1, X1Y1, X0Y1};
  //   XY2[7:0] = {X7Y2, X6Y2, X5Y2, X4Y2, X3Y2, X2Y2, X1Y2, X0Y2};
  //   XY3[7:0] = {X7Y3, X6Y3, X5Y3, X4Y3, X3Y3, X2Y3, X1Y3, X0Y3};
  //   XY4[7:0] = {X7Y4, X6Y4, X5Y4, X4Y4, X3Y4, X2Y4, X1Y4, X0Y4};
  //   XY5[7:0] = {X7Y5, X6Y5, X5Y5, X4Y5, X3Y5, X2Y5, X1Y5, X0Y5};
  //   XY6[7:0] = {X7Y6, X6Y6, X5Y6, X4Y6, X3Y6, X2Y6, X1Y6, X0Y6};
  //   XY7[7:0] = {X7Y7, X6Y7, X5Y7, X4Y7, X3Y7, X2Y7, X1Y7, X0Y7}
endmodule

// ALU
module ALU (
  input  [31:0] X,
  input  [31:0] Y,
  input  [3:0] AluOP,
  output Signed_Overflow,
  output UnSigned_Overflow,
  output Equal,
  output [31:0] Result,
  output [31:0] Result_2
);

  wire and_3_out, and_4_out, and_5_out, and_6_out, comparator_2_gt, \n32位快速加法器_1_cout ,
       \n32位快速加法器_1_overflow , or_3_out;
  wire [0:0] comparator_1_lt, xor_2_out;
  wire [31:0] and_1_out, divider_1_out, divider_1_rem, multiplexer_2_out, multiplier_1_cout,
       multiplier_1_out, \n32位快速加法器_1_s , not_1_out, not_2_out, or_1_out, shifter_1_out, shifter_2_out,
       shifter_3_out, xor_1_out;

  // Probe on X
  // Probe on X
  multi multi_1 ();  // open: out, out_2, x, y
  // Probe on Y
  // Probe on Y
  Shifter #(.width(32)) shifter_1 (.in(X), .\dist (Y[4:0]), .out(shifter_1_out));
  Shifter #(.width(32), .shift("ar")) shifter_2 (.in(X), .\dist (Y[4:0]), .out(shifter_2_out));
  Shifter #(.width(32), .shift("lr")) shifter_3 (.in(X), .\dist (Y[4:0]), .out(shifter_3_out));
  Multiplier #(.width(32)) multiplier_1 (.a(X), .b(Y), .out(multiplier_1_out), .cout(multiplier_1_cout));  // open: cin
  Divider #(.width(32)) divider_1 (.a(X), .b(Y), .out(divider_1_out), .rem(divider_1_rem));  // open: upper
  assign and_1_out = X & Y;  // AND_Gate and_1, 32 bits wide
  assign or_1_out = X | Y;  // OR_Gate or_1, 32 bits wide
  assign xor_1_out = X ^ Y;  // XOR_Gate xor_1, 32 bits wide
  Comparator #(.width(32), .mode("unsigned")) comparator_1 (
    .a(X), .b(Y), .eq(Equal), .lt(comparator_1_lt[0]));  // open: gt
  Multiplexer #(.select(4), .width(32), .enable("false")) multiplexer_1 (
    .in0(shifter_1_out), .in1(shifter_2_out), .in2(shifter_3_out), .in3(multiplier_1_out),
    .in4(divider_1_out), .in5(\n32位快速加法器_1_s ), .in6(\n32位快速加法器_1_s ), .in7(and_1_out), .in8(or_1_out),
    .in9(xor_1_out), .in10(not_1_out), .in11({{31{1'b0}}, xor_2_out[0]}),
    .in12({{31{1'b0}}, comparator_1_lt[0]}), .in13({32{1'b0}}), .in14({32{1'b0}}), .in15({32{1'b0}}),
    .out(Result), .sel(AluOP));
  assign not_1_out = ~or_1_out;  // NOT_Gate not_1, 32 bits wide
  // Probe on AluOP
  xor xor_2 (xor_2_out[0], xor_1_out[31], comparator_1_lt[0]);
  // Probe on Result
  // Probe on Result
  \_32位快速加法器  \u_32位快速加法器_1  (
    .X(X), .Y(multiplexer_2_out), .Cin(AluOP[1]), .S(\n32位快速加法器_1_s ), .Cout(\n32位快速加法器_1_cout ),
    .Overflow(\n32位快速加法器_1_overflow ));
  Multiplexer #(.width(32), .enable("false")) multiplexer_2 (
    .in0(Y), .in1(not_2_out), .out(multiplexer_2_out), .sel(AluOP[1]));
  assign not_2_out = ~Y;  // NOT_Gate not_2, 32 bits wide
  // Probe on Result_2
  Multiplexer #(.select(4), .width(32), .disabled(0), .enable("false")) multiplexer_3 (
    .in0({32{1'b0}}), .in1({32{1'b0}}), .in2({32{1'b0}}), .in3(multiplier_1_cout), .in4(divider_1_rem),
    .in5({32{1'b0}}), .in6({32{1'b0}}), .in7({32{1'b0}}), .in8({32{1'b0}}), .in9({32{1'b0}}),
    .in10({32{1'b0}}), .in11({32{1'b0}}), .in12({32{1'b0}}), .in13({32{1'b0}}), .in14({32{1'b0}}),
    .in15({32{1'b0}}), .out(Result_2), .sel(AluOP));
  Comparator #(.width(32), .mode("unsigned")) comparator_2 (
    .a(\n32位快速加法器_1_s ), .b(X), .gt(comparator_2_gt));  // open: eq, lt
  and and_2 (Signed_Overflow, \n32位快速加法器_1_overflow , or_3_out);
  or or_2 (UnSigned_Overflow, and_4_out, and_3_out);
  and and_3 (and_3_out, comparator_2_gt, and_6_out);
  and and_4 (and_4_out, \n32位快速加法器_1_cout , and_5_out);
  or or_3 (or_3_out, and_5_out, and_6_out);
  and and_5 (and_5_out, AluOP[0], ~AluOP[1], AluOP[2], ~AluOP[3]);  // AND_Gate
  and and_6 (and_6_out, ~AluOP[0], AluOP[1], AluOP[2], ~AluOP[3]);  // AND_Gate

  // Other names for the same wires on the sheet: OF = Signed_Overflow; Result2[31:0] = Result_2; S[3:0] = AluOP;
  //   UOF = UnSigned_Overflow

  // Notes on the sheet:
  //   不要改变此引脚区域内容，也不要改变ALU封装形式
  //   输入引脚
  //   请在下方利用上方输入输出引脚的隧道信号构建ALU电路，ctrl+d复制选择部件
  //   华中科技大学计算机学院 计算机组成原理，鸣谢加州大学伯克利CS61C课程
  //   输出引脚
  //   探测区域
endmodule

module \运算器测试电路  (
  input  [31:0] X,
  input  [31:0] Y,
  input  [3:0] ALUOP,
  output Signed_Overflow,
  output Unsigned_overflow,
  output [31:0] Result,
  output [31:0] Result_2,
  output Equal
);

  // Probe on X
  // Probe on X
  ALU alu_1 (
    .AluOP(ALUOP), .X(X), .Equal(Equal), .Result(Result), .Signed_Overflow(Signed_Overflow), .Y(Y),
    .Result_2(Result_2), .UnSigned_Overflow(Unsigned_overflow));
  // Probe on ALUOP
  // Probe on Y
  // Probe on Y
  // Probe on Result
  // Probe on Result
  // Probe on Result_2

  // Notes on the sheet:
  //   ALu电路无需调整位置即可连接在该电路中，并且不能出现蓝色线缆和三态输出
endmodule

module \华莱士树  (
);

  wire undriven, undriven_2, undriven_3, undriven_4, undriven_5, undriven_6, undriven_7, undriven_8,
       undriven_9, undriven_10, undriven_11, undriven_12, undriven_13, undriven_14, undriven_15, undriven_16,
       undriven_17, undriven_18, undriven_19, undriven_20, undriven_21, undriven_22, undriven_23,
       undriven_24, undriven_25, undriven_26, undriven_27, undriven_28, undriven_29, undriven_30,
       undriven_31, undriven_32, undriven_33, undriven_34, undriven_35, undriven_36, undriven_37,
       undriven_38, undriven_39, undriven_40, undriven_41, undriven_42, undriven_43, undriven_44,
       undriven_45, undriven_46, undriven_47, undriven_48, undriven_49, undriven_50, undriven_51,
       undriven_52, undriven_53, undriven_54, undriven_55, undriven_56, undriven_57, undriven_58,
       undriven_59, undriven_60, undriven_61, undriven_62, undriven_63, undriven_64, undriven_65,
       undriven_66, undriven_67, undriven_68, undriven_69, undriven_70, undriven_71, undriven_72,
       undriven_73, undriven_74, undriven_75, undriven_76, undriven_77, undriven_78, undriven_79,
       undriven_80, undriven_81, undriven_82, undriven_83, undriven_84, undriven_85, undriven_86,
       undriven_87, undriven_88, undriven_89, undriven_90, undriven_91, undriven_92, undriven_93,
       undriven_94, undriven_95, undriven_96, undriven_97, undriven_98, undriven_99, undriven_100,
       undriven_101, undriven_102, undriven_103, undriven_104, undriven_105, undriven_106, undriven_107,
       undriven_108, undriven_109, undriven_110, undriven_111, undriven_112, undriven_113, undriven_114,
       undriven_115, undriven_116, undriven_117, undriven_118, undriven_119, undriven_120, undriven_121,
       undriven_122, undriven_123, undriven_124, undriven_125, undriven_126, undriven_127, undriven_128,
       undriven_130, \一位全加器fa封装2_2_cout , \一位全加器fa封装2_2_si , \一位全加器fa封装2_3_si , \一位全加器fa封装2_4_cout ,
       \一位全加器fa封装2_4_si , \一位全加器fa封装2_5_si , \一位全加器fa封装2_6_si , \一位全加器fa封装2_7_si , \一位全加器fa封装2_8_si ,
       \一位全加器fa封装2_10_si , \一位全加器fa封装2_11_cout , \一位全加器fa封装2_11_si , \一位全加器fa封装2_12_si ,
       \一位全加器fa封装2_13_cout , \一位全加器fa封装2_13_si , \一位全加器fa封装2_14_si , \一位全加器fa封装2_15_si , \一位全加器fa封装2_17_si ,
       \一位全加器fa封装2_18_cout , \一位全加器fa封装2_18_si , \一位全加器fa封装2_19_si , \一位全加器fa封装2_20_cout ,
       \一位全加器fa封装2_20_si , \一位全加器fa封装2_21_si , \一位全加器fa封装2_22_si , \一位全加器fa封装2_23_si , \一位全加器fa封装2_24_si ,
       \一位全加器fa封装2_26_si , \一位全加器fa封装2_27_cout , \一位全加器fa封装2_27_si , \一位全加器fa封装2_28_si ,
       \一位全加器fa封装2_29_cout , \一位全加器fa封装2_29_si , \一位全加器fa封装2_30_si , \一位全加器fa封装2_31_si , \一位全加器fa封装2_32_si ,
       \一位全加器fa封装2_34_cout , \一位全加器fa封装2_34_si , \一位全加器fa封装2_35_si , \一位全加器fa封装2_36_cout ,
       \一位全加器fa封装2_36_si , \一位全加器fa封装2_37_si , \一位全加器fa封装2_38_si , \一位全加器fa封装2_39_si , \一位全加器fa封装2_40_si ,
       \一位全加器fa封装2_42_si , \一位全加器fa封装2_43_cout , \一位全加器fa封装2_43_si , \一位全加器fa封装2_44_si ,
       \一位全加器fa封装2_45_cout , \一位全加器fa封装2_45_si , \一位全加器fa封装2_46_si , \一位全加器fa封装2_47_si , \一位全加器fa封装2_49_si ,
       \一位全加器fa封装2_50_cout , \一位全加器fa封装2_50_si , \一位全加器fa封装2_51_si , \一位全加器fa封装2_52_cout ,
       \一位全加器fa封装2_52_si , \一位全加器fa封装2_53_si , \一位全加器fa封装2_54_si , \一位全加器fa封装2_55_si , \一位全加器fa封装2_56_si ,
       \一位全加器fa封装2_58_si , \一位全加器fa封装2_59_cout , \一位全加器fa封装2_59_si , \一位全加器fa封装2_60_si ,
       \一位全加器fa封装2_61_cout , \一位全加器fa封装2_61_si , \一位全加器fa封装2_62_si , \一位全加器fa封装2_63_si , \一位全加器fa封装2_64_si ,
       \一位全加器fa封装2_66_cout , \一位全加器fa封装2_66_si , \一位全加器fa封装2_67_si , \一位全加器fa封装2_68_cout ,
       \一位全加器fa封装2_68_si , \一位全加器fa封装2_69_si , \一位全加器fa封装2_70_si , \一位全加器fa封装2_71_si , \一位全加器fa封装2_72_si ,
       \一位全加器fa封装2_74_si , \一位全加器fa封装2_75_cout , \一位全加器fa封装2_75_si , \一位全加器fa封装2_76_si ,
       \一位全加器fa封装2_77_cout , \一位全加器fa封装2_77_si , \一位全加器fa封装2_78_si , \一位全加器fa封装2_79_si , \一位全加器fa封装2_81_si ,
       \一位全加器fa封装2_82_cout , \一位全加器fa封装2_82_si , \一位全加器fa封装2_83_si , \一位全加器fa封装2_84_cout ,
       \一位全加器fa封装2_84_si , \一位全加器fa封装2_85_si , \一位全加器fa封装2_86_si , \一位全加器fa封装2_87_si , \一位全加器fa封装2_88_si ,
       \一位全加器fa封装2_90_si , \一位全加器fa封装2_91_cout , \一位全加器fa封装2_91_si , \一位全加器fa封装2_92_si ,
       \一位全加器fa封装2_93_cout , \一位全加器fa封装2_93_si , \一位全加器fa封装2_94_si , \一位全加器fa封装2_95_si , \一位全加器fa封装2_96_si ,
       \一位全加器fa封装2_98_cout , \一位全加器fa封装2_98_si , \一位全加器fa封装2_99_si , \一位全加器fa封装2_100_cout ,
       \一位全加器fa封装2_100_si , \一位全加器fa封装2_101_si , \一位全加器fa封装2_102_si , \一位全加器fa封装2_103_si ,
       \一位全加器fa封装2_104_si , \一位全加器fa封装2_106_si , \一位全加器fa封装2_107_cout , \一位全加器fa封装2_107_si ,
       \一位全加器fa封装2_108_si , \一位全加器fa封装2_109_cout , \一位全加器fa封装2_109_si , \一位全加器fa封装2_110_si ,
       \一位全加器fa封装2_111_si , \一位全加器fa封装2_113_si , \一位全加器fa封装2_114_cout , \一位全加器fa封装2_114_si ,
       \一位全加器fa封装2_115_si , \一位全加器fa封装2_116_cout , \一位全加器fa封装2_116_si , \一位全加器fa封装2_117_si ,
       \一位全加器fa封装2_118_si , \一位全加器fa封装2_119_si , \一位全加器fa封装2_120_si , \一位全加器fa封装2_122_si ,
       \一位全加器fa封装2_123_cout , \一位全加器fa封装2_123_si , \一位全加器fa封装2_124_si , \一位全加器fa封装2_125_cout ,
       \一位全加器fa封装2_125_si , \一位全加器fa封装2_126_si , \一位全加器fa封装2_127_si , \一位全加器fa封装2_128_si ;
  wire [1:0] undriven_131, \一位全加器fa封装2_5_cout , \一位全加器fa封装2_12_cout , \一位全加器fa封装2_19_cout ,
       \一位全加器fa封装2_26_cout , \一位全加器fa封装2_37_cout , \一位全加器fa封装2_44_cout , \一位全加器fa封装2_51_cout ,
       \一位全加器fa封装2_58_cout , \一位全加器fa封装2_69_cout , \一位全加器fa封装2_76_cout , \一位全加器fa封装2_83_cout ,
       \一位全加器fa封装2_90_cout , \一位全加器fa封装2_101_cout , \一位全加器fa封装2_108_cout , \一位全加器fa封装2_115_cout ,
       \一位全加器fa封装2_122_cout ;
  wire [2:0] undriven_129, \一位全加器fa封装2_8_cout , \一位全加器fa封装2_17_cout , \一位全加器fa封装2_24_cout ,
       \一位全加器fa封装2_31_cout , \一位全加器fa封装2_39_cout , \一位全加器fa封装2_49_cout , \一位全加器fa封装2_56_cout ,
       \一位全加器fa封装2_64_cout , \一位全加器fa封装2_72_cout , \一位全加器fa封装2_81_cout , \一位全加器fa封装2_88_cout ,
       \一位全加器fa封装2_95_cout , \一位全加器fa封装2_103_cout , \一位全加器fa封装2_113_cout , \一位全加器fa封装2_120_cout ,
       \一位全加器fa封装2_128_cout ;

  shape shape_1 ();
  \一位全加器FA封装2  \u_一位全加器fa封装2_1  ();  // open: Cout, Si, Cin, Xi, Yi
  \一位全加器FA封装2  \u_一位全加器fa封装2_2  (
    .Cout(\一位全加器fa封装2_2_cout ), .Si(\一位全加器fa封装2_2_si ), .Cin(\一位全加器fa封装2_8_si ), .Xi(\一位全加器fa封装2_3_si ),
    .Yi(\一位全加器fa封装2_7_si ));
  \一位全加器FA封装2  \u_一位全加器fa封装2_3  (
    .Cout(\一位全加器fa封装2_8_cout [2]), .Si(\一位全加器fa封装2_3_si ), .Cin(undriven_3), .Xi(undriven), .Yi(undriven_2));
  \一位全加器FA封装2  \u_一位全加器fa封装2_4  (
    .Cout(\一位全加器fa封装2_4_cout ), .Si(\一位全加器fa封装2_4_si ), .Cin(\一位全加器fa封装2_12_cout [0]),
    .Xi(\一位全加器fa封装2_5_si ), .Yi(\一位全加器fa封装2_12_cout [1]));
  \一位全加器FA封装2  \u_一位全加器fa封装2_5  (
    .Cout(\一位全加器fa封装2_5_cout [0]), .Si(\一位全加器fa封装2_5_si ), .Cin(\一位全加器fa封装2_13_cout ),
    .Xi(\一位全加器fa封装2_2_si ), .Yi(\一位全加器fa封装2_6_si ));
  \一位全加器FA封装2  \u_一位全加器fa封装2_6  (
    .Cout(\一位全加器fa封装2_5_cout [1]), .Si(\一位全加器fa封装2_6_si ), .Cin(\一位全加器fa封装2_17_cout [0]),
    .Xi(\一位全加器fa封装2_17_cout [2]), .Yi(\一位全加器fa封装2_17_cout [1]));
  \一位全加器FA封装2  \u_一位全加器fa封装2_7  (
    .Cout(\一位全加器fa封装2_8_cout [1]), .Si(\一位全加器fa封装2_7_si ), .Cin(undriven_6), .Xi(undriven_4), .Yi(undriven_5));
  \一位全加器FA封装2  \u_一位全加器fa封装2_8  (
    .Cout(\一位全加器fa封装2_8_cout [0]), .Si(\一位全加器fa封装2_8_si ), .Cin(1'b0), .Xi(undriven_7), .Yi(undriven_8));
  \一位全加器FA封装2  \u_一位全加器fa封装2_9  ();  // open: Cout, Si, Cin, Xi, Yi
  \一位全加器FA封装2  \u_一位全加器fa封装2_10  (
    .Cout(\一位全加器fa封装2_17_cout [2]), .Si(\一位全加器fa封装2_10_si ), .Cin(undriven_11), .Xi(undriven_9),
    .Yi(undriven_10));
  \一位全加器FA封装2  \u_一位全加器fa封装2_11  (
    .Cout(\一位全加器fa封装2_11_cout ), .Si(\一位全加器fa封装2_11_si ), .Cin(\一位全加器fa封装2_19_cout [0]),
    .Xi(\一位全加器fa封装2_12_si ), .Yi(\一位全加器fa封装2_19_cout [1]));
  \一位全加器FA封装2  \u_一位全加器fa封装2_12  (
    .Cout(\一位全加器fa封装2_12_cout [0]), .Si(\一位全加器fa封装2_12_si ), .Cin(\一位全加器fa封装2_20_cout ),
    .Xi(\一位全加器fa封装2_13_si ), .Yi(\一位全加器fa封装2_14_si ));
  \一位全加器FA封装2  \u_一位全加器fa封装2_13  (
    .Cout(\一位全加器fa封装2_13_cout ), .Si(\一位全加器fa封装2_13_si ), .Cin(\一位全加器fa封装2_17_si ), .Xi(\一位全加器fa封装2_10_si ),
    .Yi(\一位全加器fa封装2_15_si ));
  \一位全加器FA封装2  \u_一位全加器fa封装2_14  (
    .Cout(\一位全加器fa封装2_12_cout [1]), .Si(\一位全加器fa封装2_14_si ), .Cin(\一位全加器fa封装2_24_cout [0]),
    .Xi(\一位全加器fa封装2_24_cout [2]), .Yi(\一位全加器fa封装2_24_cout [1]));
  \一位全加器FA封装2  \u_一位全加器fa封装2_15  (
    .Cout(\一位全加器fa封装2_17_cout [1]), .Si(\一位全加器fa封装2_15_si ), .Cin(undriven_14), .Xi(undriven_12),
    .Yi(undriven_13));
  \一位全加器FA封装2  \u_一位全加器fa封装2_16  ();  // open: Cout, Si, Cin, Xi, Yi
  shape shape_2 ();
  \一位全加器FA封装2  \u_一位全加器fa封装2_17  (
    .Cout(\一位全加器fa封装2_17_cout [0]), .Si(\一位全加器fa封装2_17_si ), .Cin(1'b0), .Xi(undriven_15), .Yi(undriven_16));
  \一位全加器FA封装2  \u_一位全加器fa封装2_18  (
    .Cout(\一位全加器fa封装2_18_cout ), .Si(\一位全加器fa封装2_18_si ), .Cin(\一位全加器fa封装2_26_cout [0]),
    .Xi(\一位全加器fa封装2_19_si ), .Yi(\一位全加器fa封装2_26_cout [1]));
  \一位全加器FA封装2  \u_一位全加器fa封装2_19  (
    .Cout(\一位全加器fa封装2_19_cout [0]), .Si(\一位全加器fa封装2_19_si ), .Cin(\一位全加器fa封装2_27_cout ),
    .Xi(\一位全加器fa封装2_20_si ), .Yi(\一位全加器fa封装2_23_si ));
  \一位全加器FA封装2  \u_一位全加器fa封装2_20  (
    .Cout(\一位全加器fa封装2_20_cout ), .Si(\一位全加器fa封装2_20_si ), .Cin(\一位全加器fa封装2_24_si ), .Xi(\一位全加器fa封装2_22_si ),
    .Yi(\一位全加器fa封装2_21_si ));
  \一位全加器FA封装2  \u_一位全加器fa封装2_21  (
    .Cout(\一位全加器fa封装2_24_cout [1]), .Si(\一位全加器fa封装2_21_si ), .Cin(undriven_22), .Xi(undriven_20),
    .Yi(undriven_21));
  \一位全加器FA封装2  \u_一位全加器fa封装2_22  (
    .Cout(\一位全加器fa封装2_24_cout [2]), .Si(\一位全加器fa封装2_22_si ), .Cin(undriven_19), .Xi(undriven_17),
    .Yi(undriven_18));
  \一位全加器FA封装2  \u_一位全加器fa封装2_23  (
    .Cout(\一位全加器fa封装2_19_cout [1]), .Si(\一位全加器fa封装2_23_si ), .Cin(\一位全加器fa封装2_31_cout [0]),
    .Xi(\一位全加器fa封装2_31_cout [2]), .Yi(\一位全加器fa封装2_31_cout [1]));
  \一位全加器FA封装2  \u_一位全加器fa封装2_24  (
    .Cout(\一位全加器fa封装2_24_cout [0]), .Si(\一位全加器fa封装2_24_si ), .Cin(1'b0), .Xi(undriven_23), .Yi(undriven_24));
  \一位全加器FA封装2  \u_一位全加器fa封装2_25  ();  // open: Cout, Si, Cin, Xi, Yi
  \一位全加器FA封装2  \u_一位全加器fa封装2_26  (
    .Cout(\一位全加器fa封装2_26_cout [0]), .Si(\一位全加器fa封装2_26_si ), .Cin(\一位全加器fa封装2_34_cout ),
    .Xi(\一位全加器fa封装2_27_si ), .Yi(\一位全加器fa封装2_30_si ));
  \一位全加器FA封装2  \u_一位全加器fa封装2_27  (
    .Cout(\一位全加器fa封装2_27_cout ), .Si(\一位全加器fa封装2_27_si ), .Cin(\一位全加器fa封装2_31_si ), .Xi(\一位全加器fa封装2_28_si ),
    .Yi(\一位全加器fa封装2_32_si ));
  \一位全加器FA封装2  \u_一位全加器fa封装2_28  (
    .Cout(\一位全加器fa封装2_31_cout [2]), .Si(\一位全加器fa封装2_28_si ), .Cin(undriven_27), .Xi(undriven_25),
    .Yi(undriven_26));
  shape shape_3 ();
  \一位全加器FA封装2  \u_一位全加器fa封装2_29  (
    .Cout(\一位全加器fa封装2_29_cout ), .Si(\一位全加器fa封装2_29_si ), .Cin(\一位全加器fa封装2_37_cout [0]),
    .Xi(\一位全加器fa封装2_26_si ), .Yi(\一位全加器fa封装2_37_cout [1]));
  \一位全加器FA封装2  \u_一位全加器fa封装2_30  (
    .Cout(\一位全加器fa封装2_26_cout [1]), .Si(\一位全加器fa封装2_30_si ), .Cin(\一位全加器fa封装2_39_cout [0]),
    .Xi(\一位全加器fa封装2_39_cout [2]), .Yi(\一位全加器fa封装2_39_cout [1]));
  \一位全加器FA封装2  \u_一位全加器fa封装2_31  (
    .Cout(\一位全加器fa封装2_31_cout [0]), .Si(\一位全加器fa封装2_31_si ), .Cin(1'b0), .Xi(undriven_31), .Yi(undriven_32));
  \一位全加器FA封装2  \u_一位全加器fa封装2_32  (
    .Cout(\一位全加器fa封装2_31_cout [1]), .Si(\一位全加器fa封装2_32_si ), .Cin(undriven_30), .Xi(undriven_28),
    .Yi(undriven_29));
  \一位全加器FA封装2  \u_一位全加器fa封装2_33  ();  // open: Cout, Si, Cin, Xi, Yi
  \一位全加器FA封装2  \u_一位全加器fa封装2_34  (
    .Cout(\一位全加器fa封装2_34_cout ), .Si(\一位全加器fa封装2_34_si ), .Cin(\一位全加器fa封装2_39_si ), .Xi(\一位全加器fa封装2_35_si ),
    .Yi(\一位全加器fa封装2_40_si ));
  \一位全加器FA封装2  \u_一位全加器fa封装2_35  (
    .Cout(\一位全加器fa封装2_39_cout [2]), .Si(\一位全加器fa封装2_35_si ), .Cin(undriven_35), .Xi(undriven_33),
    .Yi(undriven_34));
  \一位全加器FA封装2  \u_一位全加器fa封装2_36  (
    .Cout(\一位全加器fa封装2_36_cout ), .Si(\一位全加器fa封装2_36_si ), .Cin(\一位全加器fa封装2_44_cout [0]),
    .Xi(\一位全加器fa封装2_37_si ), .Yi(\一位全加器fa封装2_44_cout [1]));
  \一位全加器FA封装2  \u_一位全加器fa封装2_37  (
    .Cout(\一位全加器fa封装2_37_cout [0]), .Si(\一位全加器fa封装2_37_si ), .Cin(\一位全加器fa封装2_45_cout ),
    .Xi(\一位全加器fa封装2_34_si ), .Yi(\一位全加器fa封装2_38_si ));
  \一位全加器FA封装2  \u_一位全加器fa封装2_38  (
    .Cout(\一位全加器fa封装2_37_cout [1]), .Si(\一位全加器fa封装2_38_si ), .Cin(\一位全加器fa封装2_49_cout [0]),
    .Xi(\一位全加器fa封装2_49_cout [2]), .Yi(\一位全加器fa封装2_49_cout [1]));
  \一位全加器FA封装2  \u_一位全加器fa封装2_39  (
    .Cout(\一位全加器fa封装2_39_cout [0]), .Si(\一位全加器fa封装2_39_si ), .Cin(1'b0), .Xi(undriven_39), .Yi(undriven_40));
  \一位全加器FA封装2  \u_一位全加器fa封装2_40  (
    .Cout(\一位全加器fa封装2_39_cout [1]), .Si(\一位全加器fa封装2_40_si ), .Cin(undriven_38), .Xi(undriven_36),
    .Yi(undriven_37));
  \一位全加器FA封装2  \u_一位全加器fa封装2_41  ();  // open: Cout, Si, Cin, Xi, Yi
  \一位全加器FA封装2  \u_一位全加器fa封装2_42  (
    .Cout(\一位全加器fa封装2_49_cout [2]), .Si(\一位全加器fa封装2_42_si ), .Cin(undriven_43), .Xi(undriven_41),
    .Yi(undriven_42));
  \一位全加器FA封装2  \u_一位全加器fa封装2_43  (
    .Cout(\一位全加器fa封装2_43_cout ), .Si(\一位全加器fa封装2_43_si ), .Cin(\一位全加器fa封装2_51_cout [0]),
    .Xi(\一位全加器fa封装2_44_si ), .Yi(\一位全加器fa封装2_51_cout [1]));
  \一位全加器FA封装2  \u_一位全加器fa封装2_44  (
    .Cout(\一位全加器fa封装2_44_cout [0]), .Si(\一位全加器fa封装2_44_si ), .Cin(\一位全加器fa封装2_52_cout ),
    .Xi(\一位全加器fa封装2_45_si ), .Yi(\一位全加器fa封装2_46_si ));
  \一位全加器FA封装2  \u_一位全加器fa封装2_45  (
    .Cout(\一位全加器fa封装2_45_cout ), .Si(\一位全加器fa封装2_45_si ), .Cin(\一位全加器fa封装2_49_si ), .Xi(\一位全加器fa封装2_42_si ),
    .Yi(\一位全加器fa封装2_47_si ));
  \一位全加器FA封装2  \u_一位全加器fa封装2_46  (
    .Cout(\一位全加器fa封装2_44_cout [1]), .Si(\一位全加器fa封装2_46_si ), .Cin(\一位全加器fa封装2_56_cout [0]),
    .Xi(\一位全加器fa封装2_56_cout [2]), .Yi(\一位全加器fa封装2_56_cout [1]));
  \一位全加器FA封装2  \u_一位全加器fa封装2_47  (
    .Cout(\一位全加器fa封装2_49_cout [1]), .Si(\一位全加器fa封装2_47_si ), .Cin(undriven_46), .Xi(undriven_44),
    .Yi(undriven_45));
  \一位全加器FA封装2  \u_一位全加器fa封装2_48  ();  // open: Cout, Si, Cin, Xi, Yi
  shape shape_4 ();
  \一位全加器FA封装2  \u_一位全加器fa封装2_49  (
    .Cout(\一位全加器fa封装2_49_cout [0]), .Si(\一位全加器fa封装2_49_si ), .Cin(1'b0), .Xi(undriven_47), .Yi(undriven_48));
  \一位全加器FA封装2  \u_一位全加器fa封装2_50  (
    .Cout(\一位全加器fa封装2_50_cout ), .Si(\一位全加器fa封装2_50_si ), .Cin(\一位全加器fa封装2_58_cout [0]),
    .Xi(\一位全加器fa封装2_51_si ), .Yi(\一位全加器fa封装2_58_cout [1]));
  \一位全加器FA封装2  \u_一位全加器fa封装2_51  (
    .Cout(\一位全加器fa封装2_51_cout [0]), .Si(\一位全加器fa封装2_51_si ), .Cin(\一位全加器fa封装2_59_cout ),
    .Xi(\一位全加器fa封装2_52_si ), .Yi(\一位全加器fa封装2_55_si ));
  \一位全加器FA封装2  \u_一位全加器fa封装2_52  (
    .Cout(\一位全加器fa封装2_52_cout ), .Si(\一位全加器fa封装2_52_si ), .Cin(\一位全加器fa封装2_56_si ), .Xi(\一位全加器fa封装2_53_si ),
    .Yi(\一位全加器fa封装2_54_si ));
  \一位全加器FA封装2  \u_一位全加器fa封装2_53  (
    .Cout(\一位全加器fa封装2_56_cout [2]), .Si(\一位全加器fa封装2_53_si ), .Cin(undriven_51), .Xi(undriven_49),
    .Yi(undriven_50));
  \一位全加器FA封装2  \u_一位全加器fa封装2_54  (
    .Cout(\一位全加器fa封装2_56_cout [1]), .Si(\一位全加器fa封装2_54_si ), .Cin(undriven_54), .Xi(undriven_52),
    .Yi(undriven_53));
  \一位全加器FA封装2  \u_一位全加器fa封装2_55  (
    .Cout(\一位全加器fa封装2_51_cout [1]), .Si(\一位全加器fa封装2_55_si ), .Cin(\一位全加器fa封装2_64_cout [0]),
    .Xi(\一位全加器fa封装2_64_cout [2]), .Yi(\一位全加器fa封装2_64_cout [1]));
  \一位全加器FA封装2  \u_一位全加器fa封装2_56  (
    .Cout(\一位全加器fa封装2_56_cout [0]), .Si(\一位全加器fa封装2_56_si ), .Cin(1'b0), .Xi(undriven_55), .Yi(undriven_56));
  \一位全加器FA封装2  \u_一位全加器fa封装2_57  ();  // open: Cout, Si, Cin, Xi, Yi
  \一位全加器FA封装2  \u_一位全加器fa封装2_58  (
    .Cout(\一位全加器fa封装2_58_cout [0]), .Si(\一位全加器fa封装2_58_si ), .Cin(\一位全加器fa封装2_66_cout ),
    .Xi(\一位全加器fa封装2_59_si ), .Yi(\一位全加器fa封装2_62_si ));
  \一位全加器FA封装2  \u_一位全加器fa封装2_59  (
    .Cout(\一位全加器fa封装2_59_cout ), .Si(\一位全加器fa封装2_59_si ), .Cin(\一位全加器fa封装2_64_si ), .Xi(\一位全加器fa封装2_60_si ),
    .Yi(\一位全加器fa封装2_63_si ));
  \一位全加器FA封装2  \u_一位全加器fa封装2_60  (
    .Cout(\一位全加器fa封装2_64_cout [2]), .Si(\一位全加器fa封装2_60_si ), .Cin(undriven_59), .Xi(undriven_57),
    .Yi(undriven_58));
  shape shape_5 ();
  \一位全加器FA封装2  \u_一位全加器fa封装2_61  (
    .Cout(\一位全加器fa封装2_61_cout ), .Si(\一位全加器fa封装2_61_si ), .Cin(\一位全加器fa封装2_69_cout [0]),
    .Xi(\一位全加器fa封装2_58_si ), .Yi(\一位全加器fa封装2_69_cout [1]));
  \一位全加器FA封装2  \u_一位全加器fa封装2_62  (
    .Cout(\一位全加器fa封装2_58_cout [1]), .Si(\一位全加器fa封装2_62_si ), .Cin(\一位全加器fa封装2_72_cout [0]),
    .Xi(\一位全加器fa封装2_72_cout [2]), .Yi(\一位全加器fa封装2_72_cout [1]));
  \一位全加器FA封装2  \u_一位全加器fa封装2_63  (
    .Cout(\一位全加器fa封装2_64_cout [1]), .Si(\一位全加器fa封装2_63_si ), .Cin(undriven_62), .Xi(undriven_60),
    .Yi(undriven_61));
  \一位全加器FA封装2  \u_一位全加器fa封装2_64  (
    .Cout(\一位全加器fa封装2_64_cout [0]), .Si(\一位全加器fa封装2_64_si ), .Cin(1'b0), .Xi(undriven_63), .Yi(undriven_64));
  \一位全加器FA封装2  \u_一位全加器fa封装2_65  ();  // open: Cout, Si, Cin, Xi, Yi
  \一位全加器FA封装2  \u_一位全加器fa封装2_66  (
    .Cout(\一位全加器fa封装2_66_cout ), .Si(\一位全加器fa封装2_66_si ), .Cin(\一位全加器fa封装2_72_si ), .Xi(\一位全加器fa封装2_67_si ),
    .Yi(\一位全加器fa封装2_71_si ));
  \一位全加器FA封装2  \u_一位全加器fa封装2_67  (
    .Cout(\一位全加器fa封装2_72_cout [2]), .Si(\一位全加器fa封装2_67_si ), .Cin(undriven_67), .Xi(undriven_65),
    .Yi(undriven_66));
  \一位全加器FA封装2  \u_一位全加器fa封装2_68  (
    .Cout(\一位全加器fa封装2_68_cout ), .Si(\一位全加器fa封装2_68_si ), .Cin(\一位全加器fa封装2_76_cout [0]),
    .Xi(\一位全加器fa封装2_69_si ), .Yi(\一位全加器fa封装2_76_cout [1]));
  \一位全加器FA封装2  \u_一位全加器fa封装2_69  (
    .Cout(\一位全加器fa封装2_69_cout [0]), .Si(\一位全加器fa封装2_69_si ), .Cin(\一位全加器fa封装2_77_cout ),
    .Xi(\一位全加器fa封装2_66_si ), .Yi(\一位全加器fa封装2_70_si ));
  \一位全加器FA封装2  \u_一位全加器fa封装2_70  (
    .Cout(\一位全加器fa封装2_69_cout [1]), .Si(\一位全加器fa封装2_70_si ), .Cin(\一位全加器fa封装2_81_cout [0]),
    .Xi(\一位全加器fa封装2_81_cout [2]), .Yi(\一位全加器fa封装2_81_cout [1]));
  \一位全加器FA封装2  \u_一位全加器fa封装2_71  (
    .Cout(\一位全加器fa封装2_72_cout [1]), .Si(\一位全加器fa封装2_71_si ), .Cin(undriven_70), .Xi(undriven_68),
    .Yi(undriven_69));
  \一位全加器FA封装2  \u_一位全加器fa封装2_72  (
    .Cout(\一位全加器fa封装2_72_cout [0]), .Si(\一位全加器fa封装2_72_si ), .Cin(1'b0), .Xi(undriven_71), .Yi(undriven_72));
  \一位全加器FA封装2  \u_一位全加器fa封装2_73  ();  // open: Cout, Si, Cin, Xi, Yi
  \一位全加器FA封装2  \u_一位全加器fa封装2_74  (
    .Cout(\一位全加器fa封装2_81_cout [2]), .Si(\一位全加器fa封装2_74_si ), .Cin(undriven_75), .Xi(undriven_73),
    .Yi(undriven_74));
  \一位全加器FA封装2  \u_一位全加器fa封装2_75  (
    .Cout(\一位全加器fa封装2_75_cout ), .Si(\一位全加器fa封装2_75_si ), .Cin(\一位全加器fa封装2_83_cout [0]),
    .Xi(\一位全加器fa封装2_76_si ), .Yi(\一位全加器fa封装2_83_cout [1]));
  \一位全加器FA封装2  \u_一位全加器fa封装2_76  (
    .Cout(\一位全加器fa封装2_76_cout [0]), .Si(\一位全加器fa封装2_76_si ), .Cin(\一位全加器fa封装2_84_cout ),
    .Xi(\一位全加器fa封装2_77_si ), .Yi(\一位全加器fa封装2_78_si ));
  \一位全加器FA封装2  \u_一位全加器fa封装2_77  (
    .Cout(\一位全加器fa封装2_77_cout ), .Si(\一位全加器fa封装2_77_si ), .Cin(\一位全加器fa封装2_81_si ), .Xi(\一位全加器fa封装2_74_si ),
    .Yi(\一位全加器fa封装2_79_si ));
  \一位全加器FA封装2  \u_一位全加器fa封装2_78  (
    .Cout(\一位全加器fa封装2_76_cout [1]), .Si(\一位全加器fa封装2_78_si ), .Cin(\一位全加器fa封装2_88_cout [0]),
    .Xi(\一位全加器fa封装2_88_cout [2]), .Yi(\一位全加器fa封装2_88_cout [1]));
  \一位全加器FA封装2  \u_一位全加器fa封装2_79  (
    .Cout(\一位全加器fa封装2_81_cout [1]), .Si(\一位全加器fa封装2_79_si ), .Cin(undriven_78), .Xi(undriven_76),
    .Yi(undriven_77));
  \一位全加器FA封装2  \u_一位全加器fa封装2_80  ();  // open: Cout, Si, Cin, Xi, Yi
  shape shape_6 ();
  \一位全加器FA封装2  \u_一位全加器fa封装2_81  (
    .Cout(\一位全加器fa封装2_81_cout [0]), .Si(\一位全加器fa封装2_81_si ), .Cin(1'b0), .Xi(undriven_79), .Yi(undriven_80));
  \一位全加器FA封装2  \u_一位全加器fa封装2_82  (
    .Cout(\一位全加器fa封装2_82_cout ), .Si(\一位全加器fa封装2_82_si ), .Cin(\一位全加器fa封装2_90_cout [0]),
    .Xi(\一位全加器fa封装2_83_si ), .Yi(\一位全加器fa封装2_90_cout [1]));
  \一位全加器FA封装2  \u_一位全加器fa封装2_83  (
    .Cout(\一位全加器fa封装2_83_cout [0]), .Si(\一位全加器fa封装2_83_si ), .Cin(\一位全加器fa封装2_91_cout ),
    .Xi(\一位全加器fa封装2_84_si ), .Yi(\一位全加器fa封装2_87_si ));
  \一位全加器FA封装2  \u_一位全加器fa封装2_84  (
    .Cout(\一位全加器fa封装2_84_cout ), .Si(\一位全加器fa封装2_84_si ), .Cin(\一位全加器fa封装2_88_si ), .Xi(\一位全加器fa封装2_86_si ),
    .Yi(\一位全加器fa封装2_85_si ));
  \一位全加器FA封装2  \u_一位全加器fa封装2_85  (
    .Cout(\一位全加器fa封装2_88_cout [1]), .Si(\一位全加器fa封装2_85_si ), .Cin(undriven_86), .Xi(undriven_84),
    .Yi(undriven_85));
  \一位全加器FA封装2  \u_一位全加器fa封装2_86  (
    .Cout(\一位全加器fa封装2_88_cout [2]), .Si(\一位全加器fa封装2_86_si ), .Cin(undriven_83), .Xi(undriven_81),
    .Yi(undriven_82));
  \一位全加器FA封装2  \u_一位全加器fa封装2_87  (
    .Cout(\一位全加器fa封装2_83_cout [1]), .Si(\一位全加器fa封装2_87_si ), .Cin(\一位全加器fa封装2_95_cout [0]),
    .Xi(\一位全加器fa封装2_95_cout [2]), .Yi(\一位全加器fa封装2_95_cout [1]));
  \一位全加器FA封装2  \u_一位全加器fa封装2_88  (
    .Cout(\一位全加器fa封装2_88_cout [0]), .Si(\一位全加器fa封装2_88_si ), .Cin(1'b0), .Xi(undriven_87), .Yi(undriven_88));
  \一位全加器FA封装2  \u_一位全加器fa封装2_89  ();  // open: Cout, Si, Cin, Xi, Yi
  \一位全加器FA封装2  \u_一位全加器fa封装2_90  (
    .Cout(\一位全加器fa封装2_90_cout [0]), .Si(\一位全加器fa封装2_90_si ), .Cin(\一位全加器fa封装2_98_cout ),
    .Xi(\一位全加器fa封装2_91_si ), .Yi(\一位全加器fa封装2_94_si ));
  \一位全加器FA封装2  \u_一位全加器fa封装2_91  (
    .Cout(\一位全加器fa封装2_91_cout ), .Si(\一位全加器fa封装2_91_si ), .Cin(\一位全加器fa封装2_95_si ), .Xi(\一位全加器fa封装2_92_si ),
    .Yi(\一位全加器fa封装2_96_si ));
  \一位全加器FA封装2  \u_一位全加器fa封装2_92  (
    .Cout(\一位全加器fa封装2_95_cout [2]), .Si(\一位全加器fa封装2_92_si ), .Cin(undriven_91), .Xi(undriven_89),
    .Yi(undriven_90));
  shape shape_7 ();
  \一位全加器FA封装2  \u_一位全加器fa封装2_93  (
    .Cout(\一位全加器fa封装2_93_cout ), .Si(\一位全加器fa封装2_93_si ), .Cin(\一位全加器fa封装2_101_cout [0]),
    .Xi(\一位全加器fa封装2_90_si ), .Yi(\一位全加器fa封装2_101_cout [1]));
  \一位全加器FA封装2  \u_一位全加器fa封装2_94  (
    .Cout(\一位全加器fa封装2_90_cout [1]), .Si(\一位全加器fa封装2_94_si ), .Cin(\一位全加器fa封装2_103_cout [0]),
    .Xi(\一位全加器fa封装2_103_cout [2]), .Yi(\一位全加器fa封装2_103_cout [1]));
  \一位全加器FA封装2  \u_一位全加器fa封装2_95  (
    .Cout(\一位全加器fa封装2_95_cout [0]), .Si(\一位全加器fa封装2_95_si ), .Cin(1'b0), .Xi(undriven_95), .Yi(undriven_96));
  \一位全加器FA封装2  \u_一位全加器fa封装2_96  (
    .Cout(\一位全加器fa封装2_95_cout [1]), .Si(\一位全加器fa封装2_96_si ), .Cin(undriven_94), .Xi(undriven_92),
    .Yi(undriven_93));
  \一位全加器FA封装2  \u_一位全加器fa封装2_97  ();  // open: Cout, Si, Cin, Xi, Yi
  \一位全加器FA封装2  \u_一位全加器fa封装2_98  (
    .Cout(\一位全加器fa封装2_98_cout ), .Si(\一位全加器fa封装2_98_si ), .Cin(\一位全加器fa封装2_103_si ), .Xi(\一位全加器fa封装2_99_si ),
    .Yi(\一位全加器fa封装2_104_si ));
  \一位全加器FA封装2  \u_一位全加器fa封装2_99  (
    .Cout(\一位全加器fa封装2_103_cout [2]), .Si(\一位全加器fa封装2_99_si ), .Cin(undriven_99), .Xi(undriven_97),
    .Yi(undriven_98));
  \一位全加器FA封装2  \u_一位全加器fa封装2_100  (
    .Cout(\一位全加器fa封装2_100_cout ), .Si(\一位全加器fa封装2_100_si ), .Cin(\一位全加器fa封装2_108_cout [0]),
    .Xi(\一位全加器fa封装2_101_si ), .Yi(\一位全加器fa封装2_108_cout [1]));
  \一位全加器FA封装2  \u_一位全加器fa封装2_101  (
    .Cout(\一位全加器fa封装2_101_cout [0]), .Si(\一位全加器fa封装2_101_si ), .Cin(\一位全加器fa封装2_109_cout ),
    .Xi(\一位全加器fa封装2_98_si ), .Yi(\一位全加器fa封装2_102_si ));
  \一位全加器FA封装2  \u_一位全加器fa封装2_102  (
    .Cout(\一位全加器fa封装2_101_cout [1]), .Si(\一位全加器fa封装2_102_si ), .Cin(\一位全加器fa封装2_113_cout [0]),
    .Xi(\一位全加器fa封装2_113_cout [2]), .Yi(\一位全加器fa封装2_113_cout [1]));
  \一位全加器FA封装2  \u_一位全加器fa封装2_103  (
    .Cout(\一位全加器fa封装2_103_cout [0]), .Si(\一位全加器fa封装2_103_si ), .Cin(1'b0), .Xi(undriven_103),
    .Yi(undriven_104));
  \一位全加器FA封装2  \u_一位全加器fa封装2_104  (
    .Cout(\一位全加器fa封装2_103_cout [1]), .Si(\一位全加器fa封装2_104_si ), .Cin(undriven_102), .Xi(undriven_100),
    .Yi(undriven_101));
  \一位全加器FA封装2  \u_一位全加器fa封装2_105  ();  // open: Cout, Si, Cin, Xi, Yi
  \一位全加器FA封装2  \u_一位全加器fa封装2_106  (
    .Cout(\一位全加器fa封装2_113_cout [2]), .Si(\一位全加器fa封装2_106_si ), .Cin(undriven_107), .Xi(undriven_105),
    .Yi(undriven_106));
  \一位全加器FA封装2  \u_一位全加器fa封装2_107  (
    .Cout(\一位全加器fa封装2_107_cout ), .Si(\一位全加器fa封装2_107_si ), .Cin(\一位全加器fa封装2_115_cout [0]),
    .Xi(\一位全加器fa封装2_108_si ), .Yi(\一位全加器fa封装2_115_cout [1]));
  \一位全加器FA封装2  \u_一位全加器fa封装2_108  (
    .Cout(\一位全加器fa封装2_108_cout [0]), .Si(\一位全加器fa封装2_108_si ), .Cin(\一位全加器fa封装2_116_cout ),
    .Xi(\一位全加器fa封装2_109_si ), .Yi(\一位全加器fa封装2_110_si ));
  \一位全加器FA封装2  \u_一位全加器fa封装2_109  (
    .Cout(\一位全加器fa封装2_109_cout ), .Si(\一位全加器fa封装2_109_si ), .Cin(\一位全加器fa封装2_113_si ),
    .Xi(\一位全加器fa封装2_106_si ), .Yi(\一位全加器fa封装2_111_si ));
  \一位全加器FA封装2  \u_一位全加器fa封装2_110  (
    .Cout(\一位全加器fa封装2_108_cout [1]), .Si(\一位全加器fa封装2_110_si ), .Cin(\一位全加器fa封装2_120_cout [0]),
    .Xi(\一位全加器fa封装2_120_cout [2]), .Yi(\一位全加器fa封装2_120_cout [1]));
  \一位全加器FA封装2  \u_一位全加器fa封装2_111  (
    .Cout(\一位全加器fa封装2_113_cout [1]), .Si(\一位全加器fa封装2_111_si ), .Cin(undriven_110), .Xi(undriven_108),
    .Yi(undriven_109));
  \一位全加器FA封装2  \u_一位全加器fa封装2_112  ();  // open: Cout, Si, Cin, Xi, Yi
  shape shape_8 ();
  \一位全加器FA封装2  \u_一位全加器fa封装2_113  (
    .Cout(\一位全加器fa封装2_113_cout [0]), .Si(\一位全加器fa封装2_113_si ), .Cin(1'b0), .Xi(undriven_111),
    .Yi(undriven_112));
  \一位全加器FA封装2  \u_一位全加器fa封装2_114  (
    .Cout(\一位全加器fa封装2_114_cout ), .Si(\一位全加器fa封装2_114_si ), .Cin(\一位全加器fa封装2_122_cout [0]),
    .Xi(\一位全加器fa封装2_115_si ), .Yi(\一位全加器fa封装2_122_cout [1]));
  \一位全加器FA封装2  \u_一位全加器fa封装2_115  (
    .Cout(\一位全加器fa封装2_115_cout [0]), .Si(\一位全加器fa封装2_115_si ), .Cin(\一位全加器fa封装2_123_cout ),
    .Xi(\一位全加器fa封装2_116_si ), .Yi(\一位全加器fa封装2_119_si ));
  \一位全加器FA封装2  \u_一位全加器fa封装2_116  (
    .Cout(\一位全加器fa封装2_116_cout ), .Si(\一位全加器fa封装2_116_si ), .Cin(\一位全加器fa封装2_120_si ),
    .Xi(\一位全加器fa封装2_118_si ), .Yi(\一位全加器fa封装2_117_si ));
  \一位全加器FA封装2  \u_一位全加器fa封装2_117  (
    .Cout(\一位全加器fa封装2_120_cout [1]), .Si(\一位全加器fa封装2_117_si ), .Cin(undriven_118), .Xi(undriven_116),
    .Yi(undriven_117));
  \一位全加器FA封装2  \u_一位全加器fa封装2_118  (
    .Cout(\一位全加器fa封装2_120_cout [2]), .Si(\一位全加器fa封装2_118_si ), .Cin(undriven_115), .Xi(undriven_113),
    .Yi(undriven_114));
  \一位全加器FA封装2  \u_一位全加器fa封装2_119  (
    .Cout(\一位全加器fa封装2_115_cout [1]), .Si(\一位全加器fa封装2_119_si ), .Cin(\一位全加器fa封装2_128_cout [0]),
    .Xi(\一位全加器fa封装2_128_cout [2]), .Yi(\一位全加器fa封装2_128_cout [1]));
  \一位全加器FA封装2  \u_一位全加器fa封装2_120  (
    .Cout(\一位全加器fa封装2_120_cout [0]), .Si(\一位全加器fa封装2_120_si ), .Cin(1'b0), .Xi(undriven_119),
    .Yi(undriven_120));
  \一位全加器FA封装2  \u_一位全加器fa封装2_121  ();  // open: Cout, Si, Cin, Xi, Yi
  \一位全加器FA封装2  \u_一位全加器fa封装2_122  (
    .Cout(\一位全加器fa封装2_122_cout [0]), .Si(\一位全加器fa封装2_122_si ), .Cin(undriven_125), .Xi(\一位全加器fa封装2_123_si ),
    .Yi(\一位全加器fa封装2_126_si ));
  \一位全加器FA封装2  \u_一位全加器fa封装2_123  (
    .Cout(\一位全加器fa封装2_123_cout ), .Si(\一位全加器fa封装2_123_si ), .Cin(\一位全加器fa封装2_128_si ),
    .Xi(\一位全加器fa封装2_124_si ), .Yi(\一位全加器fa封装2_127_si ));
  \一位全加器FA封装2  \u_一位全加器fa封装2_124  (
    .Cout(\一位全加器fa封装2_128_cout [2]), .Si(\一位全加器fa封装2_124_si ), .Cin(undriven_123), .Xi(undriven_121),
    .Yi(undriven_122));
  \一位全加器FA封装2  \u_一位全加器fa封装2_125  (
    .Cout(\一位全加器fa封装2_125_cout ), .Si(\一位全加器fa封装2_125_si ), .Cin(undriven_131[0]), .Xi(\一位全加器fa封装2_122_si ),
    .Yi(undriven_131[1]));
  \一位全加器FA封装2  \u_一位全加器fa封装2_126  (
    .Cout(\一位全加器fa封装2_122_cout [1]), .Si(\一位全加器fa封装2_126_si ), .Cin(undriven_129[0]), .Xi(undriven_129[2]),
    .Yi(undriven_129[1]));
  \一位全加器FA封装2  \u_一位全加器fa封装2_127  (
    .Cout(\一位全加器fa封装2_128_cout [1]), .Si(\一位全加器fa封装2_127_si ), .Cin(undriven_127), .Xi(undriven_124),
    .Yi(undriven_126));
  \一位全加器FA封装2  \u_一位全加器fa封装2_128  (
    .Cout(\一位全加器fa封装2_128_cout [0]), .Si(\一位全加器fa封装2_128_si ), .Cin(1'b0), .Xi(undriven_128),
    .Yi(undriven_130));

  // Notes on the sheet:
  //   16
  //   15
  //   14
  //   13
  //   12
  //   11
  //   10
  //   9
  //   8
  //   7
  //   6
  //   5
  //   2^4
  //   2^2
  //   2^3
  //   2^2
  //   2^2
  //   2^1
  //   2^1
  //   2^1
  //   2^1
  //   2^1
  //   2^0
  //   2^0
  //   2^0
endmodule

module multi (
  input  x,
  input  y,
  output out,
  output out_2
);
endmodule
