// Logisim project 流水线日志记录.circ as structural Verilog: 1 circuit, main circuit main
module main (
);

  wire [31:0] and_1_out, and_2_out, and_3_out, and_4_out, and_5_out, Count, EX_PC, ID_PC, IF_PC, MEM_PC,
       WB_PC;

  // Probe on Count
  assign and_1_out = IF_PC & 32'hfff;  // AND_Gate and_1, 32 bits wide
  assign and_2_out = ID_PC & 32'hfff;  // AND_Gate and_2, 32 bits wide
  assign and_3_out = EX_PC & 32'hfff;  // AND_Gate and_3, 32 bits wide
  assign and_4_out = MEM_PC & 32'hfff;  // AND_Gate and_4, 32 bits wide
  assign and_5_out = WB_PC & 32'hfff;  // AND_Gate and_5, 32 bits wide
  // Probe on and_1_out
  // Probe on and_2_out
  // Probe on and_3_out
  // Probe on and_4_out
  // Probe on and_5_out
endmodule
